// Logisim project cpu24.circ as structural Verilog: 22 circuits, main circuit ◇单周期MIPS
module \单周期MIPS  (
  output RegWrite,
  output MemWrite,
  output [31:0] PC,
  output [31:0] IR,
  output [31:0] RDin,
  output [31:0] MDin,
  output [31:0] LedData
);

  wire and_1_out, and_3_out, and_4_out, CLK, comparator_1_eq, Go, IR1, IR2, IR3, JAL, JMP, JR,
       mips_alu_1_equal, not_1_out, not_2_out, not_3_out, or_1_out, SignedExt, stop, Syscall, W1, W2, W3,
       \单周期硬布线控制器_1_alu_src , \单周期硬布线控制器_1_beq , \单周期硬布线控制器_1_bne , \单周期硬布线控制器_1_memtoreg ,
       \单周期硬布线控制器_1_regdst ;
  wire [3:0] \单周期硬布线控制器_1_alu_op ;
  wire [4:0] multiplexer_4_out, multiplexer_5_out, multiplexer_6_out, multiplexer_7_out;
  wire [15:0] \总周期数 ;
  wire [27:0] PC_4;
  wire [31:0] adder_2_out, bit_extender_1_out, bit_extender_2_out, bit_extender_3_out, JMP_PC, JR_PC,
       mips_alu_1_result, multiplexer_1_out, multiplexer_2_out, multiplexer_3_out, multiplexer_8_out,
       multiplexer_9_out, multiplexer_11_out, ram_1_data, shifter_2_out;
  wire [31:28] shifter_1_out;

  Clock #(.highDuration(1), .lowDuration(1)) clock_1 (.out(CLK));
  Button _1 (.out(IR1));
  Button _2 (.out(IR2));
  Button _3 (.out(IR3));
  Button \u_继续运行  (.out(Go));
  LED #(.active("true")) led_1 (.in(W1));
  LED #(.active("true")) led_2 (.in(W2));
  LED #(.active("true")) led_3 (.in(W3));
  Multiplexer #(.select(1), .width(32), .disabled("Z"), .enable("false")) multiplexer_1 (
    .in0({JMP_PC[31:28], PC_4}), .in1(adder_2_out), .out(multiplexer_1_out), .sel(or_1_out));
  Hex_Digit_Display hex_digit_display_1 (.value(LedData[31:28]));  // open: dp
  Multiplexer #(.select(2), .width(32), .disabled("Z"), .enable("false")) multiplexer_2 (
    .in0(multiplexer_1_out), .in1(JMP_PC), .in2(JR_PC), .in3(JR_PC), .out(multiplexer_2_out), .sel({JR, JMP}));
  not not_1 (not_1_out, stop);
  Comparator #(.width(32), .mode("twosComplement")) comparator_1 (
    .a(JR_PC), .b(32'h22), .eq(comparator_1_eq));  // open: gt, lt
  not not_2 (not_2_out, comparator_1_eq);
  Hex_Digit_Display hex_digit_display_2 (.value(LedData[27:24]));  // open: dp
  Hex_Digit_Display hex_digit_display_3 (.value(LedData[23:20]));  // open: dp
  Register #(.width(32), .trigger("rising"), .Select("low")) u_PC (
    .D(multiplexer_2_out), .en(not_1_out), .Q(PC), .clk(CLK), .clr(1'b0));
  Counter #(.width(16), .max('hffff), .ongoal("wrap"), .trigger("rising"), .behavior("old")) counter_1 (
    .D({16{1'b0}}), .count(not_1_out), .Q(\总周期数 ), .clk(CLK), .clr(1'b0));  // open: load, carry, preset
  and and_1 (and_1_out, Syscall, comparator_1_eq);
  and and_2 (stop, not_2_out, Syscall);
  Hex_Digit_Display hex_digit_display_4 (.value(LedData[15:12]));  // open: dp
  Hex_Digit_Display hex_digit_display_5 (.value(LedData[19:16]));  // open: dp
  Hex_Digit_Display hex_digit_display_6 (.value(LedData[7:4]));  // open: dp
  Hex_Digit_Display hex_digit_display_7 (.value(LedData[11:8]));  // open: dp
  // Probe on \总周期数 
  Adder #(.width(32)) adder_1 (.a(PC), .b(32'h4), .out({JMP_PC[31:28], PC_4}), .cin(1'b0));  // open: cout
  Multiplexer #(.select(1), .width(32), .disabled("Z"), .enable("false")) multiplexer_3 (
    .in1(MDin), .out(multiplexer_3_out), .sel(and_1_out));  // open: in0
  Hex_Digit_Display hex_digit_display_8 (.value(LedData[3:0]));  // open: dp
  Register #(.width(32), .trigger("rising"), .Select("low")) PC_2 (
    .D(multiplexer_3_out), .Q(LedData), .clk(CLK));  // open: en, clr
  ROM #(.addrWidth(10), .dataWidth(32), .Select("high")) rom_1 (.addr(PC[11:2]), .data(IR));
  \单周期硬布线控制器  \u_单周期硬布线控制器_1  (
    .Func(IR[5:0]), .OP(IR[31:26]), .ALU_OP(\单周期硬布线控制器_1_alu_op ), .MemToReg(\单周期硬布线控制器_1_memtoreg ),
    .MemWrite(MemWrite), .ALU_SRC(\单周期硬布线控制器_1_alu_src ), .RegWrite(RegWrite), .SysCALL(Syscall),
    .SignedExt(SignedExt), .RegDst(\单周期硬布线控制器_1_regdst ), .JR(JR), .JMP(JMP), .Beq(\单周期硬布线控制器_1_beq ),
    .JAL(JAL), .Bne(\单周期硬布线控制器_1_bne ));
  Multiplexer #(.select(1), .width(5), .disabled("Z"), .enable("false")) multiplexer_4 (
    .in0(IR[20:16]), .in1(IR[15:11]), .out(multiplexer_4_out), .sel(\单周期硬布线控制器_1_regdst ));
  assign bit_extender_1_out = {{6{1'b0}}, IR[25:0]};  // Bit_Extender bit_extender_1
  assign bit_extender_2_out = {{16{1'b0}}, IR[15:0]};  // Bit_Extender bit_extender_2
  assign bit_extender_3_out = {{16{IR[15]}}, IR[15:0]};  // Bit_Extender bit_extender_3
  Multiplexer #(.select(1), .width(5), .disabled("Z"), .enable("false")) multiplexer_5 (
    .in0(IR[25:21]), .in1(5'b00010), .out(multiplexer_5_out), .sel(Syscall));
  Multiplexer #(.select(1), .width(5), .disabled("Z"), .enable("false")) multiplexer_6 (
    .in0(IR[20:16]), .in1(5'b00100), .out(multiplexer_6_out), .sel(Syscall));
  Multiplexer #(.select(1), .width(5), .disabled("Z"), .enable("false")) multiplexer_7 (
    .in0(multiplexer_4_out), .in1({5{1'b1}}), .out(multiplexer_7_out), .sel(JAL));
  MIPS_Regifile mips_regifile_1 (
    .Din(RDin), .Clk(CLK), .R1(JR_PC), .R2(MDin), .WE(RegWrite), .W_num(multiplexer_7_out),
    .R1_num(multiplexer_5_out), .R2_num(multiplexer_6_out));
  Shifter #(.width(32), .shift("ll")) shifter_1 (
    .in(bit_extender_1_out), .\dist (5'b00010), .out({shifter_1_out, JMP_PC[27:0]}));
  Multiplexer #(.select(1), .width(32), .disabled("Z"), .enable("false")) multiplexer_8 (
    .in0(bit_extender_2_out), .in1(bit_extender_3_out), .out(multiplexer_8_out), .sel(SignedExt));
  Shifter #(.width(32), .shift("ll")) shifter_2 (.in(bit_extender_3_out), .\dist (5'b00010), .out(shifter_2_out));
  and and_3 (and_3_out, \单周期硬布线控制器_1_beq , mips_alu_1_equal);
  Multiplexer #(.select(1), .width(32), .disabled("Z"), .enable("false")) multiplexer_9 (
    .in0(MDin), .in1(multiplexer_8_out), .out(multiplexer_9_out), .sel(\单周期硬布线控制器_1_alu_src ));
  Adder #(.width(32)) adder_2 (
    .a(shifter_2_out), .b({JMP_PC[31:28], PC_4}), .out(adder_2_out), .cin(1'b0));  // open: cout
  or or_1 (or_1_out, and_3_out, and_4_out);
  and and_4 (and_4_out, \单周期硬布线控制器_1_bne , not_3_out);
  not not_3 (not_3_out, mips_alu_1_equal);
  MIPS_ALU mips_alu_1 (
    .X(JR_PC), .Y(multiplexer_9_out), .AluOP(\单周期硬布线控制器_1_alu_op ), .Equal(mips_alu_1_equal),
    .Result(mips_alu_1_result), .shamt(IR[10:6]));  // open: Result_2
  Multiplexer #(.select(1), .width(32), .disabled("Z"), .enable("false")) multiplexer_10 (
    .in0(multiplexer_11_out), .in1({JMP_PC[31:28], PC_4}), .out(RDin), .sel(JAL));
  Multiplexer #(.select(1), .width(32), .disabled("Z"), .enable("false")) multiplexer_11 (
    .in0(mips_alu_1_result), .in1(ram_1_data), .out(multiplexer_11_out), .sel(\单周期硬布线控制器_1_memtoreg ));
  RAM #(.addrWidth(10), .dataWidth(32), .bus("separate"), .Select("high")) ram_1 (
    .addr(mips_alu_1_result[11:2]), .din(MDin), .data(ram_1_data), .str(MemWrite), .sel(1'b1), .clk(CLK),
    .clr(1'b0));  // open: ld

  // Other names for the same wires on the sheet: a0[31:0] = MDin; PC_4[31:28] = JMP_PC[31:28]; v0[31:0] = JR_PC

  // Notes on the sheet:
  //   中断源
  //   中断等待指示
  //   总复位信号应将除ROM以外所有存储组件全部清零
  //   数码管输出
  //   数码管输出应该用寄存器锁存，否则显示数据只能一闪而过
  //   指令存储器
  //   JMP
  //   JR
  //   OP
  //   Func
  //   rs
  //   contents of rom_1 (hex, n*v repeats v):
  //   20110001 8000c05 20110001 20120002 20130003 8000c09 20110001 20120002 20130003 8000c0d 20110001
  //   20120002 20130003 8000c11 20110001 20120002 20130003 c000cb8 20100001 20110001 118fc0 112020
  //   20020022 c 118882 12200001 8000c15 112020 20020022 c 20110001 118880 112020 20020022 c 12200001
  //   8000c1f 20110001 118fc0 112020 20020022 c 1188c3 112020 20020022 c 118903 112020 20020022 c 118903
  //   112020 20020022 c 118903 112020 20020022 c 118903 112020 20020022 c 118903 112020 20020022 c 118903
  //   112020 20020022 c 118903 112020 20020022 c 20100001 109fc0 139fc3 8021 2012000c 24160003 26100001
  //   3210000f 20080008 20090001 139900 2709825 132020 20020022 c 1094022 1500fff9 22100001 2018000f
  //   2188024 108700 20080008 20090001 139902 2709825 132021 20020022 c 1094022 1500fff9 108702 2c9b022
  //   12c00001 8000c50 4020 1084027 84400 3508ffff 82021 20020022 c 2010ffff 20110000 ae300000 22100001
  //   22310004 ae300000 22100001 22310004 ae300000 22100001 22310004 ae300000 22100001 22310004 ae300000
  //   22100001 22310004 ae300000 22100001 22310004 ae300000 22100001 22310004 ae300000 22100001 22310004
  //   ae300000 22100001 22310004 ae300000 22100001 22310004 ae300000 22100001 22310004 ae300000 22100001
  //   22310004 ae300000 22100001 22310004 ae300000 22100001 22310004 ae300000 22100001 22310004 ae300000
  //   22100001 22310004 22100001 8020 2011003c 8e130000 8e340000 274402a 11000002 ae330000 ae140000
  //   2231fffc 1611fff8 102020 20020022 c 22100004 2011003c 1611fff2 20020032 c 20100000 22100001 102020
  //   20020022 c 22100002 102020 20020022 c 22100003 102020 20020022 c 22100004 102020 20020022 c 22100005
  //   102020 20020022 c 22100006 102020 20020022 c 22100007 102020 20020022 c 22100008 102020 20020022
  //   20020022 c 3e00008
  //   rt
  //   rd
  //   shamt
  //   Beq
  //   Bne
  //   JAL
  //   RegDst
  //   MemToReg
  //   MemWrite
  //   AluOP
  //   AluSrcB
  //   RegWrite
  //   为方便自动评测，需要输出PC，IR，寄存器文件写入端口RDin，内存写入端口MDin等信号
endmodule

// 单周期硬布线控制器
module \单周期硬布线控制器  (
  input  [5:0] OP,
  input  [5:0] Func,
  output [3:0] ALU_OP,
  output MemToReg,
  output MemWrite,
  output ALU_SRC,
  output RegWrite,
  output SysCALL,
  output SignedExt,
  output RegDst,
  output Beq,
  output Bne,
  output JR,
  output JMP,
  output JAL
);

  \运算控制器自动生成  \u_运算控制器自动生成_1  (
    .OP0(OP[0]), .OP1(OP[1]), .OP2(OP[2]), .OP3(OP[3]), .OP4(OP[4]), .OP5(OP[5]), .F0(Func[0]), .F1(Func[1]),
    .F2(Func[2]), .F3(Func[3]), .F4(Func[4]), .F5(Func[5]), .S0(ALU_OP[0]), .S1(ALU_OP[1]), .S2(ALU_OP[2]),
    .S3(ALU_OP[3]));
  \控制信号自动生成  \u_控制信号自动生成_1  (
    .OP0(OP[0]), .OP1(OP[1]), .OP2(OP[2]), .OP3(OP[3]), .OP4(OP[4]), .OP5(OP[5]), .F0(Func[0]), .F1(Func[1]),
    .F2(Func[2]), .F3(Func[3]), .F4(Func[4]), .F5(Func[5]), .MemToReg(MemToReg), .MemWrite(MemWrite),
    .ALU_SRC(ALU_SRC), .RegWrite(RegWrite), .SysCALL(SysCALL), .SignedExt(SignedExt), .RegDst(RegDst),
    .BEQ(Beq), .BNE(Bne), .JR(JR), .JUMP(JMP), .JAL(JAL));

  // Other names for the same wires on the sheet: OP_CODE[5:0] = OP

  // Notes on the sheet:
  //   运算器控制器，根据指令生成运算器功能选择信号
  //   控制信号生成，产生数据通路需要的其他控制信号
endmodule

// 运算器控制器
module \运算控制器自动生成  (
  input  OP0,
  input  OP1,
  input  OP2,
  input  OP3,
  input  OP4,
  input  OP5,
  input  F0,
  input  F1,
  input  F2,
  input  F3,
  input  F4,
  input  F5,
  output S0,
  output S1,
  output S2,
  output S3
);

  wire and_1_out, and_2_out, and_3_out, and_4_out, and_5_out, and_6_out, and_7_out, and_8_out, and_9_out,
       and_10_out, and_11_out, and_12_out, and_13_out, and_14_out, and_15_out, and_16_out, and_17_out,
       and_18_out, and_19_out, and_20_out, and_21_out, and_22_out, and_23_out, and_24_out, and_25_out,
       and_26_out, and_27_out, and_28_out, and_29_out, and_30_out, and_31_out, and_32_out, and_33_out,
       and_34_out, not_1_out, not_2_out, not_3_out, not_4_out, not_5_out, not_6_out, not_7_out, not_8_out,
       not_9_out, not_10_out, not_11_out, not_12_out, not_13_out, not_14_out, not_15_out, not_16_out,
       not_17_out, not_18_out, not_19_out, not_20_out, not_21_out, not_22_out, not_23_out, not_24_out,
       not_25_out, not_26_out, not_27_out, not_28_out, not_29_out, not_30_out, not_31_out, not_32_out,
       not_33_out, not_34_out, not_35_out, not_36_out, not_37_out, not_38_out, not_39_out, not_40_out,
       not_41_out, not_42_out, not_43_out, not_44_out, not_45_out, not_46_out, not_47_out, not_48_out,
       not_49_out, not_50_out, not_51_out, not_52_out, not_53_out, not_54_out, not_55_out, not_56_out,
       not_57_out, not_58_out, not_59_out, not_60_out, not_61_out, not_62_out, not_63_out, not_64_out,
       not_65_out, not_66_out, not_67_out, not_68_out, not_69_out, not_70_out, not_71_out, not_72_out,
       not_73_out, not_74_out, not_75_out, not_76_out, not_77_out, not_78_out, not_79_out, not_80_out,
       not_81_out, not_82_out, not_83_out, not_84_out, not_85_out, not_86_out, not_87_out, not_88_out,
       not_89_out, not_90_out, not_91_out, not_92_out, not_93_out, not_94_out, not_95_out, not_96_out,
       not_97_out, not_98_out, not_99_out, not_100_out, not_101_out, not_102_out, not_103_out, not_104_out,
       not_105_out, not_106_out, not_107_out, not_108_out, not_109_out, not_110_out, not_111_out,
       not_112_out, not_113_out, not_114_out, not_115_out, not_116_out, not_117_out, not_118_out,
       not_119_out, not_120_out, not_121_out, not_122_out, not_123_out, not_124_out, not_125_out,
       not_126_out, not_127_out, not_128_out, not_129_out, not_130_out, not_131_out, not_132_out,
       not_133_out, not_134_out, not_135_out, not_136_out, not_137_out, not_138_out, not_139_out,
       not_140_out, not_141_out, not_142_out, not_143_out, not_144_out, not_145_out, not_146_out,
       not_147_out, not_148_out, not_149_out, not_150_out, not_151_out, not_152_out, not_153_out,
       not_154_out, not_155_out, not_156_out, not_157_out, not_158_out, not_159_out, not_160_out,
       not_161_out, not_162_out, not_163_out, not_164_out, not_165_out, not_166_out, not_167_out,
       not_168_out, not_169_out, not_170_out, not_171_out, not_172_out, not_173_out, not_174_out,
       not_175_out, not_176_out, not_177_out, not_178_out, not_179_out, not_180_out, not_181_out,
       not_182_out, not_183_out, not_184_out, not_185_out, not_186_out, not_187_out, not_188_out,
       not_189_out, not_190_out, not_191_out, not_192_out, not_193_out, not_194_out, not_195_out,
       not_196_out, not_197_out, not_198_out, not_199_out, not_200_out, not_201_out, not_202_out,
       not_203_out, not_204_out, not_205_out, not_206_out, not_207_out, not_208_out, not_209_out,
       not_210_out, not_211_out, not_212_out, not_213_out, not_214_out, not_215_out, not_216_out,
       not_217_out, not_218_out, not_219_out, not_220_out, not_221_out, not_222_out, not_223_out,
       not_224_out, not_225_out, not_226_out, not_227_out, not_228_out, not_229_out, not_230_out,
       not_231_out, not_232_out, not_233_out, not_234_out, not_235_out, not_236_out;

  not not_1 (not_1_out, OP5);
  not not_2 (not_2_out, OP4);
  not not_3 (not_3_out, OP3);
  not not_4 (not_4_out, OP2);
  not not_5 (not_5_out, OP1);
  not not_6 (not_6_out, OP0);
  not not_7 (not_7_out, F5);
  not not_8 (not_8_out, F4);
  not not_9 (not_9_out, F3);
  not not_10 (not_10_out, F2);
  not not_11 (not_11_out, OP5);
  not not_12 (not_12_out, OP4);
  not not_13 (not_13_out, OP3);
  not not_14 (not_14_out, OP2);
  not not_15 (not_15_out, OP1);
  not not_16 (not_16_out, OP0);
  not not_17 (not_17_out, F4);
  not not_18 (not_18_out, F3);
  not not_19 (not_19_out, F2);
  not not_20 (not_20_out, F1);
  not not_21 (not_21_out, F0);
  not not_22 (not_22_out, OP5);
  not not_23 (not_23_out, OP4);
  not not_24 (not_24_out, OP3);
  not not_25 (not_25_out, OP2);
  not not_26 (not_26_out, OP1);
  not not_27 (not_27_out, OP0);
  not not_28 (not_28_out, F4);
  not not_29 (not_29_out, F3);
  not not_30 (not_30_out, F2);
  not not_31 (not_31_out, F1);
  not not_32 (not_32_out, OP5);
  not not_33 (not_33_out, OP4);
  not not_34 (not_34_out, OP3);
  not not_35 (not_35_out, OP2);
  not not_36 (not_36_out, OP1);
  not not_37 (not_37_out, OP0);
  not not_38 (not_38_out, F4);
  not not_39 (not_39_out, F3);
  not not_40 (not_40_out, F1);
  not not_41 (not_41_out, F0);
  not not_42 (not_42_out, OP5);
  not not_43 (not_43_out, OP4);
  not not_44 (not_44_out, OP3);
  not not_45 (not_45_out, OP2);
  not not_46 (not_46_out, OP1);
  not not_47 (not_47_out, OP0);
  not not_48 (not_48_out, F4);
  not not_49 (not_49_out, F2);
  not not_50 (not_50_out, F0);
  not not_51 (not_51_out, OP5);
  not not_52 (not_52_out, OP4);
  not not_53 (not_53_out, OP2);
  not not_54 (not_54_out, OP1);
  not not_55 (not_55_out, OP0);
  not not_56 (not_56_out, OP5);
  not not_57 (not_57_out, OP4);
  not not_58 (not_58_out, OP1);
  not not_59 (not_59_out, OP0);
  not not_60 (not_60_out, OP5);
  not not_61 (not_61_out, OP4);
  not not_62 (not_62_out, OP2);
  not not_63 (not_63_out, OP1);
  not not_64 (not_64_out, OP5);
  not not_65 (not_65_out, OP4);
  not not_66 (not_66_out, OP2);
  not not_67 (not_67_out, OP0);
  not not_68 (not_68_out, OP4);
  not not_69 (not_69_out, OP3);
  not not_70 (not_70_out, OP2);
  not not_71 (not_71_out, OP4);
  not not_72 (not_72_out, OP2);
  not not_73 (not_73_out, OP5);
  not not_74 (not_74_out, OP4);
  not not_75 (not_75_out, OP3);
  not not_76 (not_76_out, OP2);
  not not_77 (not_77_out, OP1);
  not not_78 (not_78_out, OP0);
  not not_79 (not_79_out, F5);
  not not_80 (not_80_out, F4);
  not not_81 (not_81_out, F3);
  not not_82 (not_82_out, F2);
  not not_83 (not_83_out, F0);
  not not_84 (not_84_out, OP5);
  not not_85 (not_85_out, OP4);
  not not_86 (not_86_out, OP3);
  not not_87 (not_87_out, OP2);
  not not_88 (not_88_out, OP1);
  not not_89 (not_89_out, OP0);
  not not_90 (not_90_out, F4);
  not not_91 (not_91_out, F3);
  not not_92 (not_92_out, F2);
  not not_93 (not_93_out, F0);
  not not_94 (not_94_out, OP5);
  not not_95 (not_95_out, OP4);
  not not_96 (not_96_out, OP3);
  not not_97 (not_97_out, OP2);
  not not_98 (not_98_out, OP1);
  not not_99 (not_99_out, OP0);
  not not_100 (not_100_out, F4);
  not not_101 (not_101_out, F3);
  not not_102 (not_102_out, F1);
  not not_103 (not_103_out, F0);
  not not_104 (not_104_out, OP5);
  not not_105 (not_105_out, OP4);
  not not_106 (not_106_out, OP3);
  not not_107 (not_107_out, OP2);
  not not_108 (not_108_out, OP1);
  not not_109 (not_109_out, OP0);
  not not_110 (not_110_out, F4);
  not not_111 (not_111_out, F3);
  not not_112 (not_112_out, OP5);
  not not_113 (not_113_out, OP4);
  not not_114 (not_114_out, OP3);
  not not_115 (not_115_out, OP2);
  not not_116 (not_116_out, OP1);
  not not_117 (not_117_out, OP0);
  not not_118 (not_118_out, F4);
  not not_119 (not_119_out, F2);
  not not_120 (not_120_out, F0);
  not not_121 (not_121_out, OP5);
  not not_122 (not_122_out, OP4);
  not not_123 (not_123_out, OP1);
  not not_124 (not_124_out, OP0);
  not not_125 (not_125_out, OP5);
  not not_126 (not_126_out, OP4);
  not not_127 (not_127_out, OP2);
  not not_128 (not_128_out, OP0);
  not not_129 (not_129_out, OP5);
  not not_130 (not_130_out, OP4);
  not not_131 (not_131_out, OP3);
  not not_132 (not_132_out, OP2);
  not not_133 (not_133_out, OP1);
  not not_134 (not_134_out, OP0);
  not not_135 (not_135_out, F4);
  not not_136 (not_136_out, F3);
  not not_137 (not_137_out, F2);
  not not_138 (not_138_out, F1);
  not not_139 (not_139_out, F0);
  not not_140 (not_140_out, OP5);
  not not_141 (not_141_out, OP4);
  not not_142 (not_142_out, OP3);
  not not_143 (not_143_out, OP2);
  not not_144 (not_144_out, OP1);
  not not_145 (not_145_out, OP0);
  not not_146 (not_146_out, F4);
  not not_147 (not_147_out, F3);
  not not_148 (not_148_out, F2);
  not not_149 (not_149_out, F1);
  not not_150 (not_150_out, OP5);
  not not_151 (not_151_out, OP4);
  not not_152 (not_152_out, OP3);
  not not_153 (not_153_out, OP2);
  not not_154 (not_154_out, OP1);
  not not_155 (not_155_out, OP0);
  not not_156 (not_156_out, F4);
  not not_157 (not_157_out, F3);
  not not_158 (not_158_out, F2);
  not not_159 (not_159_out, F0);
  not not_160 (not_160_out, OP5);
  not not_161 (not_161_out, OP4);
  not not_162 (not_162_out, OP3);
  not not_163 (not_163_out, OP2);
  not not_164 (not_164_out, OP1);
  not not_165 (not_165_out, OP0);
  not not_166 (not_166_out, F4);
  not not_167 (not_167_out, F3);
  not not_168 (not_168_out, F1);
  not not_169 (not_169_out, F0);
  not not_170 (not_170_out, OP5);
  not not_171 (not_171_out, OP4);
  not not_172 (not_172_out, OP3);
  not not_173 (not_173_out, OP2);
  not not_174 (not_174_out, OP1);
  not not_175 (not_175_out, OP0);
  not not_176 (not_176_out, F4);
  not not_177 (not_177_out, F2);
  not not_178 (not_178_out, OP5);
  not not_179 (not_179_out, OP4);
  not not_180 (not_180_out, OP2);
  not not_181 (not_181_out, OP1);
  not not_182 (not_182_out, OP0);
  not not_183 (not_183_out, OP5);
  not not_184 (not_184_out, OP4);
  not not_185 (not_185_out, OP1);
  not not_186 (not_186_out, OP0);
  not not_187 (not_187_out, OP5);
  not not_188 (not_188_out, OP4);
  not not_189 (not_189_out, OP2);
  not not_190 (not_190_out, OP1);
  not not_191 (not_191_out, OP4);
  not not_192 (not_192_out, OP3);
  not not_193 (not_193_out, OP2);
  not not_194 (not_194_out, OP4);
  not not_195 (not_195_out, OP2);
  not not_196 (not_196_out, OP5);
  not not_197 (not_197_out, OP4);
  not not_198 (not_198_out, OP3);
  not not_199 (not_199_out, OP2);
  not not_200 (not_200_out, OP1);
  not not_201 (not_201_out, OP0);
  not not_202 (not_202_out, F4);
  not not_203 (not_203_out, F3);
  not not_204 (not_204_out, F1);
  not not_205 (not_205_out, OP5);
  not not_206 (not_206_out, OP4);
  not not_207 (not_207_out, OP3);
  not not_208 (not_208_out, OP2);
  not not_209 (not_209_out, OP1);
  not not_210 (not_210_out, OP0);
  not not_211 (not_211_out, F4);
  not not_212 (not_212_out, F3);
  not not_213 (not_213_out, OP5);
  not not_214 (not_214_out, OP4);
  not not_215 (not_215_out, OP3);
  not not_216 (not_216_out, OP2);
  not not_217 (not_217_out, OP1);
  not not_218 (not_218_out, OP0);
  not not_219 (not_219_out, F4);
  not not_220 (not_220_out, F2);
  not not_221 (not_221_out, F0);
  not not_222 (not_222_out, OP5);
  not not_223 (not_223_out, OP4);
  not not_224 (not_224_out, OP3);
  not not_225 (not_225_out, OP2);
  not not_226 (not_226_out, OP1);
  not not_227 (not_227_out, OP0);
  not not_228 (not_228_out, F4);
  not not_229 (not_229_out, F2);
  not not_230 (not_230_out, OP5);
  not not_231 (not_231_out, OP4);
  not not_232 (not_232_out, OP2);
  not not_233 (not_233_out, OP0);
  not not_234 (not_234_out, OP5);
  not not_235 (not_235_out, OP4);
  not not_236 (not_236_out, OP1);
  and and_1 (and_1_out, not_1_out, not_2_out, not_3_out, not_4_out, not_5_out, not_6_out, not_7_out, not_8_out, not_9_out, not_10_out, F1, F0);
  and and_2 (and_2_out, not_11_out, not_12_out, not_13_out, not_14_out, not_15_out, not_16_out, F5, not_17_out, not_18_out, not_19_out, not_20_out, not_21_out);
  and and_3 (and_3_out, not_22_out, not_23_out, not_24_out, not_25_out, not_26_out, not_27_out, F5, not_28_out, not_29_out, not_30_out, not_31_out, F0);
  and and_4 (and_4_out, not_32_out, not_33_out, not_34_out, not_35_out, not_36_out, not_37_out, F5, not_38_out, not_39_out, F2, not_40_out, not_41_out);
  and and_5 (and_5_out, not_42_out, not_43_out, not_44_out, not_45_out, not_46_out, not_47_out, F5, not_48_out, F3, not_49_out, F1, not_50_out);
  and and_6 (and_6_out, not_51_out, not_52_out, OP3, not_53_out, not_54_out, not_55_out);
  and and_7 (and_7_out, not_56_out, not_57_out, OP3, OP2, not_58_out, not_59_out);
  and and_8 (and_8_out, not_60_out, not_61_out, OP3, not_62_out, not_63_out, OP0);
  and and_9 (and_9_out, not_64_out, not_65_out, OP3, not_66_out, OP1, not_67_out);
  and and_10 (and_10_out, OP5, not_68_out, not_69_out, not_70_out, OP1, OP0);
  and and_11 (and_11_out, OP5, not_71_out, OP3, not_72_out, OP1, OP0);
  and and_12 (and_12_out, not_73_out, not_74_out, not_75_out, not_76_out, not_77_out, not_78_out, not_79_out, not_80_out, not_81_out, not_82_out, F1, not_83_out);
  and and_13 (and_13_out, not_84_out, not_85_out, not_86_out, not_87_out, not_88_out, not_89_out, F5, not_90_out, not_91_out, not_92_out, F1, not_93_out);
  and and_14 (and_14_out, not_94_out, not_95_out, not_96_out, not_97_out, not_98_out, not_99_out, F5, not_100_out, not_101_out, F2, not_102_out, not_103_out);
  and and_15 (and_15_out, not_104_out, not_105_out, not_106_out, not_107_out, not_108_out, not_109_out, F5, not_110_out, not_111_out, F2, F1, F0);
  and and_16 (and_16_out, not_112_out, not_113_out, not_114_out, not_115_out, not_116_out, not_117_out, F5, not_118_out, F3, not_119_out, F1, not_120_out);
  and and_17 (and_17_out, not_121_out, not_122_out, OP3, OP2, not_123_out, not_124_out);
  and and_18 (and_18_out, not_125_out, not_126_out, OP3, not_127_out, OP1, not_128_out);
  and and_19 (and_19_out, not_129_out, not_130_out, not_131_out, not_132_out, not_133_out, not_134_out, F5, not_135_out, not_136_out, not_137_out, not_138_out, not_139_out);
  and and_20 (and_20_out, not_140_out, not_141_out, not_142_out, not_143_out, not_144_out, not_145_out, F5, not_146_out, not_147_out, not_148_out, not_149_out, F0);
  and and_21 (and_21_out, not_150_out, not_151_out, not_152_out, not_153_out, not_154_out, not_155_out, F5, not_156_out, not_157_out, not_158_out, F1, not_159_out);
  and and_22 (and_22_out, not_160_out, not_161_out, not_162_out, not_163_out, not_164_out, not_165_out, F5, not_166_out, not_167_out, F2, not_168_out, not_169_out);
  and and_23 (and_23_out, not_170_out, not_171_out, not_172_out, not_173_out, not_174_out, not_175_out, F5, not_176_out, F3, not_177_out, F1, F0);
  and and_24 (and_24_out, not_178_out, not_179_out, OP3, not_180_out, not_181_out, not_182_out);
  and and_25 (and_25_out, not_183_out, not_184_out, OP3, OP2, not_185_out, not_186_out);
  and and_26 (and_26_out, not_187_out, not_188_out, OP3, not_189_out, not_190_out, OP0);
  and and_27 (and_27_out, OP5, not_191_out, not_192_out, not_193_out, OP1, OP0);
  and and_28 (and_28_out, OP5, not_194_out, OP3, not_195_out, OP1, OP0);
  and and_29 (and_29_out, not_196_out, not_197_out, not_198_out, not_199_out, not_200_out, not_201_out, F5, not_202_out, not_203_out, F2, not_204_out, F0);
  and and_30 (and_30_out, not_205_out, not_206_out, not_207_out, not_208_out, not_209_out, not_210_out, F5, not_211_out, not_212_out, F2, F1, F0);
  and and_31 (and_31_out, not_213_out, not_214_out, not_215_out, not_216_out, not_217_out, not_218_out, F5, not_219_out, F3, not_220_out, F1, not_221_out);
  and and_32 (and_32_out, not_222_out, not_223_out, not_224_out, not_225_out, not_226_out, not_227_out, F5, not_228_out, F3, not_229_out, F1, F0);
  and and_33 (and_33_out, not_230_out, not_231_out, OP3, not_232_out, OP1, not_233_out);
  and and_34 (and_34_out, not_234_out, not_235_out, OP3, OP2, not_236_out, OP0);
  or or_1 (S0, and_1_out, and_2_out, and_3_out, and_4_out, and_5_out, and_6_out, and_7_out, and_8_out, and_9_out, and_10_out, and_11_out);
  or or_2 (S1, and_12_out, and_13_out, and_14_out, and_15_out, and_16_out, and_17_out, and_18_out);
  or or_3 (S2, and_19_out, and_20_out, and_21_out, and_22_out, and_23_out, and_24_out, and_25_out, and_26_out, and_27_out, and_28_out);
  or or_4 (S3, and_29_out, and_30_out, and_31_out, and_32_out, and_33_out, and_34_out);
endmodule

// 控制信号生成
module \控制信号自动生成  (
  input  OP0,
  input  OP1,
  input  OP2,
  input  OP3,
  input  OP4,
  input  OP5,
  input  F0,
  input  F1,
  input  F2,
  input  F3,
  input  F4,
  input  F5,
  output MemToReg,
  output MemWrite,
  output ALU_SRC,
  output RegWrite,
  output SysCALL,
  output SignedExt,
  output RegDst,
  output BEQ,
  output BNE,
  output JR,
  output JUMP,
  output JAL
);

  wire and_3_out, and_4_out, and_5_out, and_6_out, and_7_out, and_8_out, and_9_out, and_10_out, and_11_out,
       and_12_out, and_13_out, and_15_out, and_16_out, and_17_out, and_18_out, and_19_out, and_20_out,
       and_21_out, and_22_out, and_23_out, and_24_out, and_25_out, and_26_out, and_27_out, and_31_out,
       and_32_out, not_1_out, not_2_out, not_3_out, not_4_out, not_5_out, not_6_out, not_7_out, not_8_out,
       not_9_out, not_10_out, not_11_out, not_12_out, not_13_out, not_14_out, not_15_out, not_16_out,
       not_17_out, not_18_out, not_19_out, not_20_out, not_21_out, not_22_out, not_23_out, not_24_out,
       not_25_out, not_26_out, not_27_out, not_28_out, not_29_out, not_30_out, not_31_out, not_32_out,
       not_33_out, not_34_out, not_35_out, not_36_out, not_37_out, not_38_out, not_39_out, not_40_out,
       not_41_out, not_42_out, not_43_out, not_44_out, not_45_out, not_46_out, not_47_out, not_48_out,
       not_49_out, not_50_out, not_51_out, not_52_out, not_53_out, not_54_out, not_55_out, not_56_out,
       not_57_out, not_58_out, not_59_out, not_60_out, not_61_out, not_62_out, not_63_out, not_64_out,
       not_65_out, not_66_out, not_67_out, not_68_out, not_69_out, not_70_out, not_71_out, not_72_out,
       not_73_out, not_74_out, not_75_out, not_76_out, not_77_out, not_78_out, not_79_out, not_80_out,
       not_81_out, not_82_out, not_83_out, not_84_out, not_85_out, not_86_out, not_87_out, not_88_out,
       not_89_out, not_90_out, not_91_out, not_92_out, not_93_out, not_94_out, not_95_out, not_96_out,
       not_97_out, not_98_out, not_99_out, not_100_out, not_101_out, not_102_out, not_103_out, not_104_out,
       not_105_out, not_106_out, not_107_out, not_108_out, not_109_out, not_110_out, not_111_out,
       not_112_out, not_113_out, not_114_out, not_115_out, not_116_out, not_117_out, not_118_out,
       not_119_out, not_120_out, not_121_out, not_122_out, not_123_out, not_124_out, not_125_out,
       not_126_out, not_127_out, not_128_out, not_129_out, not_130_out, not_131_out, not_132_out,
       not_133_out, not_134_out, not_135_out, not_136_out, not_137_out, not_138_out, not_139_out,
       not_140_out, not_141_out, not_142_out, not_143_out, not_144_out, not_145_out, not_146_out,
       not_147_out, not_148_out, not_149_out, not_150_out, not_151_out, not_152_out, not_153_out,
       not_154_out, not_155_out, not_156_out, not_157_out, not_158_out, not_159_out, not_160_out,
       not_161_out, not_162_out, not_163_out, not_164_out, not_165_out, not_166_out, not_167_out,
       not_168_out, not_169_out, not_170_out, not_171_out, not_172_out, not_173_out, not_174_out,
       not_175_out, not_176_out, not_177_out, not_178_out, not_179_out, not_180_out, not_181_out,
       not_182_out, not_183_out, not_184_out, not_185_out, not_186_out, not_187_out, not_188_out,
       not_189_out, not_190_out, not_191_out, not_192_out, not_193_out, not_194_out, not_195_out;

  not not_1 (not_1_out, OP2);
  not not_2 (not_2_out, OP3);
  not not_3 (not_3_out, OP4);
  not not_4 (not_4_out, OP2);
  not not_5 (not_5_out, OP4);
  not not_6 (not_6_out, OP0);
  not not_7 (not_7_out, OP2);
  not not_8 (not_8_out, OP4);
  not not_9 (not_9_out, OP5);
  not not_10 (not_10_out, OP1);
  not not_11 (not_11_out, OP4);
  not not_12 (not_12_out, OP5);
  not not_13 (not_13_out, OP2);
  not not_14 (not_14_out, OP4);
  not not_15 (not_15_out, OP0);
  not not_16 (not_16_out, OP1);
  not not_17 (not_17_out, OP2);
  not not_18 (not_18_out, OP4);
  not not_19 (not_19_out, OP5);
  not not_20 (not_20_out, F0);
  not not_21 (not_21_out, F2);
  not not_22 (not_22_out, F3);
  not not_23 (not_23_out, F4);
  not not_24 (not_24_out, OP0);
  not not_25 (not_25_out, OP1);
  not not_26 (not_26_out, OP2);
  not not_27 (not_27_out, OP4);
  not not_28 (not_28_out, OP5);
  not not_29 (not_29_out, F1);
  not not_30 (not_30_out, F3);
  not not_31 (not_31_out, F4);
  not not_32 (not_32_out, OP0);
  not not_33 (not_33_out, OP1);
  not not_34 (not_34_out, OP2);
  not not_35 (not_35_out, OP4);
  not not_36 (not_36_out, OP5);
  not not_37 (not_37_out, F2);
  not not_38 (not_38_out, F3);
  not not_39 (not_39_out, F4);
  not not_40 (not_40_out, F5);
  not not_41 (not_41_out, OP0);
  not not_42 (not_42_out, OP1);
  not not_43 (not_43_out, OP2);
  not not_44 (not_44_out, OP4);
  not not_45 (not_45_out, OP5);
  not not_46 (not_46_out, F2);
  not not_47 (not_47_out, F4);
  not not_48 (not_48_out, OP0);
  not not_49 (not_49_out, OP1);
  not not_50 (not_50_out, OP2);
  not not_51 (not_51_out, OP4);
  not not_52 (not_52_out, OP5);
  not not_53 (not_53_out, F3);
  not not_54 (not_54_out, F4);
  not not_55 (not_55_out, OP0);
  not not_56 (not_56_out, OP2);
  not not_57 (not_57_out, OP4);
  not not_58 (not_58_out, OP5);
  not not_59 (not_59_out, OP1);
  not not_60 (not_60_out, OP4);
  not not_61 (not_61_out, OP5);
  not not_62 (not_62_out, OP2);
  not not_63 (not_63_out, OP3);
  not not_64 (not_64_out, OP4);
  not not_65 (not_65_out, OP0);
  not not_66 (not_66_out, OP1);
  not not_67 (not_67_out, OP2);
  not not_68 (not_68_out, OP3);
  not not_69 (not_69_out, OP4);
  not not_70 (not_70_out, OP5);
  not not_71 (not_71_out, F0);
  not not_72 (not_72_out, F1);
  not not_73 (not_73_out, F4);
  not not_74 (not_74_out, F5);
  not not_75 (not_75_out, OP5);
  not not_76 (not_76_out, OP4);
  not not_77 (not_77_out, OP3);
  not not_78 (not_78_out, OP1);
  not not_79 (not_79_out, OP0);
  not not_80 (not_80_out, OP5);
  not not_81 (not_81_out, OP4);
  not not_82 (not_82_out, OP3);
  not not_83 (not_83_out, OP1);
  not not_84 (not_84_out, OP5);
  not not_85 (not_85_out, OP4);
  not not_86 (not_86_out, OP2);
  not not_87 (not_87_out, OP1);
  not not_88 (not_88_out, OP0);
  not not_89 (not_89_out, OP5);
  not not_90 (not_90_out, OP4);
  not not_91 (not_91_out, OP2);
  not not_92 (not_92_out, OP1);
  not not_93 (not_93_out, OP5);
  not not_94 (not_94_out, OP4);
  not not_95 (not_95_out, OP2);
  not not_96 (not_96_out, OP0);
  not not_97 (not_97_out, OP4);
  not not_98 (not_98_out, OP3);
  not not_99 (not_99_out, OP2);
  not not_100 (not_100_out, OP4);
  not not_101 (not_101_out, OP2);
  not not_102 (not_102_out, OP0);
  not not_103 (not_103_out, OP1);
  not not_104 (not_104_out, OP2);
  not not_105 (not_105_out, OP3);
  not not_106 (not_106_out, OP4);
  not not_107 (not_107_out, OP5);
  not not_108 (not_108_out, F0);
  not not_109 (not_109_out, F1);
  not not_110 (not_110_out, F2);
  not not_111 (not_111_out, F4);
  not not_112 (not_112_out, F5);
  not not_113 (not_113_out, OP0);
  not not_114 (not_114_out, OP1);
  not not_115 (not_115_out, OP2);
  not not_116 (not_116_out, OP3);
  not not_117 (not_117_out, OP4);
  not not_118 (not_118_out, OP5);
  not not_119 (not_119_out, F0);
  not not_120 (not_120_out, F2);
  not not_121 (not_121_out, F3);
  not not_122 (not_122_out, F4);
  not not_123 (not_123_out, OP0);
  not not_124 (not_124_out, OP1);
  not not_125 (not_125_out, OP2);
  not not_126 (not_126_out, OP3);
  not not_127 (not_127_out, OP4);
  not not_128 (not_128_out, OP5);
  not not_129 (not_129_out, F1);
  not not_130 (not_130_out, F3);
  not not_131 (not_131_out, F4);
  not not_132 (not_132_out, OP0);
  not not_133 (not_133_out, OP1);
  not not_134 (not_134_out, OP2);
  not not_135 (not_135_out, OP3);
  not not_136 (not_136_out, OP4);
  not not_137 (not_137_out, OP5);
  not not_138 (not_138_out, F2);
  not not_139 (not_139_out, F3);
  not not_140 (not_140_out, F4);
  not not_141 (not_141_out, F5);
  not not_142 (not_142_out, OP0);
  not not_143 (not_143_out, OP1);
  not not_144 (not_144_out, OP2);
  not not_145 (not_145_out, OP3);
  not not_146 (not_146_out, OP4);
  not not_147 (not_147_out, OP5);
  not not_148 (not_148_out, F2);
  not not_149 (not_149_out, F4);
  not not_150 (not_150_out, OP0);
  not not_151 (not_151_out, OP1);
  not not_152 (not_152_out, OP2);
  not not_153 (not_153_out, OP3);
  not not_154 (not_154_out, OP4);
  not not_155 (not_155_out, OP5);
  not not_156 (not_156_out, F3);
  not not_157 (not_157_out, F4);
  not not_158 (not_158_out, OP5);
  not not_159 (not_159_out, OP4);
  not not_160 (not_160_out, OP3);
  not not_161 (not_161_out, OP1);
  not not_162 (not_162_out, OP0);
  not not_163 (not_163_out, OP5);
  not not_164 (not_164_out, OP4);
  not not_165 (not_165_out, OP3);
  not not_166 (not_166_out, OP1);
  not not_167 (not_167_out, OP0);
  not not_168 (not_168_out, OP1);
  not not_169 (not_169_out, OP2);
  not not_170 (not_170_out, OP3);
  not not_171 (not_171_out, OP4);
  not not_172 (not_172_out, OP5);
  not not_173 (not_173_out, F0);
  not not_174 (not_174_out, F1);
  not not_175 (not_175_out, F2);
  not not_176 (not_176_out, F4);
  not not_177 (not_177_out, F5);
  not not_178 (not_178_out, OP0);
  not not_179 (not_179_out, OP2);
  not not_180 (not_180_out, OP3);
  not not_181 (not_181_out, OP4);
  not not_182 (not_182_out, OP5);
  not not_183 (not_183_out, F0);
  not not_184 (not_184_out, F1);
  not not_185 (not_185_out, F2);
  not not_186 (not_186_out, F4);
  not not_187 (not_187_out, F5);
  not not_188 (not_188_out, OP2);
  not not_189 (not_189_out, OP3);
  not not_190 (not_190_out, OP4);
  not not_191 (not_191_out, OP5);
  not not_192 (not_192_out, OP2);
  not not_193 (not_193_out, OP3);
  not not_194 (not_194_out, OP4);
  not not_195 (not_195_out, OP5);
  and and_1 (MemToReg, OP0, OP1, not_1_out, not_2_out, not_3_out, OP5);
  and and_2 (MemWrite, OP0, OP1, not_4_out, OP3, not_5_out, OP5);
  and and_3 (and_3_out, not_6_out, not_7_out, OP3, not_8_out, not_9_out);
  or or_1 (ALU_SRC, and_3_out, and_4_out, and_5_out);
  and and_4 (and_4_out, not_10_out, OP3, not_11_out, not_12_out);
  and and_5 (and_5_out, OP0, OP1, not_13_out, not_14_out, OP5);
  and and_6 (and_6_out, not_15_out, not_16_out, not_17_out, not_18_out, not_19_out, not_20_out, not_21_out, not_22_out, not_23_out);
  and and_7 (and_7_out, not_24_out, not_25_out, not_26_out, not_27_out, not_28_out, not_29_out, not_30_out, not_31_out, F5);
  and and_8 (and_8_out, not_32_out, not_33_out, not_34_out, not_35_out, not_36_out, F1, not_37_out, not_38_out, not_39_out, not_40_out);
  and and_9 (and_9_out, not_41_out, not_42_out, not_43_out, not_44_out, not_45_out, F1, not_46_out, F3, not_47_out, F5);
  and and_10 (and_10_out, not_48_out, not_49_out, not_50_out, not_51_out, not_52_out, F0, F2, not_53_out, not_54_out, F5);
  and and_11 (and_11_out, not_55_out, not_56_out, OP3, not_57_out, not_58_out);
  and and_12 (and_12_out, not_59_out, OP3, not_60_out, not_61_out);
  and and_13 (and_13_out, OP0, OP1, not_62_out, not_63_out, not_64_out);
  and and_14 (SysCALL, not_65_out, not_66_out, not_67_out, not_68_out, not_69_out, not_70_out, not_71_out, not_72_out, F2, F3, not_73_out, not_74_out);
  and and_15 (and_15_out, not_75_out, not_76_out, not_77_out, OP2, not_78_out, not_79_out);
  and and_16 (and_16_out, not_80_out, not_81_out, not_82_out, OP2, not_83_out, OP0);
  and and_17 (and_17_out, not_84_out, not_85_out, OP3, not_86_out, not_87_out, not_88_out);
  and and_18 (and_18_out, not_89_out, not_90_out, OP3, not_91_out, not_92_out, OP0);
  and and_19 (and_19_out, not_93_out, not_94_out, OP3, not_95_out, OP1, not_96_out);
  and and_20 (and_20_out, OP5, not_97_out, not_98_out, not_99_out, OP1, OP0);
  and and_21 (and_21_out, OP5, not_100_out, OP3, not_101_out, OP1, OP0);
  and and_22 (and_22_out, not_102_out, not_103_out, not_104_out, not_105_out, not_106_out, not_107_out, not_108_out, not_109_out, not_110_out, not_111_out, not_112_out);
  and and_23 (and_23_out, not_113_out, not_114_out, not_115_out, not_116_out, not_117_out, not_118_out, not_119_out, not_120_out, not_121_out, not_122_out);
  and and_24 (and_24_out, not_123_out, not_124_out, not_125_out, not_126_out, not_127_out, not_128_out, not_129_out, not_130_out, not_131_out, F5);
  and and_25 (and_25_out, not_132_out, not_133_out, not_134_out, not_135_out, not_136_out, not_137_out, F1, not_138_out, not_139_out, not_140_out, not_141_out);
  and and_26 (and_26_out, not_142_out, not_143_out, not_144_out, not_145_out, not_146_out, not_147_out, F1, not_148_out, F3, not_149_out, F5);
  and and_27 (and_27_out, not_150_out, not_151_out, not_152_out, not_153_out, not_154_out, not_155_out, F0, F2, not_156_out, not_157_out, F5);
  and and_28 (BEQ, not_158_out, not_159_out, not_160_out, OP2, not_161_out, not_162_out);
  and and_29 (BNE, not_163_out, not_164_out, not_165_out, OP2, not_166_out, OP0);
  and and_30 (JR, not_167_out, not_168_out, not_169_out, not_170_out, not_171_out, not_172_out, not_173_out, not_174_out, not_175_out, F3, not_176_out, not_177_out);
  and and_31 (and_31_out, not_178_out, not_179_out, not_180_out, not_181_out, not_182_out, not_183_out, not_184_out, not_185_out, F3, not_186_out, not_187_out);
  and and_32 (and_32_out, OP1, not_188_out, not_189_out, not_190_out, not_191_out);
  and and_33 (JAL, OP0, OP1, not_192_out, not_193_out, not_194_out, not_195_out);
  or or_2 (RegWrite, and_6_out, and_7_out, and_8_out, and_9_out, and_10_out, and_11_out, and_12_out, and_13_out);
  or or_3 (SignedExt, and_15_out, and_16_out, and_17_out, and_18_out, and_19_out, and_20_out, and_21_out);
  or or_4 (RegDst, and_22_out, and_23_out, and_24_out, and_25_out, and_26_out, and_27_out);
  or or_5 (JUMP, and_31_out, and_32_out);
endmodule

// ALU
module MIPS_ALU (
  input  [4:0] shamt,
  input  [31:0] X,
  input  [31:0] Y,
  input  [3:0] AluOP,
  output Equal,
  output [31:0] Result,
  output [31:0] Result_2
);

  wire [0:0] comparator_1_lt, comparator_2_lt;
  wire [31:0] adder_1_out, AND_out, divider_1_out, divider_1_rem, multiplier_1_cout, multiplier_1_out,
       NOR_out, OR_out, shifter_1_out, shifter_2_out, shifter_3_out, subtractor_1_out, XOR_out;

  assign AND_out = X & Y;  // AND_Gate AND, 32 bits wide
  assign OR_out = X | Y;  // OR_Gate OR, 32 bits wide
  Shifter #(.width(32), .shift("ll")) shifter_1 (.in(Y), .\dist (shamt), .out(shifter_1_out));
  Shifter #(.width(32), .shift("ar")) shifter_2 (.in(Y), .\dist (shamt), .out(shifter_2_out));
  Shifter #(.width(32), .shift("lr")) shifter_3 (.in(Y), .\dist (shamt), .out(shifter_3_out));
  Multiplier #(.width(32)) multiplier_1 (.a(X), .b(Y), .out(multiplier_1_out), .cout(multiplier_1_cout));  // open: cin
  Divider #(.width(32)) divider_1 (.a(X), .b(Y), .out(divider_1_out), .rem(divider_1_rem));  // open: upper
  Adder #(.width(32)) adder_1 (.a(X), .b(Y), .out(adder_1_out));  // open: cin, cout
  Subtractor #(.width(32)) subtractor_1 (.a(X), .b(Y), .out(subtractor_1_out));  // open: bin, bout
  assign XOR_out = X ^ Y;  // XOR_Gate XOR, 32 bits wide
  assign NOR_out = ~(X | Y);  // NOR_Gate NOR, 32 bits wide
  Comparator #(.width(32), .mode("twosComplement")) comparator_1 (
    .a(X), .b(Y), .eq(Equal), .lt(comparator_1_lt[0]));  // open: gt
  Comparator #(.width(32), .mode("unsigned")) comparator_2 (.a(X), .b(Y), .lt(comparator_2_lt[0]));  // open: gt, eq
  Multiplexer #(.select(4), .width(32), .disabled("Z"), .enable("false")) multiplexer_1 (
    .in0(shifter_1_out), .in1(shifter_2_out), .in2(shifter_3_out), .in3(multiplier_1_out),
    .in4(divider_1_out), .in5(adder_1_out), .in6(subtractor_1_out), .in7(AND_out), .in8(OR_out),
    .in9(XOR_out), .in10(NOR_out), .in11({{31{1'b0}}, comparator_1_lt[0]}),
    .in12({{31{1'b0}}, comparator_2_lt[0]}), .in13({32{1'b0}}), .in14({32{1'b0}}), .in15({32{1'b0}}),
    .out(Result), .sel(AluOP));
  Multiplexer #(.select(4), .width(32), .disabled("Z"), .enable("false")) multiplexer_2 (
    .in0({32{1'b0}}), .in1({32{1'b0}}), .in2({32{1'b0}}), .in3(multiplier_1_cout), .in4(divider_1_rem),
    .in5({32{1'b0}}), .in6({32{1'b0}}), .in7({32{1'b0}}), .in8({32{1'b0}}), .in9({32{1'b0}}),
    .in10({32{1'b0}}), .in11({32{1'b0}}), .in12({32{1'b0}}), .in13({32{1'b0}}), .in14({32{1'b0}}),
    .in15({32{1'b0}}), .out(Result_2), .sel(AluOP));

  // Other names for the same wires on the sheet: Result2[31:0] = Result_2; S[3:0] = AluOP

  // Notes on the sheet:
  //   不要改变此引脚区域内容，也不要改变ALU封装形式
  //   输入引脚
  //   输出引脚
endmodule

module MIPS_Regifile (
  input  [31:0] Din,
  input  Clk,
  input  WE,
  input  [4:0] R1_num,
  input  [4:0] W_num,
  input  [4:0] R2_num,
  output [31:0] R1,
  output [31:0] R2
);

  // RegisterFile registerfile_1: pin names not known; wires that end beside it: Din, Clk, WE, W_num, R1_num, R2_num, R1, R2
endmodule

module \理想流水线  (
  output RegWrite,
  output MemWrite,
  output [31:0] IF_PC,
  output [31:0] ID_PC,
  output [31:0] EX_PC,
  output [31:0] M_PC,
  output [31:0] WB_PC,
  output [31:0] RDin,
  output [31:0] MDin,
  output [31:0] LedData
);

  wire CLK, Go, IR1, IR2, IR3, not_1_out, RST, Syscall, W1, W2, W3, \单周期硬布线控制器_1_alu_src ,
       \单周期硬布线控制器_1_memtoreg , \单周期硬布线控制器_1_memwrite , \单周期硬布线控制器_1_regdst , \单周期硬布线控制器_1_regwrite ,
       \流水接口_2_alusrcb_2 , \流水接口_2_memchoose_2 , \流水接口_2_memwrite_2 , \流水接口_2_regdst_2 , \流水接口_2_regwrite_2 ,
       \流水接口_3_memchoose_2 , \流水接口_3_regdst_2 , \流水接口_3_regwrite_2 , \流水接口_4_memchoose_2 , \流水接口_4_regdst_2 ;
  wire [3:0] \单周期硬布线控制器_1_alu_op , \流水接口_2_aluop_2 ;
  wire [4:0] multiplexer_1_out;
  wire [15:0] \LoadUse次数 , \总周期数 , \插入气泡数 , \无条件分支数 , \条件分支成功数 ;
  wire [31:0] adder_1_out, bit_extender_1_out, mips_alu_1_result, mips_regifile_1_r1, mips_regifile_1_r2,
       multiplexer_2_out, ram_1_data, rom_1_data, \流水接口_1_ir_2 , \流水接口_2_a_2 , \流水接口_2_b_2 , \流水接口_2_imm_2 ,
       \流水接口_2_ir_2 , \流水接口_3_a_2 , \流水接口_3_ir_2 , \流水接口_4_a_2 , \流水接口_4_b_2 , \流水接口_4_ir_2 ;

  Button \u_总复位  (.out(RST));
  Button _1 (.out(IR1));
  Button _2 (.out(IR2));
  Button _3 (.out(IR3));
  Button \u_继续运行  (.out(Go));
  LED #(.active("true")) led_1 (.in(W1));
  LED #(.active("true")) led_2 (.in(W2));
  LED #(.active("true")) led_3 (.in(W3));
  not not_1 (not_1_out, Syscall);
  Hex_Digit_Display hex_digit_display_1 (.value(4'b0000));  // open: dp
  Counter #(.width(16), .max('hffff), .ongoal("wrap"), .trigger("rising"), .behavior("old")) counter_1 (
    .D({16{1'b0}}), .count(not_1_out), .Q(\总周期数 ), .clk(CLK), .clr(RST));  // open: load, carry, preset
  Register #(.width(32), .trigger("rising"), .Select("low")) PC (
    .D(adder_1_out), .en(not_1_out), .Q(IF_PC), .clk(CLK), .clr(RST));
  Hex_Digit_Display hex_digit_display_2 (.value(4'b0000));  // open: dp
  Hex_Digit_Display hex_digit_display_3 (.value(4'b0000));  // open: dp
  Adder #(.width(32)) adder_1 (.a(IF_PC), .b(32'h4), .out(adder_1_out), .cin(1'b0));  // open: cout
  Hex_Digit_Display hex_digit_display_4 (.value(4'b0000));  // open: dp
  Hex_Digit_Display hex_digit_display_5 (.value(4'b0000));  // open: dp
  ROM #(.addrWidth(10), .dataWidth(32), .Select("high")) rom_1 (.addr(IF_PC[11:2]), .data(rom_1_data));
  Hex_Digit_Display hex_digit_display_6 (.value(4'b0000));  // open: dp
  Hex_Digit_Display hex_digit_display_7 (.value(4'b0000));  // open: dp
  Clock #(.highDuration(1), .lowDuration(1)) clock_1 (.out(CLK));
  \流水接口  \u_流水接口_1  (
    .IR(rom_1_data), .PC(IF_PC), .CLK(CLK), .IR_2(\流水接口_1_ir_2 ), .PC_2(ID_PC), .\同步清零_高电平有效 (RST),
    .\使能端_低电平有效 (Syscall));  // open: regdst, regwrite, memchoose, memwrite, aluop, alusrcb, A, B, IMM, regdst_2, regwrite_2, memchoose_2, memwrite_2, aluop_2, alusrcb_2, A_2, B_2, IMM_2
  Hex_Digit_Display hex_digit_display_8 (.value(4'b0000));  // open: dp
  \单周期硬布线控制器  \u_单周期硬布线控制器_1  (
    .Func(\流水接口_1_ir_2 [5:0]), .OP(\流水接口_1_ir_2 [31:26]), .ALU_OP(\单周期硬布线控制器_1_alu_op ),
    .MemToReg(\单周期硬布线控制器_1_memtoreg ), .MemWrite(\单周期硬布线控制器_1_memwrite ), .ALU_SRC(\单周期硬布线控制器_1_alu_src ),
    .RegWrite(\单周期硬布线控制器_1_regwrite ), .RegDst(\单周期硬布线控制器_1_regdst ));  // open: SysCALL, SignedExt, JR, JMP, Beq, JAL, Bne
  Multiplexer #(.select(1), .width(5), .disabled("Z"), .enable("false")) multiplexer_1 (
    .in0(\流水接口_4_ir_2 [20:16]), .in1(\流水接口_4_ir_2 [15:11]), .out(multiplexer_1_out), .sel(\流水接口_4_regdst_2 ));
  assign bit_extender_1_out = {{16{\流水接口_1_ir_2 [15]}}, \流水接口_1_ir_2 [15:0]};  // Bit_Extender bit_extender_1
  // Probe on \总周期数 
  // Probe on \无条件分支数 
  // Probe on \条件分支成功数 
  // Probe on \插入气泡数 
  // Probe on \LoadUse次数 
  // Probe on IF_PC[11:0]
  MIPS_Regifile mips_regifile_1 (
    .Din(RDin), .Clk(CLK), .R1(mips_regifile_1_r1), .R2(mips_regifile_1_r2), .WE(RegWrite),
    .W_num(multiplexer_1_out), .R1_num(\流水接口_1_ir_2 [25:21]), .R2_num(\流水接口_1_ir_2 [20:16]));
  // Probe on EX_PC[11:0]
  // Probe on ID_PC[11:0]
  \流水接口  \u_流水接口_2  (
    .regdst(\单周期硬布线控制器_1_regdst ), .regwrite(\单周期硬布线控制器_1_regwrite ), .memchoose(\单周期硬布线控制器_1_memtoreg ),
    .memwrite(\单周期硬布线控制器_1_memwrite ), .aluop(\单周期硬布线控制器_1_alu_op ), .alusrcb(\单周期硬布线控制器_1_alu_src ),
    .A(mips_regifile_1_r1), .B(mips_regifile_1_r2), .IR(\流水接口_1_ir_2 ), .IMM(bit_extender_1_out), .PC(ID_PC),
    .CLK(CLK), .regdst_2(\流水接口_2_regdst_2 ), .regwrite_2(\流水接口_2_regwrite_2 ),
    .memchoose_2(\流水接口_2_memchoose_2 ), .memwrite_2(\流水接口_2_memwrite_2 ), .aluop_2(\流水接口_2_aluop_2 ),
    .alusrcb_2(\流水接口_2_alusrcb_2 ), .A_2(\流水接口_2_a_2 ), .B_2(\流水接口_2_b_2 ), .IR_2(\流水接口_2_ir_2 ),
    .IMM_2(\流水接口_2_imm_2 ), .PC_2(EX_PC), .\同步清零_高电平有效 (RST), .\使能端_低电平有效 (Syscall));
  // Probe on M_PC[11:0]
  Multiplexer #(.select(1), .width(32), .disabled("Z"), .enable("false")) multiplexer_2 (
    .in0(\流水接口_2_b_2 ), .in1(\流水接口_2_imm_2 ), .out(multiplexer_2_out), .sel(\流水接口_2_alusrcb_2 ));
  // Probe on WB_PC[11:0]
  MIPS_ALU mips_alu_1 (
    .X(\流水接口_2_a_2 ), .Y(multiplexer_2_out), .AluOP(\流水接口_2_aluop_2 ), .Result(mips_alu_1_result),
    .shamt({5{1'b0}}));  // open: Equal, Result_2
  \流水接口  \u_流水接口_3  (
    .regdst(\流水接口_2_regdst_2 ), .regwrite(\流水接口_2_regwrite_2 ), .memchoose(\流水接口_2_memchoose_2 ),
    .memwrite(\流水接口_2_memwrite_2 ), .A(mips_alu_1_result), .B(\流水接口_2_b_2 ), .IR(\流水接口_2_ir_2 ), .PC(EX_PC),
    .CLK(CLK), .regdst_2(\流水接口_3_regdst_2 ), .regwrite_2(\流水接口_3_regwrite_2 ),
    .memchoose_2(\流水接口_3_memchoose_2 ), .memwrite_2(MemWrite), .A_2(\流水接口_3_a_2 ), .B_2(MDin),
    .IR_2(\流水接口_3_ir_2 ), .PC_2(M_PC), .\同步清零_高电平有效 (RST), .\使能端_低电平有效 (Syscall));  // open: aluop, alusrcb, IMM, aluop_2, alusrcb_2, IMM_2
  \流水接口  \u_流水接口_4  (
    .regdst(\流水接口_3_regdst_2 ), .regwrite(\流水接口_3_regwrite_2 ), .memchoose(\流水接口_3_memchoose_2 ),
    .A(\流水接口_3_a_2 ), .B(ram_1_data), .IR(\流水接口_3_ir_2 ), .PC(M_PC), .CLK(CLK), .regdst_2(\流水接口_4_regdst_2 ),
    .regwrite_2(RegWrite), .memchoose_2(\流水接口_4_memchoose_2 ), .A_2(\流水接口_4_a_2 ), .B_2(\流水接口_4_b_2 ),
    .IR_2(\流水接口_4_ir_2 ), .PC_2(WB_PC), .\同步清零_高电平有效 (RST), .\使能端_低电平有效 (Syscall));  // open: memwrite, aluop, alusrcb, IMM, memwrite_2, aluop_2, alusrcb_2, IMM_2
  RAM #(.addrWidth(10), .dataWidth(32), .bus("separate"), .Select("high")) ram_1 (
    .addr(\流水接口_3_a_2 [11:2]), .din(MDin), .data(ram_1_data), .str(MemWrite), .sel(1'b1), .clk(CLK), .clr(RST));  // open: ld
  Multiplexer #(.select(1), .width(32), .disabled("Z"), .enable("false")) multiplexer_3 (
    .in0(\流水接口_4_a_2 ), .in1(\流水接口_4_b_2 ), .out(RDin), .sel(\流水接口_4_memchoose_2 ));
  Comparator #(.width(32), .mode("twosComplement")) comparator_1 (
    .a(\流水接口_4_ir_2 ), .b(32'hc), .eq(Syscall));  // open: gt, lt

  assign LedData = {32{1'b0}};

  // Other names for the same wires on the sheet: MEM_PC[31:0] = M_PC

  // Notes on the sheet:
  //   中断源
  //   中断等待指示
  //   数码管输出
  //   指令存储器
  //   contents of rom_1 (hex, n*v repeats v):
  //   20100000 20110000 20120000 20130000 36100000 36310001 36520002 36730003 ae100000 ae110004 ae120008
  //   ae13000c 2002000a 20110000 20120000 20130000 c
  //   OP
  //   Func
  //   rs
  //   rt
  //   rd
  //   RegDst
  //   MemToReg
  //   MemWrite
  //   AluOP
  //   AluSrcB
  //   RegWrite
  //   流水调试日志用
  //   为方便自动评测，需要输出流水线各段保存的PC值，注意是PC不是PC+4，另外ID段寄存器写入信息，Mem段内存写入信息也要输出
endmodule

module \气泡流水线  (
  output RegWrite,
  output MemWrite,
  output [31:0] IF_PC,
  output [31:0] ID_PC,
  output [31:0] EX_PC,
  output [31:0] M_PC,
  output [31:0] WB_PC,
  output [31:0] RDin,
  output [31:0] MDin,
  output [31:0] LedData
);

  wire and_3_out, and_4_out, and_5_out, CLK, comparator_1_eq, EXBranch, Go, IR1, IR2, IR3, jal, JMP, JR,
       mips_alu_1_equal, not_1_out, not_2_out, not_3_out, not_4_out, not_5_out, or_1_out, or_2_out, or_3_out,
       \output , regdst, relative, stop, Syscall, W1, W2, W3, \单周期硬布线控制器_1_alu_src , \单周期硬布线控制器_1_beq ,
       \单周期硬布线控制器_1_bne , \单周期硬布线控制器_1_jmp , \单周期硬布线控制器_1_jr , \单周期硬布线控制器_1_memtoreg ,
       \单周期硬布线控制器_1_memwrite , \单周期硬布线控制器_1_regwrite , \单周期硬布线控制器_1_syscall , \流水接口2_2_alusrcb_2 ,
       \流水接口2_2_beq_2 , \流水接口2_2_bne_2 , \流水接口2_2_jal_2 , \流水接口2_2_memchoose_2 , \流水接口2_2_memwrite_2 ,
       \流水接口2_2_regdst_2 , \流水接口2_2_regwrite_2 , \流水接口2_3_jal_2 , \流水接口2_3_memchoose_2 , \流水接口2_3_regdst_2 ,
       \流水接口2_3_regwrite_2 , \流水接口2_4_jal_2 , \流水接口2_4_memchoose_2 , \流水接口2_4_regdst_2 , \源寄存器使用情况_1_r1used ,
       \源寄存器使用情况_1_r2used ;
  wire [3:0] \单周期硬布线控制器_1_alu_op , \流水接口2_2_aluop_2 ;
  wire [4:0] multiplexer_3_out, multiplexer_4_out, multiplexer_5_out, multiplexer_6_out, multiplexer_7_out,
       multiplexer_8_out, \流水接口2_2_shamt_2 , \流水接口2_2_writereg_2 , \流水接口2_3_writereg_2 ;
  wire [15:0] \LoadUse次数 , \总周期数 , \插入气泡数 , \无条件分支数 , \条件分支成功数 ;
  wire [27:0] \流水接口2_2_pc_2 ;
  wire [31:0] a0, adder_2_out, bit_extender_1_out, bit_extender_2_out, controlled_buffer_1_out, IR, JMP_PC,
       JR_PC, mips_alu_1_result, mips_regifile_1_r1, mips_regifile_1_r2, multiplexer_1_out,
       multiplexer_2_out, multiplexer_9_out, multiplexer_10_out, PC, ram_1_data, shifter_2_out, v0,
       \流水接口2_1_ir_2 , \流水接口2_1_pc_2 , \流水接口2_2_a_2 , \流水接口2_2_b_2 , \流水接口2_2_b_prime_2 , \流水接口2_2_imm2_2 ,
       \流水接口2_2_imm_2 , \流水接口2_2_ir_2 , \流水接口2_3_a_2 , \流水接口2_3_a_prime_2 , \流水接口2_3_b_prime_2 ,
       \流水接口2_3_ir_2 , \流水接口2_3_pc_2 , \流水接口2_4_a_2 , \流水接口2_4_b_2 , \流水接口2_4_ir_2 , \流水接口2_4_pc_2 ;
  wire [31:28] shifter_1_out;

  Clock #(.highDuration(1), .lowDuration(1)) clock_1 (.out(CLK));
  Button _1 (.out(IR1));
  Button _2 (.out(IR2));
  Button _3 (.out(IR3));
  Multiplexer #(.select(1), .width(32), .disabled("Z"), .enable("false")) multiplexer_1 (
    .in0(PC), .in1(adder_2_out), .out(multiplexer_1_out), .sel(EXBranch));
  Button \u_继续运行  (.out(Go));
  LED #(.active("true")) led_1 (.in(W1));
  LED #(.active("true")) led_2 (.in(W2));
  LED #(.active("true")) led_3 (.in(W3));
  Hex_Digit_Display hex_digit_display_1 (.value(LedData[31:28]));  // open: dp
  not not_1 (not_1_out, stop);
  Multiplexer #(.select(2), .width(32), .disabled("Z"), .enable("false")) multiplexer_2 (
    .in0(multiplexer_1_out), .in1(JMP_PC), .in2(JR_PC), .in3(JR_PC), .out(multiplexer_2_out), .sel({JR, JMP}));
  not not_2 (not_2_out, or_1_out);
  or or_1 (or_1_out, relative, stop);
  Comparator #(.width(32), .mode("twosComplement")) comparator_1 (
    .a(v0), .b(32'h22), .eq(comparator_1_eq));  // open: gt, lt
  not not_3 (not_3_out, comparator_1_eq);
  Counter #(.width(16), .max('hffff), .ongoal("wrap"), .trigger("rising"), .behavior("old")) counter_1 (
    .D({16{1'b0}}), .count(JMP), .Q(\无条件分支数 ), .clk(CLK));  // open: load, carry, clr, preset
  Hex_Digit_Display hex_digit_display_2 (.value(LedData[27:24]));  // open: dp
  Hex_Digit_Display hex_digit_display_3 (.value(LedData[23:20]));  // open: dp
  Counter #(.width(16), .max('hffff), .ongoal("wrap"), .trigger("rising"), .behavior("old")) counter_2 (
    .D({16{1'b0}}), .count(not_1_out), .Q(\总周期数 ), .clk(CLK));  // open: load, carry, clr, preset
  Register #(.width(32), .trigger("rising"), .Select("low")) u_PC (
    .D(multiplexer_2_out), .en(not_2_out), .Q(IF_PC), .clk(CLK));  // open: clr
  and and_1 (\output , Syscall, comparator_1_eq);
  and and_2 (stop, not_3_out, Syscall);
  Hex_Digit_Display hex_digit_display_4 (.value(LedData[15:12]));  // open: dp
  Hex_Digit_Display hex_digit_display_5 (.value(LedData[19:16]));  // open: dp
  Adder #(.width(32)) adder_1 (.a(IF_PC), .b(32'h4), .out(PC), .cin(1'b0));  // open: cout
  Hex_Digit_Display hex_digit_display_6 (.value(LedData[11:8]));  // open: dp
  Hex_Digit_Display hex_digit_display_7 (.value(LedData[7:4]));  // open: dp
  // Probe on \总周期数 
  // Probe on \插入气泡数 
  or or_2 (or_2_out, JMP, EXBranch);
  assign controlled_buffer_1_out = \output  ? a0 : 32'bz;  // Controlled_Buffer controlled_buffer_1
  Counter #(.width(16), .max('hffff), .ongoal("wrap"), .trigger("rising"), .behavior("old")) counter_3 (
    .D({16{1'b0}}), .count(EXBranch), .Q(\条件分支成功数 ), .clk(CLK));  // open: load, carry, clr, preset
  Hex_Digit_Display hex_digit_display_8 (.value(LedData[3:0]));  // open: dp
  \流水接口2  \u_流水接口2_1  (
    .IR(IR), .PC(PC), .CLK(CLK), .IR_2(\流水接口2_1_ir_2 ), .PC_2(\流水接口2_1_pc_2 ), .\同步清零_高电平有效 (or_2_out),
    .\使能端_低电平有效 (or_1_out), .PCtest_2(ID_PC), .PCtest(IF_PC));  // open: J, JR, JAL, BEQ, BNE, regdst, regwrite, memchoose, memwrite, aluop, alusrcb, A, B, IMM, IMM2, J_2, JR_2, JAL_2, BEQ_2, BNE_2, regdst_2, regwrite_2, memchoose_2, memwrite_2, aluop_2, alusrcb_2, A_2, B_2, IMM_2, IMM2_2, A_prime, A_prime_2, B_prime, B_prime_2, writereg, writereg_2, shamt, shamt_2, cR1, cR1_2, cR2, cR2_2, status, status_2, hit, hit_2, 原来的_PC, 原来的PC
  ROM #(.addrWidth(10), .dataWidth(32), .Select("high")) rom_1 (.addr(IF_PC[11:2]), .data(IR));
  or or_3 (or_3_out, or_2_out, relative);
  Register #(.width(32), .trigger("rising"), .Select("low")) PC_2 (
    .D(controlled_buffer_1_out), .Q(LedData), .clk(CLK));  // open: en, clr
  // Probe on \总周期数 
  // Probe on \无条件分支数 
  // Probe on \条件分支成功数 
  // Probe on \插入气泡数 
  // Probe on \LoadUse次数 
  \源寄存器使用情况  \u_源寄存器使用情况_1  (
    .OP0(\流水接口2_1_ir_2 [26]), .OP1(\流水接口2_1_ir_2 [27]), .OP2(\流水接口2_1_ir_2 [28]), .OP3(\流水接口2_1_ir_2 [29]),
    .OP4(\流水接口2_1_ir_2 [30]), .OP5(\流水接口2_1_ir_2 [31]), .F0(\流水接口2_1_ir_2 [0]), .F1(\流水接口2_1_ir_2 [1]),
    .F2(\流水接口2_1_ir_2 [2]), .F3(\流水接口2_1_ir_2 [3]), .F4(\流水接口2_1_ir_2 [4]), .F5(\流水接口2_1_ir_2 [5]),
    .R1used(\源寄存器使用情况_1_r1used ), .R2used(\源寄存器使用情况_1_r2used ));
  \单周期硬布线控制器  \u_单周期硬布线控制器_1  (
    .Func(\流水接口2_1_ir_2 [5:0]), .OP(\流水接口2_1_ir_2 [31:26]), .ALU_OP(\单周期硬布线控制器_1_alu_op ),
    .MemToReg(\单周期硬布线控制器_1_memtoreg ), .MemWrite(\单周期硬布线控制器_1_memwrite ), .ALU_SRC(\单周期硬布线控制器_1_alu_src ),
    .RegWrite(\单周期硬布线控制器_1_regwrite ), .SysCALL(\单周期硬布线控制器_1_syscall ), .RegDst(regdst),
    .JR(\单周期硬布线控制器_1_jr ), .JMP(\单周期硬布线控制器_1_jmp ), .Beq(\单周期硬布线控制器_1_beq ), .JAL(jal),
    .Bne(\单周期硬布线控制器_1_bne ));  // open: SignedExt
  Multiplexer #(.select(1), .width(5), .disabled("Z"), .enable("false")) multiplexer_3 (
    .in0(\流水接口2_1_ir_2 [25:21]), .in1(5'b00010), .out(multiplexer_3_out), .sel(\单周期硬布线控制器_1_syscall ));
  Multiplexer #(.select(1), .width(5), .disabled("Z"), .enable("false")) multiplexer_4 (
    .in0(\流水接口2_1_ir_2 [20:16]), .in1(5'b00100), .out(multiplexer_4_out), .sel(\单周期硬布线控制器_1_syscall ));
  Multiplexer #(.select(1), .width(5), .disabled("Z"), .enable("false")) multiplexer_5 (
    .in0(\流水接口2_4_ir_2 [20:16]), .in1(\流水接口2_4_ir_2 [15:11]), .out(multiplexer_5_out),
    .sel(\流水接口2_4_regdst_2 ));
  Multiplexer #(.select(1), .width(5), .disabled("Z"), .enable("false")) multiplexer_6 (
    .in0(multiplexer_5_out), .in1({5{1'b1}}), .out(multiplexer_6_out), .sel(\流水接口2_4_jal_2 ));
  assign bit_extender_1_out = {{16{\流水接口2_1_ir_2 [15]}}, \流水接口2_1_ir_2 [15:0]};  // Bit_Extender bit_extender_1
  assign bit_extender_2_out = {{6{\流水接口2_1_ir_2 [25]}}, \流水接口2_1_ir_2 [25:0]};  // Bit_Extender bit_extender_2
  Multiplexer #(.select(1), .width(5), .disabled("Z"), .enable("false")) multiplexer_7 (
    .in0(\流水接口2_1_ir_2 [20:16]), .in1(\流水接口2_1_ir_2 [15:11]), .out(multiplexer_7_out), .sel(regdst));
  Multiplexer #(.select(1), .width(5), .disabled("Z"), .enable("false")) multiplexer_8 (
    .in0(multiplexer_7_out), .in1({5{1'b1}}), .out(multiplexer_8_out), .sel(jal));
  and and_3 (and_3_out, relative, not_4_out);
  not not_4 (not_4_out, stop);
  // Probe on IF_PC[11:0]
  // Probe on EX_PC[11:0]
  // Probe on ID_PC[11:0]
  \数据相关检测逻辑  \u_数据相关检测逻辑_1  (
    .R1used(\源寄存器使用情况_1_r1used ), .EX_RegWrite(\流水接口2_2_regwrite_2 ), .R1_num(multiplexer_3_out),
    .R2_num(multiplexer_4_out), .EX_WriteReg_num(\流水接口2_2_writereg_2 ),
    .MEM_WriteReg_num(\流水接口2_3_writereg_2 ), .R2used(\源寄存器使用情况_1_r2used ),
    .MEM_RegWrite(\流水接口2_3_regwrite_2 ), .relative(relative));
  MIPS_Regifile mips_regifile_1 (
    .Din(RDin), .Clk(CLK), .R1(mips_regifile_1_r1), .R2(mips_regifile_1_r2), .WE(RegWrite),
    .W_num(multiplexer_6_out), .R1_num(multiplexer_3_out), .R2_num(multiplexer_4_out));
  Counter #(.width(16), .max('hffff), .ongoal("wrap"), .trigger("rising"), .behavior("old")) counter_4 (
    .D({16{1'b0}}), .count(and_3_out), .Q(\插入气泡数 ), .clk(CLK));  // open: load, carry, clr, preset
  // Probe on M_PC[11:0]
  \流水接口2  \u_流水接口2_2  (
    .J(\单周期硬布线控制器_1_jmp ), .JR(\单周期硬布线控制器_1_jr ), .JAL(jal), .BEQ(\单周期硬布线控制器_1_beq ),
    .BNE(\单周期硬布线控制器_1_bne ), .regdst(regdst), .regwrite(\单周期硬布线控制器_1_regwrite ),
    .memchoose(\单周期硬布线控制器_1_memtoreg ), .memwrite(\单周期硬布线控制器_1_memwrite ), .aluop(\单周期硬布线控制器_1_alu_op ),
    .alusrcb(\单周期硬布线控制器_1_alu_src ), .A(mips_regifile_1_r1), .B(mips_regifile_1_r2), .IR(\流水接口2_1_ir_2 ),
    .IMM(bit_extender_1_out), .IMM2(bit_extender_2_out), .PC(\流水接口2_1_pc_2 ), .CLK(CLK), .J_2(JMP),
    .JR_2(JR), .JAL_2(\流水接口2_2_jal_2 ), .BEQ_2(\流水接口2_2_beq_2 ), .BNE_2(\流水接口2_2_bne_2 ),
    .regdst_2(\流水接口2_2_regdst_2 ), .regwrite_2(\流水接口2_2_regwrite_2 ), .memchoose_2(\流水接口2_2_memchoose_2 ),
    .memwrite_2(\流水接口2_2_memwrite_2 ), .aluop_2(\流水接口2_2_aluop_2 ), .alusrcb_2(\流水接口2_2_alusrcb_2 ),
    .A_2(\流水接口2_2_a_2 ), .B_2(\流水接口2_2_b_2 ), .IR_2(\流水接口2_2_ir_2 ), .IMM_2(\流水接口2_2_imm_2 ),
    .IMM2_2(\流水接口2_2_imm2_2 ), .PC_2({JMP_PC[31:28], \流水接口2_2_pc_2 }), .\同步清零_高电平有效 (or_3_out),
    .\使能端_低电平有效 (stop), .A_prime(mips_regifile_1_r1), .A_prime_2(JR_PC), .B_prime(mips_regifile_1_r2),
    .B_prime_2(\流水接口2_2_b_prime_2 ), .writereg(multiplexer_8_out), .writereg_2(\流水接口2_2_writereg_2 ),
    .shamt(\流水接口2_1_ir_2 [10:6]), .shamt_2(\流水接口2_2_shamt_2 ), .PCtest_2(EX_PC), .PCtest(ID_PC));  // open: cR1, cR1_2, cR2, cR2_2, status, status_2, hit, hit_2, 原来的_PC, 原来的PC
  // Probe on WB_PC[11:0]
  or or_4 (EXBranch, and_4_out, and_5_out);
  and and_4 (and_4_out, \流水接口2_2_bne_2 , not_5_out);
  not not_5 (not_5_out, mips_alu_1_equal);
  Multiplexer #(.select(1), .width(32), .disabled("Z"), .enable("false")) multiplexer_9 (
    .in0(\流水接口2_2_b_2 ), .in1(\流水接口2_2_imm_2 ), .out(multiplexer_9_out), .sel(\流水接口2_2_alusrcb_2 ));
  Shifter #(.width(32), .shift("ll")) shifter_1 (
    .in(\流水接口2_2_imm2_2 ), .\dist (5'b00010), .out({shifter_1_out, JMP_PC[27:0]}));
  and and_5 (and_5_out, \流水接口2_2_beq_2 , mips_alu_1_equal);
  MIPS_ALU mips_alu_1 (
    .X(\流水接口2_2_a_2 ), .Y(multiplexer_9_out), .AluOP(\流水接口2_2_aluop_2 ), .Equal(mips_alu_1_equal),
    .Result(mips_alu_1_result), .shamt(\流水接口2_2_shamt_2 ));  // open: Result_2
  Shifter #(.width(32), .shift("ll")) shifter_2 (.in(\流水接口2_2_imm_2 ), .\dist (5'b00010), .out(shifter_2_out));
  \流水接口2  \u_流水接口2_3  (
    .JAL(\流水接口2_2_jal_2 ), .regdst(\流水接口2_2_regdst_2 ), .regwrite(\流水接口2_2_regwrite_2 ),
    .memchoose(\流水接口2_2_memchoose_2 ), .memwrite(\流水接口2_2_memwrite_2 ), .A(mips_alu_1_result),
    .B(\流水接口2_2_b_2 ), .IR(\流水接口2_2_ir_2 ), .PC({JMP_PC[31:28], \流水接口2_2_pc_2 }), .CLK(CLK),
    .JAL_2(\流水接口2_3_jal_2 ), .regdst_2(\流水接口2_3_regdst_2 ), .regwrite_2(\流水接口2_3_regwrite_2 ),
    .memchoose_2(\流水接口2_3_memchoose_2 ), .memwrite_2(MemWrite), .A_2(\流水接口2_3_a_2 ), .B_2(MDin),
    .IR_2(\流水接口2_3_ir_2 ), .PC_2(\流水接口2_3_pc_2 ), .\使能端_低电平有效 (stop), .A_prime(JR_PC),
    .A_prime_2(\流水接口2_3_a_prime_2 ), .B_prime(\流水接口2_2_b_prime_2 ), .B_prime_2(\流水接口2_3_b_prime_2 ),
    .writereg(\流水接口2_2_writereg_2 ), .writereg_2(\流水接口2_3_writereg_2 ), .PCtest_2(M_PC), .PCtest(EX_PC));  // open: J, JR, BEQ, BNE, aluop, alusrcb, IMM, IMM2, J_2, JR_2, BEQ_2, BNE_2, aluop_2, alusrcb_2, IMM_2, IMM2_2, 同步清零_高电平有效, shamt, shamt_2, cR1, cR1_2, cR2, cR2_2, status, status_2, hit, hit_2, 原来的_PC, 原来的PC
  Adder #(.width(32)) adder_2 (
    .a({JMP_PC[31:28], \流水接口2_2_pc_2 }), .b(shifter_2_out), .out(adder_2_out));  // open: cin, cout
  \流水接口2  \u_流水接口2_4  (
    .JAL(\流水接口2_3_jal_2 ), .regdst(\流水接口2_3_regdst_2 ), .regwrite(\流水接口2_3_regwrite_2 ),
    .memchoose(\流水接口2_3_memchoose_2 ), .A(\流水接口2_3_a_2 ), .B(ram_1_data), .IR(\流水接口2_3_ir_2 ),
    .PC(\流水接口2_3_pc_2 ), .CLK(CLK), .JAL_2(\流水接口2_4_jal_2 ), .regdst_2(\流水接口2_4_regdst_2 ),
    .regwrite_2(RegWrite), .memchoose_2(\流水接口2_4_memchoose_2 ), .A_2(\流水接口2_4_a_2 ), .B_2(\流水接口2_4_b_2 ),
    .IR_2(\流水接口2_4_ir_2 ), .PC_2(\流水接口2_4_pc_2 ), .\使能端_低电平有效 (stop), .A_prime(\流水接口2_3_a_prime_2 ),
    .A_prime_2(v0), .B_prime(\流水接口2_3_b_prime_2 ), .B_prime_2(a0), .PCtest_2(WB_PC), .PCtest(M_PC));  // open: J, JR, BEQ, BNE, memwrite, aluop, alusrcb, IMM, IMM2, J_2, JR_2, BEQ_2, BNE_2, memwrite_2, aluop_2, alusrcb_2, IMM_2, IMM2_2, 同步清零_高电平有效, writereg, writereg_2, shamt, shamt_2, cR1, cR1_2, cR2, cR2_2, status, status_2, hit, hit_2, 原来的_PC, 原来的PC
  RAM #(.addrWidth(10), .dataWidth(32), .bus("separate"), .Select("high")) ram_1 (
    .addr(\流水接口2_3_a_2 [11:2]), .din(MDin), .data(ram_1_data), .str(MemWrite), .sel(1'b1), .clk(CLK));  // open: ld, clr
  Multiplexer #(.select(1), .width(32), .disabled("Z"), .enable("false")) multiplexer_10 (
    .in0(\流水接口2_4_a_2 ), .in1(\流水接口2_4_b_2 ), .out(multiplexer_10_out), .sel(\流水接口2_4_memchoose_2 ));
  Multiplexer #(.select(1), .width(32), .disabled("Z"), .enable("false")) multiplexer_11 (
    .in0(multiplexer_10_out), .in1(\流水接口2_4_pc_2 ), .out(RDin), .sel(\流水接口2_4_jal_2 ));
  Comparator #(.width(32), .mode("twosComplement")) comparator_2 (
    .a(\流水接口2_4_ir_2 ), .b(32'hc), .eq(Syscall));  // open: gt, lt

  // Other names for the same wires on the sheet: MEM_PC[31:0] = M_PC

  // Notes on the sheet:
  //   中断源
  //   中断等待指示
  //   数码管输出
  //   指令存储器
  //   contents of rom_1 (hex, n*v repeats v):
  //   20110001 8000c05 20110001 20120002 20130003 8000c09 20110001 20120002 20130003 8000c0d 20110001
  //   20120002 20130003 8000c11 20110001 20120002 20130003 c000cb8 20100001 20110001 118fc0 112020
  //   20020022 c 118882 12200001 8000c15 112020 20020022 c 20110001 118880 112020 20020022 c 12200001
  //   8000c1f 20110001 118fc0 112020 20020022 c 1188c3 112020 20020022 c 118903 112020 20020022 c 118903
  //   112020 20020022 c 118903 112020 20020022 c 118903 112020 20020022 c 118903 112020 20020022 c 118903
  //   112020 20020022 c 118903 112020 20020022 c 20100001 109fc0 139fc3 8021 2012000c 24160003 26100001
  //   3210000f 20080008 20090001 139900 2709825 132020 20020022 c 1094022 1500fff9 22100001 2018000f
  //   2188024 108700 20080008 20090001 139902 2709825 132021 20020022 c 1094022 1500fff9 108702 2c9b022
  //   12c00001 8000c50 4020 1084027 84400 3508ffff 82021 20020022 c 2010ffff 20110000 ae300000 22100001
  //   22310004 ae300000 22100001 22310004 ae300000 22100001 22310004 ae300000 22100001 22310004 ae300000
  //   22100001 22310004 ae300000 22100001 22310004 ae300000 22100001 22310004 ae300000 22100001 22310004
  //   ae300000 22100001 22310004 ae300000 22100001 22310004 ae300000 22100001 22310004 ae300000 22100001
  //   22310004 ae300000 22100001 22310004 ae300000 22100001 22310004 ae300000 22100001 22310004 ae300000
  //   22100001 22310004 22100001 8020 2011003c 8e130000 8e340000 274402a 11000002 ae330000 ae140000
  //   2231fffc 1611fff8 102020 20020022 c 22100004 2011003c 1611fff2 20020032 c 20100000 22100001 102020
  //   20020022 c 22100002 102020 20020022 c 22100003 102020 20020022 c 22100004 102020 20020022 c 22100005
  //   102020 20020022 c 22100006 102020 20020022 c 22100007 102020 20020022 c 22100008 102020 20020022
  //   20020022 c 3e00008
  //   rs
  //   rt
  //   rt
  //   rd
  //   shamt
  //   rt
  //   rd
  //   JMP
  //   JR
  //   OP
  //   Func
  //   Beq
  //   Bne
  //   MemToReg
  //   MemWrite
  //   AluOP
  //   AluSrcB
  //   RegWrite
  //   JAL
  //   RegDst
  //   流水调试日志用
  //   为方便自动评测，需要输出流水线各段保存的PC值，注意是PC不是PC+4，另外ID段寄存器写入信息，Mem段内存写入信息也要输出
endmodule

module \重定向流水线  (
  output RegWrite,
  output MemWrite,
  output [31:0] IF_PC,
  output [31:0] ID_PC,
  output [31:0] EX_PC,
  output [31:0] M_PC,
  output [31:0] WB_PC,
  output [31:0] RDin,
  output [31:0] MDin,
  output [31:0] LedData
);

  wire and_3_out, and_4_out, and_5_out, CLK, comparator_1_eq, EXBranch, Go, IR1, IR2, IR3, jal, JMP, JR,
       mips_alu_1_equal, not_1_out, not_2_out, not_3_out, not_4_out, not_5_out, or_1_out, or_2_out, or_3_out,
       \output , regdst, relative, stop, Syscall, W1, W2, W3, \单周期硬布线控制器_1_alu_src , \单周期硬布线控制器_1_beq ,
       \单周期硬布线控制器_1_bne , \单周期硬布线控制器_1_jmp , \单周期硬布线控制器_1_jr , \单周期硬布线控制器_1_memtoreg ,
       \单周期硬布线控制器_1_memwrite , \单周期硬布线控制器_1_regwrite , \单周期硬布线控制器_1_syscall , \流水接口2_2_alusrcb_2 ,
       \流水接口2_2_beq_2 , \流水接口2_2_bne_2 , \流水接口2_2_jal_2 , \流水接口2_2_memchoose_2 , \流水接口2_2_memwrite_2 ,
       \流水接口2_2_regdst_2 , \流水接口2_2_regwrite_2 , \流水接口2_3_jal_2 , \流水接口2_3_memchoose_2 , \流水接口2_3_regdst_2 ,
       \流水接口2_3_regwrite_2 , \流水接口2_4_jal_2 , \流水接口2_4_memchoose_2 , \流水接口2_4_regdst_2 , \源寄存器使用情况_1_r1used ,
       \源寄存器使用情况_1_r2used ;
  wire [1:0] CR1, CR2, \流水接口2_2_cr1_2 , \流水接口2_2_cr2_2 ;
  wire [3:0] \单周期硬布线控制器_1_alu_op , \流水接口2_2_aluop_2 ;
  wire [4:0] multiplexer_3_out, multiplexer_4_out, multiplexer_5_out, multiplexer_6_out, multiplexer_7_out,
       multiplexer_8_out, \流水接口2_2_shamt_2 , \流水接口2_2_writereg_2 , \流水接口2_3_writereg_2 ;
  wire [5:0] \流水接口2_2_ir_2_2 ;
  wire [15:0] \LoadUse次数 , \总周期数 , \插入气泡数 , \无条件分支数 , \条件分支成功数 ;
  wire [25:0] \流水接口2_2_ir_2 ;
  wire [27:0] \流水接口2_2_pc_2 ;
  wire [31:0] A, a0, adder_2_out, ALU_1, ALU_2, B, bit_extender_1_out, bit_extender_2_out,
       controlled_buffer_1_out, EXR1, EXR2, IR, JMP_PC, JR_PC, mips_alu_1_result, mips_regifile_1_r1,
       mips_regifile_1_r2, multiplexer_1_out, multiplexer_2_out, multiplexer_9_out, multiplexer_12_out, PC,
       ram_1_data, shifter_2_out, v0, WB, \流水接口2_1_ir_2 , \流水接口2_1_pc_2 , \流水接口2_2_imm2_2 , \流水接口2_2_imm_2 ,
       \流水接口2_3_a_prime_2 , \流水接口2_3_b_prime_2 , \流水接口2_3_ir_2 , \流水接口2_3_pc_2 , \流水接口2_4_ir_2 ,
       \流水接口2_4_pc_2 ;
  wire [31:28] shifter_1_out;

  Clock #(.highDuration(1), .lowDuration(1)) clock_1 (.out(CLK));
  Button _1 (.out(IR1));
  Button _2 (.out(IR2));
  Button _3 (.out(IR3));
  Multiplexer #(.select(1), .width(32), .disabled("Z"), .enable("false")) multiplexer_1 (
    .in0(PC), .in1(adder_2_out), .out(multiplexer_1_out), .sel(EXBranch));
  Button \u_继续运行  (.out(Go));
  LED #(.active("true")) led_1 (.in(W1));
  LED #(.active("true")) led_2 (.in(W2));
  LED #(.active("true")) led_3 (.in(W3));
  Hex_Digit_Display hex_digit_display_1 (.value(LedData[31:28]));  // open: dp
  not not_1 (not_1_out, stop);
  Multiplexer #(.select(2), .width(32), .disabled("Z"), .enable("false")) multiplexer_2 (
    .in0(multiplexer_1_out), .in1(JMP_PC), .in2(JR_PC), .in3(JR_PC), .out(multiplexer_2_out), .sel({JR, JMP}));
  not not_2 (not_2_out, or_1_out);
  or or_1 (or_1_out, relative, stop);
  Comparator #(.width(32), .mode("twosComplement")) comparator_1 (
    .a(v0), .b(32'h22), .eq(comparator_1_eq));  // open: gt, lt
  not not_3 (not_3_out, comparator_1_eq);
  Hex_Digit_Display hex_digit_display_2 (.value(LedData[27:24]));  // open: dp
  Hex_Digit_Display hex_digit_display_3 (.value(LedData[23:20]));  // open: dp
  Counter #(.width(16), .max('hffff), .ongoal("wrap"), .trigger("rising"), .behavior("old")) counter_1 (
    .D({16{1'b0}}), .count(not_1_out), .Q(\总周期数 ), .clk(CLK));  // open: load, carry, clr, preset
  Register #(.width(32), .trigger("rising"), .Select("low")) u_PC (
    .D(multiplexer_2_out), .en(not_2_out), .Q(IF_PC), .clk(CLK));  // open: clr
  and and_1 (\output , Syscall, comparator_1_eq);
  and and_2 (stop, not_3_out, Syscall);
  and and_3 (and_3_out, relative, not_4_out);
  not not_4 (not_4_out, stop);
  Hex_Digit_Display hex_digit_display_4 (.value(LedData[19:16]));  // open: dp
  Hex_Digit_Display hex_digit_display_5 (.value(LedData[15:12]));  // open: dp
  Adder #(.width(32)) adder_1 (.a(IF_PC), .b(32'h4), .out(PC), .cin(1'b0));  // open: cout
  Counter #(.width(16), .max('hffff), .ongoal("wrap"), .trigger("rising"), .behavior("old")) counter_2 (
    .D({16{1'b0}}), .count(and_3_out), .Q(\插入气泡数 ), .clk(CLK));  // open: load, carry, clr, preset
  Hex_Digit_Display hex_digit_display_6 (.value(LedData[7:4]));  // open: dp
  Hex_Digit_Display hex_digit_display_7 (.value(LedData[11:8]));  // open: dp
  // Probe on \总周期数 
  // Probe on \插入气泡数 
  or or_2 (or_2_out, JMP, EXBranch);
  assign controlled_buffer_1_out = \output  ? a0 : 32'bz;  // Controlled_Buffer controlled_buffer_1
  Hex_Digit_Display hex_digit_display_8 (.value(LedData[3:0]));  // open: dp
  \流水接口2  \u_流水接口2_1  (
    .IR(IR), .PC(PC), .CLK(CLK), .IR_2(\流水接口2_1_ir_2 ), .PC_2(\流水接口2_1_pc_2 ), .\同步清零_高电平有效 (or_2_out),
    .\使能端_低电平有效 (or_1_out), .PCtest_2(ID_PC), .PCtest(IF_PC));  // open: J, JR, JAL, BEQ, BNE, regdst, regwrite, memchoose, memwrite, aluop, alusrcb, A, B, IMM, IMM2, J_2, JR_2, JAL_2, BEQ_2, BNE_2, regdst_2, regwrite_2, memchoose_2, memwrite_2, aluop_2, alusrcb_2, A_2, B_2, IMM_2, IMM2_2, A_prime, A_prime_2, B_prime, B_prime_2, writereg, writereg_2, shamt, shamt_2, cR1, cR1_2, cR2, cR2_2, status, status_2, hit, hit_2, 原来的_PC, 原来的PC
  ROM #(.addrWidth(10), .dataWidth(32), .Select("high")) rom_1 ();  // open: addr, data
  ROM #(.addrWidth(10), .dataWidth(32), .Select("high")) rom_2 (.addr(IF_PC[11:2]), .data(IR));
  or or_3 (or_3_out, or_2_out, relative);
  Register #(.width(32), .trigger("rising"), .Select("low")) PC_2 (
    .D(controlled_buffer_1_out), .Q(LedData), .clk(CLK));  // open: en, clr
  // Probe on \总周期数 
  // Probe on \无条件分支数 
  // Probe on \条件分支成功数 
  // Probe on \插入气泡数 
  // Probe on \LoadUse次数 
  \源寄存器使用情况  \u_源寄存器使用情况_1  (
    .OP0(\流水接口2_1_ir_2 [26]), .OP1(\流水接口2_1_ir_2 [27]), .OP2(\流水接口2_1_ir_2 [28]), .OP3(\流水接口2_1_ir_2 [29]),
    .OP4(\流水接口2_1_ir_2 [30]), .OP5(\流水接口2_1_ir_2 [31]), .F0(\流水接口2_1_ir_2 [0]), .F1(\流水接口2_1_ir_2 [1]),
    .F2(\流水接口2_1_ir_2 [2]), .F3(\流水接口2_1_ir_2 [3]), .F4(\流水接口2_1_ir_2 [4]), .F5(\流水接口2_1_ir_2 [5]),
    .R1used(\源寄存器使用情况_1_r1used ), .R2used(\源寄存器使用情况_1_r2used ));
  \单周期硬布线控制器  \u_单周期硬布线控制器_1  (
    .Func(\流水接口2_1_ir_2 [5:0]), .OP(\流水接口2_1_ir_2 [31:26]), .ALU_OP(\单周期硬布线控制器_1_alu_op ),
    .MemToReg(\单周期硬布线控制器_1_memtoreg ), .MemWrite(\单周期硬布线控制器_1_memwrite ), .ALU_SRC(\单周期硬布线控制器_1_alu_src ),
    .RegWrite(\单周期硬布线控制器_1_regwrite ), .SysCALL(\单周期硬布线控制器_1_syscall ), .RegDst(regdst),
    .JR(\单周期硬布线控制器_1_jr ), .JMP(\单周期硬布线控制器_1_jmp ), .Beq(\单周期硬布线控制器_1_beq ), .JAL(jal),
    .Bne(\单周期硬布线控制器_1_bne ));  // open: SignedExt
  Multiplexer #(.select(1), .width(5), .disabled("Z"), .enable("false")) multiplexer_3 (
    .in0(\流水接口2_1_ir_2 [25:21]), .in1(5'b00010), .out(multiplexer_3_out), .sel(\单周期硬布线控制器_1_syscall ));
  Multiplexer #(.select(1), .width(5), .disabled("Z"), .enable("false")) multiplexer_4 (
    .in0(\流水接口2_1_ir_2 [20:16]), .in1(5'b00100), .out(multiplexer_4_out), .sel(\单周期硬布线控制器_1_syscall ));
  Multiplexer #(.select(1), .width(5), .disabled("Z"), .enable("false")) multiplexer_5 (
    .in0(\流水接口2_4_ir_2 [20:16]), .in1(\流水接口2_4_ir_2 [15:11]), .out(multiplexer_5_out),
    .sel(\流水接口2_4_regdst_2 ));
  Multiplexer #(.select(1), .width(5), .disabled("Z"), .enable("false")) multiplexer_6 (
    .in0(multiplexer_5_out), .in1({5{1'b1}}), .out(multiplexer_6_out), .sel(\流水接口2_4_jal_2 ));
  assign bit_extender_1_out = {{16{\流水接口2_1_ir_2 [15]}}, \流水接口2_1_ir_2 [15:0]};  // Bit_Extender bit_extender_1
  assign bit_extender_2_out = {{6{\流水接口2_1_ir_2 [25]}}, \流水接口2_1_ir_2 [25:0]};  // Bit_Extender bit_extender_2
  Multiplexer #(.select(1), .width(5), .disabled("Z"), .enable("false")) multiplexer_7 (
    .in0(\流水接口2_1_ir_2 [20:16]), .in1(\流水接口2_1_ir_2 [15:11]), .out(multiplexer_7_out), .sel(regdst));
  Multiplexer #(.select(1), .width(5), .disabled("Z"), .enable("false")) multiplexer_8 (
    .in0(multiplexer_7_out), .in1({5{1'b1}}), .out(multiplexer_8_out), .sel(jal));
  // Probe on IF_PC[11:0]
  // Probe on ID_PC[11:0]
  // Probe on EX_PC[11:0]
  \重定向逻辑信号  \u_重定向逻辑信号_1  (
    .R1used(\源寄存器使用情况_1_r1used ), .EX_RegWrite(\流水接口2_2_regwrite_2 ), .R1_num(multiplexer_3_out),
    .R2_num(multiplexer_4_out), .EX_WriteReg_num(\流水接口2_2_writereg_2 ),
    .MEM_WriteReg_num(\流水接口2_3_writereg_2 ), .R2used(\源寄存器使用情况_1_r2used ),
    .MEM_RegWrite(\流水接口2_3_regwrite_2 ), .OP(\流水接口2_3_ir_2 [31:26]), .ChooseR1(CR1), .ChooseR2(CR2));
  MIPS_Regifile mips_regifile_1 (
    .Din(RDin), .Clk(CLK), .R1(mips_regifile_1_r1), .R2(mips_regifile_1_r2), .WE(RegWrite),
    .W_num(multiplexer_6_out), .R1_num(multiplexer_3_out), .R2_num(multiplexer_4_out));
  // Probe on M_PC[11:0]
  \流水接口2  \u_流水接口2_2  (
    .J(\单周期硬布线控制器_1_jmp ), .JR(\单周期硬布线控制器_1_jr ), .JAL(jal), .BEQ(\单周期硬布线控制器_1_beq ),
    .BNE(\单周期硬布线控制器_1_bne ), .regdst(regdst), .regwrite(\单周期硬布线控制器_1_regwrite ),
    .memchoose(\单周期硬布线控制器_1_memtoreg ), .memwrite(\单周期硬布线控制器_1_memwrite ), .aluop(\单周期硬布线控制器_1_alu_op ),
    .alusrcb(\单周期硬布线控制器_1_alu_src ), .A(mips_regifile_1_r1), .B(mips_regifile_1_r2), .IR(\流水接口2_1_ir_2 ),
    .IMM(bit_extender_1_out), .IMM2(bit_extender_2_out), .PC(\流水接口2_1_pc_2 ), .CLK(CLK), .J_2(JMP),
    .JR_2(JR), .JAL_2(\流水接口2_2_jal_2 ), .BEQ_2(\流水接口2_2_beq_2 ), .BNE_2(\流水接口2_2_bne_2 ),
    .regdst_2(\流水接口2_2_regdst_2 ), .regwrite_2(\流水接口2_2_regwrite_2 ), .memchoose_2(\流水接口2_2_memchoose_2 ),
    .memwrite_2(\流水接口2_2_memwrite_2 ), .aluop_2(\流水接口2_2_aluop_2 ), .alusrcb_2(\流水接口2_2_alusrcb_2 ),
    .A_2(EXR1), .B_2(EXR2), .IR_2({\流水接口2_2_ir_2_2 , \流水接口2_2_ir_2 }), .IMM_2(\流水接口2_2_imm_2 ),
    .IMM2_2(\流水接口2_2_imm2_2 ), .PC_2({JMP_PC[31:28], \流水接口2_2_pc_2 }), .\同步清零_高电平有效 (or_3_out),
    .\使能端_低电平有效 (stop), .A_prime(mips_regifile_1_r1), .A_prime_2(JR_PC), .B_prime(mips_regifile_1_r2),
    .writereg(multiplexer_8_out), .writereg_2(\流水接口2_2_writereg_2 ), .shamt(\流水接口2_1_ir_2 [10:6]),
    .shamt_2(\流水接口2_2_shamt_2 ), .cR1(CR1), .cR1_2(\流水接口2_2_cr1_2 ), .cR2(CR2), .cR2_2(\流水接口2_2_cr2_2 ),
    .PCtest_2(EX_PC), .PCtest(ID_PC));  // open: B_prime_2, status, status_2, hit, hit_2, 原来的_PC, 原来的PC
  // Probe on WB_PC[11:0]
  or or_4 (EXBranch, and_4_out, and_5_out);
  \LOAD_USE检测  \load_use检测_1  (
    .R1used(\源寄存器使用情况_1_r1used ), .EX_RegWrite(\流水接口2_2_regwrite_2 ), .R1_num(multiplexer_3_out),
    .EX_WriteReg_num(\流水接口2_2_writereg_2 ), .R2_num(multiplexer_4_out), .R2used(\源寄存器使用情况_1_r2used ),
    .OP(\流水接口2_2_ir_2_2 ), .relative(relative));
  and and_4 (and_4_out, \流水接口2_2_bne_2 , not_5_out);
  not not_5 (not_5_out, mips_alu_1_equal);
  Multiplexer #(.select(1), .width(32), .disabled("Z"), .enable("false")) multiplexer_9 (
    .in0(B), .in1(\流水接口2_2_imm_2 ), .out(multiplexer_9_out), .sel(\流水接口2_2_alusrcb_2 ));
  Shifter #(.width(32), .shift("ll")) shifter_1 (
    .in(\流水接口2_2_imm2_2 ), .\dist (5'b00010), .out({shifter_1_out, JMP_PC[27:0]}));
  Multiplexer #(.select(2), .width(32), .disabled("Z"), .enable("false")) multiplexer_10 (
    .in0(EXR1), .in1(ALU_1), .in2(ALU_2), .in3(WB), .out(A), .sel(\流水接口2_2_cr1_2 ));
  and and_5 (and_5_out, \流水接口2_2_beq_2 , mips_alu_1_equal);
  MIPS_ALU mips_alu_1 (
    .X(A), .Y(multiplexer_9_out), .AluOP(\流水接口2_2_aluop_2 ), .Equal(mips_alu_1_equal),
    .Result(mips_alu_1_result), .shamt(\流水接口2_2_shamt_2 ));  // open: Result_2
  Multiplexer #(.select(2), .width(32), .disabled("Z"), .enable("false")) multiplexer_11 (
    .in0(EXR2), .in1(ALU_1), .in2(ALU_2), .in3(WB), .out(B), .sel(\流水接口2_2_cr2_2 ));
  \流水接口2  \u_流水接口2_3  (
    .JAL(\流水接口2_2_jal_2 ), .regdst(\流水接口2_2_regdst_2 ), .regwrite(\流水接口2_2_regwrite_2 ),
    .memchoose(\流水接口2_2_memchoose_2 ), .memwrite(\流水接口2_2_memwrite_2 ), .A(mips_alu_1_result), .B(B),
    .IR({\流水接口2_2_ir_2_2 , \流水接口2_2_ir_2 }), .PC({JMP_PC[31:28], \流水接口2_2_pc_2 }), .CLK(CLK),
    .JAL_2(\流水接口2_3_jal_2 ), .regdst_2(\流水接口2_3_regdst_2 ), .regwrite_2(\流水接口2_3_regwrite_2 ),
    .memchoose_2(\流水接口2_3_memchoose_2 ), .memwrite_2(MemWrite), .A_2(ALU_1), .B_2(MDin),
    .IR_2(\流水接口2_3_ir_2 ), .PC_2(\流水接口2_3_pc_2 ), .\使能端_低电平有效 (stop), .A_prime(A),
    .A_prime_2(\流水接口2_3_a_prime_2 ), .B_prime(B), .B_prime_2(\流水接口2_3_b_prime_2 ),
    .writereg(\流水接口2_2_writereg_2 ), .writereg_2(\流水接口2_3_writereg_2 ), .PCtest_2(M_PC), .PCtest(EX_PC));  // open: J, JR, BEQ, BNE, aluop, alusrcb, IMM, IMM2, J_2, JR_2, BEQ_2, BNE_2, aluop_2, alusrcb_2, IMM_2, IMM2_2, 同步清零_高电平有效, shamt, shamt_2, cR1, cR1_2, cR2, cR2_2, status, status_2, hit, hit_2, 原来的_PC, 原来的PC
  \流水接口2  \u_流水接口2_4  (
    .JAL(\流水接口2_3_jal_2 ), .regdst(\流水接口2_3_regdst_2 ), .regwrite(\流水接口2_3_regwrite_2 ),
    .memchoose(\流水接口2_3_memchoose_2 ), .A(ALU_1), .B(ram_1_data), .IR(\流水接口2_3_ir_2 ), .PC(\流水接口2_3_pc_2 ),
    .CLK(CLK), .JAL_2(\流水接口2_4_jal_2 ), .regdst_2(\流水接口2_4_regdst_2 ), .regwrite_2(RegWrite),
    .memchoose_2(\流水接口2_4_memchoose_2 ), .A_2(ALU_2), .B_2(WB), .IR_2(\流水接口2_4_ir_2 ), .PC_2(\流水接口2_4_pc_2 ),
    .\使能端_低电平有效 (stop), .A_prime(\流水接口2_3_a_prime_2 ), .A_prime_2(v0), .B_prime(\流水接口2_3_b_prime_2 ),
    .B_prime_2(a0), .PCtest_2(WB_PC), .PCtest(M_PC));  // open: J, JR, BEQ, BNE, memwrite, aluop, alusrcb, IMM, IMM2, J_2, JR_2, BEQ_2, BNE_2, memwrite_2, aluop_2, alusrcb_2, IMM_2, IMM2_2, 同步清零_高电平有效, writereg, writereg_2, shamt, shamt_2, cR1, cR1_2, cR2, cR2_2, status, status_2, hit, hit_2, 原来的_PC, 原来的PC
  RAM #(.addrWidth(10), .dataWidth(32), .bus("separate"), .Select("high")) ram_1 (
    .addr(ALU_1[11:2]), .din(MDin), .data(ram_1_data), .str(MemWrite), .sel(1'b1), .clk(CLK));  // open: ld, clr
  Multiplexer #(.select(1), .width(32), .disabled("Z"), .enable("false")) multiplexer_12 (
    .in0(ALU_2), .in1(WB), .out(multiplexer_12_out), .sel(\流水接口2_4_memchoose_2 ));
  Shifter #(.width(32), .shift("ll")) shifter_2 (.in(\流水接口2_2_imm_2 ), .\dist (5'b00010), .out(shifter_2_out));
  Multiplexer #(.select(1), .width(32), .disabled("Z"), .enable("false")) multiplexer_13 (
    .in0(multiplexer_12_out), .in1(\流水接口2_4_pc_2 ), .out(RDin), .sel(\流水接口2_4_jal_2 ));
  Adder #(.width(32)) adder_2 (
    .a({JMP_PC[31:28], \流水接口2_2_pc_2 }), .b(shifter_2_out), .out(adder_2_out));  // open: cin, cout
  Comparator #(.width(32), .mode("twosComplement")) comparator_2 (
    .a(\流水接口2_4_ir_2 ), .b(32'hc), .eq(Syscall));  // open: gt, lt

  // Other names for the same wires on the sheet: MEM_PC[31:0] = M_PC

  // Notes on the sheet:
  //   中断源
  //   中断等待指示
  //   总复位信号应将除ROM以外所有存储组件全部清零
  //   数码管输出
  //   数码管输出应该用寄存器锁存，否则显示数据只能一闪而过
  //   指令存储器
  //   contents of rom_1 (hex, n*v repeats v):
  //   20110004 ae310000 8e320000 2252fffc 20100000 22110001 2118020 22520004 ae500000 22310001 2118020
  //   22520004 ae500000 22310001 2118020 22520004 ae500000 22310001 2118020 22520004 ae500000 22310001
  //   2118020 22520004 ae500000 22310001 2118020 22520004 ae500000 22310001 2118020 22520004 ae500000
  //   2002000a 20100000 20100000 20100000 c
  //   contents of rom_2 (hex, n*v repeats v):
  //   20110001 8000c05 20110001 20120002 20130003 8000c09 20110001 20120002 20130003 8000c0d 20110001
  //   20120002 20130003 8000c11 20110001 20120002 20130003 c000cb8 20100001 20110001 118fc0 112020
  //   20020022 c 118882 12200001 8000c15 112020 20020022 c 20110001 118880 112020 20020022 c 12200001
  //   8000c1f 20110001 118fc0 112020 20020022 c 1188c3 112020 20020022 c 118903 112020 20020022 c 118903
  //   112020 20020022 c 118903 112020 20020022 c 118903 112020 20020022 c 118903 112020 20020022 c 118903
  //   112020 20020022 c 118903 112020 20020022 c 20100001 109fc0 139fc3 8021 2012000c 24160003 26100001
  //   3210000f 20080008 20090001 139900 2709825 132020 20020022 c 1094022 1500fff9 22100001 2018000f
  //   2188024 108700 20080008 20090001 139902 2709825 132021 20020022 c 1094022 1500fff9 108702 2c9b022
  //   12c00001 8000c50 4020 1084027 84400 3508ffff 82021 20020022 c 2010ffff 20110000 ae300000 22100001
  //   22310004 ae300000 22100001 22310004 ae300000 22100001 22310004 ae300000 22100001 22310004 ae300000
  //   22100001 22310004 ae300000 22100001 22310004 ae300000 22100001 22310004 ae300000 22100001 22310004
  //   ae300000 22100001 22310004 ae300000 22100001 22310004 ae300000 22100001 22310004 ae300000 22100001
  //   22310004 ae300000 22100001 22310004 ae300000 22100001 22310004 ae300000 22100001 22310004 ae300000
  //   22100001 22310004 22100001 8020 2011003c 8e130000 8e340000 274402a 11000002 ae330000 ae140000
  //   2231fffc 1611fff8 102020 20020022 c 22100004 2011003c 1611fff2 20020032 c 20100000 22100001 102020
  //   20020022 c 22100002 102020 20020022 c 22100003 102020 20020022 c 22100004 102020 20020022 c 22100005
  //   102020 20020022 c 22100006 102020 20020022 c 22100007 102020 20020022 c 22100008 102020 20020022
  //   20020022 c 3e00008
  //   rs
  //   rt
  //   rt
  //   rd
  //   shamt
  //   rt
  //   rd
  //   JMP
  //   JR
  //   OP
  //   Func
  //   Beq
  //   Bne
  //   MemToReg
  //   MemWrite
  //   AluOP
  //   AluSrcB
  //   RegWrite
  //   JAL
  //   RegDst
  //   流水调试日志用
  //   为方便自动评测，需要输出流水线各段保存的PC值，注意是PC不是PC+4，另外ID段寄存器写入信息，Mem段内存写入信息也要输出
endmodule

module \中断按键参考电路  (
  input  \同步清零信号 ,
  output \与中断屏蔽位与 
);

  wire \_1号中断_out , and_1_out, clock_1_out, d_ff_1_q, or_1_out, or_2_out;

  Clock #(.highDuration(1), .lowDuration(1)) clock_1 (.out(clock_1_out));
  Button \_1号中断  (.out(\_1号中断_out ));
  or or_1 (or_1_out, \与中断屏蔽位与 , d_ff_1_q);
  LED #(.active("true")) \_1号中断等待指示灯  (.in(or_1_out));
  D_Flip_Flop #(.trigger("rising"), .Pre_Clr_Positions("LEGACY"), .NegatePresetClear("false"), .enable("true"), .NewFFLayout("false")) d_ff_1 (
    .clk(\_1号中断_out ), .D(1'b1), .Q(d_ff_1_q), .reset(\与中断屏蔽位与 ));  // open: Qn, preset, en
  or or_2 (or_2_out, d_ff_1_q, \与中断屏蔽位与 );
  and and_1 (and_1_out, or_2_out, ~\同步清零信号 );  // AND_Gate
  D_Flip_Flop #(.trigger("rising"), .Pre_Clr_Positions("LEGACY"), .NegatePresetClear("false"), .enable("true"), .NewFFLayout("false")) IR1 (
    .clk(clock_1_out), .D(and_1_out), .Q(\与中断屏蔽位与 ));  // open: Qn, preset, en, reset
  \单周期硬布线控制器  \u_单周期硬布线控制器_1  ();  // open: Func, OP, ALU_OP, MemToReg, MemWrite, ALU_SRC, RegWrite, SysCALL, SignedExt, RegDst, JR, JMP, Beq, JAL, Bne

  // Notes on the sheet:
  //   中断信号采样参考电路
  //   Reset 
endmodule

module \流水接口  (
  input  regdst,
  input  regwrite,
  input  memchoose,
  input  memwrite,
  input  [3:0] aluop,
  input  alusrcb,
  input  [31:0] A,
  input  [31:0] B,
  input  [31:0] IR,
  input  [31:0] IMM,
  input  [31:0] PC,
  input  CLK,
  input  \同步清零_高电平有效 ,
  input  \使能端_低电平有效 ,
  output regdst_2,
  output regwrite_2,
  output memchoose_2,
  output memwrite_2,
  output [3:0] aluop_2,
  output alusrcb_2,
  output [31:0] A_2,
  output [31:0] B_2,
  output [31:0] IR_2,
  output [31:0] IMM_2,
  output [31:0] PC_2
);

  wire multiplexer_1_out, multiplexer_2_out, multiplexer_3_out, multiplexer_4_out, multiplexer_6_out,
       pull_resistor_2_node;
  wire [3:0] multiplexer_5_out;
  wire [31:0] multiplexer_7_out, multiplexer_8_out, multiplexer_9_out, multiplexer_10_out, multiplexer_11_out;

  Multiplexer #(.select(1), .width(1), .disabled("Z"), .enable("false")) multiplexer_1 (
    .in0(regdst), .in1(1'b0), .out(multiplexer_1_out), .sel(\同步清零_高电平有效 ));
  Multiplexer #(.select(1), .width(1), .disabled("Z"), .enable("false")) multiplexer_2 (
    .in0(regwrite), .in1(1'b0), .out(multiplexer_2_out), .sel(\同步清零_高电平有效 ));
  Multiplexer #(.select(1), .width(1), .disabled("Z"), .enable("false")) multiplexer_3 (
    .in0(memchoose), .in1(1'b0), .out(multiplexer_3_out), .sel(\同步清零_高电平有效 ));
  Multiplexer #(.select(1), .width(1), .disabled("Z"), .enable("false")) multiplexer_4 (
    .in0(memwrite), .in1(1'b0), .out(multiplexer_4_out), .sel(\同步清零_高电平有效 ));
  Multiplexer #(.select(1), .width(4), .disabled("Z"), .enable("false")) multiplexer_5 (
    .in0(aluop), .in1(4'b0000), .out(multiplexer_5_out), .sel(\同步清零_高电平有效 ));
  Multiplexer #(.select(1), .width(1), .disabled("Z"), .enable("false")) multiplexer_6 (
    .in0(alusrcb), .in1(1'b0), .out(multiplexer_6_out), .sel(\同步清零_高电平有效 ));
  Multiplexer #(.select(1), .width(32), .disabled("Z"), .enable("false")) multiplexer_7 (
    .in0(A), .in1({32{1'b0}}), .out(multiplexer_7_out), .sel(\同步清零_高电平有效 ));
  Multiplexer #(.select(1), .width(32), .disabled("Z"), .enable("false")) multiplexer_8 (
    .in0(B), .in1({32{1'b0}}), .out(multiplexer_8_out), .sel(\同步清零_高电平有效 ));
  Multiplexer #(.select(1), .width(32), .disabled("Z"), .enable("false")) multiplexer_9 (
    .in0(IR), .in1({32{1'b0}}), .out(multiplexer_9_out), .sel(\同步清零_高电平有效 ));
  Multiplexer #(.select(1), .width(32), .disabled("Z"), .enable("false")) multiplexer_10 (
    .in0(IMM), .in1({32{1'b0}}), .out(multiplexer_10_out), .sel(\同步清零_高电平有效 ));
  Multiplexer #(.select(1), .width(32), .disabled("Z"), .enable("false")) multiplexer_11 (
    .in0(PC), .in1({32{1'b0}}), .out(multiplexer_11_out), .sel(\同步清零_高电平有效 ));
  Pull_Resistor #(.pull(0)) pull_resistor_1 (.node(\同步清零_高电平有效 ));
  Register #(.width(1), .trigger("rising"), .Select("low")) register_1 (
    .D(multiplexer_1_out), .en(pull_resistor_2_node), .Q(regdst_2), .clk(CLK));  // open: clr
  Register #(.width(1), .trigger("rising"), .Select("low")) register_2 (
    .D(multiplexer_2_out), .en(pull_resistor_2_node), .Q(regwrite_2), .clk(CLK));  // open: clr
  Register #(.width(1), .trigger("rising"), .Select("low")) register_3 (
    .D(multiplexer_3_out), .en(pull_resistor_2_node), .Q(memchoose_2), .clk(CLK));  // open: clr
  Register #(.width(1), .trigger("rising"), .Select("low")) register_4 (
    .D(multiplexer_4_out), .en(pull_resistor_2_node), .Q(memwrite_2), .clk(CLK));  // open: clr
  Register #(.width(4), .trigger("rising"), .Select("low")) register_5 (
    .D(multiplexer_5_out), .en(pull_resistor_2_node), .Q(aluop_2), .clk(CLK));  // open: clr
  Register #(.width(1), .trigger("rising"), .Select("low")) register_6 (
    .D(multiplexer_6_out), .en(pull_resistor_2_node), .Q(alusrcb_2), .clk(CLK));  // open: clr
  Register #(.width(32), .trigger("rising"), .Select("low")) register_7 (
    .D(multiplexer_7_out), .en(pull_resistor_2_node), .Q(A_2), .clk(CLK));  // open: clr
  Register #(.width(32), .trigger("rising"), .Select("low")) register_8 (
    .D(multiplexer_8_out), .en(pull_resistor_2_node), .Q(B_2), .clk(CLK));  // open: clr
  Register #(.width(32), .trigger("rising"), .Select("low")) register_9 (
    .D(multiplexer_9_out), .en(pull_resistor_2_node), .Q(IR_2), .clk(CLK));  // open: clr
  Register #(.width(32), .trigger("rising"), .Select("low")) register_10 (
    .D(multiplexer_10_out), .en(pull_resistor_2_node), .Q(IMM_2), .clk(CLK));  // open: clr
  Register #(.width(32), .trigger("rising"), .Select("low")) register_11 (
    .D(multiplexer_11_out), .en(pull_resistor_2_node), .Q(PC_2), .clk(CLK));  // open: clr
  Pull_Resistor #(.pull(0)) pull_resistor_2 (.node(pull_resistor_2_node));
  not not_1 (pull_resistor_2_node, \使能端_低电平有效 );

  // Notes on the sheet:
  //   同步清零_高电平有效: pull=down
  //   使能端_低电平有效: pull=down
  //   下拉电阻使得引脚可以悬空
endmodule
module \分支流水线  (
  output RegWrite,
  output MemWrite,
  output [31:0] PC,
  output [31:0] IR,
  output [31:0] RDin,
  output [31:0] MDin
);

  wire and_3_out, and_4_out, CLK, comparator_1_eq, EXBranch, Go, IR1, IR2, IR3, JMP, JR, mips_alu_1_equal,
       not_1_out, not_2_out, not_3_out, \output , stop, Syscall, W1, W2, W3, \单周期硬布线控制器_1_alu_src ,
       \单周期硬布线控制器_1_beq , \单周期硬布线控制器_1_bne , \单周期硬布线控制器_1_jal , \单周期硬布线控制器_1_jmp , \单周期硬布线控制器_1_jr ,
       \单周期硬布线控制器_1_memtoreg , \单周期硬布线控制器_1_memwrite , \单周期硬布线控制器_1_regdst , \单周期硬布线控制器_1_regwrite ,
       \单周期硬布线控制器_1_syscall , \流水接口2_2_alusrcb_2 , \流水接口2_2_beq_2 , \流水接口2_2_bne_2 , \流水接口2_2_jal_2 ,
       \流水接口2_2_memchoose_2 , \流水接口2_2_memwrite_2 , \流水接口2_2_regdst_2 , \流水接口2_2_regwrite_2 ,
       \流水接口2_3_jal_2 , \流水接口2_3_memchoose_2 , \流水接口2_3_regdst_2 , \流水接口2_3_regwrite_2 , \流水接口2_4_jal_2 ,
       \流水接口2_4_memchoose_2 , \流水接口2_4_regdst_2 ;
  wire [3:0] \单周期硬布线控制器_1_alu_op , \流水接口2_2_aluop_2 ;
  wire [4:0] multiplexer_3_out, multiplexer_4_out, multiplexer_5_out, multiplexer_6_out;
  wire [15:0] \总周期数 ;
  wire [27:0] \流水接口2_2_pc_2 ;
  wire [31:0] a0, adder_2_out, bit_extender_1_out, bit_extender_2_out, controlled_buffer_1_out, JMP_PC,
       JR_PC, LedData, mips_alu_1_result, mips_regifile_1_r1, mips_regifile_1_r2, multiplexer_1_out,
       multiplexer_2_out, multiplexer_7_out, multiplexer_8_out, PC_q, ram_1_data, shifter_2_out, v0,
       \流水接口2_1_ir_2 , \流水接口2_1_pc_2 , \流水接口2_2_a_2 , \流水接口2_2_b_2 , \流水接口2_2_b_prime_2 , \流水接口2_2_imm2_2 ,
       \流水接口2_2_imm_2 , \流水接口2_2_ir_2 , \流水接口2_3_a_2 , \流水接口2_3_a_prime_2 , \流水接口2_3_b_prime_2 ,
       \流水接口2_3_ir_2 , \流水接口2_3_pc_2 , \流水接口2_4_a_2 , \流水接口2_4_b_2 , \流水接口2_4_ir_2 , \流水接口2_4_pc_2 ;
  wire [31:28] shifter_1_out;

  Clock #(.highDuration(1), .lowDuration(1)) clock_1 (.out(CLK));
  Button _1 (.out(IR1));
  Button _2 (.out(IR2));
  Button _3 (.out(IR3));
  Multiplexer #(.select(1), .width(32), .disabled("Z"), .enable("false")) multiplexer_1 (
    .in0(PC), .in1(adder_2_out), .out(multiplexer_1_out), .sel(EXBranch));
  Button \u_继续运行  (.out(Go));
  LED #(.active("true")) led_1 (.in(W1));
  LED #(.active("true")) led_2 (.in(W2));
  LED #(.active("true")) led_3 (.in(W3));
  Hex_Digit_Display hex_digit_display_1 (.value(LedData[31:28]));  // open: dp
  Multiplexer #(.select(2), .width(32), .disabled("Z"), .enable("false")) multiplexer_2 (
    .in0(multiplexer_1_out), .in1(JMP_PC), .in2(JR_PC), .in3(JR_PC), .out(multiplexer_2_out), .sel({JR, JMP}));
  not not_1 (not_1_out, stop);
  Comparator #(.width(32), .mode("twosComplement")) comparator_1 (
    .a(v0), .b(32'h22), .eq(comparator_1_eq));  // open: gt, lt
  not not_2 (not_2_out, comparator_1_eq);
  Hex_Digit_Display hex_digit_display_2 (.value(LedData[23:20]));  // open: dp
  Hex_Digit_Display hex_digit_display_3 (.value(LedData[27:24]));  // open: dp
  Counter #(.width(16), .max('hffff), .ongoal("wrap"), .trigger("rising"), .behavior("old")) counter_1 (
    .D({16{1'b0}}), .count(not_1_out), .Q(\总周期数 ), .clk(CLK));  // open: load, carry, clr, preset
  Register #(.width(32), .trigger("rising"), .Select("low")) u_PC (
    .D(multiplexer_2_out), .en(not_1_out), .Q(PC_q), .clk(CLK));  // open: clr
  and and_1 (\output , Syscall, comparator_1_eq);
  and and_2 (stop, not_2_out, Syscall);
  Hex_Digit_Display hex_digit_display_4 (.value(LedData[15:12]));  // open: dp
  Hex_Digit_Display hex_digit_display_5 (.value(LedData[19:16]));  // open: dp
  Adder #(.width(32)) adder_1 (.a(PC_q), .b(32'h4), .out(PC), .cin(1'b0));  // open: cout
  Hex_Digit_Display hex_digit_display_6 (.value(LedData[7:4]));  // open: dp
  Hex_Digit_Display hex_digit_display_7 (.value(LedData[11:8]));  // open: dp
  // Probe on \总周期数 
  assign controlled_buffer_1_out = \output  ? a0 : 32'bz;  // Controlled_Buffer controlled_buffer_1
  Hex_Digit_Display hex_digit_display_8 (.value(LedData[3:0]));  // open: dp
  \流水接口2  \u_流水接口2_1  (
    .IR(IR), .PC(PC), .CLK(CLK), .IR_2(\流水接口2_1_ir_2 ), .PC_2(\流水接口2_1_pc_2 ), .\同步清零_高电平有效 (CLK),
    .\使能端_低电平有效 (stop));  // open: J, JR, JAL, BEQ, BNE, regdst, regwrite, memchoose, memwrite, aluop, alusrcb, A, B, IMM, IMM2, J_2, JR_2, JAL_2, BEQ_2, BNE_2, regdst_2, regwrite_2, memchoose_2, memwrite_2, aluop_2, alusrcb_2, A_2, B_2, IMM_2, IMM2_2, A_prime, A_prime_2, B_prime, B_prime_2, writereg, writereg_2, shamt, shamt_2, cR1, cR1_2, cR2, cR2_2, status, status_2, hit, hit_2, 原来的_PC, 原来的PC, PCtest_2, PCtest
  ROM #(.addrWidth(10), .dataWidth(32), .Select("high")) rom_1 (.addr(PC_q[11:2]), .data(IR));
  or or_1 (CLK, JMP, EXBranch);
  Register #(.width(32), .trigger("rising"), .Select("low")) PC_2 (
    .D(controlled_buffer_1_out), .Q(LedData), .clk(CLK));  // open: en, clr
  \单周期硬布线控制器  \u_单周期硬布线控制器_1  (
    .Func(\流水接口2_1_ir_2 [5:0]), .OP(\流水接口2_1_ir_2 [31:26]), .ALU_OP(\单周期硬布线控制器_1_alu_op ),
    .MemToReg(\单周期硬布线控制器_1_memtoreg ), .MemWrite(\单周期硬布线控制器_1_memwrite ), .ALU_SRC(\单周期硬布线控制器_1_alu_src ),
    .RegWrite(\单周期硬布线控制器_1_regwrite ), .SysCALL(\单周期硬布线控制器_1_syscall ), .RegDst(\单周期硬布线控制器_1_regdst ),
    .JR(\单周期硬布线控制器_1_jr ), .JMP(\单周期硬布线控制器_1_jmp ), .Beq(\单周期硬布线控制器_1_beq ), .JAL(\单周期硬布线控制器_1_jal ),
    .Bne(\单周期硬布线控制器_1_bne ));  // open: SignedExt
  Multiplexer #(.select(1), .width(5), .disabled("Z"), .enable("false")) multiplexer_3 (
    .in0(\流水接口2_1_ir_2 [25:21]), .in1(5'b00010), .out(multiplexer_3_out), .sel(\单周期硬布线控制器_1_syscall ));
  Multiplexer #(.select(1), .width(5), .disabled("Z"), .enable("false")) multiplexer_4 (
    .in0(\流水接口2_1_ir_2 [20:16]), .in1(5'b00100), .out(multiplexer_4_out), .sel(\单周期硬布线控制器_1_syscall ));
  Multiplexer #(.select(1), .width(5), .disabled("Z"), .enable("false")) multiplexer_5 (
    .in0(\流水接口2_4_ir_2 [20:16]), .in1(\流水接口2_4_ir_2 [15:11]), .out(multiplexer_5_out),
    .sel(\流水接口2_4_regdst_2 ));
  Multiplexer #(.select(1), .width(5), .disabled("Z"), .enable("false")) multiplexer_6 (
    .in0(multiplexer_5_out), .in1({5{1'b1}}), .out(multiplexer_6_out), .sel(\流水接口2_4_jal_2 ));
  assign bit_extender_1_out = {{16{\流水接口2_1_ir_2 [15]}}, \流水接口2_1_ir_2 [15:0]};  // Bit_Extender bit_extender_1
  assign bit_extender_2_out = {{6{\流水接口2_1_ir_2 [25]}}, \流水接口2_1_ir_2 [25:0]};  // Bit_Extender bit_extender_2
  MIPS_Regifile mips_regifile_1 (
    .Din(RDin), .Clk(CLK), .R1(mips_regifile_1_r1), .R2(mips_regifile_1_r2), .WE(RegWrite),
    .W_num(multiplexer_6_out), .R1_num(multiplexer_3_out), .R2_num(multiplexer_4_out));
  \流水接口2  \u_流水接口2_2  (
    .J(\单周期硬布线控制器_1_jmp ), .JR(\单周期硬布线控制器_1_jr ), .JAL(\单周期硬布线控制器_1_jal ), .BEQ(\单周期硬布线控制器_1_beq ),
    .BNE(\单周期硬布线控制器_1_bne ), .regdst(\单周期硬布线控制器_1_regdst ), .regwrite(\单周期硬布线控制器_1_regwrite ),
    .memchoose(\单周期硬布线控制器_1_memtoreg ), .memwrite(\单周期硬布线控制器_1_memwrite ), .aluop(\单周期硬布线控制器_1_alu_op ),
    .alusrcb(\单周期硬布线控制器_1_alu_src ), .A(mips_regifile_1_r1), .B(mips_regifile_1_r2), .IR(\流水接口2_1_ir_2 ),
    .IMM(bit_extender_1_out), .IMM2(bit_extender_2_out), .PC(\流水接口2_1_pc_2 ), .CLK(CLK), .J_2(JMP),
    .JR_2(JR), .JAL_2(\流水接口2_2_jal_2 ), .BEQ_2(\流水接口2_2_beq_2 ), .BNE_2(\流水接口2_2_bne_2 ),
    .regdst_2(\流水接口2_2_regdst_2 ), .regwrite_2(\流水接口2_2_regwrite_2 ), .memchoose_2(\流水接口2_2_memchoose_2 ),
    .memwrite_2(\流水接口2_2_memwrite_2 ), .aluop_2(\流水接口2_2_aluop_2 ), .alusrcb_2(\流水接口2_2_alusrcb_2 ),
    .A_2(\流水接口2_2_a_2 ), .B_2(\流水接口2_2_b_2 ), .IR_2(\流水接口2_2_ir_2 ), .IMM_2(\流水接口2_2_imm_2 ),
    .IMM2_2(\流水接口2_2_imm2_2 ), .PC_2({JMP_PC[31:28], \流水接口2_2_pc_2 }), .\同步清零_高电平有效 (CLK),
    .\使能端_低电平有效 (stop), .A_prime(mips_regifile_1_r1), .A_prime_2(JR_PC), .B_prime(mips_regifile_1_r2),
    .B_prime_2(\流水接口2_2_b_prime_2 ));  // open: writereg, writereg_2, shamt, shamt_2, cR1, cR1_2, cR2, cR2_2, status, status_2, hit, hit_2, 原来的_PC, 原来的PC, PCtest_2, PCtest
  or or_2 (EXBranch, and_3_out, and_4_out);
  and and_3 (and_3_out, \流水接口2_2_bne_2 , not_3_out);
  not not_3 (not_3_out, mips_alu_1_equal);
  Multiplexer #(.select(1), .width(32), .disabled("Z"), .enable("false")) multiplexer_7 (
    .in0(\流水接口2_2_b_2 ), .in1(\流水接口2_2_imm_2 ), .out(multiplexer_7_out), .sel(\流水接口2_2_alusrcb_2 ));
  Shifter #(.width(32), .shift("ll")) shifter_1 (
    .in(\流水接口2_2_imm2_2 ), .\dist (5'b00010), .out({shifter_1_out, JMP_PC[27:0]}));
  and and_4 (and_4_out, \流水接口2_2_beq_2 , mips_alu_1_equal);
  MIPS_ALU mips_alu_1 (
    .X(\流水接口2_2_a_2 ), .Y(multiplexer_7_out), .AluOP(\流水接口2_2_aluop_2 ), .Equal(mips_alu_1_equal),
    .Result(mips_alu_1_result), .shamt({5{1'b0}}));  // open: Result_2
  Shifter #(.width(32), .shift("ll")) shifter_2 (.in(\流水接口2_2_imm_2 ), .\dist (5'b00010), .out(shifter_2_out));
  \流水接口2  \u_流水接口2_3  (
    .JAL(\流水接口2_2_jal_2 ), .regdst(\流水接口2_2_regdst_2 ), .regwrite(\流水接口2_2_regwrite_2 ),
    .memchoose(\流水接口2_2_memchoose_2 ), .memwrite(\流水接口2_2_memwrite_2 ), .A(mips_alu_1_result),
    .B(\流水接口2_2_b_2 ), .IR(\流水接口2_2_ir_2 ), .PC({JMP_PC[31:28], \流水接口2_2_pc_2 }), .CLK(CLK),
    .JAL_2(\流水接口2_3_jal_2 ), .regdst_2(\流水接口2_3_regdst_2 ), .regwrite_2(\流水接口2_3_regwrite_2 ),
    .memchoose_2(\流水接口2_3_memchoose_2 ), .memwrite_2(MemWrite), .A_2(\流水接口2_3_a_2 ), .B_2(MDin),
    .IR_2(\流水接口2_3_ir_2 ), .PC_2(\流水接口2_3_pc_2 ), .\使能端_低电平有效 (stop), .A_prime(JR_PC),
    .A_prime_2(\流水接口2_3_a_prime_2 ), .B_prime(\流水接口2_2_b_prime_2 ), .B_prime_2(\流水接口2_3_b_prime_2 ));  // open: J, JR, BEQ, BNE, aluop, alusrcb, IMM, IMM2, J_2, JR_2, BEQ_2, BNE_2, aluop_2, alusrcb_2, IMM_2, IMM2_2, 同步清零_高电平有效, writereg, writereg_2, shamt, shamt_2, cR1, cR1_2, cR2, cR2_2, status, status_2, hit, hit_2, 原来的_PC, 原来的PC, PCtest_2, PCtest
  Adder #(.width(32)) adder_2 (
    .a({JMP_PC[31:28], \流水接口2_2_pc_2 }), .b(shifter_2_out), .out(adder_2_out));  // open: cin, cout
  \流水接口2  \u_流水接口2_4  (
    .JAL(\流水接口2_3_jal_2 ), .regdst(\流水接口2_3_regdst_2 ), .regwrite(\流水接口2_3_regwrite_2 ),
    .memchoose(\流水接口2_3_memchoose_2 ), .A(\流水接口2_3_a_2 ), .B(ram_1_data), .IR(\流水接口2_3_ir_2 ),
    .PC(\流水接口2_3_pc_2 ), .CLK(CLK), .JAL_2(\流水接口2_4_jal_2 ), .regdst_2(\流水接口2_4_regdst_2 ),
    .regwrite_2(RegWrite), .memchoose_2(\流水接口2_4_memchoose_2 ), .A_2(\流水接口2_4_a_2 ), .B_2(\流水接口2_4_b_2 ),
    .IR_2(\流水接口2_4_ir_2 ), .PC_2(\流水接口2_4_pc_2 ), .\使能端_低电平有效 (stop), .A_prime(\流水接口2_3_a_prime_2 ),
    .A_prime_2(v0), .B_prime(\流水接口2_3_b_prime_2 ), .B_prime_2(a0));  // open: J, JR, BEQ, BNE, memwrite, aluop, alusrcb, IMM, IMM2, J_2, JR_2, BEQ_2, BNE_2, memwrite_2, aluop_2, alusrcb_2, IMM_2, IMM2_2, 同步清零_高电平有效, writereg, writereg_2, shamt, shamt_2, cR1, cR1_2, cR2, cR2_2, status, status_2, hit, hit_2, 原来的_PC, 原来的PC, PCtest_2, PCtest
  RAM #(.addrWidth(10), .dataWidth(32), .bus("separate"), .Select("high")) ram_1 (
    .addr(\流水接口2_3_a_2 [11:2]), .din(MDin), .data(ram_1_data), .str(MemWrite), .sel(1'b1), .clk(CLK));  // open: ld, clr
  Multiplexer #(.select(1), .width(32), .disabled("Z"), .enable("false")) multiplexer_8 (
    .in0(\流水接口2_4_a_2 ), .in1(\流水接口2_4_b_2 ), .out(multiplexer_8_out), .sel(\流水接口2_4_memchoose_2 ));
  Multiplexer #(.select(1), .width(32), .disabled("Z"), .enable("false")) multiplexer_9 (
    .in0(multiplexer_8_out), .in1(\流水接口2_4_pc_2 ), .out(RDin), .sel(\流水接口2_4_jal_2 ));
  Comparator #(.width(32), .mode("twosComplement")) comparator_2 (
    .a(\流水接口2_4_ir_2 ), .b(32'hc), .eq(Syscall));  // open: gt, lt

  // Notes on the sheet:
  //   中断源
  //   中断等待指示
  //   总复位信号应将除ROM以外所有存储组件全部清零
  //   数码管输出
  //   数码管输出应该用寄存器锁存，否则显示数据只能一闪而过
  //   指令存储器
  //   contents of rom_1 (hex, n*v repeats v):
  //   20110020 20020022 8000006 20110004 20120005 20130006 10000003 20110007 20120008 20130009 14110003
  //   2011000a 2012000b 2013000c c000014 2002000a 0 0 0 c 2231ffff 0 0 0 112020 0 0 0 c 1620fff6 3e00008
  //   rs
  //   rt
  //   rt
  //   rd
  //   JMP
  //   JR
  //   OP
  //   Func
  //   Beq
  //   Bne
  //   MemToReg
  //   MemWrite
  //   AluOP
  //   AluSrcB
  //   RegWrite
  //   JAL
  //   RegDst
  //   为方便自动评测，需要输出PC，IR，寄存器文件写入端口RDin，内存写入端口MDin等信号
endmodule

module \流水接口2  (
  input  J,
  input  JR,
  input  JAL,
  input  BEQ,
  input  BNE,
  input  regdst,
  input  regwrite,
  input  memchoose,
  input  memwrite,
  input  [3:0] aluop,
  input  alusrcb,
  input  [31:0] A,
  input  [31:0] B,
  input  [31:0] A_prime,
  input  [31:0] B_prime,
  input  [31:0] IR,
  input  [31:0] PCtest,
  input  [31:0] IMM,
  input  [4:0] writereg,
  input  [4:0] shamt,
  input  [31:0] IMM2,
  input  [31:0] PC,
  input  [1:0] cR1,
  input  [1:0] cR2,
  input  [1:0] status,
  input  hit,
  input  [31:0] \原来的PC ,
  input  CLK,
  input  \同步清零_高电平有效 ,
  input  \使能端_低电平有效 ,
  output J_2,
  output JR_2,
  output JAL_2,
  output BEQ_2,
  output BNE_2,
  output regdst_2,
  output regwrite_2,
  output memchoose_2,
  output memwrite_2,
  output [3:0] aluop_2,
  output alusrcb_2,
  output [31:0] A_2,
  output [31:0] B_2,
  output [31:0] A_prime_2,
  output [31:0] B_prime_2,
  output [31:0] IR_2,
  output [31:0] PCtest_2,
  output [31:0] IMM_2,
  output [4:0] writereg_2,
  output [4:0] shamt_2,
  output [31:0] IMM2_2,
  output [31:0] PC_2,
  output [1:0] cR1_2,
  output [1:0] cR2_2,
  output [1:0] status_2,
  output hit_2,
  output [31:0] \原来的_PC 
);

  wire multiplexer_1_out, multiplexer_2_out, multiplexer_3_out, multiplexer_4_out, multiplexer_5_out,
       multiplexer_6_out, multiplexer_7_out, multiplexer_8_out, multiplexer_9_out, multiplexer_11_out,
       multiplexer_26_out, pull_resistor_2_node;
  wire [1:0] multiplexer_23_out, multiplexer_24_out, multiplexer_25_out;
  wire [3:0] multiplexer_10_out;
  wire [4:0] multiplexer_19_out, multiplexer_20_out;
  wire [31:0] multiplexer_12_out, multiplexer_13_out, multiplexer_14_out, multiplexer_15_out,
       multiplexer_16_out, multiplexer_17_out, multiplexer_18_out, multiplexer_21_out, multiplexer_22_out,
       multiplexer_27_out;

  Multiplexer #(.select(1), .width(1), .disabled("Z"), .enable("false")) multiplexer_1 (
    .in0(J), .in1(1'b0), .out(multiplexer_1_out), .sel(\同步清零_高电平有效 ));
  Multiplexer #(.select(1), .width(1), .disabled("Z"), .enable("false")) multiplexer_2 (
    .in0(JR), .in1(1'b0), .out(multiplexer_2_out), .sel(\同步清零_高电平有效 ));
  Multiplexer #(.select(1), .width(1), .disabled("Z"), .enable("false")) multiplexer_3 (
    .in0(JAL), .in1(1'b0), .out(multiplexer_3_out), .sel(\同步清零_高电平有效 ));
  Multiplexer #(.select(1), .width(1), .disabled("Z"), .enable("false")) multiplexer_4 (
    .in0(BEQ), .in1(1'b0), .out(multiplexer_4_out), .sel(\同步清零_高电平有效 ));
  Multiplexer #(.select(1), .width(1), .disabled("Z"), .enable("false")) multiplexer_5 (
    .in0(BNE), .in1(1'b0), .out(multiplexer_5_out), .sel(\同步清零_高电平有效 ));
  Multiplexer #(.select(1), .width(1), .disabled("Z"), .enable("false")) multiplexer_6 (
    .in0(regdst), .in1(1'b0), .out(multiplexer_6_out), .sel(\同步清零_高电平有效 ));
  Multiplexer #(.select(1), .width(1), .disabled("Z"), .enable("false")) multiplexer_7 (
    .in0(regwrite), .in1(1'b0), .out(multiplexer_7_out), .sel(\同步清零_高电平有效 ));
  Multiplexer #(.select(1), .width(1), .disabled("Z"), .enable("false")) multiplexer_8 (
    .in0(memchoose), .in1(1'b0), .out(multiplexer_8_out), .sel(\同步清零_高电平有效 ));
  Multiplexer #(.select(1), .width(1), .disabled("Z"), .enable("false")) multiplexer_9 (
    .in0(memwrite), .in1(1'b0), .out(multiplexer_9_out), .sel(\同步清零_高电平有效 ));
  Multiplexer #(.select(1), .width(4), .disabled("Z"), .enable("false")) multiplexer_10 (
    .in0(aluop), .in1(4'b0000), .out(multiplexer_10_out), .sel(\同步清零_高电平有效 ));
  Multiplexer #(.select(1), .width(1), .disabled("Z"), .enable("false")) multiplexer_11 (
    .in0(alusrcb), .in1(1'b0), .out(multiplexer_11_out), .sel(\同步清零_高电平有效 ));
  Multiplexer #(.select(1), .width(32), .disabled("Z"), .enable("false")) multiplexer_12 (
    .in0(A), .in1({32{1'b0}}), .out(multiplexer_12_out), .sel(\同步清零_高电平有效 ));
  Multiplexer #(.select(1), .width(32), .disabled("Z"), .enable("false")) multiplexer_13 (
    .in0(B), .in1({32{1'b0}}), .out(multiplexer_13_out), .sel(\同步清零_高电平有效 ));
  Multiplexer #(.select(1), .width(32), .disabled("Z"), .enable("false")) multiplexer_14 (
    .in0(A_prime), .in1({32{1'b0}}), .out(multiplexer_14_out), .sel(\同步清零_高电平有效 ));
  Multiplexer #(.select(1), .width(32), .disabled("Z"), .enable("false")) multiplexer_15 (
    .in0(B_prime), .in1({32{1'b0}}), .out(multiplexer_15_out), .sel(\同步清零_高电平有效 ));
  Multiplexer #(.select(1), .width(32), .disabled("Z"), .enable("false")) multiplexer_16 (
    .in0(IR), .in1({32{1'b0}}), .out(multiplexer_16_out), .sel(\同步清零_高电平有效 ));
  Multiplexer #(.select(1), .width(32), .disabled("Z"), .enable("false")) multiplexer_17 (
    .in0(PCtest), .in1({32{1'b0}}), .out(multiplexer_17_out), .sel(\同步清零_高电平有效 ));
  Multiplexer #(.select(1), .width(32), .disabled("Z"), .enable("false")) multiplexer_18 (
    .in0(IMM), .in1({32{1'b0}}), .out(multiplexer_18_out), .sel(\同步清零_高电平有效 ));
  Multiplexer #(.select(1), .width(5), .disabled("Z"), .enable("false")) multiplexer_19 (
    .in0(writereg), .in1({5{1'b0}}), .out(multiplexer_19_out), .sel(\同步清零_高电平有效 ));
  Multiplexer #(.select(1), .width(5), .disabled("Z"), .enable("false")) multiplexer_20 (
    .in0(shamt), .in1({5{1'b0}}), .out(multiplexer_20_out), .sel(\同步清零_高电平有效 ));
  Multiplexer #(.select(1), .width(32), .disabled("Z"), .enable("false")) multiplexer_21 (
    .in0(IMM2), .in1({32{1'b0}}), .out(multiplexer_21_out), .sel(\同步清零_高电平有效 ));
  Multiplexer #(.select(1), .width(32), .disabled("Z"), .enable("false")) multiplexer_22 (
    .in0(PC), .in1({32{1'b0}}), .out(multiplexer_22_out), .sel(\同步清零_高电平有效 ));
  Multiplexer #(.select(1), .width(2), .disabled("Z"), .enable("false")) multiplexer_23 (
    .in0(cR1), .in1(2'b00), .out(multiplexer_23_out), .sel(\同步清零_高电平有效 ));
  Multiplexer #(.select(1), .width(2), .disabled("Z"), .enable("false")) multiplexer_24 (
    .in0(cR2), .in1(2'b00), .out(multiplexer_24_out), .sel(\同步清零_高电平有效 ));
  Multiplexer #(.select(1), .width(2), .disabled("Z"), .enable("false")) multiplexer_25 (
    .in0(status), .in1(2'b00), .out(multiplexer_25_out), .sel(\同步清零_高电平有效 ));
  Multiplexer #(.select(1), .width(1), .disabled("Z"), .enable("false")) multiplexer_26 (
    .in0(hit), .in1(1'b0), .out(multiplexer_26_out), .sel(\同步清零_高电平有效 ));
  Multiplexer #(.select(1), .width(32), .disabled("Z"), .enable("false")) multiplexer_27 (
    .in0(\原来的PC ), .in1({32{1'b0}}), .out(multiplexer_27_out), .sel(\同步清零_高电平有效 ));
  Pull_Resistor #(.pull(0)) pull_resistor_1 (.node(\同步清零_高电平有效 ));
  Register #(.width(1), .trigger("rising"), .Select("low")) register_1 (
    .D(multiplexer_1_out), .en(pull_resistor_2_node), .Q(J_2), .clk(CLK));  // open: clr
  Register #(.width(1), .trigger("rising"), .Select("low")) register_2 (
    .D(multiplexer_2_out), .en(pull_resistor_2_node), .Q(JR_2), .clk(CLK));  // open: clr
  Register #(.width(1), .trigger("rising"), .Select("low")) register_3 (
    .D(multiplexer_3_out), .en(pull_resistor_2_node), .Q(JAL_2), .clk(CLK));  // open: clr
  Register #(.width(1), .trigger("rising"), .Select("low")) register_4 (
    .D(multiplexer_4_out), .en(pull_resistor_2_node), .Q(BEQ_2), .clk(CLK));  // open: clr
  Register #(.width(1), .trigger("rising"), .Select("low")) register_5 (
    .D(multiplexer_5_out), .en(pull_resistor_2_node), .Q(BNE_2), .clk(CLK));  // open: clr
  Register #(.width(1), .trigger("rising"), .Select("low")) register_6 (
    .D(multiplexer_6_out), .en(pull_resistor_2_node), .Q(regdst_2), .clk(CLK));  // open: clr
  Register #(.width(1), .trigger("rising"), .Select("low")) register_7 (
    .D(multiplexer_7_out), .en(pull_resistor_2_node), .Q(regwrite_2), .clk(CLK));  // open: clr
  Register #(.width(1), .trigger("rising"), .Select("low")) register_8 (
    .D(multiplexer_8_out), .en(pull_resistor_2_node), .Q(memchoose_2), .clk(CLK));  // open: clr
  Register #(.width(1), .trigger("rising"), .Select("low")) register_9 (
    .D(multiplexer_9_out), .en(pull_resistor_2_node), .Q(memwrite_2), .clk(CLK));  // open: clr
  Register #(.width(4), .trigger("rising"), .Select("low")) register_10 (
    .D(multiplexer_10_out), .en(pull_resistor_2_node), .Q(aluop_2), .clk(CLK));  // open: clr
  Register #(.width(1), .trigger("rising"), .Select("low")) register_11 (
    .D(multiplexer_11_out), .en(pull_resistor_2_node), .Q(alusrcb_2), .clk(CLK));  // open: clr
  Register #(.width(32), .trigger("rising"), .Select("low")) register_12 (
    .D(multiplexer_12_out), .en(pull_resistor_2_node), .Q(A_2), .clk(CLK));  // open: clr
  Register #(.width(32), .trigger("rising"), .Select("low")) register_13 (
    .D(multiplexer_13_out), .en(pull_resistor_2_node), .Q(B_2), .clk(CLK));  // open: clr
  Register #(.width(32), .trigger("rising"), .Select("low")) register_14 (
    .D(multiplexer_14_out), .en(pull_resistor_2_node), .Q(A_prime_2), .clk(CLK));  // open: clr
  Register #(.width(32), .trigger("rising"), .Select("low")) register_15 (
    .D(multiplexer_15_out), .en(pull_resistor_2_node), .Q(B_prime_2), .clk(CLK));  // open: clr
  Register #(.width(32), .trigger("rising"), .Select("low")) register_16 (
    .D(multiplexer_16_out), .en(pull_resistor_2_node), .Q(IR_2), .clk(CLK));  // open: clr
  Register #(.width(32), .trigger("rising"), .Select("low")) register_17 (
    .D(multiplexer_17_out), .en(pull_resistor_2_node), .Q(PCtest_2), .clk(CLK));  // open: clr
  Register #(.width(32), .trigger("rising"), .Select("low")) register_18 (
    .D(multiplexer_18_out), .en(pull_resistor_2_node), .Q(IMM_2), .clk(CLK));  // open: clr
  Register #(.width(5), .trigger("rising"), .Select("low")) register_19 (
    .D(multiplexer_19_out), .en(pull_resistor_2_node), .Q(writereg_2), .clk(CLK));  // open: clr
  Register #(.width(5), .trigger("rising"), .Select("low")) register_20 (
    .D(multiplexer_20_out), .en(pull_resistor_2_node), .Q(shamt_2), .clk(CLK));  // open: clr
  Register #(.width(32), .trigger("rising"), .Select("low")) register_21 (
    .D(multiplexer_21_out), .en(pull_resistor_2_node), .Q(IMM2_2), .clk(CLK));  // open: clr
  Register #(.width(32), .trigger("rising"), .Select("low")) register_22 (
    .D(multiplexer_22_out), .en(pull_resistor_2_node), .Q(PC_2), .clk(CLK));  // open: clr
  Register #(.width(2), .trigger("rising"), .Select("low")) register_23 (
    .D(multiplexer_23_out), .en(pull_resistor_2_node), .Q(cR1_2), .clk(CLK));  // open: clr
  Register #(.width(2), .trigger("rising"), .Select("low")) register_24 (
    .D(multiplexer_24_out), .en(pull_resistor_2_node), .Q(cR2_2), .clk(CLK));  // open: clr
  Register #(.width(2), .trigger("rising"), .Select("low")) register_25 (
    .D(multiplexer_25_out), .en(pull_resistor_2_node), .Q(status_2), .clk(CLK));  // open: clr
  Register #(.width(1), .trigger("rising"), .Select("low")) register_26 (
    .D(multiplexer_26_out), .en(pull_resistor_2_node), .Q(hit_2), .clk(CLK));  // open: clr
  Register #(.width(32), .trigger("rising"), .Select("low")) register_27 (
    .D(multiplexer_27_out), .en(pull_resistor_2_node), .Q(\原来的_PC ), .clk(CLK));  // open: clr
  Pull_Resistor #(.pull(0)) pull_resistor_2 (.node(pull_resistor_2_node));
  not not_1 (pull_resistor_2_node, \使能端_低电平有效 );

  // Notes on the sheet:
  //   使能端_低电平有效: pull=down
  //   同步清零_高电平有效: pull=down
  //   下拉电阻使得引脚可以悬空
endmodule

module \源寄存器使用情况  (
  input  OP0,
  input  OP1,
  input  OP2,
  input  OP3,
  input  OP4,
  input  OP5,
  input  F0,
  input  F1,
  input  F2,
  input  F3,
  input  F4,
  input  F5,
  output R1used,
  output R2used
);

  wire and_1_out, and_2_out, and_3_out, and_4_out, and_5_out, and_6_out, and_7_out, and_8_out, and_9_out,
       and_10_out, and_11_out, and_12_out, and_13_out, and_14_out, and_15_out, and_16_out, and_17_out,
       and_18_out, and_19_out, and_20_out, and_21_out, and_22_out, and_23_out, and_24_out, and_25_out,
       and_26_out, and_27_out, and_28_out, and_29_out, and_30_out, and_31_out, and_32_out, and_33_out,
       and_34_out, and_35_out, and_36_out, and_37_out, not_1_out, not_2_out, not_3_out, not_4_out, not_5_out,
       not_6_out, not_7_out, not_8_out, not_9_out, not_10_out, not_11_out, not_12_out, not_13_out,
       not_14_out, not_15_out, not_16_out, not_17_out, not_18_out, not_19_out, not_20_out, not_21_out,
       not_22_out, not_23_out, not_24_out, not_25_out, not_26_out, not_27_out, not_28_out, not_29_out,
       not_30_out, not_31_out, not_32_out, not_33_out, not_34_out, not_35_out, not_36_out, not_37_out,
       not_38_out, not_39_out, not_40_out, not_41_out, not_42_out, not_43_out, not_44_out, not_45_out,
       not_46_out, not_47_out, not_48_out, not_49_out, not_50_out, not_51_out, not_52_out, not_53_out,
       not_54_out, not_55_out, not_56_out, not_57_out, not_58_out, not_59_out, not_60_out, not_61_out,
       not_62_out, not_63_out, not_64_out, not_65_out, not_66_out, not_67_out, not_68_out, not_69_out,
       not_70_out, not_71_out, not_72_out, not_73_out, not_74_out, not_75_out, not_76_out, not_77_out,
       not_78_out, not_79_out, not_80_out, not_81_out, not_82_out, not_83_out, not_84_out, not_85_out,
       not_86_out, not_87_out, not_88_out, not_89_out, not_90_out, not_91_out, not_92_out, not_93_out,
       not_94_out, not_95_out, not_96_out, not_97_out, not_98_out, not_99_out, not_100_out, not_101_out,
       not_102_out, not_103_out, not_104_out, not_105_out, not_106_out, not_107_out, not_108_out,
       not_109_out, not_110_out, not_111_out, not_112_out, not_113_out, not_114_out, not_115_out,
       not_116_out, not_117_out, not_118_out, not_119_out, not_120_out, not_121_out, not_122_out,
       not_123_out, not_124_out, not_125_out, not_126_out, not_127_out, not_128_out, not_129_out,
       not_130_out, not_131_out, not_132_out, not_133_out, not_134_out, not_135_out, not_136_out,
       not_137_out, not_138_out, not_139_out, not_140_out, not_141_out, not_142_out, not_143_out,
       not_144_out, not_145_out, not_146_out, not_147_out, not_148_out, not_149_out, not_150_out,
       not_151_out, not_152_out, not_153_out, not_154_out, not_155_out, not_156_out, not_157_out,
       not_158_out, not_159_out, not_160_out, not_161_out, not_162_out, not_163_out, not_164_out,
       not_165_out, not_166_out, not_167_out, not_168_out, not_169_out, not_170_out, not_171_out,
       not_172_out, not_173_out, not_174_out, not_175_out, not_176_out, not_177_out, not_178_out,
       not_179_out, not_180_out, not_181_out, not_182_out, not_183_out, not_184_out, not_185_out,
       not_186_out, not_187_out, not_188_out, not_189_out, not_190_out, not_191_out, not_192_out,
       not_193_out, not_194_out, not_195_out, not_196_out, not_197_out, not_198_out, not_199_out,
       not_200_out, not_201_out, not_202_out, not_203_out, not_204_out, not_205_out, not_206_out,
       not_207_out, not_208_out, not_209_out, not_210_out, not_211_out, not_212_out, not_213_out,
       not_214_out, not_215_out, not_216_out, not_217_out, not_218_out, not_219_out, not_220_out,
       not_221_out, not_222_out, not_223_out, not_224_out, not_225_out, not_226_out, not_227_out,
       not_228_out, not_229_out, not_230_out, not_231_out, not_232_out, not_233_out, not_234_out,
       not_235_out, not_236_out, not_237_out, not_238_out, not_239_out, not_240_out, not_241_out,
       not_242_out, not_243_out, not_244_out, not_245_out, not_246_out, not_247_out, not_248_out,
       not_249_out, not_250_out, not_251_out, not_252_out, not_253_out, not_254_out, not_255_out,
       not_256_out, not_257_out, not_258_out, not_259_out, not_260_out, not_261_out, not_262_out,
       not_263_out, not_264_out, not_265_out, not_266_out, not_267_out, not_268_out, not_269_out,
       not_270_out, not_271_out, not_272_out, not_273_out, not_274_out, not_275_out, not_276_out,
       not_277_out, not_278_out, not_279_out, not_280_out, not_281_out, not_282_out, not_283_out,
       not_284_out, not_285_out, not_286_out, not_287_out, not_288_out, not_289_out, not_290_out,
       not_291_out, not_292_out;

  not not_1 (not_1_out, OP5);
  not not_2 (not_2_out, OP4);
  not not_3 (not_3_out, OP3);
  not not_4 (not_4_out, OP2);
  not not_5 (not_5_out, OP1);
  not not_6 (not_6_out, OP0);
  not not_7 (not_7_out, F5);
  not not_8 (not_8_out, F4);
  not not_9 (not_9_out, F3);
  not not_10 (not_10_out, F2);
  not not_11 (not_11_out, F1);
  not not_12 (not_12_out, F0);
  not not_13 (not_13_out, OP5);
  not not_14 (not_14_out, OP4);
  not not_15 (not_15_out, OP3);
  not not_16 (not_16_out, OP2);
  not not_17 (not_17_out, OP1);
  not not_18 (not_18_out, OP0);
  not not_19 (not_19_out, F5);
  not not_20 (not_20_out, F4);
  not not_21 (not_21_out, F3);
  not not_22 (not_22_out, F2);
  not not_23 (not_23_out, OP5);
  not not_24 (not_24_out, OP4);
  not not_25 (not_25_out, OP3);
  not not_26 (not_26_out, OP2);
  not not_27 (not_27_out, OP1);
  not not_28 (not_28_out, OP0);
  not not_29 (not_29_out, F5);
  not not_30 (not_30_out, F4);
  not not_31 (not_31_out, F3);
  not not_32 (not_32_out, F2);
  not not_33 (not_33_out, F0);
  not not_34 (not_34_out, OP5);
  not not_35 (not_35_out, OP4);
  not not_36 (not_36_out, OP3);
  not not_37 (not_37_out, OP2);
  not not_38 (not_38_out, OP1);
  not not_39 (not_39_out, OP0);
  not not_40 (not_40_out, F4);
  not not_41 (not_41_out, F3);
  not not_42 (not_42_out, F2);
  not not_43 (not_43_out, F1);
  not not_44 (not_44_out, F0);
  not not_45 (not_45_out, OP5);
  not not_46 (not_46_out, OP4);
  not not_47 (not_47_out, OP3);
  not not_48 (not_48_out, OP2);
  not not_49 (not_49_out, OP1);
  not not_50 (not_50_out, OP0);
  not not_51 (not_51_out, F4);
  not not_52 (not_52_out, F3);
  not not_53 (not_53_out, F2);
  not not_54 (not_54_out, F1);
  not not_55 (not_55_out, OP5);
  not not_56 (not_56_out, OP4);
  not not_57 (not_57_out, OP3);
  not not_58 (not_58_out, OP2);
  not not_59 (not_59_out, OP1);
  not not_60 (not_60_out, OP0);
  not not_61 (not_61_out, F4);
  not not_62 (not_62_out, F3);
  not not_63 (not_63_out, F2);
  not not_64 (not_64_out, F0);
  not not_65 (not_65_out, OP5);
  not not_66 (not_66_out, OP4);
  not not_67 (not_67_out, OP3);
  not not_68 (not_68_out, OP2);
  not not_69 (not_69_out, OP1);
  not not_70 (not_70_out, OP0);
  not not_71 (not_71_out, F4);
  not not_72 (not_72_out, F3);
  not not_73 (not_73_out, F1);
  not not_74 (not_74_out, F0);
  not not_75 (not_75_out, OP5);
  not not_76 (not_76_out, OP4);
  not not_77 (not_77_out, OP3);
  not not_78 (not_78_out, OP2);
  not not_79 (not_79_out, OP1);
  not not_80 (not_80_out, OP0);
  not not_81 (not_81_out, F4);
  not not_82 (not_82_out, F3);
  not not_83 (not_83_out, F1);
  not not_84 (not_84_out, OP5);
  not not_85 (not_85_out, OP4);
  not not_86 (not_86_out, OP3);
  not not_87 (not_87_out, OP2);
  not not_88 (not_88_out, OP1);
  not not_89 (not_89_out, OP0);
  not not_90 (not_90_out, F4);
  not not_91 (not_91_out, F3);
  not not_92 (not_92_out, OP5);
  not not_93 (not_93_out, OP4);
  not not_94 (not_94_out, OP3);
  not not_95 (not_95_out, OP2);
  not not_96 (not_96_out, OP1);
  not not_97 (not_97_out, OP0);
  not not_98 (not_98_out, F4);
  not not_99 (not_99_out, F2);
  not not_100 (not_100_out, F0);
  not not_101 (not_101_out, OP5);
  not not_102 (not_102_out, OP4);
  not not_103 (not_103_out, OP3);
  not not_104 (not_104_out, OP2);
  not not_105 (not_105_out, OP1);
  not not_106 (not_106_out, OP0);
  not not_107 (not_107_out, F4);
  not not_108 (not_108_out, F2);
  not not_109 (not_109_out, OP5);
  not not_110 (not_110_out, OP4);
  not not_111 (not_111_out, OP3);
  not not_112 (not_112_out, OP2);
  not not_113 (not_113_out, OP1);
  not not_114 (not_114_out, OP0);
  not not_115 (not_115_out, F5);
  not not_116 (not_116_out, F4);
  not not_117 (not_117_out, F2);
  not not_118 (not_118_out, F1);
  not not_119 (not_119_out, F0);
  not not_120 (not_120_out, OP5);
  not not_121 (not_121_out, OP4);
  not not_122 (not_122_out, OP3);
  not not_123 (not_123_out, OP2);
  not not_124 (not_124_out, OP1);
  not not_125 (not_125_out, OP0);
  not not_126 (not_126_out, F5);
  not not_127 (not_127_out, F4);
  not not_128 (not_128_out, F1);
  not not_129 (not_129_out, F0);
  not not_130 (not_130_out, OP5);
  not not_131 (not_131_out, OP4);
  not not_132 (not_132_out, OP3);
  not not_133 (not_133_out, OP1);
  not not_134 (not_134_out, OP0);
  not not_135 (not_135_out, OP5);
  not not_136 (not_136_out, OP4);
  not not_137 (not_137_out, OP3);
  not not_138 (not_138_out, OP1);
  not not_139 (not_139_out, OP5);
  not not_140 (not_140_out, OP4);
  not not_141 (not_141_out, OP2);
  not not_142 (not_142_out, OP1);
  not not_143 (not_143_out, OP0);
  not not_144 (not_144_out, OP5);
  not not_145 (not_145_out, OP4);
  not not_146 (not_146_out, OP1);
  not not_147 (not_147_out, OP0);
  not not_148 (not_148_out, OP5);
  not not_149 (not_149_out, OP4);
  not not_150 (not_150_out, OP2);
  not not_151 (not_151_out, OP1);
  not not_152 (not_152_out, OP5);
  not not_153 (not_153_out, OP4);
  not not_154 (not_154_out, OP2);
  not not_155 (not_155_out, OP0);
  not not_156 (not_156_out, OP5);
  not not_157 (not_157_out, OP4);
  not not_158 (not_158_out, OP1);
  not not_159 (not_159_out, OP4);
  not not_160 (not_160_out, OP3);
  not not_161 (not_161_out, OP2);
  not not_162 (not_162_out, OP4);
  not not_163 (not_163_out, OP2);
  not not_164 (not_164_out, OP5);
  not not_165 (not_165_out, OP4);
  not not_166 (not_166_out, OP3);
  not not_167 (not_167_out, OP2);
  not not_168 (not_168_out, OP1);
  not not_169 (not_169_out, OP0);
  not not_170 (not_170_out, F5);
  not not_171 (not_171_out, F4);
  not not_172 (not_172_out, F3);
  not not_173 (not_173_out, F2);
  not not_174 (not_174_out, F1);
  not not_175 (not_175_out, F0);
  not not_176 (not_176_out, OP5);
  not not_177 (not_177_out, OP4);
  not not_178 (not_178_out, OP3);
  not not_179 (not_179_out, OP2);
  not not_180 (not_180_out, OP1);
  not not_181 (not_181_out, OP0);
  not not_182 (not_182_out, F5);
  not not_183 (not_183_out, F4);
  not not_184 (not_184_out, F3);
  not not_185 (not_185_out, F2);
  not not_186 (not_186_out, OP5);
  not not_187 (not_187_out, OP4);
  not not_188 (not_188_out, OP3);
  not not_189 (not_189_out, OP2);
  not not_190 (not_190_out, OP1);
  not not_191 (not_191_out, OP0);
  not not_192 (not_192_out, F5);
  not not_193 (not_193_out, F4);
  not not_194 (not_194_out, F3);
  not not_195 (not_195_out, F2);
  not not_196 (not_196_out, F0);
  not not_197 (not_197_out, OP5);
  not not_198 (not_198_out, OP4);
  not not_199 (not_199_out, OP3);
  not not_200 (not_200_out, OP2);
  not not_201 (not_201_out, OP1);
  not not_202 (not_202_out, OP0);
  not not_203 (not_203_out, F4);
  not not_204 (not_204_out, F3);
  not not_205 (not_205_out, F2);
  not not_206 (not_206_out, F1);
  not not_207 (not_207_out, F0);
  not not_208 (not_208_out, OP5);
  not not_209 (not_209_out, OP4);
  not not_210 (not_210_out, OP3);
  not not_211 (not_211_out, OP2);
  not not_212 (not_212_out, OP1);
  not not_213 (not_213_out, OP0);
  not not_214 (not_214_out, F4);
  not not_215 (not_215_out, F3);
  not not_216 (not_216_out, F2);
  not not_217 (not_217_out, F1);
  not not_218 (not_218_out, OP5);
  not not_219 (not_219_out, OP4);
  not not_220 (not_220_out, OP3);
  not not_221 (not_221_out, OP2);
  not not_222 (not_222_out, OP1);
  not not_223 (not_223_out, OP0);
  not not_224 (not_224_out, F4);
  not not_225 (not_225_out, F3);
  not not_226 (not_226_out, F2);
  not not_227 (not_227_out, F0);
  not not_228 (not_228_out, OP5);
  not not_229 (not_229_out, OP4);
  not not_230 (not_230_out, OP3);
  not not_231 (not_231_out, OP2);
  not not_232 (not_232_out, OP1);
  not not_233 (not_233_out, OP0);
  not not_234 (not_234_out, F4);
  not not_235 (not_235_out, F3);
  not not_236 (not_236_out, F1);
  not not_237 (not_237_out, F0);
  not not_238 (not_238_out, OP5);
  not not_239 (not_239_out, OP4);
  not not_240 (not_240_out, OP3);
  not not_241 (not_241_out, OP2);
  not not_242 (not_242_out, OP1);
  not not_243 (not_243_out, OP0);
  not not_244 (not_244_out, F4);
  not not_245 (not_245_out, F3);
  not not_246 (not_246_out, F1);
  not not_247 (not_247_out, OP5);
  not not_248 (not_248_out, OP4);
  not not_249 (not_249_out, OP3);
  not not_250 (not_250_out, OP2);
  not not_251 (not_251_out, OP1);
  not not_252 (not_252_out, OP0);
  not not_253 (not_253_out, F4);
  not not_254 (not_254_out, F3);
  not not_255 (not_255_out, OP5);
  not not_256 (not_256_out, OP4);
  not not_257 (not_257_out, OP3);
  not not_258 (not_258_out, OP2);
  not not_259 (not_259_out, OP1);
  not not_260 (not_260_out, OP0);
  not not_261 (not_261_out, F4);
  not not_262 (not_262_out, F2);
  not not_263 (not_263_out, F0);
  not not_264 (not_264_out, OP5);
  not not_265 (not_265_out, OP4);
  not not_266 (not_266_out, OP3);
  not not_267 (not_267_out, OP2);
  not not_268 (not_268_out, OP1);
  not not_269 (not_269_out, OP0);
  not not_270 (not_270_out, F4);
  not not_271 (not_271_out, F2);
  not not_272 (not_272_out, OP5);
  not not_273 (not_273_out, OP4);
  not not_274 (not_274_out, OP3);
  not not_275 (not_275_out, OP2);
  not not_276 (not_276_out, OP1);
  not not_277 (not_277_out, OP0);
  not not_278 (not_278_out, F5);
  not not_279 (not_279_out, F4);
  not not_280 (not_280_out, F1);
  not not_281 (not_281_out, F0);
  not not_282 (not_282_out, OP5);
  not not_283 (not_283_out, OP4);
  not not_284 (not_284_out, OP3);
  not not_285 (not_285_out, OP1);
  not not_286 (not_286_out, OP0);
  not not_287 (not_287_out, OP5);
  not not_288 (not_288_out, OP4);
  not not_289 (not_289_out, OP3);
  not not_290 (not_290_out, OP1);
  not not_291 (not_291_out, OP4);
  not not_292 (not_292_out, OP2);
  and and_1 (and_1_out, not_1_out, not_2_out, not_3_out, not_4_out, not_5_out, not_6_out, not_7_out, not_8_out, not_9_out, not_10_out, not_11_out, not_12_out);
  and and_2 (and_2_out, not_13_out, not_14_out, not_15_out, not_16_out, not_17_out, not_18_out, not_19_out, not_20_out, not_21_out, not_22_out, F1, F0);
  and and_3 (and_3_out, not_23_out, not_24_out, not_25_out, not_26_out, not_27_out, not_28_out, not_29_out, not_30_out, not_31_out, not_32_out, F1, not_33_out);
  and and_4 (and_4_out, not_34_out, not_35_out, not_36_out, not_37_out, not_38_out, not_39_out, F5, not_40_out, not_41_out, not_42_out, not_43_out, not_44_out);
  and and_5 (and_5_out, not_45_out, not_46_out, not_47_out, not_48_out, not_49_out, not_50_out, F5, not_51_out, not_52_out, not_53_out, not_54_out, F0);
  and and_6 (and_6_out, not_55_out, not_56_out, not_57_out, not_58_out, not_59_out, not_60_out, F5, not_61_out, not_62_out, not_63_out, F1, not_64_out);
  and and_7 (and_7_out, not_65_out, not_66_out, not_67_out, not_68_out, not_69_out, not_70_out, F5, not_71_out, not_72_out, F2, not_73_out, not_74_out);
  and and_8 (and_8_out, not_75_out, not_76_out, not_77_out, not_78_out, not_79_out, not_80_out, F5, not_81_out, not_82_out, F2, not_83_out, F0);
  and and_9 (and_9_out, not_84_out, not_85_out, not_86_out, not_87_out, not_88_out, not_89_out, F5, not_90_out, not_91_out, F2, F1, F0);
  and and_10 (and_10_out, not_92_out, not_93_out, not_94_out, not_95_out, not_96_out, not_97_out, F5, not_98_out, F3, not_99_out, F1, not_100_out);
  and and_11 (and_11_out, not_101_out, not_102_out, not_103_out, not_104_out, not_105_out, not_106_out, F5, not_107_out, F3, not_108_out, F1, F0);
  and and_12 (and_12_out, not_109_out, not_110_out, not_111_out, not_112_out, not_113_out, not_114_out, not_115_out, not_116_out, F3, not_117_out, not_118_out, not_119_out);
  and and_13 (and_13_out, not_120_out, not_121_out, not_122_out, not_123_out, not_124_out, not_125_out, not_126_out, not_127_out, F3, F2, not_128_out, not_129_out);
  and and_14 (and_14_out, not_130_out, not_131_out, not_132_out, OP2, not_133_out, not_134_out);
  and and_15 (and_15_out, not_135_out, not_136_out, not_137_out, OP2, not_138_out, OP0);
  and and_16 (and_16_out, not_139_out, not_140_out, OP3, not_141_out, not_142_out, not_143_out);
  and and_17 (and_17_out, not_144_out, not_145_out, OP3, OP2, not_146_out, not_147_out);
  and and_18 (and_18_out, not_148_out, not_149_out, OP3, not_150_out, not_151_out, OP0);
  and and_19 (and_19_out, not_152_out, not_153_out, OP3, not_154_out, OP1, not_155_out);
  and and_20 (and_20_out, not_156_out, not_157_out, OP3, OP2, not_158_out, OP0);
  and and_21 (and_21_out, OP5, not_159_out, not_160_out, not_161_out, OP1, OP0);
  and and_22 (and_22_out, OP5, not_162_out, OP3, not_163_out, OP1, OP0);
  and and_23 (and_23_out, not_164_out, not_165_out, not_166_out, not_167_out, not_168_out, not_169_out, not_170_out, not_171_out, not_172_out, not_173_out, not_174_out, not_175_out);
  and and_24 (and_24_out, not_176_out, not_177_out, not_178_out, not_179_out, not_180_out, not_181_out, not_182_out, not_183_out, not_184_out, not_185_out, F1, F0);
  and and_25 (and_25_out, not_186_out, not_187_out, not_188_out, not_189_out, not_190_out, not_191_out, not_192_out, not_193_out, not_194_out, not_195_out, F1, not_196_out);
  and and_26 (and_26_out, not_197_out, not_198_out, not_199_out, not_200_out, not_201_out, not_202_out, F5, not_203_out, not_204_out, not_205_out, not_206_out, not_207_out);
  and and_27 (and_27_out, not_208_out, not_209_out, not_210_out, not_211_out, not_212_out, not_213_out, F5, not_214_out, not_215_out, not_216_out, not_217_out, F0);
  and and_28 (and_28_out, not_218_out, not_219_out, not_220_out, not_221_out, not_222_out, not_223_out, F5, not_224_out, not_225_out, not_226_out, F1, not_227_out);
  and and_29 (and_29_out, not_228_out, not_229_out, not_230_out, not_231_out, not_232_out, not_233_out, F5, not_234_out, not_235_out, F2, not_236_out, not_237_out);
  and and_30 (and_30_out, not_238_out, not_239_out, not_240_out, not_241_out, not_242_out, not_243_out, F5, not_244_out, not_245_out, F2, not_246_out, F0);
  and and_31 (and_31_out, not_247_out, not_248_out, not_249_out, not_250_out, not_251_out, not_252_out, F5, not_253_out, not_254_out, F2, F1, F0);
  and and_32 (and_32_out, not_255_out, not_256_out, not_257_out, not_258_out, not_259_out, not_260_out, F5, not_261_out, F3, not_262_out, F1, not_263_out);
  and and_33 (and_33_out, not_264_out, not_265_out, not_266_out, not_267_out, not_268_out, not_269_out, F5, not_270_out, F3, not_271_out, F1, F0);
  and and_34 (and_34_out, not_272_out, not_273_out, not_274_out, not_275_out, not_276_out, not_277_out, not_278_out, not_279_out, F3, F2, not_280_out, not_281_out);
  and and_35 (and_35_out, not_282_out, not_283_out, not_284_out, OP2, not_285_out, not_286_out);
  and and_36 (and_36_out, not_287_out, not_288_out, not_289_out, OP2, not_290_out, OP0);
  and and_37 (and_37_out, OP5, not_291_out, OP3, not_292_out, OP1, OP0);
  or or_1 (R1used, and_1_out, and_2_out, and_3_out, and_4_out, and_5_out, and_6_out, and_7_out, and_8_out, and_9_out, and_10_out, and_11_out, and_12_out, and_13_out, and_14_out, and_15_out, and_16_out, and_17_out, and_18_out, and_19_out, and_20_out, and_21_out, and_22_out);
  or or_2 (R2used, and_23_out, and_24_out, and_25_out, and_26_out, and_27_out, and_28_out, and_29_out, and_30_out, and_31_out, and_32_out, and_33_out, and_34_out, and_35_out, and_36_out, and_37_out);
endmodule

module \数据相关检测逻辑  (
  input  R1used,
  input  EX_RegWrite,
  input  [4:0] R1_num,
  input  [4:0] R2_num,
  input  [4:0] EX_WriteReg_num,
  input  [4:0] MEM_WriteReg_num,
  input  R2used,
  input  MEM_RegWrite,
  output relative
);

  wire and_1_out, and_2_out, and_3_out, and_4_out, comparator_1_eq, comparator_2_eq, comparator_3_eq,
       comparator_4_eq, comparator_5_eq, comparator_6_eq, not_1_out, not_2_out;

  Comparator #(.width(5), .mode("twosComplement")) comparator_1 (
    .a({5{1'b0}}), .b(R1_num), .eq(comparator_1_eq));  // open: gt, lt
  Comparator #(.width(5), .mode("twosComplement")) comparator_2 (
    .a(R1_num), .b(EX_WriteReg_num), .eq(comparator_2_eq));  // open: gt, lt
  Comparator #(.width(5), .mode("twosComplement")) comparator_3 (
    .a(R1_num), .b(MEM_WriteReg_num), .eq(comparator_3_eq));  // open: gt, lt
  Comparator #(.width(5), .mode("twosComplement")) comparator_4 (
    .a(R2_num), .b(EX_WriteReg_num), .eq(comparator_4_eq));  // open: gt, lt
  Comparator #(.width(5), .mode("twosComplement")) comparator_5 (
    .a(R2_num), .b(MEM_WriteReg_num), .eq(comparator_5_eq));  // open: gt, lt
  Comparator #(.width(5), .mode("twosComplement")) comparator_6 (
    .a(R2_num), .b({5{1'b0}}), .eq(comparator_6_eq));  // open: gt, lt
  not not_1 (not_1_out, comparator_1_eq);
  not not_2 (not_2_out, comparator_6_eq);
  and and_1 (and_1_out, EX_RegWrite, R1used, not_1_out, comparator_2_eq);
  and and_2 (and_2_out, not_1_out, R1used, comparator_3_eq, MEM_RegWrite);
  and and_3 (and_3_out, EX_RegWrite, comparator_4_eq, not_2_out, R2used);
  and and_4 (and_4_out, comparator_5_eq, not_2_out, R2used, MEM_RegWrite);
  or or_1 (relative, and_1_out, and_2_out, and_3_out, and_4_out);
endmodule

module \LOAD_USE检测  (
  input  R1used,
  input  EX_RegWrite,
  input  [4:0] R1_num,
  input  [4:0] EX_WriteReg_num,
  input  [4:0] R2_num,
  input  R2used,
  input  [5:0] OP,
  output relative
);

  wire and_1_out, and_2_out, comparator_1_eq, comparator_2_eq, comparator_3_eq, comparator_4_eq,
       comparator_5_eq, not_1_out, not_2_out;

  Comparator #(.width(5), .mode("twosComplement")) comparator_1 (
    .a({5{1'b0}}), .b(R1_num), .eq(comparator_1_eq));  // open: gt, lt
  Comparator #(.width(5), .mode("twosComplement")) comparator_2 (
    .a(R1_num), .b(EX_WriteReg_num), .eq(comparator_2_eq));  // open: gt, lt
  Comparator #(.width(5), .mode("twosComplement")) comparator_3 (
    .a(EX_WriteReg_num), .b(R2_num), .eq(comparator_3_eq));  // open: gt, lt
  Comparator #(.width(5), .mode("twosComplement")) comparator_4 (
    .a(R2_num), .b({5{1'b0}}), .eq(comparator_4_eq));  // open: gt, lt
  Comparator #(.width(6), .mode("twosComplement")) comparator_5 (
    .a(OP), .b(6'b100011), .eq(comparator_5_eq));  // open: gt, lt
  not not_1 (not_1_out, comparator_1_eq);
  not not_2 (not_2_out, comparator_4_eq);
  and and_1 (and_1_out, R1used, EX_RegWrite, comparator_5_eq, not_1_out, comparator_2_eq);
  and and_2 (and_2_out, EX_RegWrite, comparator_3_eq, comparator_5_eq, not_2_out, R2used);
  or or_1 (relative, and_1_out, and_2_out);
endmodule

module \重定向逻辑信号  (
  input  R1used,
  input  EX_RegWrite,
  input  [4:0] R1_num,
  input  [4:0] R2_num,
  input  [4:0] EX_WriteReg_num,
  input  [4:0] MEM_WriteReg_num,
  input  R2used,
  input  MEM_RegWrite,
  input  [5:0] OP,
  output [1:0] ChooseR1,
  output [1:0] ChooseR2
);

  wire and_3_out, and_4_out, comparator_1_eq, comparator_2_eq, comparator_3_eq, comparator_4_eq,
       comparator_5_eq, comparator_6_eq, comparator_7_eq, EX_R1, EX_R2, MEM_ALU_R1, MEM_ALU_R2, MEM_WB_R1,
       MEM_WB_R2, not_1_out, not_2_out, not_3_out, not_4_out, not_5_out;

  not not_1 (not_1_out, comparator_1_eq);
  Comparator #(.width(5), .mode("twosComplement")) comparator_1 (
    .a({5{1'b0}}), .b(R1_num), .eq(comparator_1_eq));  // open: gt, lt
  Comparator #(.width(5), .mode("twosComplement")) comparator_2 (
    .a(R1_num), .b(EX_WriteReg_num), .eq(comparator_2_eq));  // open: gt, lt
  not not_2 (not_2_out, comparator_2_eq);
  Comparator #(.width(5), .mode("twosComplement")) comparator_3 (
    .a(R1_num), .b(MEM_WriteReg_num), .eq(comparator_3_eq));  // open: gt, lt
  Comparator #(.width(5), .mode("twosComplement")) comparator_4 (
    .a(R2_num), .b(EX_WriteReg_num), .eq(comparator_4_eq));  // open: gt, lt
  not not_3 (not_3_out, comparator_4_eq);
  Comparator #(.width(5), .mode("twosComplement")) comparator_5 (
    .a(R2_num), .b(MEM_WriteReg_num), .eq(comparator_5_eq));  // open: gt, lt
  Comparator #(.width(5), .mode("twosComplement")) comparator_6 (
    .a(R2_num), .b({5{1'b0}}), .eq(comparator_6_eq));  // open: gt, lt
  not not_4 (not_4_out, comparator_6_eq);
  Comparator #(.width(6), .mode("twosComplement")) comparator_7 (
    .a(OP), .b(6'b100011), .eq(comparator_7_eq));  // open: gt, lt
  Multiplexer #(.select(3), .width(2), .disabled("Z"), .enable("false")) multiplexer_1 (
    .in0(2'b00), .in1(2'b01), .in2(2'b10), .in4(2'b11), .out(ChooseR1), .sel({MEM_WB_R1, MEM_ALU_R1, EX_R1}));  // open: in3, in5, in6, in7
  and and_1 (EX_R1, R1used, EX_RegWrite, not_1_out, comparator_2_eq);
  and and_2 (EX_R2, EX_RegWrite, not_4_out, R2used, comparator_4_eq);
  and and_3 (and_3_out, R1used, not_1_out, not_2_out, comparator_3_eq, MEM_RegWrite);
  and and_4 (and_4_out, not_3_out, comparator_5_eq, R2used, not_4_out, MEM_RegWrite);
  and and_5 (MEM_WB_R1, and_3_out, comparator_7_eq);
  and and_6 (MEM_ALU_R1, and_3_out, not_5_out);
  not not_5 (not_5_out, comparator_7_eq);
  and and_7 (MEM_ALU_R2, not_5_out, and_4_out);
  and and_8 (MEM_WB_R2, comparator_7_eq, and_4_out);
  Multiplexer #(.select(3), .width(2), .disabled("Z"), .enable("false")) multiplexer_2 (
    .in0(2'b00), .in1(2'b01), .in2(2'b10), .in4(2'b11), .out(ChooseR2), .sel({MEM_WB_R2, MEM_ALU_R2, EX_R2}));  // open: in3, in5, in6, in7
endmodule

module \动态分支预测  (
  output RegWrite,
  output MemWrite,
  output [31:0] PC,
  output [31:0] IR,
  output [31:0] RDin,
  output [31:0] MDin
);

  wire and_1_out, and_4_out, and_5_out, and_6_out, and_7_out, and_9_out, CLK, comparator_1_eq, ex_hit,
       EXBranch, Go, hit, IR1, IR2, IR3, jal, JMP, JR, mips_alu_1_equal, not_1_out, not_2_out, not_3_out,
       not_4_out, not_5_out, or_1_out, or_3_out, \output , regdst, relative, SignedExt, stop, Syscall, W1,
       W2, W3, xnor_1_out, \分支跳转成功 , \单周期硬布线控制器_1_alu_src , \单周期硬布线控制器_1_beq , \单周期硬布线控制器_1_bne ,
       \单周期硬布线控制器_1_jmp , \单周期硬布线控制器_1_jr , \单周期硬布线控制器_1_memtoreg , \单周期硬布线控制器_1_memwrite ,
       \单周期硬布线控制器_1_regwrite , \单周期硬布线控制器_1_syscall , \是分支指令 , \流水接口2_1_hit_2 , \流水接口2_2_alusrcb_2 ,
       \流水接口2_2_beq_2 , \流水接口2_2_bne_2 , \流水接口2_2_jal_2 , \流水接口2_2_memchoose_2 , \流水接口2_2_memwrite_2 ,
       \流水接口2_2_regdst_2 , \流水接口2_2_regwrite_2 , \流水接口2_3_jal_2 , \流水接口2_3_memchoose_2 , \流水接口2_3_regdst_2 ,
       \流水接口2_3_regwrite_2 , \流水接口2_4_jal_2 , \流水接口2_4_memchoose_2 , \流水接口2_4_regdst_2 , \源寄存器使用情况_1_r1used ,
       \源寄存器使用情况_1_r2used , \预测失败 , \预测成功 ;
  wire [1:0] CR1, CR2, Status, status_t, \流水接口2_1_status_2 , \流水接口2_2_cr1_2 , \流水接口2_2_cr2_2 ;
  wire [3:0] \单周期硬布线控制器_1_alu_op , \流水接口2_2_aluop_2 ;
  wire [4:0] multiplexer_4_out, multiplexer_5_out, multiplexer_6_out, multiplexer_7_out, multiplexer_8_out,
       multiplexer_9_out, \流水接口2_2_shamt_2 , \流水接口2_2_writereg_2 , \流水接口2_3_writereg_2 ;
  wire [5:0] \流水接口2_2_ir_2_2 ;
  wire [15:0] imm16_t, \失败次数 , \总周期数 , \成功次数 , \插入气泡数 , \无条件跳转 , \有条件跳转 ;
  wire [25:0] \流水接口2_2_ir_2 ;
  wire [27:0] JMP_PC;
  wire [31:0] A, a0, adder_2_out, addr, ALU_1, ALU_2, B, bit_extender_1_out, bit_extender_2_out,
       bit_extender_3_out, controlled_buffer_1_out, destaddr, EX_PC, ex_PC_t, EXR1, EXR2, IMM16, JR_PC,
       LedData, mips_alu_1_result, mips_regifile_1_r1, mips_regifile_1_r2, multiplexer_1_out,
       multiplexer_2_out, multiplexer_3_out, multiplexer_11_out, multiplexer_14_out, PC_q, ram_1_data,
       shifter_2_out, v0, WB, \流水接口2_1_pc_2 , \流水接口2_1_原来的_pc , \流水接口2_2_imm2_2 , \流水接口2_2_imm_2 ,
       \流水接口2_3_a_prime_2 , \流水接口2_3_b_prime_2 , \流水接口2_3_ir_2 , \流水接口2_3_pc_2 , \流水接口2_4_ir_2 ,
       \流水接口2_4_pc_2 ;
  wire [31:16] \流水接口2_1_ir_2 ;
  wire [31:28] shifter_1_out;

  Clock #(.highDuration(1), .lowDuration(1)) clock_1 (.out(CLK));
  Button _1 (.out(IR1));
  Button _2 (.out(IR2));
  Button _3 (.out(IR3));
  Button \u_继续运行  (.out(Go));
  LED #(.active("true")) led_1 (.in(W1));
  LED #(.active("true")) led_2 (.in(W2));
  LED #(.active("true")) led_3 (.in(W3));
  and and_1 (and_1_out, Status[1], hit);
  Multiplexer #(.select(1), .width(32), .disabled("Z"), .enable("false")) multiplexer_1 (
    .in0(PC), .in1(destaddr), .out(multiplexer_1_out), .sel(and_1_out));
  Multiplexer #(.select(1), .width(32), .disabled("Z"), .enable("false")) multiplexer_2 (
    .in0(EX_PC), .in1(addr), .out(multiplexer_2_out), .sel(\分支跳转成功 ));
  Counter #(.width(16), .max('hffff), .ongoal("wrap"), .trigger("rising"), .behavior("old")) counter_1 (
    .D({16{1'b0}}), .count(not_1_out), .Q(\总周期数 ), .clk(CLK));  // open: load, carry, clr, preset
  not not_1 (not_1_out, stop);
  Hex_Digit_Display hex_digit_display_1 (.value(LedData[31:28]));  // open: dp
  Multiplexer #(.select(1), .width(32), .disabled("Z"), .enable("false")) multiplexer_3 (
    .in0(multiplexer_1_out), .in1(multiplexer_2_out), .out(multiplexer_3_out), .sel(\预测失败 ));
  not not_2 (not_2_out, or_1_out);
  or or_1 (or_1_out, stop, relative);
  Comparator #(.width(32), .mode("twosComplement")) comparator_1 (
    .a(v0), .b(32'h22), .eq(comparator_1_eq));  // open: gt, lt
  not not_3 (not_3_out, comparator_1_eq);
  Counter #(.width(16), .max('hffff), .ongoal("wrap"), .trigger("rising"), .behavior("old")) counter_2 (
    .D({16{1'b0}}), .count(JMP), .Q(\无条件跳转 ), .clk(CLK));  // open: load, carry, clr, preset
  Counter #(.width(16), .max('hffff), .ongoal("wrap"), .trigger("rising"), .behavior("old")) counter_3 (
    .D({16{1'b0}}), .count(\预测成功 ), .Q(\成功次数 ), .clk(CLK));  // open: load, carry, clr, preset
  Hex_Digit_Display hex_digit_display_2 (.value(LedData[27:24]));  // open: dp
  Hex_Digit_Display hex_digit_display_3 (.value(LedData[23:20]));  // open: dp
  Register #(.width(32), .trigger("rising"), .Select("low")) u_PC (
    .D(multiplexer_3_out), .en(not_2_out), .Q(PC_q), .clk(CLK));  // open: clr
  and and_2 (\output , Syscall, comparator_1_eq);
  and and_3 (stop, not_3_out, Syscall);
  and and_4 (and_4_out, relative, not_4_out);
  not not_4 (not_4_out, stop);
  Hex_Digit_Display hex_digit_display_4 (.value(LedData[15:12]));  // open: dp
  Hex_Digit_Display hex_digit_display_5 (.value(LedData[19:16]));  // open: dp
  \BHT表  \bht表_1  (
    .PC(PC_q), .addr(addr), .\分支跳转成功 (\分支跳转成功 ), .hit(hit), .ex_hit(ex_hit), .Status(Status),
    .\是分支指令 (\是分支指令 ), .ex_PC(ex_PC_t), .destaddr(destaddr), .clk(CLK));
  Counter #(.width(16), .max('hffff), .ongoal("wrap"), .trigger("rising"), .behavior("old")) counter_4 (
    .D({16{1'b0}}), .count(and_4_out), .Q(\插入气泡数 ), .clk(CLK));  // open: load, carry, clr, preset
  Hex_Digit_Display hex_digit_display_6 (.value(LedData[11:8]));  // open: dp
  Hex_Digit_Display hex_digit_display_7 (.value(LedData[7:4]));  // open: dp
  // Probe on \总周期数 
  // Probe on \插入气泡数 
  // Probe on \无条件跳转 
  // Probe on \有条件跳转 
  // Probe on \成功次数 
  // Probe on \失败次数 
  ROM #(.addrWidth(10), .dataWidth(32), .Select("high")) rom_1 (.addr(PC_q[11:2]), .data(IR));
  Adder #(.width(32)) adder_1 (.a(PC_q), .b(32'h4), .out(PC), .cin(1'b0));  // open: cout
  // Probe on destaddr
  or or_2 (\分支跳转成功 , JMP, EXBranch);
  assign controlled_buffer_1_out = \output  ? a0 : 32'bz;  // Controlled_Buffer controlled_buffer_1
  Counter #(.width(16), .max('hffff), .ongoal("wrap"), .trigger("rising"), .behavior("old")) counter_5 (
    .D({16{1'b0}}), .count(EXBranch), .Q(\有条件跳转 ), .clk(CLK));  // open: load, carry, clr, preset
  Hex_Digit_Display hex_digit_display_8 (.value(LedData[3:0]));  // open: dp
  \流水接口2  \u_流水接口2_1  (
    .IR(IR), .PC(PC), .CLK(CLK), .IR_2({\流水接口2_1_ir_2 , imm16_t}), .PC_2(\流水接口2_1_pc_2 ),
    .\同步清零_高电平有效 (\预测失败 ), .\使能端_低电平有效 (or_1_out), .status(Status), .status_2(\流水接口2_1_status_2 ), .hit(hit),
    .hit_2(\流水接口2_1_hit_2 ), .\原来的_PC (\流水接口2_1_原来的_pc ), .\原来的PC (PC_q));  // open: J, JR, JAL, BEQ, BNE, regdst, regwrite, memchoose, memwrite, aluop, alusrcb, A, B, IMM, IMM2, J_2, JR_2, JAL_2, BEQ_2, BNE_2, regdst_2, regwrite_2, memchoose_2, memwrite_2, aluop_2, alusrcb_2, A_2, B_2, IMM_2, IMM2_2, A_prime, A_prime_2, B_prime, B_prime_2, writereg, writereg_2, shamt, shamt_2, cR1, cR1_2, cR2, cR2_2, PCtest_2, PCtest
  Register #(.width(32), .trigger("rising"), .Select("low")) PC_2 (
    .D(controlled_buffer_1_out), .Q(LedData), .clk(CLK));  // open: en, clr
  Counter #(.width(16), .max('hffff), .ongoal("wrap"), .trigger("rising"), .behavior("old")) counter_6 (
    .D({16{1'b0}}), .count(\预测失败 ), .Q(\失败次数 ), .clk(CLK));  // open: load, carry, clr, preset
  \源寄存器使用情况  \u_源寄存器使用情况_1  (
    .OP0(\流水接口2_1_ir_2 [26]), .OP1(\流水接口2_1_ir_2 [27]), .OP2(\流水接口2_1_ir_2 [28]), .OP3(\流水接口2_1_ir_2 [29]),
    .OP4(\流水接口2_1_ir_2 [30]), .OP5(\流水接口2_1_ir_2 [31]), .F0(imm16_t[0]), .F1(imm16_t[1]), .F2(imm16_t[2]),
    .F3(imm16_t[3]), .F4(imm16_t[4]), .F5(imm16_t[5]), .R1used(\源寄存器使用情况_1_r1used ),
    .R2used(\源寄存器使用情况_1_r2used ));
  \单周期硬布线控制器  \u_单周期硬布线控制器_1  (
    .Func(imm16_t[5:0]), .OP(\流水接口2_1_ir_2 [31:26]), .ALU_OP(\单周期硬布线控制器_1_alu_op ),
    .MemToReg(\单周期硬布线控制器_1_memtoreg ), .MemWrite(\单周期硬布线控制器_1_memwrite ), .ALU_SRC(\单周期硬布线控制器_1_alu_src ),
    .RegWrite(\单周期硬布线控制器_1_regwrite ), .SysCALL(\单周期硬布线控制器_1_syscall ), .SignedExt(SignedExt),
    .RegDst(regdst), .JR(\单周期硬布线控制器_1_jr ), .JMP(\单周期硬布线控制器_1_jmp ), .Beq(\单周期硬布线控制器_1_beq ), .JAL(jal),
    .Bne(\单周期硬布线控制器_1_bne ));
  Multiplexer #(.select(1), .width(5), .disabled("Z"), .enable("false")) multiplexer_4 (
    .in0(\流水接口2_1_ir_2 [25:21]), .in1(5'b00010), .out(multiplexer_4_out), .sel(\单周期硬布线控制器_1_syscall ));
  Multiplexer #(.select(1), .width(5), .disabled("Z"), .enable("false")) multiplexer_5 (
    .in0(\流水接口2_1_ir_2 [20:16]), .in1(5'b00100), .out(multiplexer_5_out), .sel(\单周期硬布线控制器_1_syscall ));
  Multiplexer #(.select(1), .width(5), .disabled("Z"), .enable("false")) multiplexer_6 (
    .in0(\流水接口2_4_ir_2 [20:16]), .in1(\流水接口2_4_ir_2 [15:11]), .out(multiplexer_6_out),
    .sel(\流水接口2_4_regdst_2 ));
  Multiplexer #(.select(1), .width(5), .disabled("Z"), .enable("false")) multiplexer_7 (
    .in0(multiplexer_6_out), .in1({5{1'b1}}), .out(multiplexer_7_out), .sel(\流水接口2_4_jal_2 ));
  assign bit_extender_1_out = {{6{\流水接口2_1_ir_2 [25]}}, {\流水接口2_1_ir_2 [25:16], imm16_t}};  // Bit_Extender bit_extender_1
  Multiplexer #(.select(1), .width(5), .disabled("Z"), .enable("false")) multiplexer_8 (
    .in0(\流水接口2_1_ir_2 [20:16]), .in1(imm16_t[15:11]), .out(multiplexer_8_out), .sel(regdst));
  Multiplexer #(.select(1), .width(5), .disabled("Z"), .enable("false")) multiplexer_9 (
    .in0(multiplexer_8_out), .in1({5{1'b1}}), .out(multiplexer_9_out), .sel(jal));
  assign bit_extender_2_out = {{16{1'b0}}, imm16_t};  // Bit_Extender bit_extender_2
  Multiplexer #(.select(1), .width(32), .disabled("Z"), .enable("false")) multiplexer_10 (
    .in0(bit_extender_2_out), .in1(bit_extender_3_out), .out(IMM16), .sel(SignedExt));
  assign bit_extender_3_out = {{16{imm16_t[15]}}, imm16_t};  // Bit_Extender bit_extender_3
  \重定向逻辑信号  \u_重定向逻辑信号_1  (
    .R1used(\源寄存器使用情况_1_r1used ), .EX_RegWrite(\流水接口2_2_regwrite_2 ), .R1_num(multiplexer_4_out),
    .R2_num(multiplexer_5_out), .EX_WriteReg_num(\流水接口2_2_writereg_2 ),
    .MEM_WriteReg_num(\流水接口2_3_writereg_2 ), .R2used(\源寄存器使用情况_1_r2used ),
    .MEM_RegWrite(\流水接口2_3_regwrite_2 ), .OP(\流水接口2_3_ir_2 [31:26]), .ChooseR1(CR1), .ChooseR2(CR2));
  MIPS_Regifile mips_regifile_1 (
    .Din(RDin), .Clk(CLK), .R1(mips_regifile_1_r1), .R2(mips_regifile_1_r2), .WE(RegWrite),
    .W_num(multiplexer_7_out), .R1_num(multiplexer_4_out), .R2_num(multiplexer_5_out));
  xnor xnor_1 (xnor_1_out, status_t[1], \分支跳转成功 );
  \流水接口2  \u_流水接口2_2  (
    .J(\单周期硬布线控制器_1_jmp ), .JR(\单周期硬布线控制器_1_jr ), .JAL(jal), .BEQ(\单周期硬布线控制器_1_beq ),
    .BNE(\单周期硬布线控制器_1_bne ), .regdst(regdst), .regwrite(\单周期硬布线控制器_1_regwrite ),
    .memchoose(\单周期硬布线控制器_1_memtoreg ), .memwrite(\单周期硬布线控制器_1_memwrite ), .aluop(\单周期硬布线控制器_1_alu_op ),
    .alusrcb(\单周期硬布线控制器_1_alu_src ), .A(mips_regifile_1_r1), .B(mips_regifile_1_r2),
    .IR({\流水接口2_1_ir_2 , imm16_t}), .IMM(IMM16), .IMM2(bit_extender_1_out), .PC(\流水接口2_1_pc_2 ), .CLK(CLK),
    .J_2(JMP), .JR_2(JR), .JAL_2(\流水接口2_2_jal_2 ), .BEQ_2(\流水接口2_2_beq_2 ), .BNE_2(\流水接口2_2_bne_2 ),
    .regdst_2(\流水接口2_2_regdst_2 ), .regwrite_2(\流水接口2_2_regwrite_2 ), .memchoose_2(\流水接口2_2_memchoose_2 ),
    .memwrite_2(\流水接口2_2_memwrite_2 ), .aluop_2(\流水接口2_2_aluop_2 ), .alusrcb_2(\流水接口2_2_alusrcb_2 ),
    .A_2(EXR1), .B_2(EXR2), .IR_2({\流水接口2_2_ir_2_2 , \流水接口2_2_ir_2 }), .IMM_2(\流水接口2_2_imm_2 ),
    .IMM2_2(\流水接口2_2_imm2_2 ), .PC_2(EX_PC), .\同步清零_高电平有效 (or_3_out), .\使能端_低电平有效 (stop),
    .A_prime(mips_regifile_1_r1), .A_prime_2(JR_PC), .B_prime(mips_regifile_1_r2),
    .writereg(multiplexer_9_out), .writereg_2(\流水接口2_2_writereg_2 ), .shamt(imm16_t[10:6]),
    .shamt_2(\流水接口2_2_shamt_2 ), .cR1(CR1), .cR1_2(\流水接口2_2_cr1_2 ), .cR2(CR2), .cR2_2(\流水接口2_2_cr2_2 ),
    .status(\流水接口2_1_status_2 ), .status_2(status_t), .hit(\流水接口2_1_hit_2 ), .hit_2(ex_hit),
    .\原来的_PC (ex_PC_t), .\原来的PC (\流水接口2_1_原来的_pc ));  // open: B_prime_2, PCtest_2, PCtest
  or or_3 (or_3_out, \预测失败 , relative);
  or or_4 (EXBranch, and_5_out, and_9_out);
  \LOAD_USE检测  \load_use检测_1  (
    .R1used(\源寄存器使用情况_1_r1used ), .EX_RegWrite(\流水接口2_2_regwrite_2 ), .R1_num(multiplexer_4_out),
    .EX_WriteReg_num(\流水接口2_2_writereg_2 ), .R2_num(multiplexer_5_out), .R2used(\源寄存器使用情况_1_r2used ),
    .OP(\流水接口2_2_ir_2_2 ), .relative(relative));
  and and_5 (and_5_out, \流水接口2_2_bne_2 , not_5_out);
  not not_5 (not_5_out, mips_alu_1_equal);
  Multiplexer #(.select(1), .width(32), .disabled("Z"), .enable("false")) multiplexer_11 (
    .in0(B), .in1(\流水接口2_2_imm_2 ), .out(multiplexer_11_out), .sel(\流水接口2_2_alusrcb_2 ));
  Shifter #(.width(32), .shift("ll")) shifter_1 (
    .in(\流水接口2_2_imm2_2 ), .\dist (5'b00010), .out({shifter_1_out, JMP_PC}));
  Multiplexer #(.select(2), .width(32), .disabled("Z"), .enable("false")) multiplexer_12 (
    .in0(EXR1), .in1(ALU_1), .in2(ALU_2), .in3(WB), .out(A), .sel(\流水接口2_2_cr1_2 ));
  and and_6 (and_6_out, ex_hit, ~xnor_1_out);  // AND_Gate
  or or_5 (\预测失败 , and_6_out, and_7_out);
  and and_7 (and_7_out, ~ex_hit, \分支跳转成功 );  // AND_Gate
  and and_8 (\预测成功 , xnor_1_out, ex_hit);
  or or_6 (\是分支指令 , \流水接口2_2_beq_2 , \流水接口2_2_bne_2 , JMP);
  and and_9 (and_9_out, \流水接口2_2_beq_2 , mips_alu_1_equal);
  MIPS_ALU mips_alu_1 (
    .X(A), .Y(multiplexer_11_out), .AluOP(\流水接口2_2_aluop_2 ), .Equal(mips_alu_1_equal),
    .Result(mips_alu_1_result), .shamt(\流水接口2_2_shamt_2 ));  // open: Result_2
  Multiplexer #(.select(2), .width(32), .disabled("Z"), .enable("false")) multiplexer_13 (
    .in0(EXR2), .in1(ALU_1), .in2(ALU_2), .in3(WB), .out(B), .sel(\流水接口2_2_cr2_2 ));
  \流水接口2  \u_流水接口2_3  (
    .JAL(\流水接口2_2_jal_2 ), .regdst(\流水接口2_2_regdst_2 ), .regwrite(\流水接口2_2_regwrite_2 ),
    .memchoose(\流水接口2_2_memchoose_2 ), .memwrite(\流水接口2_2_memwrite_2 ), .A(mips_alu_1_result), .B(B),
    .IR({\流水接口2_2_ir_2_2 , \流水接口2_2_ir_2 }), .PC(EX_PC), .CLK(CLK), .JAL_2(\流水接口2_3_jal_2 ),
    .regdst_2(\流水接口2_3_regdst_2 ), .regwrite_2(\流水接口2_3_regwrite_2 ), .memchoose_2(\流水接口2_3_memchoose_2 ),
    .memwrite_2(MemWrite), .A_2(ALU_1), .B_2(MDin), .IR_2(\流水接口2_3_ir_2 ), .PC_2(\流水接口2_3_pc_2 ),
    .\使能端_低电平有效 (stop), .A_prime(A), .A_prime_2(\流水接口2_3_a_prime_2 ), .B_prime(B),
    .B_prime_2(\流水接口2_3_b_prime_2 ), .writereg(\流水接口2_2_writereg_2 ), .writereg_2(\流水接口2_3_writereg_2 ));  // open: J, JR, BEQ, BNE, aluop, alusrcb, IMM, IMM2, J_2, JR_2, BEQ_2, BNE_2, aluop_2, alusrcb_2, IMM_2, IMM2_2, 同步清零_高电平有效, shamt, shamt_2, cR1, cR1_2, cR2, cR2_2, status, status_2, hit, hit_2, 原来的_PC, 原来的PC, PCtest_2, PCtest
  \流水接口2  \u_流水接口2_4  (
    .JAL(\流水接口2_3_jal_2 ), .regdst(\流水接口2_3_regdst_2 ), .regwrite(\流水接口2_3_regwrite_2 ),
    .memchoose(\流水接口2_3_memchoose_2 ), .A(ALU_1), .B(ram_1_data), .IR(\流水接口2_3_ir_2 ), .PC(\流水接口2_3_pc_2 ),
    .CLK(CLK), .JAL_2(\流水接口2_4_jal_2 ), .regdst_2(\流水接口2_4_regdst_2 ), .regwrite_2(RegWrite),
    .memchoose_2(\流水接口2_4_memchoose_2 ), .A_2(ALU_2), .B_2(WB), .IR_2(\流水接口2_4_ir_2 ), .PC_2(\流水接口2_4_pc_2 ),
    .\使能端_低电平有效 (stop), .A_prime(\流水接口2_3_a_prime_2 ), .A_prime_2(v0), .B_prime(\流水接口2_3_b_prime_2 ),
    .B_prime_2(a0));  // open: J, JR, BEQ, BNE, memwrite, aluop, alusrcb, IMM, IMM2, J_2, JR_2, BEQ_2, BNE_2, memwrite_2, aluop_2, alusrcb_2, IMM_2, IMM2_2, 同步清零_高电平有效, writereg, writereg_2, shamt, shamt_2, cR1, cR1_2, cR2, cR2_2, status, status_2, hit, hit_2, 原来的_PC, 原来的PC, PCtest_2, PCtest
  RAM #(.addrWidth(10), .dataWidth(32), .bus("separate"), .Select("high")) ram_1 (
    .addr(ALU_1[11:2]), .din(MDin), .data(ram_1_data), .str(MemWrite), .sel(1'b1), .clk(CLK));  // open: ld, clr
  Shifter #(.width(32), .shift("ll")) shifter_2 (.in(\流水接口2_2_imm_2 ), .\dist (5'b00010), .out(shifter_2_out));
  Multiplexer #(.select(1), .width(32), .disabled("Z"), .enable("false")) multiplexer_14 (
    .in0(ALU_2), .in1(WB), .out(multiplexer_14_out), .sel(\流水接口2_4_memchoose_2 ));
  Adder #(.width(32)) adder_2 (.a(EX_PC), .b(shifter_2_out), .out(adder_2_out));  // open: cin, cout
  Multiplexer #(.select(1), .width(32), .disabled("Z"), .enable("false")) multiplexer_15 (
    .in0(multiplexer_14_out), .in1(\流水接口2_4_pc_2 ), .out(RDin), .sel(\流水接口2_4_jal_2 ));
  Multiplexer #(.select(2), .width(32), .disabled("Z"), .enable("false")) multiplexer_16 (
    .in0(adder_2_out), .in1({EX_PC[31:28], JMP_PC}), .in2(JR_PC), .in3(JR_PC), .out(addr), .sel({JR, JMP}));
  Comparator #(.width(32), .mode("twosComplement")) comparator_2 (
    .a(\流水接口2_4_ir_2 ), .b(32'hc), .eq(Syscall));  // open: gt, lt

  // Other names for the same wires on the sheet: JMP_PC[31:28] = EX_PC[31:28]

  // Notes on the sheet:
  //   中断源
  //   中断等待指示
  //   数码管输出
  //   指令存储器
  //   contents of rom_1 (hex, n*v repeats v):
  //   20110001 8000c05 20110001 20120002 20130003 8000c09 20110001 20120002 20130003 8000c0d 20110001
  //   20120002 20130003 8000c11 20110001 20120002 20130003 c000cb8 20100001 20110001 118fc0 112020
  //   20020022 c 118882 12200001 8000c15 112020 20020022 c 20110001 118880 112020 20020022 c 12200001
  //   8000c1f 20110001 118fc0 112020 20020022 c 1188c3 112020 20020022 c 118903 112020 20020022 c 118903
  //   112020 20020022 c 118903 112020 20020022 c 118903 112020 20020022 c 118903 112020 20020022 c 118903
  //   112020 20020022 c 118903 112020 20020022 c 20100001 109fc0 139fc3 8021 2012000c 24160003 26100001
  //   3210000f 20080008 20090001 139900 2709825 132020 20020022 c 1094022 1500fff9 22100001 2018000f
  //   2188024 108700 20080008 20090001 139902 2709825 132021 20020022 c 1094022 1500fff9 108702 2c9b022
  //   12c00001 8000c50 4020 1084027 84400 3508ffff 82021 20020022 c 2010ffff 20110000 ae300000 22100001
  //   22310004 ae300000 22100001 22310004 ae300000 22100001 22310004 ae300000 22100001 22310004 ae300000
  //   22100001 22310004 ae300000 22100001 22310004 ae300000 22100001 22310004 ae300000 22100001 22310004
  //   ae300000 22100001 22310004 ae300000 22100001 22310004 ae300000 22100001 22310004 ae300000 22100001
  //   22310004 ae300000 22100001 22310004 ae300000 22100001 22310004 ae300000 22100001 22310004 ae300000
  //   22100001 22310004 22100001 8020 2011003c 8e130000 8e340000 274402a 11000002 ae330000 ae140000
  //   2231fffc 1611fff8 102020 20020022 c 22100004 2011003c 1611fff2 20020032 c 20100000 22100001 102020
  //   20020022 c 22100002 102020 20020022 c 22100003 102020 20020022 c 22100004 102020 20020022 c 22100005
  //   102020 20020022 c 22100006 102020 20020022 c 22100007 102020 20020022 c 22100008 102020 20020022
  //   20020022 c 3e00008
  //   rs
  //   rt
  //   rt
  //   rd
  //   shamt
  //   rt
  //   rd
  //   JMP
  //   JR
  //   OP
  //   Func
  //   Beq
  //   Bne
  //   MemToReg
  //   MemWrite
  //   AluOP
  //   AluSrcB
  //   RegWrite
  //   JAL
  //   RegDst
  //   为方便自动评测，需要输出PC，IR，寄存器文件写入端口RDin，内存写入端口MDin等信号
  //   总复位信号应将除ROM以外所有存储组件全部清零
  //   数码管输出应该用寄存器锁存，否则显示数据只能一闪而过
endmodule

module \BHT表  (
  input  [31:0] PC,
  input  [31:0] addr,
  input  \分支跳转成功 ,
  input  ex_hit,
  input  \是分支指令 ,
  input  [31:0] ex_PC,
  input  clk,
  output hit,
  output [1:0] Status,
  output [31:0] destaddr
);

  wire and_1_out, and_2_out, and_3_out, and_4_out, and_5_out, and_6_out, and_7_out, and_8_out, and_9_out,
       and_18_out, and_19_out, and_20_out, and_21_out, and_22_out, and_23_out, and_24_out, and_25_out,
       comparator_1_eq, comparator_2_eq, comparator_3_eq, comparator_4_eq, comparator_5_eq, comparator_6_eq,
       comparator_7_eq, comparator_8_eq, comparator_9_eq, comparator_10_eq, comparator_11_eq,
       comparator_12_eq, comparator_13_eq, comparator_14_eq, comparator_15_eq, comparator_16_eq,
       decoder_1_out0, decoder_1_out1, decoder_1_out2, decoder_1_out3, decoder_1_out4, decoder_1_out5,
       decoder_1_out6, decoder_1_out7, en0, en1, en2, en3, en4, en5, en6, en7, h0, h1, h2, h3, h4, h5, h6,
       h7, L0, L1, L2, L3, L4, L5, L6, L7, not_1_out, or_1_out, or_2_out, or_3_out, or_4_out, or_5_out,
       or_6_out, or_7_out, or_8_out, or_9_out, or_10_out, or_11_out, or_12_out, or_13_out, or_14_out,
       or_15_out, or_16_out, V0, V1, V2, V3, V4, V5, V6, V7, WriteL0, WriteL1, WriteL2, WriteL3, WriteL4,
       WriteL5, WriteL6, WriteL7, \优先级封装_1_v0_2 , \优先级封装_1_v1_2 , \优先级封装_1_v2_2 , \优先级封装_1_v3_2 ,
       \优先级封装_1_v4_2 , \优先级封装_1_v5_2 , \优先级封装_1_v6_2 , \优先级封装_1_v7_2 ;
  wire [1:0] \分支预测历史_2_q , \分支预测历史_3_q , \分支预测历史_4_q , \分支预测历史_5_q , \分支预测历史_6_q , \分支预测历史_7_q ,
       \分支预测历史_8_q , \分支预测历史_q , \状态转换_1_newstatus , \状态转换_2_newstatus , \状态转换_3_newstatus ,
       \状态转换_4_newstatus , \状态转换_5_newstatus , \状态转换_6_newstatus , \状态转换_7_newstatus , \状态转换_8_newstatus ;
  wire [2:0] max, \max2归并比较_1_max_num , \max2归并比较_2_max_num , \max2归并比较_3_max_num , \max2归并比较_4_max_num ,
       \max2归并比较_5_max_num , \max2归并比较_6_max_num ;
  wire [15:0] C0, C1, C2, C3, C4, C5, C6, C7, \max2归并比较_1_max , \max2归并比较_2_max , \max2归并比较_3_max ,
       \max2归并比较_4_max , \max2归并比较_5_max , \max2归并比较_6_max ;
  wire [31:0] PC0, PC1, PC2, PC3, PC4, PC5, PC6, PC7, \分支目标地址_2_q , \分支目标地址_3_q , \分支目标地址_4_q , \分支目标地址_5_q ,
       \分支目标地址_6_q , \分支目标地址_7_q , \分支目标地址_8_q , \分支目标地址_q ;

  // Probe on PC
  // Probe on ex_PC
  Register #(.width(1), .trigger("rising"), .Select("low")) valid (.D(1'b1), .en(en1), .Q(V1), .clk(clk));  // open: clr
  Register #(.width(1), .trigger("rising"), .Select("low")) valid_2 (
    .D(1'b1), .en(en2), .Q(V2), .clk(clk));  // open: clr
  Register #(.width(1), .trigger("rising"), .Select("low")) valid_3 (
    .D(1'b1), .en(en3), .Q(V3), .clk(clk));  // open: clr
  Register #(.width(1), .trigger("rising"), .Select("low")) valid_4 (
    .D(1'b1), .en(en4), .Q(V4), .clk(clk));  // open: clr
  Register #(.width(1), .trigger("rising"), .Select("low")) valid_5 (
    .D(1'b1), .en(en5), .Q(V5), .clk(clk));  // open: clr
  Register #(.width(1), .trigger("rising"), .Select("low")) valid_6 (
    .D(1'b1), .en(en6), .Q(V6), .clk(clk));  // open: clr
  Register #(.width(1), .trigger("rising"), .Select("low")) valid_7 (
    .D(1'b1), .en(en7), .Q(V7), .clk(clk));  // open: clr
  Register #(.width(1), .trigger("rising"), .Select("low")) valid_8 (
    .D(1'b1), .en(en0), .Q(V0), .clk(clk));  // open: clr
  // Probe on addr
  Register #(.width(32), .trigger("rising"), .Select("low")) \u_分支指令地址  (
    .D(ex_PC), .en(WriteL0), .Q(PC0), .clk(clk));  // open: clr
  Register #(.width(32), .trigger("rising"), .Select("low")) \u_分支指令地址_2  (
    .D(ex_PC), .en(WriteL1), .Q(PC1), .clk(clk));  // open: clr
  Register #(.width(32), .trigger("rising"), .Select("low")) \u_分支指令地址_3  (
    .D(ex_PC), .en(WriteL2), .Q(PC2), .clk(clk));  // open: clr
  Register #(.width(32), .trigger("rising"), .Select("low")) \u_分支指令地址_4  (
    .D(ex_PC), .en(WriteL3), .Q(PC3), .clk(clk));  // open: clr
  Register #(.width(32), .trigger("rising"), .Select("low")) \u_分支指令地址_5  (
    .D(ex_PC), .en(WriteL4), .Q(PC4), .clk(clk));  // open: clr
  Register #(.width(32), .trigger("rising"), .Select("low")) \u_分支指令地址_6  (
    .D(ex_PC), .en(WriteL5), .Q(PC5), .clk(clk));  // open: clr
  Register #(.width(32), .trigger("rising"), .Select("low")) \u_分支指令地址_7  (
    .D(ex_PC), .en(WriteL6), .Q(PC6), .clk(clk));  // open: clr
  Register #(.width(32), .trigger("rising"), .Select("low")) \u_分支指令地址_8  (
    .D(ex_PC), .en(WriteL7), .Q(PC7), .clk(clk));  // open: clr
  \优先级封装  \u_优先级封装_1  (
    .v0(V0), .v1(V1), .v2(V2), .v3(V3), .v4(V4), .v5(V5), .v6(V6), .v7(V7), .v0_2(\优先级封装_1_v0_2 ),
    .v1_2(\优先级封装_1_v1_2 ), .v2_2(\优先级封装_1_v2_2 ), .v3_2(\优先级封装_1_v3_2 ), .v4_2(\优先级封装_1_v4_2 ),
    .v5_2(\优先级封装_1_v5_2 ), .v6_2(\优先级封装_1_v6_2 ), .v7_2(\优先级封装_1_v7_2 ));
  and and_1 (and_1_out, V0, V1, V2, V3, V4, V5, V6, V7);
  not not_1 (not_1_out, ex_hit);
  and and_2 (and_2_out, not_1_out, \优先级封装_1_v0_2 );
  and and_3 (and_3_out, not_1_out, \优先级封装_1_v1_2 );
  and and_4 (and_4_out, not_1_out, \优先级封装_1_v2_2 );
  and and_5 (and_5_out, not_1_out, \优先级封装_1_v3_2 );
  and and_6 (and_6_out, not_1_out, \优先级封装_1_v4_2 );
  and and_7 (and_7_out, not_1_out, \优先级封装_1_v5_2 );
  and and_8 (and_8_out, not_1_out, \优先级封装_1_v6_2 );
  and and_9 (and_9_out, not_1_out, \优先级封装_1_v7_2 );
  Decoder #(.select(3), .tristate("false"), .disabled(0), .enable("true")) decoder_1 (
    .out0(decoder_1_out0), .out1(decoder_1_out1), .out2(decoder_1_out2), .out3(decoder_1_out3),
    .out4(decoder_1_out4), .out5(decoder_1_out5), .out6(decoder_1_out6), .out7(decoder_1_out7), .sel(max),
    .en(and_1_out));
  \状态转换  \u_状态转换_1  (.oldstatus(Status), .key({ex_hit, \分支跳转成功 }), .newstatus(\状态转换_1_newstatus ));
  \状态转换  \u_状态转换_2  (.oldstatus(Status), .key({ex_hit, \分支跳转成功 }), .newstatus(\状态转换_2_newstatus ));
  \状态转换  \u_状态转换_3  (.oldstatus(Status), .key({ex_hit, \分支跳转成功 }), .newstatus(\状态转换_3_newstatus ));
  \状态转换  \u_状态转换_4  (.oldstatus(Status), .key({ex_hit, \分支跳转成功 }), .newstatus(\状态转换_4_newstatus ));
  \状态转换  \u_状态转换_5  (.oldstatus(Status), .key({ex_hit, \分支跳转成功 }), .newstatus(\状态转换_5_newstatus ));
  \状态转换  \u_状态转换_6  (.oldstatus(Status), .key({ex_hit, \分支跳转成功 }), .newstatus(\状态转换_6_newstatus ));
  \状态转换  \u_状态转换_7  (.oldstatus(Status), .key({ex_hit, \分支跳转成功 }), .newstatus(\状态转换_7_newstatus ));
  \状态转换  \u_状态转换_8  (.oldstatus(Status), .key({ex_hit, \分支跳转成功 }), .newstatus(\状态转换_8_newstatus ));
  assign Status = or_1_out ? \分支预测历史_q  : 2'bz;  // Controlled_Buffer controlled_buffer_1
  Register #(.width(2), .trigger("rising"), .Select("low")) \u_分支预测历史  (
    .D(\状态转换_1_newstatus ), .en(en0), .Q(\分支预测历史_q ), .clk(clk));  // open: clr
  or or_1 (or_1_out, h0, L0);
  assign Status = or_2_out ? \分支预测历史_2_q  : 2'bz;  // Controlled_Buffer controlled_buffer_2
  Register #(.width(2), .trigger("rising"), .Select("low")) \u_分支预测历史_2  (
    .D(\状态转换_2_newstatus ), .en(en1), .Q(\分支预测历史_2_q ), .clk(clk));  // open: clr
  or or_2 (or_2_out, h1, L1);
  assign Status = or_3_out ? \分支预测历史_3_q  : 2'bz;  // Controlled_Buffer controlled_buffer_3
  Register #(.width(2), .trigger("rising"), .Select("low")) \u_分支预测历史_3  (
    .D(\状态转换_3_newstatus ), .en(en2), .Q(\分支预测历史_3_q ), .clk(clk));  // open: clr
  or or_3 (or_3_out, h2, L2);
  assign Status = or_4_out ? \分支预测历史_4_q  : 2'bz;  // Controlled_Buffer controlled_buffer_4
  Register #(.width(2), .trigger("rising"), .Select("low")) \u_分支预测历史_4  (
    .D(\状态转换_4_newstatus ), .en(en3), .Q(\分支预测历史_4_q ), .clk(clk));  // open: clr
  or or_4 (or_4_out, h3, L3);
  Register #(.width(2), .trigger("rising"), .Select("low")) \u_分支预测历史_5  (
    .D(\状态转换_5_newstatus ), .en(en4), .Q(\分支预测历史_5_q ), .clk(clk));  // open: clr
  assign Status = or_5_out ? \分支预测历史_5_q  : 2'bz;  // Controlled_Buffer controlled_buffer_5
  or or_5 (or_5_out, h4, L4);
  Register #(.width(2), .trigger("rising"), .Select("low")) \u_分支预测历史_6  (
    .D(\状态转换_6_newstatus ), .en(en5), .Q(\分支预测历史_6_q ), .clk(clk));  // open: clr
  assign Status = or_6_out ? \分支预测历史_6_q  : 2'bz;  // Controlled_Buffer controlled_buffer_6
  or or_6 (or_6_out, h5, L5);
  assign Status = or_7_out ? \分支预测历史_7_q  : 2'bz;  // Controlled_Buffer controlled_buffer_7
  Register #(.width(2), .trigger("rising"), .Select("low")) \u_分支预测历史_7  (
    .D(\状态转换_7_newstatus ), .en(en6), .Q(\分支预测历史_7_q ), .clk(clk));  // open: clr
  or or_7 (or_7_out, h6, L6);
  assign Status = or_8_out ? \分支预测历史_8_q  : 2'bz;  // Controlled_Buffer controlled_buffer_8
  Register #(.width(2), .trigger("rising"), .Select("low")) \u_分支预测历史_8  (
    .D(\状态转换_8_newstatus ), .en(en7), .Q(\分支预测历史_8_q ), .clk(clk));  // open: clr
  or or_8 (or_8_out, h7, L7);
  or or_9 (or_9_out, and_2_out, decoder_1_out0);
  or or_10 (or_10_out, and_3_out, decoder_1_out1);
  or or_11 (or_11_out, and_4_out, decoder_1_out2);
  or or_12 (or_12_out, and_5_out, decoder_1_out3);
  or or_13 (or_13_out, and_6_out, decoder_1_out4);
  or or_14 (or_14_out, and_7_out, decoder_1_out5);
  or or_15 (or_15_out, and_8_out, decoder_1_out6);
  or or_16 (or_16_out, and_9_out, decoder_1_out7);
  and and_10 (WriteL0, \是分支指令 , not_1_out, or_9_out);
  and and_11 (WriteL1, \是分支指令 , not_1_out, or_10_out);
  and and_12 (WriteL2, \是分支指令 , not_1_out, or_11_out);
  and and_13 (WriteL3, \是分支指令 , not_1_out, or_12_out);
  and and_14 (WriteL4, \是分支指令 , not_1_out, or_13_out);
  and and_15 (WriteL5, \是分支指令 , not_1_out, or_14_out);
  and and_16 (WriteL6, \是分支指令 , not_1_out, or_15_out);
  and and_17 (WriteL7, \是分支指令 , not_1_out, or_16_out);
  Counter #(.width(16), .max('hffff), .ongoal("wrap"), .trigger("rising"), .behavior("old")) \u_淘汰标志位  (
    .load(1'b0), .count(\是分支指令 ), .Q(C0), .clk(clk), .clr(L0));  // open: D, carry, preset
  Counter #(.width(16), .max('hffff), .ongoal("wrap"), .trigger("rising"), .behavior("old")) \u_淘汰标志位_2  (
    .load(1'b0), .count(\是分支指令 ), .Q(C1), .clk(clk), .clr(L1));  // open: D, carry, preset
  Counter #(.width(16), .max('hffff), .ongoal("wrap"), .trigger("rising"), .behavior("old")) \u_淘汰标志位_3  (
    .load(1'b0), .count(\是分支指令 ), .Q(C2), .clk(clk), .clr(L2));  // open: D, carry, preset
  Counter #(.width(16), .max('hffff), .ongoal("wrap"), .trigger("rising"), .behavior("old")) \u_淘汰标志位_4  (
    .load(1'b0), .count(\是分支指令 ), .Q(C3), .clk(clk), .clr(L3));  // open: D, carry, preset
  Counter #(.width(16), .max('hffff), .ongoal("wrap"), .trigger("rising"), .behavior("old")) \u_淘汰标志位_5  (
    .load(1'b0), .count(\是分支指令 ), .Q(C4), .clk(clk), .clr(L4));  // open: D, carry, preset
  Counter #(.width(16), .max('hffff), .ongoal("wrap"), .trigger("rising"), .behavior("old")) \u_淘汰标志位_6  (
    .load(1'b0), .count(\是分支指令 ), .Q(C5), .clk(clk), .clr(L5));  // open: D, carry, preset
  Counter #(.width(16), .max('hffff), .ongoal("wrap"), .trigger("rising"), .behavior("old")) \u_淘汰标志位_7  (
    .load(1'b0), .count(\是分支指令 ), .Q(C6), .clk(clk), .clr(L6));  // open: D, carry, preset
  Counter #(.width(16), .max('hffff), .ongoal("wrap"), .trigger("rising"), .behavior("old")) \u_淘汰标志位_8  (
    .load(1'b0), .count(\是分支指令 ), .Q(C7), .clk(clk), .clr(L7));  // open: D, carry, preset
  Register #(.width(32), .trigger("rising"), .Select("low")) \u_分支目标地址  (
    .D(addr), .en(WriteL0), .Q(\分支目标地址_q ), .clk(clk));  // open: clr
  Register #(.width(32), .trigger("rising"), .Select("low")) \u_分支目标地址_2  (
    .D(addr), .en(WriteL1), .Q(\分支目标地址_2_q ), .clk(clk));  // open: clr
  Register #(.width(32), .trigger("rising"), .Select("low")) \u_分支目标地址_3  (
    .D(addr), .en(WriteL2), .Q(\分支目标地址_3_q ), .clk(clk));  // open: clr
  Register #(.width(32), .trigger("rising"), .Select("low")) \u_分支目标地址_4  (
    .D(addr), .en(WriteL3), .Q(\分支目标地址_4_q ), .clk(clk));  // open: clr
  Register #(.width(32), .trigger("rising"), .Select("low")) \u_分支目标地址_5  (
    .D(addr), .en(WriteL4), .Q(\分支目标地址_5_q ), .clk(clk));  // open: clr
  Register #(.width(32), .trigger("rising"), .Select("low")) \u_分支目标地址_6  (
    .D(addr), .en(WriteL5), .Q(\分支目标地址_6_q ), .clk(clk));  // open: clr
  Register #(.width(32), .trigger("rising"), .Select("low")) \u_分支目标地址_7  (
    .D(addr), .en(WriteL6), .Q(\分支目标地址_7_q ), .clk(clk));  // open: clr
  Register #(.width(32), .trigger("rising"), .Select("low")) \u_分支目标地址_8  (
    .D(addr), .en(WriteL7), .Q(\分支目标地址_8_q ), .clk(clk));  // open: clr
  assign destaddr = h0 ? \分支目标地址_q  : 32'bz;  // Controlled_Buffer controlled_buffer_9
  assign destaddr = h1 ? \分支目标地址_2_q  : 32'bz;  // Controlled_Buffer controlled_buffer_10
  assign destaddr = h2 ? \分支目标地址_3_q  : 32'bz;  // Controlled_Buffer controlled_buffer_11
  assign destaddr = h3 ? \分支目标地址_4_q  : 32'bz;  // Controlled_Buffer controlled_buffer_12
  assign destaddr = h4 ? \分支目标地址_5_q  : 32'bz;  // Controlled_Buffer controlled_buffer_13
  assign destaddr = h5 ? \分支目标地址_6_q  : 32'bz;  // Controlled_Buffer controlled_buffer_14
  assign destaddr = h6 ? \分支目标地址_7_q  : 32'bz;  // Controlled_Buffer controlled_buffer_15
  assign destaddr = h7 ? \分支目标地址_8_q  : 32'bz;  // Controlled_Buffer controlled_buffer_16
  Comparator #(.width(32), .mode("twosComplement")) comparator_1 (
    .a(PC), .b(PC0), .eq(comparator_1_eq));  // open: gt, lt
  Comparator #(.width(32), .mode("twosComplement")) comparator_2 (
    .a(PC), .b(PC1), .eq(comparator_2_eq));  // open: gt, lt
  Comparator #(.width(32), .mode("twosComplement")) comparator_3 (
    .a(PC), .b(PC2), .eq(comparator_3_eq));  // open: gt, lt
  Comparator #(.width(32), .mode("twosComplement")) comparator_4 (
    .a(PC), .b(PC3), .eq(comparator_4_eq));  // open: gt, lt
  Comparator #(.width(32), .mode("twosComplement")) comparator_5 (
    .a(PC), .b(PC4), .eq(comparator_5_eq));  // open: gt, lt
  Comparator #(.width(32), .mode("twosComplement")) comparator_6 (
    .a(PC), .b(PC5), .eq(comparator_6_eq));  // open: gt, lt
  Comparator #(.width(32), .mode("twosComplement")) comparator_7 (
    .a(PC), .b(PC6), .eq(comparator_7_eq));  // open: gt, lt
  Comparator #(.width(32), .mode("twosComplement")) comparator_8 (
    .a(PC), .b(PC7), .eq(comparator_8_eq));  // open: gt, lt
  \MAX2归并比较  \max2归并比较_1  (
    .Y(C1), .X(C0), .Y_num(3'b001), .X_num(3'b000), .MAX(\max2归并比较_1_max ), .MAX_num(\max2归并比较_1_max_num ));
  \MAX2归并比较  \max2归并比较_2  (
    .Y(C3), .X(C2), .Y_num(3'b011), .X_num(3'b010), .MAX(\max2归并比较_2_max ), .MAX_num(\max2归并比较_2_max_num ));
  \MAX2归并比较  \max2归并比较_3  (
    .Y(C5), .X(C4), .Y_num(3'b101), .X_num(3'b100), .MAX(\max2归并比较_3_max ), .MAX_num(\max2归并比较_3_max_num ));
  \MAX2归并比较  \max2归并比较_4  (
    .Y(C7), .X(C6), .Y_num(3'b111), .X_num(3'b110), .MAX(\max2归并比较_4_max ), .MAX_num(\max2归并比较_4_max_num ));
  and and_18 (and_18_out, ex_hit, \是分支指令 , L0);
  and and_19 (and_19_out, ex_hit, \是分支指令 , L1);
  and and_20 (and_20_out, ex_hit, \是分支指令 , L2);
  and and_21 (and_21_out, ex_hit, \是分支指令 , L3);
  and and_22 (and_22_out, ex_hit, \是分支指令 , L4);
  and and_23 (and_23_out, ex_hit, \是分支指令 , L5);
  and and_24 (and_24_out, ex_hit, \是分支指令 , L6);
  and and_25 (and_25_out, ex_hit, \是分支指令 , L7);
  and and_26 (h0, comparator_1_eq, V0);
  and and_27 (h1, comparator_2_eq, V1);
  and and_28 (h2, comparator_3_eq, V2);
  and and_29 (h3, comparator_4_eq, V3);
  and and_30 (h4, comparator_5_eq, V4);
  and and_31 (h5, comparator_6_eq, V5);
  and and_32 (h6, comparator_7_eq, V6);
  and and_33 (h7, comparator_8_eq, V7);
  \MAX2归并比较  \max2归并比较_5  (
    .Y(\max2归并比较_2_max ), .X(\max2归并比较_1_max ), .Y_num(\max2归并比较_2_max_num ), .X_num(\max2归并比较_1_max_num ),
    .MAX(\max2归并比较_5_max ), .MAX_num(\max2归并比较_5_max_num ));
  \MAX2归并比较  \max2归并比较_6  (
    .Y(\max2归并比较_4_max ), .X(\max2归并比较_3_max ), .Y_num(\max2归并比较_4_max_num ), .X_num(\max2归并比较_3_max_num ),
    .MAX(\max2归并比较_6_max ), .MAX_num(\max2归并比较_6_max_num ));
  \MAX2归并比较  \max2归并比较_7  (
    .Y(\max2归并比较_6_max ), .X(\max2归并比较_5_max ), .Y_num(\max2归并比较_6_max_num ), .X_num(\max2归并比较_5_max_num ),
    .MAX_num(max));  // open: MAX
  or or_17 (en0, and_18_out, WriteL0);
  or or_18 (en1, and_19_out, WriteL1);
  or or_19 (en2, and_20_out, WriteL2);
  or or_20 (en3, and_21_out, WriteL3);
  or or_21 (en4, and_22_out, WriteL4);
  or or_22 (en5, and_23_out, WriteL5);
  or or_23 (en6, and_24_out, WriteL6);
  or or_24 (en7, and_25_out, WriteL7);
  or or_25 (hit, h0, h1, h2, h3, h4, h5, h6, h7);
  Comparator #(.width(32), .mode("twosComplement")) comparator_9 (
    .a(ex_PC), .b(PC0), .eq(comparator_9_eq));  // open: gt, lt
  Comparator #(.width(32), .mode("twosComplement")) comparator_10 (
    .a(ex_PC), .b(PC1), .eq(comparator_10_eq));  // open: gt, lt
  Comparator #(.width(32), .mode("twosComplement")) comparator_11 (
    .a(ex_PC), .b(PC2), .eq(comparator_11_eq));  // open: gt, lt
  Comparator #(.width(32), .mode("twosComplement")) comparator_12 (
    .a(ex_PC), .b(PC3), .eq(comparator_12_eq));  // open: gt, lt
  Comparator #(.width(32), .mode("twosComplement")) comparator_13 (
    .a(ex_PC), .b(PC4), .eq(comparator_13_eq));  // open: gt, lt
  Comparator #(.width(32), .mode("twosComplement")) comparator_14 (
    .a(ex_PC), .b(PC5), .eq(comparator_14_eq));  // open: gt, lt
  Comparator #(.width(32), .mode("twosComplement")) comparator_15 (
    .a(ex_PC), .b(PC6), .eq(comparator_15_eq));  // open: gt, lt
  Comparator #(.width(32), .mode("twosComplement")) comparator_16 (
    .a(ex_PC), .b(PC7), .eq(comparator_16_eq));  // open: gt, lt
  and and_34 (L0, comparator_9_eq, V0);
  and and_35 (L1, comparator_10_eq, V1);
  and and_36 (L2, comparator_11_eq, V2);
  and and_37 (L3, comparator_12_eq, V3);
  and and_38 (L4, comparator_13_eq, V4);
  and and_39 (L5, comparator_14_eq, V5);
  and and_40 (L6, comparator_15_eq, V6);
  and and_41 (L7, comparator_16_eq, V7);

  // Other names for the same wires on the sheet: 状态[1:0] = Status
endmodule

module \MAX2归并比较  (
  input  [15:0] Y,
  input  [15:0] X,
  input  [2:0] Y_num,
  input  [2:0] X_num,
  output [15:0] MAX,
  output [2:0] MAX_num
);

  wire comparator_1_eq, comparator_1_gt, or_1_out;

  Multiplexer #(.select(1), .width(16), .disabled("Z"), .enable("true")) multiplexer_1 (
    .in0(Y), .in1(X), .out(MAX), .sel(or_1_out), .en(1'b1));
  Comparator #(.width(16), .mode("unsigned")) comparator_1 (
    .a(X), .b(Y), .gt(comparator_1_gt), .eq(comparator_1_eq));  // open: lt
  or or_1 (or_1_out, comparator_1_gt, comparator_1_eq);
  Multiplexer #(.select(1), .width(3), .disabled("Z"), .enable("false")) multiplexer_2 (
    .in0(Y_num), .in1(X_num), .out(MAX_num), .sel(or_1_out));

  // Notes on the sheet:
  //   输出两个输入中的较大值，并输出较大值的2位编号
endmodule

module \状态转换  (
  input  [1:0] oldstatus,
  input  [1:0] key,
  output [1:0] newstatus
);

  wire [1:0] multiplexer_1_out, multiplexer_2_out;

  Multiplexer #(.select(2), .width(2), .disabled("Z"), .enable("false")) multiplexer_1 (
    .in0(2'b00), .in1(2'b00), .in2(2'b11), .in3(2'b00), .out(multiplexer_1_out), .sel(oldstatus));
  Multiplexer #(.select(2), .width(2), .disabled("Z"), .enable("false")) multiplexer_2 (
    .in0(2'b01), .in1(2'b10), .in2(2'b10), .in3(2'b10), .out(multiplexer_2_out), .sel(oldstatus));
  Multiplexer #(.select(2), .width(2), .disabled("Z"), .enable("false")) multiplexer_3 (
    .in0(2'b00), .in1(2'b10), .in2(multiplexer_1_out), .in3(multiplexer_2_out), .out(newstatus), .sel(key));
endmodule

module \优先级封装  (
  input  v0,
  input  v1,
  input  v2,
  input  v3,
  input  v4,
  input  v5,
  input  v6,
  input  v7,
  output v0_2,
  output v1_2,
  output v2_2,
  output v3_2,
  output v4_2,
  output v5_2,
  output v6_2,
  output v7_2
);

  wire not_2_out, not_3_out, not_4_out, not_5_out, not_6_out, not_7_out, not_8_out;

  not not_1 (v0_2, v0);
  not not_2 (not_2_out, v1);
  not not_3 (not_3_out, v2);
  not not_4 (not_4_out, v3);
  not not_5 (not_5_out, v4);
  not not_6 (not_6_out, v5);
  not not_7 (not_7_out, v6);
  not not_8 (not_8_out, v7);
  and and_1 (v1_2, v0, not_2_out);
  and and_2 (v2_2, not_3_out, v0, v1);
  and and_3 (v3_2, not_4_out, v0, v1, v2);
  and and_4 (v4_2, not_5_out, v0, v1, v2, v3);
  and and_5 (v5_2, not_6_out, v0, v1, v2, v3, v4);
  and and_6 (v6_2, not_7_out, v0, v1, v2, v3, v4, v5);
  and and_7 (v7_2, not_8_out, v0, v1, v2, v3, v4, v5, v6);
endmodule
