// Logisim project cpu24中断.circ as structural Verilog: 19 circuits, main circuit ◇单周期MIPS
module \单周期MIPS  (
  output RegWrite,
  output MemWrite,
  output [31:0] PC,
  output [31:0] IR,
  output [31:0] RDin,
  output [31:0] MDin
);

  wire and_3_out, and_4_out, and_5_out, BLEZ, branch, CLK, comparator_1_eq, Go, IR1, IR2, IR3, JAL, JMP, JR,
       LB, mips_alu_1_blez, mips_alu_1_equal, not_1_out, not_2_out, not_3_out, \output , SignedExt, stop,
       Syscall, W1, W2, W3, \单周期硬布线控制器_1_alu_src , \单周期硬布线控制器_1_beq , \单周期硬布线控制器_1_bne ,
       \单周期硬布线控制器_1_memtoreg , \单周期硬布线控制器_1_regdst ;
  wire [3:0] \单周期硬布线控制器_1_alu_op ;
  wire [4:0] multiplexer_3_out, multiplexer_4_out, multiplexer_5_out, multiplexer_6_out;
  wire [7:0] multiplexer_10_out;
  wire [15:0] \总周期数 , \无条件跳转数 , \有条件跳转数 ;
  wire [27:0] PC_4;
  wire [31:0] adder_2_out, bit_extender_1_out, bit_extender_2_out, bit_extender_3_out, bit_extender_4_out,
       controlled_buffer_1_out, JMP_PC, JR_PC, LedData, mips_alu_1_result, multiplexer_1_out,
       multiplexer_2_out, multiplexer_7_out, multiplexer_8_out, multiplexer_11_out, multiplexer_12_out,
       ram_1_data, shifter_2_out;
  wire [31:28] shifter_1_out;

  Clock #(.highDuration(1), .lowDuration(1)) clock_1 (.out(CLK));
  Button _1 (.out(IR1));
  Button _2 (.out(IR2));
  Button _3 (.out(IR3));
  Button \u_继续运行  (.out(Go));
  LED #(.active("true")) led_1 (.in(W1));
  LED #(.active("true")) led_2 (.in(W2));
  LED #(.active("true")) led_3 (.in(W3));
  Multiplexer #(.select(1), .width(32), .disabled("Z"), .enable("false")) multiplexer_1 (
    .in0({JMP_PC[31:28], PC_4}), .in1(adder_2_out), .out(multiplexer_1_out), .sel(branch));
  Hex_Digit_Display hex_digit_display_1 (.value(LedData[31:28]));  // open: dp
  Multiplexer #(.select(2), .width(32), .disabled("Z"), .enable("false")) multiplexer_2 (
    .in0(multiplexer_1_out), .in1(JMP_PC), .in2(JR_PC), .in3(JR_PC), .out(multiplexer_2_out), .sel({JR, JMP}));
  not not_1 (not_1_out, stop);
  Comparator #(.width(32), .mode("twosComplement")) comparator_1 (
    .a(JR_PC), .b(32'h22), .eq(comparator_1_eq));  // open: gt, lt
  not not_2 (not_2_out, comparator_1_eq);
  Hex_Digit_Display hex_digit_display_2 (.value(LedData[27:24]));  // open: dp
  Hex_Digit_Display hex_digit_display_3 (.value(LedData[23:20]));  // open: dp
  Register #(.width(32), .trigger("rising"), .Select("low")) u_PC (
    .D(multiplexer_2_out), .en(not_1_out), .Q(PC), .clk(CLK), .clr(1'b0));
  Counter #(.width(16), .max('hffff), .ongoal("wrap"), .trigger("rising"), .behavior("old")) counter_1 (
    .D({16{1'b0}}), .count(not_1_out), .Q(\总周期数 ), .clk(CLK), .clr(1'b0));  // open: load, carry, preset
  and and_1 (\output , Syscall, comparator_1_eq);
  and and_2 (stop, not_2_out, Syscall);
  Hex_Digit_Display hex_digit_display_4 (.value(LedData[15:12]));  // open: dp
  Hex_Digit_Display hex_digit_display_5 (.value(LedData[19:16]));  // open: dp
  Hex_Digit_Display hex_digit_display_6 (.value(LedData[7:4]));  // open: dp
  Hex_Digit_Display hex_digit_display_7 (.value(LedData[11:8]));  // open: dp
  // Probe on \无条件跳转数 
  // Probe on \有条件跳转数 
  Adder #(.width(32)) adder_1 (.a(PC), .b(32'h4), .out({JMP_PC[31:28], PC_4}), .cin(1'b0));  // open: cout
  assign controlled_buffer_1_out = \output  ? MDin : 32'bz;  // Controlled_Buffer controlled_buffer_1
  Hex_Digit_Display hex_digit_display_8 (.value(LedData[3:0]));  // open: dp
  // Probe on \总周期数 
  Register #(.width(32), .trigger("rising"), .Select("low")) PC_2 (
    .D(controlled_buffer_1_out), .Q(LedData), .clk(CLK));  // open: en, clr
  ROM #(.addrWidth(10), .dataWidth(32), .Select("high")) rom_1 (.addr(PC[11:2]), .data(IR));
  \单周期硬布线控制器  \u_单周期硬布线控制器_1  (
    .Func(IR[5:0]), .OP(IR[31:26]), .ALU_OP(\单周期硬布线控制器_1_alu_op ), .MemToReg(\单周期硬布线控制器_1_memtoreg ),
    .MemWrite(MemWrite), .ALU_SRC(\单周期硬布线控制器_1_alu_src ), .RegWrite(RegWrite), .SysCALL(Syscall),
    .SignedExt(SignedExt), .RegDst(\单周期硬布线控制器_1_regdst ), .JR(JR), .JMP(JMP), .Beq(\单周期硬布线控制器_1_beq ),
    .JAL(JAL), .Bne(\单周期硬布线控制器_1_bne ), .BLEZ(BLEZ), .LB(LB));
  Multiplexer #(.select(1), .width(5), .disabled("Z"), .enable("false")) multiplexer_3 (
    .in0(IR[20:16]), .in1(IR[15:11]), .out(multiplexer_3_out), .sel(\单周期硬布线控制器_1_regdst ));
  assign bit_extender_1_out = {{6{1'b0}}, IR[25:0]};  // Bit_Extender bit_extender_1
  assign bit_extender_2_out = {{16{1'b0}}, IR[15:0]};  // Bit_Extender bit_extender_2
  assign bit_extender_3_out = {{16{IR[15]}}, IR[15:0]};  // Bit_Extender bit_extender_3
  Counter #(.width(16), .max('hffff), .ongoal("wrap"), .trigger("rising"), .behavior("old")) counter_2 (
    .D({16{1'b0}}), .count(JMP), .Q(\无条件跳转数 ), .clk(CLK));  // open: load, carry, clr, preset
  Multiplexer #(.select(1), .width(5), .disabled("Z"), .enable("false")) multiplexer_4 (
    .in0(IR[25:21]), .in1(5'b00010), .out(multiplexer_4_out), .sel(Syscall));
  Multiplexer #(.select(1), .width(5), .disabled("Z"), .enable("false")) multiplexer_5 (
    .in0(IR[20:16]), .in1(5'b00100), .out(multiplexer_5_out), .sel(Syscall));
  Multiplexer #(.select(1), .width(5), .disabled("Z"), .enable("false")) multiplexer_6 (
    .in0(multiplexer_3_out), .in1({5{1'b1}}), .out(multiplexer_6_out), .sel(JAL));
  MIPS_Regifile mips_regifile_1 (
    .Din(RDin), .Clk(CLK), .R1(JR_PC), .R2(MDin), .WE(RegWrite), .W_num(multiplexer_6_out),
    .R1_num(multiplexer_4_out), .R2_num(multiplexer_5_out));
  Shifter #(.width(32), .shift("ll")) shifter_1 (
    .in(bit_extender_1_out), .\dist (5'b00010), .out({shifter_1_out, JMP_PC[27:0]}));
  Multiplexer #(.select(1), .width(32), .disabled("Z"), .enable("false")) multiplexer_7 (
    .in0(bit_extender_2_out), .in1(bit_extender_3_out), .out(multiplexer_7_out), .sel(SignedExt));
  Shifter #(.width(32), .shift("ll")) shifter_2 (.in(bit_extender_3_out), .\dist (5'b00010), .out(shifter_2_out));
  or or_1 (branch, and_3_out, and_4_out, and_5_out);
  and and_3 (and_3_out, \单周期硬布线控制器_1_beq , mips_alu_1_equal);
  and and_4 (and_4_out, \单周期硬布线控制器_1_bne , not_3_out);
  Multiplexer #(.select(1), .width(32), .disabled("Z"), .enable("false")) multiplexer_8 (
    .in0(MDin), .in1(multiplexer_7_out), .out(multiplexer_8_out), .sel(\单周期硬布线控制器_1_alu_src ));
  Adder #(.width(32)) adder_2 (
    .a(shifter_2_out), .b({JMP_PC[31:28], PC_4}), .out(adder_2_out), .cin(1'b0));  // open: cout
  Counter #(.width(16), .max('hffff), .ongoal("wrap"), .trigger("rising"), .behavior("old")) counter_3 (
    .D({16{1'b0}}), .count(branch), .Q(\有条件跳转数 ), .clk(CLK));  // open: load, carry, clr, preset
  and and_5 (and_5_out, mips_alu_1_blez, BLEZ);
  not not_3 (not_3_out, mips_alu_1_equal);
  MIPS_ALU mips_alu_1 (
    .X(JR_PC), .Y(multiplexer_8_out), .AluOP(\单周期硬布线控制器_1_alu_op ), .Equal(mips_alu_1_equal),
    .Result(mips_alu_1_result), .shamt(IR[10:6]), .BLEZ(mips_alu_1_blez));  // open: Result_2
  Multiplexer #(.select(1), .width(32), .disabled("Z"), .enable("false")) multiplexer_9 (
    .in0(multiplexer_12_out), .in1({JMP_PC[31:28], PC_4}), .out(RDin), .sel(JAL));
  RAM #(.addrWidth(10), .dataWidth(32), .bus("separate"), .Select("high")) ram_1 (
    .addr(mips_alu_1_result[11:2]), .din(MDin), .data(ram_1_data), .str(MemWrite), .sel(1'b1), .clk(CLK),
    .clr(1'b0));  // open: ld
  assign bit_extender_4_out = {{24{multiplexer_10_out[7]}}, multiplexer_10_out};  // Bit_Extender bit_extender_4
  Multiplexer #(.select(2), .width(8), .disabled("Z"), .enable("false")) multiplexer_10 (
    .in0(ram_1_data[7:0]), .in1(ram_1_data[15:8]), .in2(ram_1_data[23:16]), .in3(ram_1_data[31:24]),
    .out(multiplexer_10_out), .sel(mips_alu_1_result[1:0]));
  Multiplexer #(.select(1), .width(32), .disabled("Z"), .enable("false")) multiplexer_11 (
    .in0(ram_1_data), .in1(bit_extender_4_out), .out(multiplexer_11_out), .sel(LB));
  Multiplexer #(.select(1), .width(32), .disabled("Z"), .enable("false")) multiplexer_12 (
    .in0(mips_alu_1_result), .in1(multiplexer_11_out), .out(multiplexer_12_out), .sel(\单周期硬布线控制器_1_memtoreg ));

  // Other names for the same wires on the sheet: a0[31:0] = MDin; PC_4[31:28] = JMP_PC[31:28]; v0[31:0] = JR_PC

  // Notes on the sheet:
  //   中断源
  //   中断等待指示
  //   总复位信号应将除ROM以外所有存储组件全部清零
  //   数码管输出
  //   数码管输出应该用寄存器锁存，否则显示数据只能一闪而过
  //   指令存储器
  //   JMP
  //   JR
  //   OP
  //   Func
  //   rs
  //   contents of rom_1 (hex, n*v repeats v):
  //   20110001 8000c05 20110001 20120002 20130003 8000c09 20110001 20120002 20130003 8000c0d 20110001
  //   20120002 20130003 8000c11 20110001 20120002 20130003 c000cb8 20100001 20110001 118fc0 112020
  //   20020022 c 118882 12200001 8000c15 112020 20020022 c 20110001 118880 112020 20020022 c 12200001
  //   8000c1f 20110001 118fc0 112020 20020022 c 1188c3 112020 20020022 c 118903 112020 20020022 c 118903
  //   112020 20020022 c 118903 112020 20020022 c 118903 112020 20020022 c 118903 112020 20020022 c 118903
  //   112020 20020022 c 118903 112020 20020022 c 20100001 109fc0 139fc3 8021 2012000c 24160003 26100001
  //   3210000f 20080008 20090001 139900 2709825 132020 20020022 c 1094022 1500fff9 22100001 2018000f
  //   2188024 108700 20080008 20090001 139902 2709825 132021 20020022 c 1094022 1500fff9 108702 2c9b022
  //   12c00001 8000c50 4020 1084027 84400 3508ffff 82021 20020022 c 2010ffff 20110000 ae300000 22100001
  //   22310004 ae300000 22100001 22310004 ae300000 22100001 22310004 ae300000 22100001 22310004 ae300000
  //   22100001 22310004 ae300000 22100001 22310004 ae300000 22100001 22310004 ae300000 22100001 22310004
  //   ae300000 22100001 22310004 ae300000 22100001 22310004 ae300000 22100001 22310004 ae300000 22100001
  //   22310004 ae300000 22100001 22310004 ae300000 22100001 22310004 ae300000 22100001 22310004 ae300000
  //   22100001 22310004 22100001 8020 2011003c 8e130000 8e340000 274402a 11000002 ae330000 ae140000
  //   2231fffc 1611fff8 102020 20020022 c 22100004 2011003c 1611fff2 2002000a c 20100000 22100001 102020
  //   20020022 c 22100002 102020 20020022 c 22100003 102020 20020022 c 22100004 102020 20020022 c 22100005
  //   102020 20020022 c 22100006 102020 20020022 c 22100007 102020 20020022 c 22100008 102020 20020022
  //   20020022 c 3e00008
  //   rt
  //   rd
  //   shamt
  //   Beq
  //   Bne
  //   JAL
  //   RegDst
  //   MemToReg
  //   MemWrite
  //   AluOP
  //   AluSrcB
  //   RegWrite
  //   为方便自动评测，需要输出PC，IR，寄存器文件写入端口RDin，内存写入端口MDin等信号
endmodule

// 单周期硬布线控制器
module \单周期硬布线控制器  (
  input  [5:0] OP,
  input  [5:0] Func,
  output [3:0] ALU_OP,
  output MemToReg,
  output MemWrite,
  output ALU_SRC,
  output RegWrite,
  output SysCALL,
  output SignedExt,
  output RegDst,
  output Beq,
  output Bne,
  output JR,
  output JMP,
  output JAL,
  output LB,
  output BLEZ
);

  \运算控制器自动生成  \u_运算控制器自动生成_1  (
    .OP0(OP[0]), .OP1(OP[1]), .OP2(OP[2]), .OP3(OP[3]), .OP4(OP[4]), .OP5(OP[5]), .F0(Func[0]), .F1(Func[1]),
    .F2(Func[2]), .F3(Func[3]), .F4(Func[4]), .F5(Func[5]), .S0(ALU_OP[0]), .S1(ALU_OP[1]), .S2(ALU_OP[2]),
    .S3(ALU_OP[3]));
  \控制信号自动生成  \u_控制信号自动生成_1  (
    .OP0(OP[0]), .OP1(OP[1]), .OP2(OP[2]), .MemToReg(MemToReg), .OP3(OP[3]), .OP4(OP[4]), .OP5(OP[5]),
    .MemWrite(MemWrite), .F0(Func[0]), .F1(Func[1]), .BLEZ(BLEZ), .F2(Func[2]), .F3(Func[3]), .F4(Func[4]),
    .LB(LB), .F5(Func[5]), .ALU_SRC(ALU_SRC), .RegWrite(RegWrite), .SysCALL(SysCALL), .SignedExt(SignedExt),
    .RegDst(RegDst), .BEQ(Beq), .BNE(Bne), .JR(JR), .JUMP(JMP), .JAL(JAL));

  // Other names for the same wires on the sheet: OP_CODE[5:0] = OP

  // Notes on the sheet:
  //   运算器控制器，根据指令生成运算器功能选择信号
  //   控制信号生成，产生数据通路需要的其他控制信号
endmodule

// 运算器控制器
module \运算控制器自动生成  (
  input  OP0,
  input  OP1,
  input  OP2,
  input  OP3,
  input  OP4,
  input  OP5,
  input  F0,
  input  F1,
  input  F2,
  input  F3,
  input  F4,
  input  F5,
  output S0,
  output S1,
  output S2,
  output S3
);

  wire and_1_out, and_2_out, and_3_out, and_4_out, and_5_out, and_6_out, and_7_out, and_8_out, and_9_out,
       and_10_out, and_11_out, and_12_out, and_13_out, and_14_out, and_15_out, and_16_out, and_17_out,
       and_18_out, and_19_out, and_20_out, and_21_out, and_22_out, and_23_out, and_24_out, and_25_out,
       and_26_out, and_27_out, and_28_out, and_29_out, and_30_out, and_31_out, and_32_out, and_33_out,
       and_34_out, and_35_out, and_36_out, and_37_out, and_38_out, and_39_out, and_40_out, not_1_out,
       not_2_out, not_3_out, not_4_out, not_5_out, not_6_out, not_7_out, not_8_out, not_9_out, not_10_out,
       not_11_out, not_12_out, not_13_out, not_14_out, not_15_out, not_16_out, not_17_out, not_18_out,
       not_19_out, not_20_out, not_21_out, not_22_out, not_23_out, not_24_out, not_25_out, not_26_out,
       not_27_out, not_28_out, not_29_out, not_30_out, not_31_out, not_32_out, not_33_out, not_34_out,
       not_35_out, not_36_out, not_37_out, not_38_out, not_39_out, not_40_out, not_41_out, not_42_out,
       not_43_out, not_44_out, not_45_out, not_46_out, not_47_out, not_48_out, not_49_out, not_50_out,
       not_51_out, not_52_out, not_53_out, not_54_out, not_55_out, not_56_out, not_57_out, not_58_out,
       not_59_out, not_60_out, not_61_out, not_62_out, not_63_out, not_64_out, not_65_out, not_66_out,
       not_67_out, not_68_out, not_69_out, not_70_out, not_71_out, not_72_out, not_73_out, not_74_out,
       not_75_out, not_76_out, not_77_out, not_78_out, not_79_out, not_80_out, not_81_out, not_82_out,
       not_83_out, not_84_out, not_85_out, not_86_out, not_87_out, not_88_out, not_89_out, not_90_out,
       not_91_out, not_92_out, not_93_out, not_94_out, not_95_out, not_96_out, not_97_out, not_98_out,
       not_99_out, not_100_out, not_101_out, not_102_out, not_103_out, not_104_out, not_105_out, not_106_out,
       not_107_out, not_108_out, not_109_out, not_110_out, not_111_out, not_112_out, not_113_out,
       not_114_out, not_115_out, not_116_out, not_117_out, not_118_out, not_119_out, not_120_out,
       not_121_out, not_122_out, not_123_out, not_124_out, not_125_out, not_126_out, not_127_out,
       not_128_out, not_129_out, not_130_out, not_131_out, not_132_out, not_133_out, not_134_out,
       not_135_out, not_136_out, not_137_out, not_138_out, not_139_out, not_140_out, not_141_out,
       not_142_out, not_143_out, not_144_out, not_145_out, not_146_out, not_147_out, not_148_out,
       not_149_out, not_150_out, not_151_out, not_152_out, not_153_out, not_154_out, not_155_out,
       not_156_out, not_157_out, not_158_out, not_159_out, not_160_out, not_161_out, not_162_out,
       not_163_out, not_164_out, not_165_out, not_166_out, not_167_out, not_168_out, not_169_out,
       not_170_out, not_171_out, not_172_out, not_173_out, not_174_out, not_175_out, not_176_out,
       not_177_out, not_178_out, not_179_out, not_180_out, not_181_out, not_182_out, not_183_out,
       not_184_out, not_185_out, not_186_out, not_187_out, not_188_out, not_189_out, not_190_out,
       not_191_out, not_192_out, not_193_out, not_194_out, not_195_out, not_196_out, not_197_out,
       not_198_out, not_199_out, not_200_out, not_201_out, not_202_out, not_203_out, not_204_out,
       not_205_out, not_206_out, not_207_out, not_208_out, not_209_out, not_210_out, not_211_out,
       not_212_out, not_213_out, not_214_out, not_215_out, not_216_out, not_217_out, not_218_out,
       not_219_out, not_220_out, not_221_out, not_222_out, not_223_out, not_224_out, not_225_out,
       not_226_out, not_227_out, not_228_out, not_229_out, not_230_out, not_231_out, not_232_out,
       not_233_out, not_234_out, not_235_out, not_236_out, not_237_out, not_238_out, not_239_out,
       not_240_out, not_241_out, not_242_out, not_243_out, not_244_out, not_245_out, not_246_out,
       not_247_out, not_248_out, not_249_out, not_250_out, not_251_out, not_252_out, not_253_out,
       not_254_out, not_255_out, not_256_out, not_257_out, not_258_out, not_259_out, not_260_out,
       not_261_out, not_262_out, not_263_out, not_264_out, not_265_out, not_266_out, not_267_out,
       not_268_out, not_269_out, not_270_out, not_271_out, not_272_out, not_273_out, not_274_out,
       not_275_out, not_276_out, not_277_out, not_278_out, not_279_out, not_280_out, not_281_out, not_282_out;

  not not_1 (not_1_out, OP5);
  not not_2 (not_2_out, OP4);
  not not_3 (not_3_out, OP3);
  not not_4 (not_4_out, OP2);
  not not_5 (not_5_out, OP1);
  not not_6 (not_6_out, OP0);
  not not_7 (not_7_out, F5);
  not not_8 (not_8_out, F4);
  not not_9 (not_9_out, F3);
  not not_10 (not_10_out, F2);
  not not_11 (not_11_out, OP5);
  not not_12 (not_12_out, OP4);
  not not_13 (not_13_out, OP3);
  not not_14 (not_14_out, OP2);
  not not_15 (not_15_out, OP1);
  not not_16 (not_16_out, OP0);
  not not_17 (not_17_out, F4);
  not not_18 (not_18_out, F3);
  not not_19 (not_19_out, F2);
  not not_20 (not_20_out, F1);
  not not_21 (not_21_out, F0);
  not not_22 (not_22_out, OP5);
  not not_23 (not_23_out, OP4);
  not not_24 (not_24_out, OP3);
  not not_25 (not_25_out, OP2);
  not not_26 (not_26_out, OP1);
  not not_27 (not_27_out, OP0);
  not not_28 (not_28_out, F4);
  not not_29 (not_29_out, F3);
  not not_30 (not_30_out, F2);
  not not_31 (not_31_out, F1);
  not not_32 (not_32_out, OP5);
  not not_33 (not_33_out, OP4);
  not not_34 (not_34_out, OP3);
  not not_35 (not_35_out, OP2);
  not not_36 (not_36_out, OP1);
  not not_37 (not_37_out, OP0);
  not not_38 (not_38_out, F4);
  not not_39 (not_39_out, F3);
  not not_40 (not_40_out, F1);
  not not_41 (not_41_out, F0);
  not not_42 (not_42_out, OP5);
  not not_43 (not_43_out, OP4);
  not not_44 (not_44_out, OP3);
  not not_45 (not_45_out, OP2);
  not not_46 (not_46_out, OP1);
  not not_47 (not_47_out, OP0);
  not not_48 (not_48_out, F4);
  not not_49 (not_49_out, F2);
  not not_50 (not_50_out, F0);
  not not_51 (not_51_out, OP5);
  not not_52 (not_52_out, OP4);
  not not_53 (not_53_out, OP2);
  not not_54 (not_54_out, OP1);
  not not_55 (not_55_out, OP0);
  not not_56 (not_56_out, OP5);
  not not_57 (not_57_out, OP4);
  not not_58 (not_58_out, OP1);
  not not_59 (not_59_out, OP0);
  not not_60 (not_60_out, OP5);
  not not_61 (not_61_out, OP4);
  not not_62 (not_62_out, OP2);
  not not_63 (not_63_out, OP1);
  not not_64 (not_64_out, OP5);
  not not_65 (not_65_out, OP4);
  not not_66 (not_66_out, OP2);
  not not_67 (not_67_out, OP0);
  not not_68 (not_68_out, OP4);
  not not_69 (not_69_out, OP3);
  not not_70 (not_70_out, OP2);
  not not_71 (not_71_out, OP4);
  not not_72 (not_72_out, OP2);
  not not_73 (not_73_out, OP5);
  not not_74 (not_74_out, OP4);
  not not_75 (not_75_out, OP3);
  not not_76 (not_76_out, OP2);
  not not_77 (not_77_out, OP1);
  not not_78 (not_78_out, OP0);
  not not_79 (not_79_out, F4);
  not not_80 (not_80_out, F3);
  not not_81 (not_81_out, F0);
  not not_82 (not_82_out, OP4);
  not not_83 (not_83_out, OP3);
  not not_84 (not_84_out, OP2);
  not not_85 (not_85_out, OP1);
  not not_86 (not_86_out, OP0);
  not not_87 (not_87_out, OP5);
  not not_88 (not_88_out, OP4);
  not not_89 (not_89_out, OP3);
  not not_90 (not_90_out, OP2);
  not not_91 (not_91_out, OP1);
  not not_92 (not_92_out, OP0);
  not not_93 (not_93_out, F5);
  not not_94 (not_94_out, F4);
  not not_95 (not_95_out, F3);
  not not_96 (not_96_out, F2);
  not not_97 (not_97_out, F0);
  not not_98 (not_98_out, OP5);
  not not_99 (not_99_out, OP4);
  not not_100 (not_100_out, OP3);
  not not_101 (not_101_out, OP2);
  not not_102 (not_102_out, OP1);
  not not_103 (not_103_out, OP0);
  not not_104 (not_104_out, F4);
  not not_105 (not_105_out, F3);
  not not_106 (not_106_out, F2);
  not not_107 (not_107_out, F0);
  not not_108 (not_108_out, OP5);
  not not_109 (not_109_out, OP4);
  not not_110 (not_110_out, OP3);
  not not_111 (not_111_out, OP2);
  not not_112 (not_112_out, OP1);
  not not_113 (not_113_out, OP0);
  not not_114 (not_114_out, F4);
  not not_115 (not_115_out, F3);
  not not_116 (not_116_out, F1);
  not not_117 (not_117_out, F0);
  not not_118 (not_118_out, OP5);
  not not_119 (not_119_out, OP4);
  not not_120 (not_120_out, OP3);
  not not_121 (not_121_out, OP2);
  not not_122 (not_122_out, OP1);
  not not_123 (not_123_out, OP0);
  not not_124 (not_124_out, F4);
  not not_125 (not_125_out, F3);
  not not_126 (not_126_out, OP5);
  not not_127 (not_127_out, OP4);
  not not_128 (not_128_out, OP3);
  not not_129 (not_129_out, OP2);
  not not_130 (not_130_out, OP1);
  not not_131 (not_131_out, OP0);
  not not_132 (not_132_out, F4);
  not not_133 (not_133_out, F2);
  not not_134 (not_134_out, F0);
  not not_135 (not_135_out, OP5);
  not not_136 (not_136_out, OP4);
  not not_137 (not_137_out, OP1);
  not not_138 (not_138_out, OP0);
  not not_139 (not_139_out, OP5);
  not not_140 (not_140_out, OP4);
  not not_141 (not_141_out, OP2);
  not not_142 (not_142_out, OP0);
  not not_143 (not_143_out, OP5);
  not not_144 (not_144_out, OP4);
  not not_145 (not_145_out, OP3);
  not not_146 (not_146_out, OP2);
  not not_147 (not_147_out, OP1);
  not not_148 (not_148_out, OP0);
  not not_149 (not_149_out, F4);
  not not_150 (not_150_out, F3);
  not not_151 (not_151_out, F2);
  not not_152 (not_152_out, OP5);
  not not_153 (not_153_out, OP4);
  not not_154 (not_154_out, OP3);
  not not_155 (not_155_out, OP2);
  not not_156 (not_156_out, OP1);
  not not_157 (not_157_out, OP0);
  not not_158 (not_158_out, F4);
  not not_159 (not_159_out, F3);
  not not_160 (not_160_out, F2);
  not not_161 (not_161_out, F1);
  not not_162 (not_162_out, F0);
  not not_163 (not_163_out, OP5);
  not not_164 (not_164_out, OP4);
  not not_165 (not_165_out, OP3);
  not not_166 (not_166_out, OP2);
  not not_167 (not_167_out, OP1);
  not not_168 (not_168_out, OP0);
  not not_169 (not_169_out, F4);
  not not_170 (not_170_out, F3);
  not not_171 (not_171_out, F2);
  not not_172 (not_172_out, F1);
  not not_173 (not_173_out, OP5);
  not not_174 (not_174_out, OP4);
  not not_175 (not_175_out, OP3);
  not not_176 (not_176_out, OP2);
  not not_177 (not_177_out, OP1);
  not not_178 (not_178_out, OP0);
  not not_179 (not_179_out, F4);
  not not_180 (not_180_out, F3);
  not not_181 (not_181_out, F2);
  not not_182 (not_182_out, F0);
  not not_183 (not_183_out, OP5);
  not not_184 (not_184_out, OP4);
  not not_185 (not_185_out, OP3);
  not not_186 (not_186_out, OP2);
  not not_187 (not_187_out, OP1);
  not not_188 (not_188_out, OP0);
  not not_189 (not_189_out, F4);
  not not_190 (not_190_out, F3);
  not not_191 (not_191_out, F1);
  not not_192 (not_192_out, F0);
  not not_193 (not_193_out, OP5);
  not not_194 (not_194_out, OP4);
  not not_195 (not_195_out, OP3);
  not not_196 (not_196_out, OP2);
  not not_197 (not_197_out, OP1);
  not not_198 (not_198_out, OP0);
  not not_199 (not_199_out, F4);
  not not_200 (not_200_out, F2);
  not not_201 (not_201_out, OP5);
  not not_202 (not_202_out, OP4);
  not not_203 (not_203_out, OP2);
  not not_204 (not_204_out, OP1);
  not not_205 (not_205_out, OP0);
  not not_206 (not_206_out, OP5);
  not not_207 (not_207_out, OP4);
  not not_208 (not_208_out, OP1);
  not not_209 (not_209_out, OP0);
  not not_210 (not_210_out, OP5);
  not not_211 (not_211_out, OP4);
  not not_212 (not_212_out, OP2);
  not not_213 (not_213_out, OP1);
  not not_214 (not_214_out, OP4);
  not not_215 (not_215_out, OP3);
  not not_216 (not_216_out, OP2);
  not not_217 (not_217_out, OP4);
  not not_218 (not_218_out, OP2);
  not not_219 (not_219_out, OP5);
  not not_220 (not_220_out, OP4);
  not not_221 (not_221_out, OP3);
  not not_222 (not_222_out, OP2);
  not not_223 (not_223_out, OP1);
  not not_224 (not_224_out, OP0);
  not not_225 (not_225_out, F4);
  not not_226 (not_226_out, F3);
  not not_227 (not_227_out, F2);
  not not_228 (not_228_out, OP4);
  not not_229 (not_229_out, OP3);
  not not_230 (not_230_out, OP2);
  not not_231 (not_231_out, OP1);
  not not_232 (not_232_out, OP0);
  not not_233 (not_233_out, OP5);
  not not_234 (not_234_out, OP4);
  not not_235 (not_235_out, OP3);
  not not_236 (not_236_out, OP2);
  not not_237 (not_237_out, OP1);
  not not_238 (not_238_out, OP0);
  not not_239 (not_239_out, F4);
  not not_240 (not_240_out, F3);
  not not_241 (not_241_out, F1);
  not not_242 (not_242_out, OP5);
  not not_243 (not_243_out, OP4);
  not not_244 (not_244_out, OP3);
  not not_245 (not_245_out, OP2);
  not not_246 (not_246_out, OP1);
  not not_247 (not_247_out, OP0);
  not not_248 (not_248_out, F4);
  not not_249 (not_249_out, F3);
  not not_250 (not_250_out, OP5);
  not not_251 (not_251_out, OP4);
  not not_252 (not_252_out, OP3);
  not not_253 (not_253_out, OP2);
  not not_254 (not_254_out, OP1);
  not not_255 (not_255_out, OP0);
  not not_256 (not_256_out, F4);
  not not_257 (not_257_out, F2);
  not not_258 (not_258_out, F0);
  not not_259 (not_259_out, OP5);
  not not_260 (not_260_out, OP4);
  not not_261 (not_261_out, OP3);
  not not_262 (not_262_out, OP2);
  not not_263 (not_263_out, OP1);
  not not_264 (not_264_out, OP0);
  not not_265 (not_265_out, F4);
  not not_266 (not_266_out, F2);
  not not_267 (not_267_out, OP5);
  not not_268 (not_268_out, OP4);
  not not_269 (not_269_out, OP2);
  not not_270 (not_270_out, OP0);
  not not_271 (not_271_out, OP5);
  not not_272 (not_272_out, OP4);
  not not_273 (not_273_out, OP1);
  not not_274 (not_274_out, OP5);
  not not_275 (not_275_out, OP4);
  not not_276 (not_276_out, OP3);
  not not_277 (not_277_out, OP2);
  not not_278 (not_278_out, OP1);
  not not_279 (not_279_out, OP0);
  not not_280 (not_280_out, F4);
  not not_281 (not_281_out, F3);
  not not_282 (not_282_out, F0);
  and and_1 (and_1_out, not_1_out, not_2_out, not_3_out, not_4_out, not_5_out, not_6_out, not_7_out, not_8_out, not_9_out, not_10_out, F1, F0);
  and and_2 (and_2_out, not_11_out, not_12_out, not_13_out, not_14_out, not_15_out, not_16_out, F5, not_17_out, not_18_out, not_19_out, not_20_out, not_21_out);
  and and_3 (and_3_out, not_22_out, not_23_out, not_24_out, not_25_out, not_26_out, not_27_out, F5, not_28_out, not_29_out, not_30_out, not_31_out, F0);
  and and_4 (and_4_out, not_32_out, not_33_out, not_34_out, not_35_out, not_36_out, not_37_out, F5, not_38_out, not_39_out, F2, not_40_out, not_41_out);
  and and_5 (and_5_out, not_42_out, not_43_out, not_44_out, not_45_out, not_46_out, not_47_out, F5, not_48_out, F3, not_49_out, F1, not_50_out);
  and and_6 (and_6_out, not_51_out, not_52_out, OP3, not_53_out, not_54_out, not_55_out);
  and and_7 (and_7_out, not_56_out, not_57_out, OP3, OP2, not_58_out, not_59_out);
  and and_8 (and_8_out, not_60_out, not_61_out, OP3, not_62_out, not_63_out, OP0);
  and and_9 (and_9_out, not_64_out, not_65_out, OP3, not_66_out, OP1, not_67_out);
  and and_10 (and_10_out, OP5, not_68_out, not_69_out, not_70_out, OP1, OP0);
  and and_11 (and_11_out, OP5, not_71_out, OP3, not_72_out, OP1, OP0);
  and and_12 (and_12_out, not_73_out, not_74_out, not_75_out, not_76_out, not_77_out, not_78_out, F5, not_79_out, not_80_out, F2, F1, not_81_out);
  and and_13 (and_13_out, OP5, not_82_out, not_83_out, not_84_out, not_85_out, not_86_out);
  and and_14 (and_14_out, not_87_out, not_88_out, not_89_out, not_90_out, not_91_out, not_92_out, not_93_out, not_94_out, not_95_out, not_96_out, F1, not_97_out);
  and and_15 (and_15_out, not_98_out, not_99_out, not_100_out, not_101_out, not_102_out, not_103_out, F5, not_104_out, not_105_out, not_106_out, F1, not_107_out);
  and and_16 (and_16_out, not_108_out, not_109_out, not_110_out, not_111_out, not_112_out, not_113_out, F5, not_114_out, not_115_out, F2, not_116_out, not_117_out);
  and and_17 (and_17_out, not_118_out, not_119_out, not_120_out, not_121_out, not_122_out, not_123_out, F5, not_124_out, not_125_out, F2, F1, F0);
  and and_18 (and_18_out, not_126_out, not_127_out, not_128_out, not_129_out, not_130_out, not_131_out, F5, not_132_out, F3, not_133_out, F1, not_134_out);
  and and_19 (and_19_out, not_135_out, not_136_out, OP3, OP2, not_137_out, not_138_out);
  and and_20 (and_20_out, not_139_out, not_140_out, OP3, not_141_out, OP1, not_142_out);
  and and_21 (and_21_out, not_143_out, not_144_out, not_145_out, not_146_out, not_147_out, not_148_out, F5, not_149_out, not_150_out, not_151_out, F1, F0);
  and and_22 (and_22_out, not_152_out, not_153_out, not_154_out, not_155_out, not_156_out, not_157_out, F5, not_158_out, not_159_out, not_160_out, not_161_out, not_162_out);
  and and_23 (and_23_out, not_163_out, not_164_out, not_165_out, not_166_out, not_167_out, not_168_out, F5, not_169_out, not_170_out, not_171_out, not_172_out, F0);
  and and_24 (and_24_out, not_173_out, not_174_out, not_175_out, not_176_out, not_177_out, not_178_out, F5, not_179_out, not_180_out, not_181_out, F1, not_182_out);
  and and_25 (and_25_out, not_183_out, not_184_out, not_185_out, not_186_out, not_187_out, not_188_out, F5, not_189_out, not_190_out, F2, not_191_out, not_192_out);
  and and_26 (and_26_out, not_193_out, not_194_out, not_195_out, not_196_out, not_197_out, not_198_out, F5, not_199_out, F3, not_200_out, F1, F0);
  and and_27 (and_27_out, not_201_out, not_202_out, OP3, not_203_out, not_204_out, not_205_out);
  and and_28 (and_28_out, not_206_out, not_207_out, OP3, OP2, not_208_out, not_209_out);
  and and_29 (and_29_out, not_210_out, not_211_out, OP3, not_212_out, not_213_out, OP0);
  and and_30 (and_30_out, OP5, not_214_out, not_215_out, not_216_out, OP1, OP0);
  and and_31 (and_31_out, OP5, not_217_out, OP3, not_218_out, OP1, OP0);
  and and_32 (and_32_out, not_219_out, not_220_out, not_221_out, not_222_out, not_223_out, not_224_out, F5, not_225_out, not_226_out, not_227_out, F1, F0);
  and and_33 (and_33_out, OP5, not_228_out, not_229_out, not_230_out, not_231_out, not_232_out);
  and and_34 (and_34_out, not_233_out, not_234_out, not_235_out, not_236_out, not_237_out, not_238_out, F5, not_239_out, not_240_out, F2, not_241_out, F0);
  and and_35 (and_35_out, not_242_out, not_243_out, not_244_out, not_245_out, not_246_out, not_247_out, F5, not_248_out, not_249_out, F2, F1, F0);
  and and_36 (and_36_out, not_250_out, not_251_out, not_252_out, not_253_out, not_254_out, not_255_out, F5, not_256_out, F3, not_257_out, F1, not_258_out);
  and and_37 (and_37_out, not_259_out, not_260_out, not_261_out, not_262_out, not_263_out, not_264_out, F5, not_265_out, F3, not_266_out, F1, F0);
  and and_38 (and_38_out, not_267_out, not_268_out, OP3, not_269_out, OP1, not_270_out);
  and and_39 (and_39_out, not_271_out, not_272_out, OP3, OP2, not_273_out, OP0);
  and and_40 (and_40_out, not_274_out, not_275_out, not_276_out, not_277_out, not_278_out, not_279_out, F5, not_280_out, not_281_out, F2, F1, not_282_out);
  or or_1 (S1, and_14_out, and_15_out, and_16_out, and_17_out, and_18_out, and_19_out, and_20_out, and_21_out);
  or or_2 (S3, and_34_out, and_35_out, and_36_out, and_37_out, and_38_out, and_39_out, and_40_out);
  or or_3 (S0, and_1_out, and_2_out, and_3_out, and_4_out, and_5_out, and_6_out, and_7_out, and_8_out, and_9_out, and_10_out, and_11_out, and_12_out, and_13_out);
  or or_4 (S2, and_22_out, and_23_out, and_24_out, and_25_out, and_26_out, and_27_out, and_28_out, and_29_out, and_30_out, and_31_out, and_32_out, and_33_out);
endmodule

// 控制信号生成
module \控制信号自动生成  (
  input  OP0,
  input  OP1,
  input  OP2,
  input  OP3,
  input  OP4,
  input  OP5,
  input  F0,
  input  F1,
  input  F2,
  input  F3,
  input  F4,
  input  F5,
  output MemToReg,
  output MemWrite,
  output BLEZ,
  output LB,
  output ALU_SRC,
  output RegWrite,
  output SysCALL,
  output SignedExt,
  output RegDst,
  output BEQ,
  output BNE,
  output JR,
  output JUMP,
  output JAL
);

  wire and_1_out, and_2_out, and_6_out, and_7_out, and_8_out, and_9_out, and_10_out, and_11_out, and_12_out,
       and_13_out, and_14_out, and_15_out, and_16_out, and_17_out, and_19_out, and_20_out, and_21_out,
       and_22_out, and_23_out, and_24_out, and_25_out, and_26_out, and_27_out, and_28_out, and_29_out,
       and_30_out, and_34_out, and_35_out, not_1_out, not_2_out, not_3_out, not_4_out, not_5_out, not_6_out,
       not_7_out, not_8_out, not_9_out, not_10_out, not_11_out, not_12_out, not_13_out, not_14_out,
       not_15_out, not_16_out, not_17_out, not_18_out, not_19_out, not_20_out, not_21_out, not_22_out,
       not_23_out, not_24_out, not_25_out, not_26_out, not_27_out, not_28_out, not_29_out, not_30_out,
       not_31_out, not_32_out, not_33_out, not_34_out, not_35_out, not_36_out, not_37_out, not_38_out,
       not_39_out, not_40_out, not_41_out, not_42_out, not_43_out, not_44_out, not_45_out, not_46_out,
       not_47_out, not_48_out, not_49_out, not_50_out, not_51_out, not_52_out, not_53_out, not_54_out,
       not_55_out, not_56_out, not_57_out, not_58_out, not_59_out, not_60_out, not_61_out, not_62_out,
       not_63_out, not_64_out, not_65_out, not_66_out, not_67_out, not_68_out, not_69_out, not_70_out,
       not_71_out, not_72_out, not_73_out, not_74_out, not_75_out, not_76_out, not_77_out, not_78_out,
       not_79_out, not_80_out, not_81_out, not_82_out, not_83_out, not_84_out, not_85_out, not_86_out,
       not_87_out, not_88_out, not_89_out, not_90_out, not_91_out, not_92_out, not_93_out, not_94_out,
       not_95_out, not_96_out, not_97_out, not_98_out, not_99_out, not_100_out, not_101_out, not_102_out,
       not_103_out, not_104_out, not_105_out, not_106_out, not_107_out, not_108_out, not_109_out,
       not_110_out, not_111_out, not_112_out, not_113_out, not_114_out, not_115_out, not_116_out,
       not_117_out, not_118_out, not_119_out, not_120_out, not_121_out, not_122_out, not_123_out,
       not_124_out, not_125_out, not_126_out, not_127_out, not_128_out, not_129_out, not_130_out,
       not_131_out, not_132_out, not_133_out, not_134_out, not_135_out, not_136_out, not_137_out,
       not_138_out, not_139_out, not_140_out, not_141_out, not_142_out, not_143_out, not_144_out,
       not_145_out, not_146_out, not_147_out, not_148_out, not_149_out, not_150_out, not_151_out,
       not_152_out, not_153_out, not_154_out, not_155_out, not_156_out, not_157_out, not_158_out,
       not_159_out, not_160_out, not_161_out, not_162_out, not_163_out, not_164_out, not_165_out,
       not_166_out, not_167_out, not_168_out, not_169_out, not_170_out, not_171_out, not_172_out,
       not_173_out, not_174_out, not_175_out, not_176_out, not_177_out, not_178_out, not_179_out,
       not_180_out, not_181_out, not_182_out, not_183_out, not_184_out, not_185_out, not_186_out,
       not_187_out, not_188_out, not_189_out, not_190_out, not_191_out, not_192_out, not_193_out,
       not_194_out, not_195_out;

  not not_1 (not_1_out, OP0);
  not not_2 (not_2_out, OP1);
  not not_3 (not_3_out, OP2);
  not not_4 (not_4_out, OP3);
  not not_5 (not_5_out, OP4);
  not not_6 (not_6_out, OP2);
  not not_7 (not_7_out, OP3);
  not not_8 (not_8_out, OP4);
  not not_9 (not_9_out, OP2);
  not not_10 (not_10_out, OP4);
  not not_11 (not_11_out, OP0);
  not not_12 (not_12_out, OP3);
  not not_13 (not_13_out, OP4);
  not not_14 (not_14_out, OP5);
  not not_15 (not_15_out, OP0);
  not not_16 (not_16_out, OP1);
  not not_17 (not_17_out, OP2);
  not not_18 (not_18_out, OP3);
  not not_19 (not_19_out, OP4);
  not not_20 (not_20_out, OP0);
  not not_21 (not_21_out, OP1);
  not not_22 (not_22_out, OP2);
  not not_23 (not_23_out, OP3);
  not not_24 (not_24_out, OP4);
  not not_25 (not_25_out, OP0);
  not not_26 (not_26_out, OP2);
  not not_27 (not_27_out, OP4);
  not not_28 (not_28_out, OP5);
  not not_29 (not_29_out, OP1);
  not not_30 (not_30_out, OP4);
  not not_31 (not_31_out, OP5);
  not not_32 (not_32_out, OP2);
  not not_33 (not_33_out, OP4);
  not not_34 (not_34_out, OP0);
  not not_35 (not_35_out, OP1);
  not not_36 (not_36_out, OP2);
  not not_37 (not_37_out, OP3);
  not not_38 (not_38_out, OP4);
  not not_39 (not_39_out, F0);
  not not_40 (not_40_out, F2);
  not not_41 (not_41_out, F3);
  not not_42 (not_42_out, F4);
  not not_43 (not_43_out, OP0);
  not not_44 (not_44_out, OP1);
  not not_45 (not_45_out, OP2);
  not not_46 (not_46_out, OP3);
  not not_47 (not_47_out, OP4);
  not not_48 (not_48_out, F3);
  not not_49 (not_49_out, F4);
  not not_50 (not_50_out, OP0);
  not not_51 (not_51_out, OP1);
  not not_52 (not_52_out, OP2);
  not not_53 (not_53_out, OP3);
  not not_54 (not_54_out, OP4);
  not not_55 (not_55_out, F2);
  not not_56 (not_56_out, F3);
  not not_57 (not_57_out, F4);
  not not_58 (not_58_out, OP0);
  not not_59 (not_59_out, OP1);
  not not_60 (not_60_out, OP2);
  not not_61 (not_61_out, OP3);
  not not_62 (not_62_out, OP4);
  not not_63 (not_63_out, F2);
  not not_64 (not_64_out, F4);
  not not_65 (not_65_out, OP0);
  not not_66 (not_66_out, OP1);
  not not_67 (not_67_out, OP2);
  not not_68 (not_68_out, OP3);
  not not_69 (not_69_out, OP4);
  not not_70 (not_70_out, OP0);
  not not_71 (not_71_out, OP2);
  not not_72 (not_72_out, OP4);
  not not_73 (not_73_out, OP5);
  not not_74 (not_74_out, OP1);
  not not_75 (not_75_out, OP4);
  not not_76 (not_76_out, OP5);
  not not_77 (not_77_out, OP2);
  not not_78 (not_78_out, OP3);
  not not_79 (not_79_out, OP4);
  not not_80 (not_80_out, OP0);
  not not_81 (not_81_out, OP1);
  not not_82 (not_82_out, OP2);
  not not_83 (not_83_out, OP3);
  not not_84 (not_84_out, OP4);
  not not_85 (not_85_out, OP5);
  not not_86 (not_86_out, F0);
  not not_87 (not_87_out, F1);
  not not_88 (not_88_out, F4);
  not not_89 (not_89_out, F5);
  not not_90 (not_90_out, OP5);
  not not_91 (not_91_out, OP4);
  not not_92 (not_92_out, OP3);
  not not_93 (not_93_out, OP1);
  not not_94 (not_94_out, OP0);
  not not_95 (not_95_out, OP5);
  not not_96 (not_96_out, OP4);
  not not_97 (not_97_out, OP3);
  not not_98 (not_98_out, OP1);
  not not_99 (not_99_out, OP5);
  not not_100 (not_100_out, OP4);
  not not_101 (not_101_out, OP2);
  not not_102 (not_102_out, OP1);
  not not_103 (not_103_out, OP0);
  not not_104 (not_104_out, OP5);
  not not_105 (not_105_out, OP4);
  not not_106 (not_106_out, OP2);
  not not_107 (not_107_out, OP1);
  not not_108 (not_108_out, OP5);
  not not_109 (not_109_out, OP4);
  not not_110 (not_110_out, OP2);
  not not_111 (not_111_out, OP0);
  not not_112 (not_112_out, OP4);
  not not_113 (not_113_out, OP3);
  not not_114 (not_114_out, OP2);
  not not_115 (not_115_out, OP4);
  not not_116 (not_116_out, OP2);
  not not_117 (not_117_out, OP4);
  not not_118 (not_118_out, OP3);
  not not_119 (not_119_out, OP2);
  not not_120 (not_120_out, OP1);
  not not_121 (not_121_out, OP0);
  not not_122 (not_122_out, OP0);
  not not_123 (not_123_out, OP1);
  not not_124 (not_124_out, OP2);
  not not_125 (not_125_out, OP3);
  not not_126 (not_126_out, OP4);
  not not_127 (not_127_out, OP5);
  not not_128 (not_128_out, F0);
  not not_129 (not_129_out, F1);
  not not_130 (not_130_out, F2);
  not not_131 (not_131_out, F4);
  not not_132 (not_132_out, F5);
  not not_133 (not_133_out, OP0);
  not not_134 (not_134_out, OP1);
  not not_135 (not_135_out, OP2);
  not not_136 (not_136_out, OP3);
  not not_137 (not_137_out, OP4);
  not not_138 (not_138_out, OP5);
  not not_139 (not_139_out, F3);
  not not_140 (not_140_out, F4);
  not not_141 (not_141_out, OP0);
  not not_142 (not_142_out, OP1);
  not not_143 (not_143_out, OP2);
  not not_144 (not_144_out, OP3);
  not not_145 (not_145_out, OP4);
  not not_146 (not_146_out, OP5);
  not not_147 (not_147_out, F2);
  not not_148 (not_148_out, F3);
  not not_149 (not_149_out, F4);
  not not_150 (not_150_out, OP0);
  not not_151 (not_151_out, OP1);
  not not_152 (not_152_out, OP2);
  not not_153 (not_153_out, OP3);
  not not_154 (not_154_out, OP4);
  not not_155 (not_155_out, OP5);
  not not_156 (not_156_out, F2);
  not not_157 (not_157_out, F4);
  not not_158 (not_158_out, OP5);
  not not_159 (not_159_out, OP4);
  not not_160 (not_160_out, OP3);
  not not_161 (not_161_out, OP1);
  not not_162 (not_162_out, OP0);
  not not_163 (not_163_out, OP5);
  not not_164 (not_164_out, OP4);
  not not_165 (not_165_out, OP3);
  not not_166 (not_166_out, OP1);
  not not_167 (not_167_out, OP0);
  not not_168 (not_168_out, OP1);
  not not_169 (not_169_out, OP2);
  not not_170 (not_170_out, OP3);
  not not_171 (not_171_out, OP4);
  not not_172 (not_172_out, OP5);
  not not_173 (not_173_out, F0);
  not not_174 (not_174_out, F1);
  not not_175 (not_175_out, F2);
  not not_176 (not_176_out, F4);
  not not_177 (not_177_out, F5);
  not not_178 (not_178_out, OP0);
  not not_179 (not_179_out, OP2);
  not not_180 (not_180_out, OP3);
  not not_181 (not_181_out, OP4);
  not not_182 (not_182_out, OP5);
  not not_183 (not_183_out, F0);
  not not_184 (not_184_out, F1);
  not not_185 (not_185_out, F2);
  not not_186 (not_186_out, F4);
  not not_187 (not_187_out, F5);
  not not_188 (not_188_out, OP2);
  not not_189 (not_189_out, OP3);
  not not_190 (not_190_out, OP4);
  not not_191 (not_191_out, OP5);
  not not_192 (not_192_out, OP2);
  not not_193 (not_193_out, OP3);
  not not_194 (not_194_out, OP4);
  not not_195 (not_195_out, OP5);
  and and_1 (and_1_out, not_1_out, not_2_out, not_3_out, not_4_out, not_5_out, OP5);
  and and_2 (and_2_out, OP0, OP1, not_6_out, not_7_out, not_8_out, OP5);
  and and_3 (MemWrite, OP0, OP1, not_9_out, OP3, not_10_out, OP5);
  and and_4 (BLEZ, not_11_out, OP1, OP2, not_12_out, not_13_out, not_14_out);
  and and_5 (LB, not_15_out, not_16_out, not_17_out, not_18_out, not_19_out, OP5);
  and and_6 (and_6_out, not_20_out, not_21_out, not_22_out, not_23_out, not_24_out, OP5);
  and and_7 (and_7_out, not_25_out, not_26_out, OP3, not_27_out, not_28_out);
  and and_8 (and_8_out, not_29_out, OP3, not_30_out, not_31_out);
  and and_9 (and_9_out, OP0, OP1, not_32_out, not_33_out, OP5);
  and and_10 (and_10_out, not_34_out, not_35_out, not_36_out, not_37_out, not_38_out, not_39_out, not_40_out, not_41_out, not_42_out);
  and and_11 (and_11_out, not_43_out, not_44_out, not_45_out, not_46_out, not_47_out, not_48_out, not_49_out, F5);
  and and_12 (and_12_out, not_50_out, not_51_out, not_52_out, not_53_out, not_54_out, F1, not_55_out, not_56_out, not_57_out);
  and and_13 (and_13_out, not_58_out, not_59_out, not_60_out, not_61_out, not_62_out, F1, not_63_out, not_64_out, F5);
  and and_14 (and_14_out, not_65_out, not_66_out, not_67_out, not_68_out, not_69_out, OP5);
  and and_15 (and_15_out, not_70_out, not_71_out, OP3, not_72_out, not_73_out);
  and and_16 (and_16_out, not_74_out, OP3, not_75_out, not_76_out);
  and and_17 (and_17_out, OP0, OP1, not_77_out, not_78_out, not_79_out);
  and and_18 (SysCALL, not_80_out, not_81_out, not_82_out, not_83_out, not_84_out, not_85_out, not_86_out, not_87_out, F2, F3, not_88_out, not_89_out);
  and and_19 (and_19_out, not_90_out, not_91_out, not_92_out, OP2, not_93_out, not_94_out);
  and and_20 (and_20_out, not_95_out, not_96_out, not_97_out, OP2, not_98_out, OP0);
  and and_21 (and_21_out, not_99_out, not_100_out, OP3, not_101_out, not_102_out, not_103_out);
  and and_22 (and_22_out, not_104_out, not_105_out, OP3, not_106_out, not_107_out, OP0);
  and and_23 (and_23_out, not_108_out, not_109_out, OP3, not_110_out, OP1, not_111_out);
  and and_24 (and_24_out, OP5, not_112_out, not_113_out, not_114_out, OP1, OP0);
  and and_25 (and_25_out, OP5, not_115_out, OP3, not_116_out, OP1, OP0);
  and and_26 (and_26_out, OP5, not_117_out, not_118_out, not_119_out, not_120_out, not_121_out);
  and and_27 (and_27_out, not_122_out, not_123_out, not_124_out, not_125_out, not_126_out, not_127_out, not_128_out, not_129_out, not_130_out, not_131_out, not_132_out);
  and and_28 (and_28_out, not_133_out, not_134_out, not_135_out, not_136_out, not_137_out, not_138_out, not_139_out, not_140_out, F5);
  and and_29 (and_29_out, not_141_out, not_142_out, not_143_out, not_144_out, not_145_out, not_146_out, F1, not_147_out, not_148_out, not_149_out);
  and and_30 (and_30_out, not_150_out, not_151_out, not_152_out, not_153_out, not_154_out, not_155_out, F1, not_156_out, not_157_out, F5);
  and and_31 (BEQ, not_158_out, not_159_out, not_160_out, OP2, not_161_out, not_162_out);
  and and_32 (BNE, not_163_out, not_164_out, not_165_out, OP2, not_166_out, OP0);
  and and_33 (JR, not_167_out, not_168_out, not_169_out, not_170_out, not_171_out, not_172_out, not_173_out, not_174_out, not_175_out, F3, not_176_out, not_177_out);
  and and_34 (and_34_out, not_178_out, not_179_out, not_180_out, not_181_out, not_182_out, not_183_out, not_184_out, not_185_out, F3, not_186_out, not_187_out);
  and and_35 (and_35_out, OP1, not_188_out, not_189_out, not_190_out, not_191_out);
  and and_36 (JAL, OP0, OP1, not_192_out, not_193_out, not_194_out, not_195_out);
  or or_1 (MemToReg, and_1_out, and_2_out);
  or or_2 (ALU_SRC, and_6_out, and_7_out, and_8_out, and_9_out);
  or or_3 (RegWrite, and_10_out, and_11_out, and_12_out, and_13_out, and_14_out, and_15_out, and_16_out, and_17_out);
  or or_4 (SignedExt, and_19_out, and_20_out, and_21_out, and_22_out, and_23_out, and_24_out, and_25_out, and_26_out);
  or or_5 (RegDst, and_27_out, and_28_out, and_29_out, and_30_out);
  or or_6 (JUMP, and_34_out, and_35_out);
endmodule

// ALU
module MIPS_ALU (
  input  [4:0] shamt,
  input  [31:0] X,
  input  [31:0] Y,
  input  [3:0] AluOP,
  output Equal,
  output [31:0] Result,
  output [31:0] Result_2,
  output BLEZ
);

  wire comparator_3_eq, comparator_3_lt;
  wire [0:0] comparator_1_lt, comparator_2_lt;
  wire [31:0] adder_1_out, AND_out, divider_1_out, divider_1_rem, multiplier_1_cout, multiplier_1_out,
       NOR_out, OR_out, shifter_1_out, shifter_2_out, shifter_3_out, subtractor_1_out, XOR_out;

  assign AND_out = X & Y;  // AND_Gate AND, 32 bits wide
  assign OR_out = X | Y;  // OR_Gate OR, 32 bits wide
  Shifter #(.width(32), .shift("ll")) shifter_1 (.in(Y), .\dist (shamt), .out(shifter_1_out));
  Shifter #(.width(32), .shift("ar")) shifter_2 (.in(Y), .\dist (shamt), .out(shifter_2_out));
  Shifter #(.width(32), .shift("lr")) shifter_3 (.in(Y), .\dist (shamt), .out(shifter_3_out));
  Multiplier #(.width(32)) multiplier_1 (.a(X), .b(Y), .out(multiplier_1_out), .cout(multiplier_1_cout));  // open: cin
  Divider #(.width(32)) divider_1 (.a(X), .b(Y), .out(divider_1_out), .rem(divider_1_rem));  // open: upper
  Adder #(.width(32)) adder_1 (.a(X), .b(Y), .out(adder_1_out));  // open: cin, cout
  Subtractor #(.width(32)) subtractor_1 (.a(X), .b(Y), .out(subtractor_1_out));  // open: bin, bout
  assign XOR_out = X ^ Y;  // XOR_Gate XOR, 32 bits wide
  assign NOR_out = ~(X | Y);  // NOR_Gate NOR, 32 bits wide
  Comparator #(.width(32), .mode("twosComplement")) comparator_1 (
    .a(X), .b(Y), .eq(Equal), .lt(comparator_1_lt[0]));  // open: gt
  Comparator #(.width(32), .mode("unsigned")) comparator_2 (.a(X), .b(Y), .lt(comparator_2_lt[0]));  // open: gt, eq
  Comparator #(.width(32), .mode("twosComplement")) comparator_3 (
    .a(X), .b({32{1'b0}}), .eq(comparator_3_eq), .lt(comparator_3_lt));  // open: gt
  or or_2 (BLEZ, comparator_3_eq, comparator_3_lt);
  Multiplexer #(.select(4), .width(32), .disabled("Z"), .enable("false")) multiplexer_1 (
    .in0(shifter_1_out), .in1(shifter_2_out), .in2(shifter_3_out), .in3(multiplier_1_out),
    .in4(divider_1_out), .in5(adder_1_out), .in6(subtractor_1_out), .in7(AND_out), .in8(OR_out),
    .in9(XOR_out), .in10(NOR_out), .in11({{31{1'b0}}, comparator_1_lt[0]}),
    .in12({{31{1'b0}}, comparator_2_lt[0]}), .in13({32{1'b0}}), .in14({32{1'b0}}), .in15({32{1'b0}}),
    .out(Result), .sel(AluOP));
  Multiplexer #(.select(4), .width(32), .disabled("Z"), .enable("false")) multiplexer_2 (
    .in0({32{1'b0}}), .in1({32{1'b0}}), .in2({32{1'b0}}), .in3(multiplier_1_cout), .in4(divider_1_rem),
    .in5({32{1'b0}}), .in6({32{1'b0}}), .in7({32{1'b0}}), .in8({32{1'b0}}), .in9({32{1'b0}}),
    .in10({32{1'b0}}), .in11({32{1'b0}}), .in12({32{1'b0}}), .in13({32{1'b0}}), .in14({32{1'b0}}),
    .in15({32{1'b0}}), .out(Result_2), .sel(AluOP));

  // Other names for the same wires on the sheet: Result2[31:0] = Result_2; S[3:0] = AluOP

  // Notes on the sheet:
  //   不要改变此引脚区域内容，也不要改变ALU封装形式
  //   输入引脚
  //   输出引脚
endmodule

module MIPS_Regifile (
  input  [31:0] Din,
  input  Clk,
  input  WE,
  input  [4:0] R1_num,
  input  [4:0] W_num,
  input  [4:0] R2_num,
  output [31:0] R1,
  output [31:0] R2
);

  // RegisterFile registerfile_1: pin names not known; wires that end beside it: Din, Clk, WE, W_num, R1_num, R2_num, R1, R2
endmodule

module \理想流水线  (
);

  wire CLK, Go, IR1, IR2, IR3, not_1_out, RST, Syscall, W1, W2, W3, \单周期硬布线控制器_1_alu_src ,
       \单周期硬布线控制器_1_memtoreg , \单周期硬布线控制器_1_memwrite , \单周期硬布线控制器_1_regdst , \单周期硬布线控制器_1_regwrite ,
       \流水接口_2_alusrcb_2 , \流水接口_2_memchoose_2 , \流水接口_2_memwrite_2 , \流水接口_2_regdst_2 , \流水接口_2_regwrite_2 ,
       \流水接口_3_memchoose_2 , \流水接口_3_memwrite_2 , \流水接口_3_regdst_2 , \流水接口_3_regwrite_2 ,
       \流水接口_4_memchoose_2 , \流水接口_4_regdst_2 , \流水接口_4_regwrite_2 ;
  wire [3:0] \单周期硬布线控制器_1_alu_op , \流水接口_2_aluop_2 ;
  wire [4:0] multiplexer_1_out;
  wire [15:0] \LoadUse次数 , \总周期数 , \插入气泡数 , \无条件分支数 , \条件分支成功数 ;
  wire [31:0] bit_extender_1_out, EX_PC, ID_PC, IF_PC, LedData, MEM_PC, mips_alu_1_p5, mips_regifile_1_r1,
       mips_regifile_1_r2, multiplexer_2_out, multiplexer_3_out, PC_q, ram_1_data, rom_1_data, WB_PC,
       \流水接口_1_ir_2 , \流水接口_2_a_2 , \流水接口_2_b_2 , \流水接口_2_imm_2 , \流水接口_2_ir_2 , \流水接口_3_a_2 , \流水接口_3_b_2 ,
       \流水接口_3_ir_2 , \流水接口_4_a_2 , \流水接口_4_b_2 , \流水接口_4_ir_2 ;

  Button \u_总复位  (.out(RST));
  Button _1 (.out(IR1));
  Button _2 (.out(IR2));
  Button _3 (.out(IR3));
  Button \u_继续运行  (.out(Go));
  LED #(.active("true")) led_1 (.in(W1));
  LED #(.active("true")) led_2 (.in(W2));
  LED #(.active("true")) led_3 (.in(W3));
  not not_1 (not_1_out, Syscall);
  Hex_Digit_Display hex_digit_display_1 (.value(LedData[31:28]));  // open: dp
  Counter #(.width(16), .max('hffff), .ongoal("wrap"), .trigger("rising"), .behavior("old")) counter_1 (
    .D({16{1'b0}}), .count(not_1_out), .Q(\总周期数 ), .clk(CLK), .clr(RST));  // open: load, carry, preset
  Register #(.width(32), .trigger("rising"), .Select("low")) PC (
    .D(IF_PC), .en(not_1_out), .Q(PC_q), .clk(CLK), .clr(RST));
  Hex_Digit_Display hex_digit_display_2 (.value(LedData[23:20]));  // open: dp
  Hex_Digit_Display hex_digit_display_3 (.value(LedData[27:24]));  // open: dp
  Adder #(.width(32)) adder_1 (.a(PC_q), .b(32'h4), .out(IF_PC), .cin(1'b0));  // open: cout
  Hex_Digit_Display hex_digit_display_4 (.value(LedData[15:12]));  // open: dp
  Hex_Digit_Display hex_digit_display_5 (.value(LedData[19:16]));  // open: dp
  ROM #(.addrWidth(10), .dataWidth(32), .Select("high")) rom_1 (.addr(PC_q[11:2]), .data(rom_1_data));
  Hex_Digit_Display hex_digit_display_6 (.value(LedData[11:8]));  // open: dp
  Hex_Digit_Display hex_digit_display_7 (.value(LedData[7:4]));  // open: dp
  Clock #(.highDuration(1), .lowDuration(1)) clock_1 (.out(CLK));
  \流水接口  \u_流水接口_1  (
    .IR(rom_1_data), .PC(IF_PC), .CLK(CLK), .IR_2(\流水接口_1_ir_2 ), .PC_2(ID_PC), .\同步清零_高电平有效 (RST),
    .\使能端_低电平有效 (Syscall));  // open: regdst, regwrite, memchoose, memwrite, aluop, alusrcb, A, B, IMM, regdst_2, regwrite_2, memchoose_2, memwrite_2, aluop_2, alusrcb_2, A_2, B_2, IMM_2
  Hex_Digit_Display hex_digit_display_8 (.value(LedData[3:0]));  // open: dp
  \单周期硬布线控制器  \u_单周期硬布线控制器_1  (
    .Func(\流水接口_1_ir_2 [5:0]), .OP(\流水接口_1_ir_2 [31:26]), .ALU_OP(\单周期硬布线控制器_1_alu_op ),
    .MemToReg(\单周期硬布线控制器_1_memtoreg ), .MemWrite(\单周期硬布线控制器_1_memwrite ), .ALU_SRC(\单周期硬布线控制器_1_alu_src ),
    .RegWrite(\单周期硬布线控制器_1_regwrite ), .RegDst(\单周期硬布线控制器_1_regdst ));  // open: SysCALL, SignedExt, JR, JMP, Beq, JAL, Bne, BLEZ, LB
  Multiplexer #(.select(1), .width(5), .disabled("Z"), .enable("false")) multiplexer_1 (
    .in0(\流水接口_4_ir_2 [20:16]), .in1(\流水接口_4_ir_2 [15:11]), .out(multiplexer_1_out), .sel(\流水接口_4_regdst_2 ));
  assign bit_extender_1_out = {{16{\流水接口_1_ir_2 [15]}}, \流水接口_1_ir_2 [15:0]};  // Bit_Extender bit_extender_1
  // Probe on \总周期数 
  // Probe on \无条件分支数 
  // Probe on \条件分支成功数 
  // Probe on \插入气泡数 
  // Probe on \LoadUse次数 
  // Probe on IF_PC[11:0]
  MIPS_Regifile mips_regifile_1 (
    .Din(multiplexer_3_out), .Clk(CLK), .R1(mips_regifile_1_r1), .R2(mips_regifile_1_r2),
    .WE(\流水接口_4_regwrite_2 ), .W_num(multiplexer_1_out), .R1_num(\流水接口_1_ir_2 [25:21]),
    .R2_num(\流水接口_1_ir_2 [20:16]));
  // Probe on ID_PC[11:0]
  // Probe on EX_PC[11:0]
  \流水接口  \u_流水接口_2  (
    .regdst(\单周期硬布线控制器_1_regdst ), .regwrite(\单周期硬布线控制器_1_regwrite ), .memchoose(\单周期硬布线控制器_1_memtoreg ),
    .memwrite(\单周期硬布线控制器_1_memwrite ), .aluop(\单周期硬布线控制器_1_alu_op ), .alusrcb(\单周期硬布线控制器_1_alu_src ),
    .A(mips_regifile_1_r1), .B(mips_regifile_1_r2), .IR(\流水接口_1_ir_2 ), .IMM(bit_extender_1_out), .PC(ID_PC),
    .CLK(CLK), .regdst_2(\流水接口_2_regdst_2 ), .regwrite_2(\流水接口_2_regwrite_2 ),
    .memchoose_2(\流水接口_2_memchoose_2 ), .memwrite_2(\流水接口_2_memwrite_2 ), .aluop_2(\流水接口_2_aluop_2 ),
    .alusrcb_2(\流水接口_2_alusrcb_2 ), .A_2(\流水接口_2_a_2 ), .B_2(\流水接口_2_b_2 ), .IR_2(\流水接口_2_ir_2 ),
    .IMM_2(\流水接口_2_imm_2 ), .PC_2(EX_PC), .\同步清零_高电平有效 (RST), .\使能端_低电平有效 (Syscall));
  // Probe on MEM_PC[11:0]
  Multiplexer #(.select(1), .width(32), .disabled("Z"), .enable("false")) multiplexer_2 (
    .in0(\流水接口_2_b_2 ), .in1(\流水接口_2_imm_2 ), .out(multiplexer_2_out), .sel(\流水接口_2_alusrcb_2 ));
  // Probe on WB_PC[11:0]
  // MIPS_ALU mips_alu_1: pin names not known; wires that end beside it: \流水接口_2_a_2 , multiplexer_2_out, \流水接口_2_aluop_2 , {5{1'b0}}, mips_alu_1_p5
  \流水接口  \u_流水接口_3  (
    .regdst(\流水接口_2_regdst_2 ), .regwrite(\流水接口_2_regwrite_2 ), .memchoose(\流水接口_2_memchoose_2 ),
    .memwrite(\流水接口_2_memwrite_2 ), .A(mips_alu_1_p5), .B(\流水接口_2_b_2 ), .IR(\流水接口_2_ir_2 ), .PC(EX_PC),
    .CLK(CLK), .regdst_2(\流水接口_3_regdst_2 ), .regwrite_2(\流水接口_3_regwrite_2 ),
    .memchoose_2(\流水接口_3_memchoose_2 ), .memwrite_2(\流水接口_3_memwrite_2 ), .A_2(\流水接口_3_a_2 ),
    .B_2(\流水接口_3_b_2 ), .IR_2(\流水接口_3_ir_2 ), .PC_2(MEM_PC), .\同步清零_高电平有效 (RST), .\使能端_低电平有效 (Syscall));  // open: aluop, alusrcb, IMM, aluop_2, alusrcb_2, IMM_2
  \流水接口  \u_流水接口_4  (
    .regdst(\流水接口_3_regdst_2 ), .regwrite(\流水接口_3_regwrite_2 ), .memchoose(\流水接口_3_memchoose_2 ),
    .A(\流水接口_3_a_2 ), .B(ram_1_data), .IR(\流水接口_3_ir_2 ), .PC(MEM_PC), .CLK(CLK),
    .regdst_2(\流水接口_4_regdst_2 ), .regwrite_2(\流水接口_4_regwrite_2 ), .memchoose_2(\流水接口_4_memchoose_2 ),
    .A_2(\流水接口_4_a_2 ), .B_2(\流水接口_4_b_2 ), .IR_2(\流水接口_4_ir_2 ), .PC_2(WB_PC), .\同步清零_高电平有效 (RST),
    .\使能端_低电平有效 (Syscall));  // open: memwrite, aluop, alusrcb, IMM, memwrite_2, aluop_2, alusrcb_2, IMM_2
  RAM #(.addrWidth(10), .dataWidth(32), .bus("separate"), .Select("high")) ram_1 (
    .addr(\流水接口_3_a_2 [11:2]), .din(\流水接口_3_b_2 ), .data(ram_1_data), .str(\流水接口_3_memwrite_2 ), .sel(1'b1),
    .clk(CLK), .clr(RST));  // open: ld
  Multiplexer #(.select(1), .width(32), .disabled("Z"), .enable("false")) multiplexer_3 (
    .in0(\流水接口_4_a_2 ), .in1(\流水接口_4_b_2 ), .out(multiplexer_3_out), .sel(\流水接口_4_memchoose_2 ));
  Comparator #(.width(32), .mode("twosComplement")) comparator_1 (
    .a(\流水接口_4_ir_2 ), .b(32'hc), .eq(Syscall));  // open: gt, lt

  // Notes on the sheet:
  //   中断源
  //   中断等待指示
  //   数码管输出
  //   指令存储器
  //   contents of rom_1 (hex, n*v repeats v):
  //   20100000 20110000 20120000 20130000 36100000 36310001 36520002 36730003 ae100000 ae110004 ae120008
  //   ae13000c 2002000a 20110000 20120000 20130000 c
  //   OP
  //   Func
  //   rs
  //   rt
  //   rd
  //   RegDst
  //   MemToReg
  //   MemWrite
  //   AluOP
  //   AluSrcB
  //   RegWrite
  //   流水调试日志用
endmodule

module \气泡流水线  (
  output RegWrite,
  output MemWrite,
  output [31:0] PC,
  output [31:0] IR,
  output [31:0] RDin,
  output [31:0] MDin
);

  wire and_1_out, and_4_out, and_5_out, and_6_out, CLK, comparator_1_eq, EXBranch, Go, IR1, IR2, IR3, jal,
       JMP, JR, mips_alu_1_blez, mips_alu_1_equal, not_1_out, not_2_out, not_3_out, not_4_out, not_5_out,
       or_1_out, or_2_out, or_3_out, \output , regdst, relative, SignedExt, stop, Syscall, W1, W2, W3,
       \单周期硬布线控制器_1_alu_src , \单周期硬布线控制器_1_beq , \单周期硬布线控制器_1_blez , \单周期硬布线控制器_1_bne , \单周期硬布线控制器_1_jmp ,
       \单周期硬布线控制器_1_jr , \单周期硬布线控制器_1_lb , \单周期硬布线控制器_1_memtoreg , \单周期硬布线控制器_1_memwrite ,
       \单周期硬布线控制器_1_regwrite , \单周期硬布线控制器_1_syscall , \流水接口2_2_alusrcb_2 , \流水接口2_2_beq_2 , \流水接口2_2_blez_2 ,
       \流水接口2_2_bne_2 , \流水接口2_2_jal_2 , \流水接口2_2_lb_2 , \流水接口2_2_memchoose_2 , \流水接口2_2_memwrite_2 ,
       \流水接口2_2_regdst_2 , \流水接口2_2_regwrite_2 , \流水接口2_3_jal_2 , \流水接口2_3_lb_2 , \流水接口2_3_memchoose_2 ,
       \流水接口2_3_regdst_2 , \流水接口2_3_regwrite_2 , \流水接口2_4_jal_2 , \流水接口2_4_lb_2 , \流水接口2_4_memchoose_2 ,
       \流水接口2_4_regdst_2 , \源寄存器使用情况_1_r1used , \源寄存器使用情况_1_r2used ;
  wire [3:0] \单周期硬布线控制器_1_alu_op , \流水接口2_2_aluop_2 ;
  wire [4:0] multiplexer_3_out, multiplexer_4_out, multiplexer_5_out, multiplexer_6_out, multiplexer_7_out,
       multiplexer_8_out, \流水接口2_2_shamt_2 , \流水接口2_2_writereg_2 , \流水接口2_3_writereg_2 ;
  wire [7:0] multiplexer_11_out;
  wire [15:0] imm16_t, \总周期数 , \插入气泡数 ;
  wire [27:0] \流水接口2_2_pc_2 ;
  wire [31:0] a0, adder_2_out, bit_extender_1_out, bit_extender_2_out, bit_extender_3_out,
       bit_extender_4_out, controlled_buffer_1_out, IMM16, JMP_PC, JR_PC, LedData, mips_alu_1_result,
       mips_regifile_1_r1, mips_regifile_1_r2, multiplexer_1_out, multiplexer_2_out, multiplexer_10_out,
       multiplexer_12_out, multiplexer_13_out, PC_q, ram_1_data, shifter_2_out, v0, \流水接口2_1_pc_2 ,
       \流水接口2_2_a_2 , \流水接口2_2_b_2 , \流水接口2_2_b_prime_2 , \流水接口2_2_imm2_2 , \流水接口2_2_imm_2 , \流水接口2_2_ir_2 ,
       \流水接口2_3_a_2 , \流水接口2_3_a_prime_2 , \流水接口2_3_b_prime_2 , \流水接口2_3_ir_2 , \流水接口2_3_pc_2 ,
       \流水接口2_4_a_2 , \流水接口2_4_b_2 , \流水接口2_4_ir_2 , \流水接口2_4_pc_2 ;
  wire [31:16] \流水接口2_1_ir_2 ;
  wire [31:28] shifter_1_out;

  Clock #(.highDuration(1), .lowDuration(1)) clock_1 (.out(CLK));
  Button _1 (.out(IR1));
  Button _2 (.out(IR2));
  Button _3 (.out(IR3));
  Multiplexer #(.select(1), .width(32), .disabled("Z"), .enable("false")) multiplexer_1 (
    .in0(PC), .in1(adder_2_out), .out(multiplexer_1_out), .sel(EXBranch));
  Button \u_继续运行  (.out(Go));
  LED #(.active("true")) led_1 (.in(W1));
  LED #(.active("true")) led_2 (.in(W2));
  LED #(.active("true")) led_3 (.in(W3));
  Hex_Digit_Display hex_digit_display_1 (.value(LedData[31:28]));  // open: dp
  not not_1 (not_1_out, stop);
  Multiplexer #(.select(2), .width(32), .disabled("Z"), .enable("false")) multiplexer_2 (
    .in0(multiplexer_1_out), .in1(JMP_PC), .in2(JR_PC), .in3(JR_PC), .out(multiplexer_2_out), .sel({JR, JMP}));
  not not_2 (not_2_out, or_1_out);
  or or_1 (or_1_out, relative, stop);
  Comparator #(.width(32), .mode("twosComplement")) comparator_1 (
    .a(v0), .b(32'h22), .eq(comparator_1_eq));  // open: gt, lt
  not not_3 (not_3_out, comparator_1_eq);
  and and_1 (and_1_out, relative, not_4_out);
  not not_4 (not_4_out, stop);
  Hex_Digit_Display hex_digit_display_2 (.value(LedData[27:24]));  // open: dp
  Hex_Digit_Display hex_digit_display_3 (.value(LedData[23:20]));  // open: dp
  Counter #(.width(16), .max('hffff), .ongoal("wrap"), .trigger("rising"), .behavior("old")) counter_1 (
    .D({16{1'b0}}), .count(not_1_out), .Q(\总周期数 ), .clk(CLK));  // open: load, carry, clr, preset
  Register #(.width(32), .trigger("rising"), .Select("low")) u_PC (
    .D(multiplexer_2_out), .en(not_2_out), .Q(PC_q), .clk(CLK));  // open: clr
  and and_2 (\output , Syscall, comparator_1_eq);
  and and_3 (stop, not_3_out, Syscall);
  Counter #(.width(16), .max('hffff), .ongoal("wrap"), .trigger("rising"), .behavior("old")) counter_2 (
    .D({16{1'b0}}), .count(and_1_out), .Q(\插入气泡数 ), .clk(CLK));  // open: load, carry, clr, preset
  Hex_Digit_Display hex_digit_display_4 (.value(LedData[15:12]));  // open: dp
  Hex_Digit_Display hex_digit_display_5 (.value(LedData[19:16]));  // open: dp
  Adder #(.width(32)) adder_1 (.a(PC_q), .b(32'h4), .out(PC), .cin(1'b0));  // open: cout
  Hex_Digit_Display hex_digit_display_6 (.value(LedData[11:8]));  // open: dp
  Hex_Digit_Display hex_digit_display_7 (.value(LedData[7:4]));  // open: dp
  // Probe on \总周期数 
  // Probe on \插入气泡数 
  or or_2 (or_2_out, JMP, EXBranch);
  assign controlled_buffer_1_out = \output  ? a0 : 32'bz;  // Controlled_Buffer controlled_buffer_1
  Hex_Digit_Display hex_digit_display_8 (.value(LedData[3:0]));  // open: dp
  \流水接口2  \u_流水接口2_1  (
    .IR(IR), .PC(PC), .CLK(CLK), .IR_2({\流水接口2_1_ir_2 , imm16_t}), .PC_2(\流水接口2_1_pc_2 ),
    .\同步清零_高电平有效 (or_2_out), .\使能端_低电平有效 (or_1_out));  // open: J, JR, JAL, BEQ, BNE, regdst, regwrite, memchoose, memwrite, aluop, alusrcb, A, B, IMM, IMM2, J_2, JR_2, JAL_2, BEQ_2, BNE_2, regdst_2, regwrite_2, memchoose_2, memwrite_2, aluop_2, alusrcb_2, A_2, B_2, IMM_2, IMM2_2, A_prime, A_prime_2, B_prime, B_prime_2, writereg, writereg_2, shamt, shamt_2, cR1, cR1_2, cR2, cR2_2, BLEZ_2, BLEZ, LB_2, LB
  ROM #(.addrWidth(10), .dataWidth(32), .Select("high")) rom_1 ();  // open: addr, data
  ROM #(.addrWidth(10), .dataWidth(32), .Select("high")) rom_2 (.addr(PC_q[11:2]), .data(IR));
  or or_3 (or_3_out, or_2_out, relative);
  Register #(.width(32), .trigger("rising"), .Select("low")) PC_2 (
    .D(controlled_buffer_1_out), .Q(LedData), .clk(CLK));  // open: en, clr
  \源寄存器使用情况  \u_源寄存器使用情况_1  (
    .OP0(\流水接口2_1_ir_2 [26]), .OP1(\流水接口2_1_ir_2 [27]), .OP2(\流水接口2_1_ir_2 [28]), .OP3(\流水接口2_1_ir_2 [29]),
    .OP4(\流水接口2_1_ir_2 [30]), .OP5(\流水接口2_1_ir_2 [31]), .F0(imm16_t[0]), .F1(imm16_t[1]), .F2(imm16_t[2]),
    .F3(imm16_t[3]), .F4(imm16_t[4]), .F5(imm16_t[5]), .R1used(\源寄存器使用情况_1_r1used ),
    .R2used(\源寄存器使用情况_1_r2used ));
  \单周期硬布线控制器  \u_单周期硬布线控制器_1  (
    .Func(imm16_t[5:0]), .OP(\流水接口2_1_ir_2 [31:26]), .ALU_OP(\单周期硬布线控制器_1_alu_op ),
    .MemToReg(\单周期硬布线控制器_1_memtoreg ), .MemWrite(\单周期硬布线控制器_1_memwrite ), .ALU_SRC(\单周期硬布线控制器_1_alu_src ),
    .RegWrite(\单周期硬布线控制器_1_regwrite ), .SysCALL(\单周期硬布线控制器_1_syscall ), .SignedExt(SignedExt),
    .RegDst(regdst), .JR(\单周期硬布线控制器_1_jr ), .JMP(\单周期硬布线控制器_1_jmp ), .Beq(\单周期硬布线控制器_1_beq ), .JAL(jal),
    .Bne(\单周期硬布线控制器_1_bne ), .BLEZ(\单周期硬布线控制器_1_blez ), .LB(\单周期硬布线控制器_1_lb ));
  Multiplexer #(.select(1), .width(5), .disabled("Z"), .enable("false")) multiplexer_3 (
    .in0(\流水接口2_1_ir_2 [25:21]), .in1(5'b00010), .out(multiplexer_3_out), .sel(\单周期硬布线控制器_1_syscall ));
  Multiplexer #(.select(1), .width(5), .disabled("Z"), .enable("false")) multiplexer_4 (
    .in0(\流水接口2_1_ir_2 [20:16]), .in1(5'b00100), .out(multiplexer_4_out), .sel(\单周期硬布线控制器_1_syscall ));
  Multiplexer #(.select(1), .width(5), .disabled("Z"), .enable("false")) multiplexer_5 (
    .in0(\流水接口2_4_ir_2 [20:16]), .in1(\流水接口2_4_ir_2 [15:11]), .out(multiplexer_5_out),
    .sel(\流水接口2_4_regdst_2 ));
  Multiplexer #(.select(1), .width(5), .disabled("Z"), .enable("false")) multiplexer_6 (
    .in0(multiplexer_5_out), .in1({5{1'b1}}), .out(multiplexer_6_out), .sel(\流水接口2_4_jal_2 ));
  assign bit_extender_1_out = {{6{\流水接口2_1_ir_2 [25]}}, {\流水接口2_1_ir_2 [25:16], imm16_t}};  // Bit_Extender bit_extender_1
  Multiplexer #(.select(1), .width(5), .disabled("Z"), .enable("false")) multiplexer_7 (
    .in0(\流水接口2_1_ir_2 [20:16]), .in1(imm16_t[15:11]), .out(multiplexer_7_out), .sel(regdst));
  Multiplexer #(.select(1), .width(5), .disabled("Z"), .enable("false")) multiplexer_8 (
    .in0(multiplexer_7_out), .in1({5{1'b1}}), .out(multiplexer_8_out), .sel(jal));
  assign bit_extender_2_out = {{16{1'b0}}, imm16_t};  // Bit_Extender bit_extender_2
  Multiplexer #(.select(1), .width(32), .disabled("Z"), .enable("false")) multiplexer_9 (
    .in0(bit_extender_2_out), .in1(bit_extender_3_out), .out(IMM16), .sel(SignedExt));
  assign bit_extender_3_out = {{16{imm16_t[15]}}, imm16_t};  // Bit_Extender bit_extender_3
  \数据相关检测逻辑  \u_数据相关检测逻辑_1  (
    .R1used(\源寄存器使用情况_1_r1used ), .EX_RegWrite(\流水接口2_2_regwrite_2 ), .R1_num(multiplexer_3_out),
    .R2_num(multiplexer_4_out), .EX_WriteReg_num(\流水接口2_2_writereg_2 ),
    .MEM_WriteReg_num(\流水接口2_3_writereg_2 ), .R2used(\源寄存器使用情况_1_r2used ),
    .MEM_RegWrite(\流水接口2_3_regwrite_2 ), .relative(relative));
  MIPS_Regifile mips_regifile_1 (
    .Din(RDin), .Clk(CLK), .R1(mips_regifile_1_r1), .R2(mips_regifile_1_r2), .WE(RegWrite),
    .W_num(multiplexer_6_out), .R1_num(multiplexer_3_out), .R2_num(multiplexer_4_out));
  \流水接口2  \u_流水接口2_2  (
    .J(\单周期硬布线控制器_1_jmp ), .JR(\单周期硬布线控制器_1_jr ), .JAL(jal), .BEQ(\单周期硬布线控制器_1_beq ),
    .BNE(\单周期硬布线控制器_1_bne ), .regdst(regdst), .regwrite(\单周期硬布线控制器_1_regwrite ),
    .memchoose(\单周期硬布线控制器_1_memtoreg ), .memwrite(\单周期硬布线控制器_1_memwrite ), .aluop(\单周期硬布线控制器_1_alu_op ),
    .alusrcb(\单周期硬布线控制器_1_alu_src ), .A(mips_regifile_1_r1), .B(mips_regifile_1_r2),
    .IR({\流水接口2_1_ir_2 , imm16_t}), .IMM(IMM16), .IMM2(bit_extender_1_out), .PC(\流水接口2_1_pc_2 ), .CLK(CLK),
    .J_2(JMP), .JR_2(JR), .JAL_2(\流水接口2_2_jal_2 ), .BEQ_2(\流水接口2_2_beq_2 ), .BNE_2(\流水接口2_2_bne_2 ),
    .regdst_2(\流水接口2_2_regdst_2 ), .regwrite_2(\流水接口2_2_regwrite_2 ), .memchoose_2(\流水接口2_2_memchoose_2 ),
    .memwrite_2(\流水接口2_2_memwrite_2 ), .aluop_2(\流水接口2_2_aluop_2 ), .alusrcb_2(\流水接口2_2_alusrcb_2 ),
    .A_2(\流水接口2_2_a_2 ), .B_2(\流水接口2_2_b_2 ), .IR_2(\流水接口2_2_ir_2 ), .IMM_2(\流水接口2_2_imm_2 ),
    .IMM2_2(\流水接口2_2_imm2_2 ), .PC_2({JMP_PC[31:28], \流水接口2_2_pc_2 }), .\同步清零_高电平有效 (or_3_out),
    .\使能端_低电平有效 (stop), .A_prime(mips_regifile_1_r1), .A_prime_2(JR_PC), .B_prime(mips_regifile_1_r2),
    .B_prime_2(\流水接口2_2_b_prime_2 ), .writereg(multiplexer_8_out), .writereg_2(\流水接口2_2_writereg_2 ),
    .shamt(imm16_t[10:6]), .shamt_2(\流水接口2_2_shamt_2 ), .BLEZ_2(\流水接口2_2_blez_2 ), .BLEZ(\单周期硬布线控制器_1_blez ),
    .LB_2(\流水接口2_2_lb_2 ), .LB(\单周期硬布线控制器_1_lb ));  // open: cR1, cR1_2, cR2, cR2_2
  and and_4 (and_4_out, \流水接口2_2_bne_2 , not_5_out);
  not not_5 (not_5_out, mips_alu_1_equal);
  Multiplexer #(.select(1), .width(32), .disabled("Z"), .enable("false")) multiplexer_10 (
    .in0(\流水接口2_2_b_2 ), .in1(\流水接口2_2_imm_2 ), .out(multiplexer_10_out), .sel(\流水接口2_2_alusrcb_2 ));
  Shifter #(.width(32), .shift("ll")) shifter_1 (
    .in(\流水接口2_2_imm2_2 ), .\dist (5'b00010), .out({shifter_1_out, JMP_PC[27:0]}));
  or or_4 (EXBranch, and_4_out, and_5_out, and_6_out);
  and and_5 (and_5_out, \流水接口2_2_beq_2 , mips_alu_1_equal);
  and and_6 (and_6_out, mips_alu_1_blez, \流水接口2_2_blez_2 );
  MIPS_ALU mips_alu_1 (
    .X(\流水接口2_2_a_2 ), .Y(multiplexer_10_out), .AluOP(\流水接口2_2_aluop_2 ), .Equal(mips_alu_1_equal),
    .Result(mips_alu_1_result), .shamt(\流水接口2_2_shamt_2 ), .BLEZ(mips_alu_1_blez));  // open: Result_2
  Shifter #(.width(32), .shift("ll")) shifter_2 (.in(\流水接口2_2_imm_2 ), .\dist (5'b00010), .out(shifter_2_out));
  \流水接口2  \u_流水接口2_3  (
    .JAL(\流水接口2_2_jal_2 ), .regdst(\流水接口2_2_regdst_2 ), .regwrite(\流水接口2_2_regwrite_2 ),
    .memchoose(\流水接口2_2_memchoose_2 ), .memwrite(\流水接口2_2_memwrite_2 ), .A(mips_alu_1_result),
    .B(\流水接口2_2_b_2 ), .IR(\流水接口2_2_ir_2 ), .PC({JMP_PC[31:28], \流水接口2_2_pc_2 }), .CLK(CLK),
    .JAL_2(\流水接口2_3_jal_2 ), .regdst_2(\流水接口2_3_regdst_2 ), .regwrite_2(\流水接口2_3_regwrite_2 ),
    .memchoose_2(\流水接口2_3_memchoose_2 ), .memwrite_2(MemWrite), .A_2(\流水接口2_3_a_2 ), .B_2(MDin),
    .IR_2(\流水接口2_3_ir_2 ), .PC_2(\流水接口2_3_pc_2 ), .\使能端_低电平有效 (stop), .A_prime(JR_PC),
    .A_prime_2(\流水接口2_3_a_prime_2 ), .B_prime(\流水接口2_2_b_prime_2 ), .B_prime_2(\流水接口2_3_b_prime_2 ),
    .writereg(\流水接口2_2_writereg_2 ), .writereg_2(\流水接口2_3_writereg_2 ), .LB_2(\流水接口2_3_lb_2 ),
    .LB(\流水接口2_2_lb_2 ));  // open: J, JR, BEQ, BNE, aluop, alusrcb, IMM, IMM2, J_2, JR_2, BEQ_2, BNE_2, aluop_2, alusrcb_2, IMM_2, IMM2_2, 同步清零_高电平有效, shamt, shamt_2, cR1, cR1_2, cR2, cR2_2, BLEZ_2, BLEZ
  Adder #(.width(32)) adder_2 (
    .a({JMP_PC[31:28], \流水接口2_2_pc_2 }), .b(shifter_2_out), .out(adder_2_out));  // open: cin, cout
  \流水接口2  \u_流水接口2_4  (
    .JAL(\流水接口2_3_jal_2 ), .regdst(\流水接口2_3_regdst_2 ), .regwrite(\流水接口2_3_regwrite_2 ),
    .memchoose(\流水接口2_3_memchoose_2 ), .A(\流水接口2_3_a_2 ), .B(ram_1_data), .IR(\流水接口2_3_ir_2 ),
    .PC(\流水接口2_3_pc_2 ), .CLK(CLK), .JAL_2(\流水接口2_4_jal_2 ), .regdst_2(\流水接口2_4_regdst_2 ),
    .regwrite_2(RegWrite), .memchoose_2(\流水接口2_4_memchoose_2 ), .A_2(\流水接口2_4_a_2 ), .B_2(\流水接口2_4_b_2 ),
    .IR_2(\流水接口2_4_ir_2 ), .PC_2(\流水接口2_4_pc_2 ), .\使能端_低电平有效 (stop), .A_prime(\流水接口2_3_a_prime_2 ),
    .A_prime_2(v0), .B_prime(\流水接口2_3_b_prime_2 ), .B_prime_2(a0), .LB_2(\流水接口2_4_lb_2 ), .LB(\流水接口2_3_lb_2 ));  // open: J, JR, BEQ, BNE, memwrite, aluop, alusrcb, IMM, IMM2, J_2, JR_2, BEQ_2, BNE_2, memwrite_2, aluop_2, alusrcb_2, IMM_2, IMM2_2, 同步清零_高电平有效, writereg, writereg_2, shamt, shamt_2, cR1, cR1_2, cR2, cR2_2, BLEZ_2, BLEZ
  RAM #(.addrWidth(10), .dataWidth(32), .bus("separate"), .Select("high")) ram_1 (
    .addr(\流水接口2_3_a_2 [11:2]), .din(MDin), .data(ram_1_data), .str(MemWrite), .sel(1'b1), .clk(CLK));  // open: ld, clr
  Multiplexer #(.select(2), .width(8), .disabled("Z"), .enable("false")) multiplexer_11 (
    .in0(\流水接口2_4_b_2 [7:0]), .in1(\流水接口2_4_b_2 [15:8]), .in2(\流水接口2_4_b_2 [23:16]),
    .in3(\流水接口2_4_b_2 [31:24]), .out(multiplexer_11_out), .sel(\流水接口2_4_a_2 [1:0]));
  assign bit_extender_4_out = {{24{multiplexer_11_out[7]}}, multiplexer_11_out};  // Bit_Extender bit_extender_4
  Multiplexer #(.select(1), .width(32), .disabled("Z"), .enable("false")) multiplexer_12 (
    .in0(\流水接口2_4_b_2 ), .in1(bit_extender_4_out), .out(multiplexer_12_out), .sel(\流水接口2_4_lb_2 ));
  Multiplexer #(.select(1), .width(32), .disabled("Z"), .enable("false")) multiplexer_13 (
    .in0(\流水接口2_4_a_2 ), .in1(multiplexer_12_out), .out(multiplexer_13_out), .sel(\流水接口2_4_memchoose_2 ));
  Multiplexer #(.select(1), .width(32), .disabled("Z"), .enable("false")) multiplexer_14 (
    .in0(multiplexer_13_out), .in1(\流水接口2_4_pc_2 ), .out(RDin), .sel(\流水接口2_4_jal_2 ));
  Comparator #(.width(32), .mode("twosComplement")) comparator_2 (
    .a(\流水接口2_4_ir_2 ), .b(32'hc), .eq(Syscall));  // open: gt, lt

  // Notes on the sheet:
  //   中断源
  //   中断等待指示
  //   数码管输出
  //   指令存储器
  //   contents of rom_1 (hex, n*v repeats v):
  //   20110004 ae310000 8e320000 2252fffc 20100000 22110001 2118020 22520004 ae500000 22310001 2118020
  //   22520004 ae500000 22310001 2118020 22520004 ae500000 22310001 2118020 22520004 ae500000 22310001
  //   2118020 22520004 ae500000 22310001 2118020 22520004 ae500000 22310001 2118020 22520004 ae500000
  //   2002000a 20100000 20100000 20100000 c
  //   contents of rom_2 (hex, n*v repeats v):
  //   20110001 8100005 20110001 20120002 20130003 8100009 20110001 20120002 20130003 810000d 20110001
  //   20120002 20130003 8100011 20110001 20120002 20130003 c1000ee 20100001 20110001 118fc0 112020
  //   20020022 c 118882 12200001 8100015 112020 20020022 c 20110001 118880 112020 20020022 c 12200001
  //   810001f 20110001 118fc0 112020 20020022 c 1188c3 112020 20020022 c 118903 112020 20020022 c 118903
  //   112020 20020022 c 118903 112020 20020022 c 118903 112020 20020022 c 118903 112020 20020022 c 118903
  //   112020 20020022 c 118903 112020 20020022 c 20100001 109fc0 139fc3 8021 2012000c 24160003 26100001
  //   3210000f 20080008 20090001 139900 2709825 132020 20020022 c 1094022 1500fff9 22100001 2018000f
  //   2188024 108700 20080008 20090001 139902 2709825 132021 20020022 c 1094022 1500fff9 108702 2c9b022
  //   12c00001 8100050 4020 1084027 84400 3508ffff 82021 20020022 c 2010ffff 20110000 ae300000 22100001
  //   22310004 ae300000 22100001 22310004 ae300000 22100001 22310004 ae300000 22100001 22310004 ae300000
  //   22100001 22310004 ae300000 22100001 22310004 ae300000 22100001 22310004 ae300000 22100001 22310004
  //   ae300000 22100001 22310004 ae300000 22100001 22310004 ae300000 22100001 22310004 ae300000 22100001
  //   22310004 ae300000 22100001 22310004 ae300000 22100001 22310004 ae300000 22100001 22310004 ae300000
  //   22100001 22310004 22100001 8020 2011003c 8e130000 8e340000 274402a 11000002 ae330000 ae140000
  //   2231fffc 1611fff8 102020 20020022 c 22100004 2011003c 1611fff2 2008ffff 20117777 112020 20020022 c
  //   200b0010 2288826 112020 20020022 c 216bffff 1560fffa 20080001 20110010 112020 20020022 c 200b0020
  //   2288823 112020 20020022 c 216bffff 1560fffa 20090000 200b0010 34118483 20120404 118c00 129400
  //   36318281 22520404 ad310000 2328820 21290004 216bffff 1560fffb 200b0020 20090000 81310000 112020
  //   20020022 c 21290001 216bffff 1560fff9 2011fff1 112020 20020022 c 22310001 1a20fffb 2002000a c
  //   2002000a c 20100000 22100001 102020 20020022 c 22100002 102020 20020022 c 22100003 102020 20020022 c
  //   22100004 102020 20020022 c 22100005 102020 20020022 c 22100006 102020 20020022 c 22100007 102020
  //   20020022 c 22100008 102020 20020022 20020022 c 3e00008
  //   rs
  //   rt
  //   rt
  //   rd
  //   shamt
  //   rt
  //   rd
  //   JMP
  //   JR
  //   OP
  //   Func
  //   Beq
  //   Bne
  //   MemToReg
  //   MemWrite
  //   AluOP
  //   AluSrcB
  //   RegWrite
  //   JAL
  //   RegDst
  //   为方便自动评测，需要输出PC，IR，寄存器文件写入端口RDin，内存写入端口MDin等信号
  //   总复位信号应将除ROM以外所有存储组件全部清零
  //   数码管输出应该用寄存器锁存，否则显示数据只能一闪而过
endmodule

module \重定向流水线  (
  output RegWrite,
  output MemWrite,
  output [31:0] PC,
  output [31:0] IR,
  output [31:0] RDin,
  output [31:0] MDin
);

  wire and_3_out, and_4_out, and_5_out, and_6_out, CLK, comparator_1_eq, EXBranch, Go, IR1, IR2, IR3, jal,
       JMP, JR, mips_alu_1_blez, mips_alu_1_equal, not_1_out, not_2_out, not_3_out, not_4_out, not_5_out,
       or_1_out, or_2_out, or_3_out, \output , regdst, relative, SignedExt, stop, Syscall, W1, W2, W3,
       \单周期硬布线控制器_1_alu_src , \单周期硬布线控制器_1_beq , \单周期硬布线控制器_1_blez , \单周期硬布线控制器_1_bne , \单周期硬布线控制器_1_jr ,
       \单周期硬布线控制器_1_lb , \单周期硬布线控制器_1_memtoreg , \单周期硬布线控制器_1_memwrite , \单周期硬布线控制器_1_regwrite ,
       \单周期硬布线控制器_1_syscall , \流水接口2_2_alusrcb_2 , \流水接口2_2_beq_2 , \流水接口2_2_blez_2 , \流水接口2_2_bne_2 ,
       \流水接口2_2_jal_2 , \流水接口2_2_lb_2 , \流水接口2_2_memchoose_2 , \流水接口2_2_memwrite_2 , \流水接口2_2_regdst_2 ,
       \流水接口2_2_regwrite_2 , \流水接口2_3_jal_2 , \流水接口2_3_lb_2 , \流水接口2_3_memchoose_2 , \流水接口2_3_regdst_2 ,
       \流水接口2_3_regwrite_2 , \流水接口2_4_jal_2 , \流水接口2_4_lb_2 , \流水接口2_4_memchoose_2 , \流水接口2_4_regdst_2 ,
       \源寄存器使用情况_1_r1used , \源寄存器使用情况_1_r2used ;
  wire [1:0] CR1, CR2, \流水接口2_2_cr1_2 , \流水接口2_2_cr2_2 ;
  wire [3:0] \单周期硬布线控制器_1_alu_op , \流水接口2_2_aluop_2 ;
  wire [4:0] multiplexer_3_out, multiplexer_4_out, multiplexer_5_out, multiplexer_6_out, multiplexer_7_out,
       multiplexer_8_out, \流水接口2_2_shamt_2 , \流水接口2_2_writereg_2 , \流水接口2_3_writereg_2 ;
  wire [5:0] \流水接口2_2_ir_2_2 ;
  wire [7:0] multiplexer_13_out;
  wire [15:0] imm16_t, \总周期数 , \插入气泡数 ;
  wire [25:0] \流水接口2_2_ir_2 ;
  wire [27:0] \流水接口2_2_pc_2 ;
  wire [31:0] A, a0, adder_2_out, ALU_1, ALU_2, B, bit_extender_1_out, bit_extender_2_out,
       bit_extender_3_out, bit_extender_4_out, controlled_buffer_1_out, EXR1, EXR2, IMM16, JMP_PC, JR_PC,
       LedData, mips_alu_1_result, mips_regifile_1_r1, mips_regifile_1_r2, multiplexer_1_out,
       multiplexer_2_out, multiplexer_11_out, multiplexer_14_out, PC_q, ram_1_data, shifter_2_out, v0, WB,
       \流水接口2_1_pc_2 , \流水接口2_2_imm2_2 , \流水接口2_2_imm_2 , \流水接口2_3_a_prime_2 , \流水接口2_3_b_prime_2 ,
       \流水接口2_3_ir_2 , \流水接口2_3_pc_2 , \流水接口2_4_b_2 , \流水接口2_4_ir_2 , \流水接口2_4_pc_2 ;
  wire [31:16] \流水接口2_1_ir_2 ;
  wire [31:28] shifter_1_out;

  Clock #(.highDuration(1), .lowDuration(1)) clock_1 (.out(CLK));
  Button _1 (.out(IR1));
  Button _2 (.out(IR2));
  Button _3 (.out(IR3));
  Multiplexer #(.select(1), .width(32), .disabled("Z"), .enable("false")) multiplexer_1 (
    .in0(PC), .in1(adder_2_out), .out(multiplexer_1_out), .sel(EXBranch));
  Button \u_继续运行  (.out(Go));
  LED #(.active("true")) led_1 (.in(W1));
  LED #(.active("true")) led_2 (.in(W2));
  LED #(.active("true")) led_3 (.in(W3));
  Hex_Digit_Display hex_digit_display_1 (.value(LedData[31:28]));  // open: dp
  not not_1 (not_1_out, stop);
  Multiplexer #(.select(2), .width(32), .disabled("Z"), .enable("false")) multiplexer_2 (
    .in0(multiplexer_1_out), .in1(JMP_PC), .in2(JR_PC), .in3(JR_PC), .out(multiplexer_2_out), .sel({JR, JMP}));
  not not_2 (not_2_out, or_1_out);
  or or_1 (or_1_out, relative, stop);
  Comparator #(.width(32), .mode("twosComplement")) comparator_1 (
    .a(v0), .b(32'h22), .eq(comparator_1_eq));  // open: gt, lt
  not not_3 (not_3_out, comparator_1_eq);
  Hex_Digit_Display hex_digit_display_2 (.value(LedData[27:24]));  // open: dp
  Hex_Digit_Display hex_digit_display_3 (.value(LedData[23:20]));  // open: dp
  Counter #(.width(16), .max('hffff), .ongoal("wrap"), .trigger("rising"), .behavior("old")) counter_1 (
    .D({16{1'b0}}), .count(not_1_out), .Q(\总周期数 ), .clk(CLK));  // open: load, carry, clr, preset
  Register #(.width(32), .trigger("rising"), .Select("low")) u_PC (
    .D(multiplexer_2_out), .en(not_2_out), .Q(PC_q), .clk(CLK));  // open: clr
  and and_1 (\output , Syscall, comparator_1_eq);
  and and_2 (stop, not_3_out, Syscall);
  and and_3 (and_3_out, relative, not_4_out);
  not not_4 (not_4_out, stop);
  Hex_Digit_Display hex_digit_display_4 (.value(LedData[19:16]));  // open: dp
  Hex_Digit_Display hex_digit_display_5 (.value(LedData[15:12]));  // open: dp
  Adder #(.width(32)) adder_1 (.a(PC_q), .b(32'h4), .out(PC), .cin(1'b0));  // open: cout
  Counter #(.width(16), .max('hffff), .ongoal("wrap"), .trigger("rising"), .behavior("old")) counter_2 (
    .D({16{1'b0}}), .count(and_3_out), .Q(\插入气泡数 ), .clk(CLK));  // open: load, carry, clr, preset
  Hex_Digit_Display hex_digit_display_6 (.value(LedData[11:8]));  // open: dp
  Hex_Digit_Display hex_digit_display_7 (.value(LedData[7:4]));  // open: dp
  // Probe on \总周期数 
  // Probe on \插入气泡数 
  or or_2 (or_2_out, JMP, EXBranch);
  assign controlled_buffer_1_out = \output  ? a0 : 32'bz;  // Controlled_Buffer controlled_buffer_1
  Hex_Digit_Display hex_digit_display_8 (.value(LedData[3:0]));  // open: dp
  \流水接口2  \u_流水接口2_1  (
    .IR(IR), .PC(PC), .CLK(CLK), .IR_2({\流水接口2_1_ir_2 , imm16_t}), .PC_2(\流水接口2_1_pc_2 ),
    .\同步清零_高电平有效 (or_2_out), .\使能端_低电平有效 (or_1_out));  // open: J, JR, JAL, BEQ, BNE, regdst, regwrite, memchoose, memwrite, aluop, alusrcb, A, B, IMM, IMM2, J_2, JR_2, JAL_2, BEQ_2, BNE_2, regdst_2, regwrite_2, memchoose_2, memwrite_2, aluop_2, alusrcb_2, A_2, B_2, IMM_2, IMM2_2, A_prime, A_prime_2, B_prime, B_prime_2, writereg, writereg_2, shamt, shamt_2, cR1, cR1_2, cR2, cR2_2, BLEZ_2, BLEZ, LB_2, LB
  ROM #(.addrWidth(10), .dataWidth(32), .Select("high")) rom_1 ();  // open: addr, data
  ROM #(.addrWidth(10), .dataWidth(32), .Select("high")) rom_2 (.addr(PC_q[11:2]), .data(IR));
  or or_3 (or_3_out, or_2_out, relative);
  Register #(.width(32), .trigger("rising"), .Select("low")) PC_2 (
    .D(controlled_buffer_1_out), .Q(LedData), .clk(CLK));  // open: en, clr
  \源寄存器使用情况  \u_源寄存器使用情况_1  (
    .OP0(\流水接口2_1_ir_2 [26]), .OP1(\流水接口2_1_ir_2 [27]), .OP2(\流水接口2_1_ir_2 [28]), .OP3(\流水接口2_1_ir_2 [29]),
    .OP4(\流水接口2_1_ir_2 [30]), .OP5(\流水接口2_1_ir_2 [31]), .F0(imm16_t[0]), .F1(imm16_t[1]), .F2(imm16_t[2]),
    .F3(imm16_t[3]), .F4(imm16_t[4]), .F5(imm16_t[5]), .R1used(\源寄存器使用情况_1_r1used ),
    .R2used(\源寄存器使用情况_1_r2used ));
  \单周期硬布线控制器  \u_单周期硬布线控制器_1  (
    .Func(imm16_t[5:0]), .OP(\流水接口2_1_ir_2 [31:26]), .ALU_OP(\单周期硬布线控制器_1_alu_op ),
    .MemToReg(\单周期硬布线控制器_1_memtoreg ), .MemWrite(\单周期硬布线控制器_1_memwrite ), .ALU_SRC(\单周期硬布线控制器_1_alu_src ),
    .RegWrite(\单周期硬布线控制器_1_regwrite ), .SysCALL(\单周期硬布线控制器_1_syscall ), .SignedExt(SignedExt),
    .RegDst(regdst), .JR(\单周期硬布线控制器_1_jr ), .JMP(\单周期硬布线控制器_1_jr ), .Beq(\单周期硬布线控制器_1_beq ), .JAL(jal),
    .Bne(\单周期硬布线控制器_1_bne ), .BLEZ(\单周期硬布线控制器_1_blez ), .LB(\单周期硬布线控制器_1_lb ));
  Multiplexer #(.select(1), .width(5), .disabled("Z"), .enable("false")) multiplexer_3 (
    .in0(\流水接口2_1_ir_2 [25:21]), .in1(5'b00010), .out(multiplexer_3_out), .sel(\单周期硬布线控制器_1_syscall ));
  Multiplexer #(.select(1), .width(5), .disabled("Z"), .enable("false")) multiplexer_4 (
    .in0(\流水接口2_1_ir_2 [20:16]), .in1(5'b00100), .out(multiplexer_4_out), .sel(\单周期硬布线控制器_1_syscall ));
  Multiplexer #(.select(1), .width(5), .disabled("Z"), .enable("false")) multiplexer_5 (
    .in0(\流水接口2_4_ir_2 [20:16]), .in1(\流水接口2_4_ir_2 [15:11]), .out(multiplexer_5_out),
    .sel(\流水接口2_4_regdst_2 ));
  Multiplexer #(.select(1), .width(5), .disabled("Z"), .enable("false")) multiplexer_6 (
    .in0(multiplexer_5_out), .in1({5{1'b1}}), .out(multiplexer_6_out), .sel(\流水接口2_4_jal_2 ));
  assign bit_extender_1_out = {{6{\流水接口2_1_ir_2 [25]}}, {\流水接口2_1_ir_2 [25:16], imm16_t}};  // Bit_Extender bit_extender_1
  Multiplexer #(.select(1), .width(5), .disabled("Z"), .enable("false")) multiplexer_7 (
    .in0(\流水接口2_1_ir_2 [20:16]), .in1(imm16_t[15:11]), .out(multiplexer_7_out), .sel(regdst));
  Multiplexer #(.select(1), .width(5), .disabled("Z"), .enable("false")) multiplexer_8 (
    .in0(multiplexer_7_out), .in1({5{1'b1}}), .out(multiplexer_8_out), .sel(jal));
  assign bit_extender_2_out = {{16{1'b0}}, imm16_t};  // Bit_Extender bit_extender_2
  assign bit_extender_3_out = {{16{imm16_t[15]}}, imm16_t};  // Bit_Extender bit_extender_3
  Multiplexer #(.select(1), .width(32), .disabled("Z"), .enable("false")) multiplexer_9 (
    .in0(bit_extender_2_out), .in1(bit_extender_3_out), .out(IMM16), .sel(SignedExt));
  \重定向逻辑信号  \u_重定向逻辑信号_1  (
    .R1used(\源寄存器使用情况_1_r1used ), .EX_RegWrite(\流水接口2_2_regwrite_2 ), .R1_num(multiplexer_3_out),
    .R2_num(multiplexer_4_out), .EX_WriteReg_num(\流水接口2_2_writereg_2 ),
    .MEM_WriteReg_num(\流水接口2_3_writereg_2 ), .R2used(\源寄存器使用情况_1_r2used ),
    .MEM_RegWrite(\流水接口2_3_regwrite_2 ), .OP(\流水接口2_3_ir_2 [31:26]), .ChooseR1(CR1), .ChooseR2(CR2));
  MIPS_Regifile mips_regifile_1 (
    .Din(RDin), .Clk(CLK), .R1(mips_regifile_1_r1), .R2(mips_regifile_1_r2), .WE(RegWrite),
    .W_num(multiplexer_6_out), .R1_num(multiplexer_3_out), .R2_num(multiplexer_4_out));
  \流水接口2  \u_流水接口2_2  (
    .J(\单周期硬布线控制器_1_jr ), .JR(\单周期硬布线控制器_1_jr ), .JAL(jal), .BEQ(\单周期硬布线控制器_1_beq ), .BNE(\单周期硬布线控制器_1_bne ),
    .regdst(regdst), .regwrite(\单周期硬布线控制器_1_regwrite ), .memchoose(\单周期硬布线控制器_1_memtoreg ),
    .memwrite(\单周期硬布线控制器_1_memwrite ), .aluop(\单周期硬布线控制器_1_alu_op ), .alusrcb(\单周期硬布线控制器_1_alu_src ),
    .A(mips_regifile_1_r1), .B(mips_regifile_1_r2), .IR({\流水接口2_1_ir_2 , imm16_t}), .IMM(IMM16),
    .IMM2(bit_extender_1_out), .PC(\流水接口2_1_pc_2 ), .CLK(CLK), .J_2(JMP), .JR_2(JR), .JAL_2(\流水接口2_2_jal_2 ),
    .BEQ_2(\流水接口2_2_beq_2 ), .BNE_2(\流水接口2_2_bne_2 ), .regdst_2(\流水接口2_2_regdst_2 ),
    .regwrite_2(\流水接口2_2_regwrite_2 ), .memchoose_2(\流水接口2_2_memchoose_2 ),
    .memwrite_2(\流水接口2_2_memwrite_2 ), .aluop_2(\流水接口2_2_aluop_2 ), .alusrcb_2(\流水接口2_2_alusrcb_2 ),
    .A_2(EXR1), .B_2(EXR2), .IR_2({\流水接口2_2_ir_2_2 , \流水接口2_2_ir_2 }), .IMM_2(\流水接口2_2_imm_2 ),
    .IMM2_2(\流水接口2_2_imm2_2 ), .PC_2({JMP_PC[31:28], \流水接口2_2_pc_2 }), .\同步清零_高电平有效 (or_3_out),
    .\使能端_低电平有效 (stop), .A_prime(mips_regifile_1_r1), .A_prime_2(JR_PC), .B_prime(mips_regifile_1_r2),
    .writereg(multiplexer_8_out), .writereg_2(\流水接口2_2_writereg_2 ), .shamt(imm16_t[10:6]),
    .shamt_2(\流水接口2_2_shamt_2 ), .cR1(CR1), .cR1_2(\流水接口2_2_cr1_2 ), .cR2(CR2), .cR2_2(\流水接口2_2_cr2_2 ),
    .BLEZ_2(\流水接口2_2_blez_2 ), .BLEZ(\单周期硬布线控制器_1_blez ), .LB_2(\流水接口2_2_lb_2 ), .LB(\单周期硬布线控制器_1_lb ));  // open: B_prime_2
  and and_4 (and_4_out, \流水接口2_2_bne_2 , not_5_out);
  \LOAD_USE检测  \load_use检测_1  (
    .R1used(\源寄存器使用情况_1_r1used ), .EX_RegWrite(\流水接口2_2_regwrite_2 ), .R1_num(multiplexer_3_out),
    .EX_WriteReg_num(\流水接口2_2_writereg_2 ), .R2_num(multiplexer_4_out), .R2used(\源寄存器使用情况_1_r2used ),
    .OP(\流水接口2_2_ir_2_2 ), .relative(relative));
  Shifter #(.width(32), .shift("ll")) shifter_1 (
    .in(\流水接口2_2_imm2_2 ), .\dist (5'b00010), .out({shifter_1_out, JMP_PC[27:0]}));
  Multiplexer #(.select(2), .width(32), .disabled("Z"), .enable("false")) multiplexer_10 (
    .in0(EXR1), .in1(ALU_1), .in2(ALU_2), .in3(WB), .out(A), .sel(\流水接口2_2_cr1_2 ));
  or or_4 (EXBranch, and_4_out, and_5_out, and_6_out);
  and and_5 (and_5_out, \流水接口2_2_beq_2 , mips_alu_1_equal);
  not not_5 (not_5_out, mips_alu_1_equal);
  MIPS_ALU mips_alu_1 (
    .X(A), .Y(multiplexer_11_out), .AluOP(\流水接口2_2_aluop_2 ), .Equal(mips_alu_1_equal),
    .Result(mips_alu_1_result), .shamt(\流水接口2_2_shamt_2 ), .BLEZ(mips_alu_1_blez));  // open: Result_2
  Multiplexer #(.select(1), .width(32), .disabled("Z"), .enable("false")) multiplexer_11 (
    .in0(B), .in1(\流水接口2_2_imm_2 ), .out(multiplexer_11_out), .sel(\流水接口2_2_alusrcb_2 ));
  and and_6 (and_6_out, mips_alu_1_blez, \流水接口2_2_blez_2 );
  \流水接口2  \u_流水接口2_3  (
    .JAL(\流水接口2_2_jal_2 ), .regdst(\流水接口2_2_regdst_2 ), .regwrite(\流水接口2_2_regwrite_2 ),
    .memchoose(\流水接口2_2_memchoose_2 ), .memwrite(\流水接口2_2_memwrite_2 ), .A(mips_alu_1_result), .B(B),
    .IR({\流水接口2_2_ir_2_2 , \流水接口2_2_ir_2 }), .PC({JMP_PC[31:28], \流水接口2_2_pc_2 }), .CLK(CLK),
    .JAL_2(\流水接口2_3_jal_2 ), .regdst_2(\流水接口2_3_regdst_2 ), .regwrite_2(\流水接口2_3_regwrite_2 ),
    .memchoose_2(\流水接口2_3_memchoose_2 ), .memwrite_2(MemWrite), .A_2(ALU_1), .B_2(MDin),
    .IR_2(\流水接口2_3_ir_2 ), .PC_2(\流水接口2_3_pc_2 ), .\使能端_低电平有效 (stop), .A_prime(A),
    .A_prime_2(\流水接口2_3_a_prime_2 ), .B_prime(B), .B_prime_2(\流水接口2_3_b_prime_2 ),
    .writereg(\流水接口2_2_writereg_2 ), .writereg_2(\流水接口2_3_writereg_2 ), .LB_2(\流水接口2_3_lb_2 ),
    .LB(\流水接口2_2_lb_2 ));  // open: J, JR, BEQ, BNE, aluop, alusrcb, IMM, IMM2, J_2, JR_2, BEQ_2, BNE_2, aluop_2, alusrcb_2, IMM_2, IMM2_2, 同步清零_高电平有效, shamt, shamt_2, cR1, cR1_2, cR2, cR2_2, BLEZ_2, BLEZ
  Shifter #(.width(32), .shift("ll")) shifter_2 (.in(\流水接口2_2_imm_2 ), .\dist (5'b00010), .out(shifter_2_out));
  Multiplexer #(.select(2), .width(32), .disabled("Z"), .enable("false")) multiplexer_12 (
    .in0(EXR2), .in1(ALU_1), .in2(ALU_2), .in3(WB), .out(B), .sel(\流水接口2_2_cr2_2 ));
  Adder #(.width(32)) adder_2 (
    .a({JMP_PC[31:28], \流水接口2_2_pc_2 }), .b(shifter_2_out), .out(adder_2_out));  // open: cin, cout
  RAM #(.addrWidth(10), .dataWidth(32), .bus("separate"), .Select("high")) ram_1 (
    .addr(ALU_1[11:2]), .din(MDin), .data(ram_1_data), .str(MemWrite), .sel(1'b1), .clk(CLK));  // open: ld, clr
  \流水接口2  \u_流水接口2_4  (
    .JAL(\流水接口2_3_jal_2 ), .regdst(\流水接口2_3_regdst_2 ), .regwrite(\流水接口2_3_regwrite_2 ),
    .memchoose(\流水接口2_3_memchoose_2 ), .A(ALU_1), .B(ram_1_data), .IR(\流水接口2_3_ir_2 ), .PC(\流水接口2_3_pc_2 ),
    .CLK(CLK), .JAL_2(\流水接口2_4_jal_2 ), .regdst_2(\流水接口2_4_regdst_2 ), .regwrite_2(RegWrite),
    .memchoose_2(\流水接口2_4_memchoose_2 ), .A_2(ALU_2), .B_2(\流水接口2_4_b_2 ), .IR_2(\流水接口2_4_ir_2 ),
    .PC_2(\流水接口2_4_pc_2 ), .\使能端_低电平有效 (stop), .A_prime(\流水接口2_3_a_prime_2 ), .A_prime_2(v0),
    .B_prime(\流水接口2_3_b_prime_2 ), .B_prime_2(a0), .LB_2(\流水接口2_4_lb_2 ), .LB(\流水接口2_3_lb_2 ));  // open: J, JR, BEQ, BNE, memwrite, aluop, alusrcb, IMM, IMM2, J_2, JR_2, BEQ_2, BNE_2, memwrite_2, aluop_2, alusrcb_2, IMM_2, IMM2_2, 同步清零_高电平有效, writereg, writereg_2, shamt, shamt_2, cR1, cR1_2, cR2, cR2_2, BLEZ_2, BLEZ
  Multiplexer #(.select(2), .width(8), .disabled("Z"), .enable("false")) multiplexer_13 (
    .in0(\流水接口2_4_b_2 [7:0]), .in1(\流水接口2_4_b_2 [15:8]), .in2(\流水接口2_4_b_2 [23:16]),
    .in3(\流水接口2_4_b_2 [31:24]), .out(multiplexer_13_out), .sel(ALU_2[1:0]));
  assign bit_extender_4_out = {{24{multiplexer_13_out[7]}}, multiplexer_13_out};  // Bit_Extender bit_extender_4
  Multiplexer #(.select(1), .width(32), .disabled("Z"), .enable("false")) multiplexer_14 (
    .in0(ALU_2), .in1(WB), .out(multiplexer_14_out), .sel(\流水接口2_4_memchoose_2 ));
  Multiplexer #(.select(1), .width(32), .disabled("Z"), .enable("false")) multiplexer_15 (
    .in0(\流水接口2_4_b_2 ), .in1(bit_extender_4_out), .out(WB), .sel(\流水接口2_4_lb_2 ));
  Multiplexer #(.select(1), .width(32), .disabled("Z"), .enable("false")) multiplexer_16 (
    .in0(multiplexer_14_out), .in1(\流水接口2_4_pc_2 ), .out(RDin), .sel(\流水接口2_4_jal_2 ));
  Comparator #(.width(32), .mode("twosComplement")) comparator_2 (
    .a(\流水接口2_4_ir_2 ), .b(32'hc), .eq(Syscall));  // open: gt, lt

  // Notes on the sheet:
  //   中断源
  //   中断等待指示
  //   总复位信号应将除ROM以外所有存储组件全部清零
  //   数码管输出应该用寄存器锁存，否则显示数据只能一闪而过
  //   数码管输出
  //   指令存储器
  //   contents of rom_1 (hex, n*v repeats v):
  //   20110004 ae310000 8e320000 2252fffc 20100000 22110001 2118020 22520004 ae500000 22310001 2118020
  //   22520004 ae500000 22310001 2118020 22520004 ae500000 22310001 2118020 22520004 ae500000 22310001
  //   2118020 22520004 ae500000 22310001 2118020 22520004 ae500000 22310001 2118020 22520004 ae500000
  //   2002000a 20100000 20100000 20100000 c
  //   contents of rom_2 (hex, n*v repeats v):
  //   8100004 8100116 8100189 81001fc 201d00f0 20110001 810000a 20110001 20120002 20130003 810000e
  //   20110001 20120002 20130003 8100012 20110001 20120002 20130003 8100016 20110001 20120002 20130003
  //   c1000f3 20100001 20110001 118fc0 112020 20020022 c 118882 12200001 810001a 112020 20020022 c
  //   20110001 118880 112020 20020022 c 12200001 8100024 20110001 118fc0 112020 20020022 c 1188c3 112020
  //   20020022 c 118903 112020 20020022 c 118903 112020 20020022 c 118903 112020 20020022 c 118903 112020
  //   20020022 c 118903 112020 20020022 c 118903 112020 20020022 c 118903 112020 20020022 c 20100001
  //   109fc0 139fc3 8021 2012000c 24160003 26100001 3210000f 20080008 20090001 139900 2709825 132020
  //   20020022 c 1094022 1500fff9 22100001 2018000f 2188024 108700 20080008 20090001 139902 2709825 132021
  //   20020022 c 1094022 1500fff9 108702 2c9b022 12c00001 8100055 4020 1084027 84400 3508ffff 82021
  //   20020022 c 2010ffff 20110000 ae300000 22100001 22310004 ae300000 22100001 22310004 ae300000 22100001
  //   22310004 ae300000 22100001 22310004 ae300000 22100001 22310004 ae300000 22100001 22310004 ae300000
  //   22100001 22310004 ae300000 22100001 22310004 ae300000 22100001 22310004 ae300000 22100001 22310004
  //   ae300000 22100001 22310004 ae300000 22100001 22310004 ae300000 22100001 22310004 ae300000 22100001
  //   22310004 ae300000 22100001 22310004 ae300000 22100001 22310004 22100001 8020 2011003c 8e130000
  //   8e340000 274402a 11000002 ae330000 ae140000 2231fffc 1611fff8 102020 20020022 c 22100004 2011003c
  //   1611fff2 2008ffff 20117777 112020 20020022 c 200b0010 2288826 112020 20020022 c 216bffff 1560fffa
  //   20080001 20110010 112020 20020022 c 200b0020 2288823 112020 20020022 c 216bffff 1560fffa 20090000
  //   200b0010 34118483 20120404 118c00 129400 36318281 22520404 ad310000 2328820 21290004 216bffff
  //   1560fffb 200b0020 20090000 81310000 112020 20020022 c 21290001 216bffff 1560fff9 2011fff1 112020
  //   20020022 c 22310001 1a20fffb 2002000a c 2002000a c 20100000 22100001 102020 20020022 c 22100002
  //   102020 20020022 c 22100003 102020 20020022 c 22100004 102020 20020022 c 22100005 102020 20020022 c
  //   22100006 102020 20020022 c 22100007 102020 20020022 c 22100008 102020 20020022 20020022 c 3e00008
  //   23bdfffc afa10000 40047000 23bdfffc afa20000 23bdfffc afa30000 23bdfffc afa40000 23bdfffc afa50000
  //   23bdfffc afa60000 23bdfffc afa70000 23bdfffc afa80000 23bdfffc afa90000 23bdfffc afaa0000 23bdfffc
  //   afab0000 23bdfffc afac0000 23bdfffc afad0000 23bdfffc afae0000 23bdfffc afaf0000 23bdfffc afb00000
  //   23bdfffc afb10000 23bdfffc afb20000 23bdfffc afb30000 23bdfffc afb40000 23bdfffc afb50000 23bdfffc
  //   afb60000 23bdfffc afb70000 23bdfffc afb80000 23bdfffc afb90000 20160001 20140006 20150001 168020
  //   108100 2149825 132020 20020022 c 1600fffa 295a022 1680fff7 8fb90000 23bd0004 8fb80000 23bd0004
  //   8fb70000 23bd0004 8fb60000 23bd0004 8fb50000 23bd0004 8fb40000 23bd0004 8fb30000 23bd0004 8fb20000
  //   23bd0004 8fb10000 23bd0004 8fb00000 23bd0004 8faf0000 23bd0004 8fae0000 23bd0004 8fad0000 23bd0004
  //   8fac0000 23bd0004 8fab0000 23bd0004 8faa0000 23bd0004 8fa90000 23bd0004 8fa80000 23bd0004 8fa70000
  //   23bd0004 8fa60000 23bd0004 8fa50000 23bd0004 8fa40000 23bd0004 8fa30000 23bd0004 8fa20000 23bd0004
  //   40847000 8fa10000 23bd0004 42000018 23bdfffc afa10000 40047000 23bdfffc afa20000 23bdfffc afa30000
  //   23bdfffc afa40000 23bdfffc afa50000 23bdfffc afa60000 23bdfffc afa70000 23bdfffc afa80000 23bdfffc
  //   afa90000 23bdfffc afaa0000 23bdfffc afab0000 23bdfffc afac0000 23bdfffc afad0000 23bdfffc afae0000
  //   23bdfffc afaf0000 23bdfffc afb00000 23bdfffc afb10000 23bdfffc afb20000 23bdfffc afb30000 23bdfffc
  //   afb40000 23bdfffc afb50000 23bdfffc afb60000 23bdfffc afb70000 23bdfffc afb80000 23bdfffc afb90000
  //   20160002 20140006 20150001 168020 108100 2149825 132020 20020022 c 1600fffa 295a022 1680fff7
  //   8fb90000 23bd0004 8fb80000 23bd0004 8fb70000 23bd0004 8fb60000 23bd0004 8fb50000 23bd0004 8fb40000
  //   23bd0004 8fb30000 23bd0004 8fb20000 23bd0004 8fb10000 23bd0004 8fb00000 23bd0004 8faf0000 23bd0004
  //   8fae0000 23bd0004 8fad0000 23bd0004 8fac0000 23bd0004 8fab0000 23bd0004 8faa0000 23bd0004 8f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
  //   rs
  //   rt
  //   rt
  //   rd
  //   shamt
  //   rt
  //   rd
  //   JMP
  //   JR
  //   OP
  //   Func
  //   Beq
  //   Bne
  //   MemToReg
  //   MemWrite
  //   AluOP
  //   AluSrcB
  //   RegWrite
  //   JAL
  //   RegDst
  //   为方便自动评测，需要输出PC，IR，寄存器文件写入端口RDin，内存写入端口MDin等信号
endmodule

module \流水接口  (
  input  regdst,
  input  regwrite,
  input  memchoose,
  input  memwrite,
  input  [3:0] aluop,
  input  alusrcb,
  input  [31:0] A,
  input  [31:0] B,
  input  [31:0] IR,
  input  [31:0] IMM,
  input  [31:0] PC,
  input  CLK,
  input  \同步清零_高电平有效 ,
  input  \使能端_低电平有效 ,
  output regdst_2,
  output regwrite_2,
  output memchoose_2,
  output memwrite_2,
  output [3:0] aluop_2,
  output alusrcb_2,
  output [31:0] A_2,
  output [31:0] B_2,
  output [31:0] IR_2,
  output [31:0] IMM_2,
  output [31:0] PC_2
);

  wire multiplexer_1_out, multiplexer_2_out, multiplexer_3_out, multiplexer_4_out, multiplexer_6_out,
       pull_resistor_2_node;
  wire [3:0] multiplexer_5_out;
  wire [31:0] multiplexer_7_out, multiplexer_8_out, multiplexer_9_out, multiplexer_10_out, multiplexer_11_out;

  Multiplexer #(.select(1), .width(1), .disabled("Z"), .enable("false")) multiplexer_1 (
    .in0(regdst), .in1(1'b0), .out(multiplexer_1_out), .sel(\同步清零_高电平有效 ));
  Multiplexer #(.select(1), .width(1), .disabled("Z"), .enable("false")) multiplexer_2 (
    .in0(regwrite), .in1(1'b0), .out(multiplexer_2_out), .sel(\同步清零_高电平有效 ));
  Multiplexer #(.select(1), .width(1), .disabled("Z"), .enable("false")) multiplexer_3 (
    .in0(memchoose), .in1(1'b0), .out(multiplexer_3_out), .sel(\同步清零_高电平有效 ));
  Multiplexer #(.select(1), .width(1), .disabled("Z"), .enable("false")) multiplexer_4 (
    .in0(memwrite), .in1(1'b0), .out(multiplexer_4_out), .sel(\同步清零_高电平有效 ));
  Multiplexer #(.select(1), .width(4), .disabled("Z"), .enable("false")) multiplexer_5 (
    .in0(aluop), .in1(4'b0000), .out(multiplexer_5_out), .sel(\同步清零_高电平有效 ));
  Multiplexer #(.select(1), .width(1), .disabled("Z"), .enable("false")) multiplexer_6 (
    .in0(alusrcb), .in1(1'b0), .out(multiplexer_6_out), .sel(\同步清零_高电平有效 ));
  Multiplexer #(.select(1), .width(32), .disabled("Z"), .enable("false")) multiplexer_7 (
    .in0(A), .in1({32{1'b0}}), .out(multiplexer_7_out), .sel(\同步清零_高电平有效 ));
  Multiplexer #(.select(1), .width(32), .disabled("Z"), .enable("false")) multiplexer_8 (
    .in0(B), .in1({32{1'b0}}), .out(multiplexer_8_out), .sel(\同步清零_高电平有效 ));
  Multiplexer #(.select(1), .width(32), .disabled("Z"), .enable("false")) multiplexer_9 (
    .in0(IR), .in1({32{1'b0}}), .out(multiplexer_9_out), .sel(\同步清零_高电平有效 ));
  Multiplexer #(.select(1), .width(32), .disabled("Z"), .enable("false")) multiplexer_10 (
    .in0(IMM), .in1({32{1'b0}}), .out(multiplexer_10_out), .sel(\同步清零_高电平有效 ));
  Multiplexer #(.select(1), .width(32), .disabled("Z"), .enable("false")) multiplexer_11 (
    .in0(PC), .in1({32{1'b0}}), .out(multiplexer_11_out), .sel(\同步清零_高电平有效 ));
  Pull_Resistor #(.pull(0)) pull_resistor_1 (.node(\同步清零_高电平有效 ));
  Register #(.width(1), .trigger("rising"), .Select("low")) register_1 (
    .D(multiplexer_1_out), .en(pull_resistor_2_node), .Q(regdst_2), .clk(CLK));  // open: clr
  Register #(.width(1), .trigger("rising"), .Select("low")) register_2 (
    .D(multiplexer_2_out), .en(pull_resistor_2_node), .Q(regwrite_2), .clk(CLK));  // open: clr
  Register #(.width(1), .trigger("rising"), .Select("low")) register_3 (
    .D(multiplexer_3_out), .en(pull_resistor_2_node), .Q(memchoose_2), .clk(CLK));  // open: clr
  Register #(.width(1), .trigger("rising"), .Select("low")) register_4 (
    .D(multiplexer_4_out), .en(pull_resistor_2_node), .Q(memwrite_2), .clk(CLK));  // open: clr
  Register #(.width(4), .trigger("rising"), .Select("low")) register_5 (
    .D(multiplexer_5_out), .en(pull_resistor_2_node), .Q(aluop_2), .clk(CLK));  // open: clr
  Register #(.width(1), .trigger("rising"), .Select("low")) register_6 (
    .D(multiplexer_6_out), .en(pull_resistor_2_node), .Q(alusrcb_2), .clk(CLK));  // open: clr
  Register #(.width(32), .trigger("rising"), .Select("low")) register_7 (
    .D(multiplexer_7_out), .en(pull_resistor_2_node), .Q(A_2), .clk(CLK));  // open: clr
  Register #(.width(32), .trigger("rising"), .Select("low")) register_8 (
    .D(multiplexer_8_out), .en(pull_resistor_2_node), .Q(B_2), .clk(CLK));  // open: clr
  Register #(.width(32), .trigger("rising"), .Select("low")) register_9 (
    .D(multiplexer_9_out), .en(pull_resistor_2_node), .Q(IR_2), .clk(CLK));  // open: clr
  Register #(.width(32), .trigger("rising"), .Select("low")) register_10 (
    .D(multiplexer_10_out), .en(pull_resistor_2_node), .Q(IMM_2), .clk(CLK));  // open: clr
  Register #(.width(32), .trigger("rising"), .Select("low")) register_11 (
    .D(multiplexer_11_out), .en(pull_resistor_2_node), .Q(PC_2), .clk(CLK));  // open: clr
  Pull_Resistor #(.pull(0)) pull_resistor_2 (.node(pull_resistor_2_node));
  not not_1 (pull_resistor_2_node, \使能端_低电平有效 );

  // Notes on the sheet:
  //   使能端_低电平有效: pull=down
  //   同步清零_高电平有效: pull=down
  //   下拉电阻使得引脚可以悬空
endmodule
module \分支流水线  (
  output RegWrite,
  output MemWrite,
  output [31:0] PC,
  output [31:0] IR,
  output [31:0] RDin,
  output [31:0] MDin
);

  wire and_3_out, and_4_out, CLK, comparator_1_eq, EXBranch, Go, IR1, IR2, IR3, JMP, JR, mips_alu_1_equal,
       not_1_out, not_2_out, not_3_out, or_1_out, \output , SignedExt, stop, Syscall, W1, W2, W3,
       \单周期硬布线控制器_1_alu_src , \单周期硬布线控制器_1_beq , \单周期硬布线控制器_1_bne , \单周期硬布线控制器_1_jal , \单周期硬布线控制器_1_jmp ,
       \单周期硬布线控制器_1_jr , \单周期硬布线控制器_1_memtoreg , \单周期硬布线控制器_1_memwrite , \单周期硬布线控制器_1_regdst ,
       \单周期硬布线控制器_1_regwrite , \单周期硬布线控制器_1_syscall , \流水接口2_2_alusrcb_2 , \流水接口2_2_beq_2 , \流水接口2_2_bne_2 ,
       \流水接口2_2_jal_2 , \流水接口2_2_memchoose_2 , \流水接口2_2_memwrite_2 , \流水接口2_2_regdst_2 ,
       \流水接口2_2_regwrite_2 , \流水接口2_3_jal_2 , \流水接口2_3_memchoose_2 , \流水接口2_3_regdst_2 ,
       \流水接口2_3_regwrite_2 , \流水接口2_4_jal_2 , \流水接口2_4_memchoose_2 , \流水接口2_4_regdst_2 ;
  wire [3:0] \单周期硬布线控制器_1_alu_op , \流水接口2_2_aluop_2 ;
  wire [4:0] multiplexer_3_out, multiplexer_4_out, multiplexer_5_out, multiplexer_6_out;
  wire [15:0] imm16_t, \总周期数 ;
  wire [27:0] \流水接口2_2_pc_2 ;
  wire [31:0] a0, adder_2_out, bit_extender_1_out, bit_extender_2_out, bit_extender_3_out,
       controlled_buffer_1_out, IMM16, JMP_PC, JR_PC, LedData, mips_alu_1_result, mips_regifile_1_r1,
       mips_regifile_1_r2, multiplexer_1_out, multiplexer_2_out, multiplexer_8_out, multiplexer_9_out, PC_q,
       ram_1_data, shifter_2_out, v0, \流水接口2_1_pc_2 , \流水接口2_2_a_2 , \流水接口2_2_b_2 , \流水接口2_2_b_prime_2 ,
       \流水接口2_2_imm2_2 , \流水接口2_2_imm_2 , \流水接口2_2_ir_2 , \流水接口2_3_a_2 , \流水接口2_3_a_prime_2 ,
       \流水接口2_3_b_prime_2 , \流水接口2_3_ir_2 , \流水接口2_3_pc_2 , \流水接口2_4_a_2 , \流水接口2_4_b_2 , \流水接口2_4_ir_2 ,
       \流水接口2_4_pc_2 ;
  wire [31:16] \流水接口2_1_ir_2 ;
  wire [31:28] shifter_1_out;

  Clock #(.highDuration(1), .lowDuration(1)) clock_1 (.out(CLK));
  Button _1 (.out(IR1));
  Button _2 (.out(IR2));
  Button _3 (.out(IR3));
  Multiplexer #(.select(1), .width(32), .disabled("Z"), .enable("false")) multiplexer_1 (
    .in0(PC), .in1(adder_2_out), .out(multiplexer_1_out), .sel(EXBranch));
  Button \u_继续运行  (.out(Go));
  LED #(.active("true")) led_1 (.in(W1));
  LED #(.active("true")) led_2 (.in(W2));
  LED #(.active("true")) led_3 (.in(W3));
  Hex_Digit_Display hex_digit_display_1 (.value(LedData[31:28]));  // open: dp
  Multiplexer #(.select(2), .width(32), .disabled("Z"), .enable("false")) multiplexer_2 (
    .in0(multiplexer_1_out), .in1(JMP_PC), .in2(JR_PC), .in3(JR_PC), .out(multiplexer_2_out), .sel({JR, JMP}));
  not not_1 (not_1_out, stop);
  Comparator #(.width(32), .mode("twosComplement")) comparator_1 (
    .a(v0), .b(32'h22), .eq(comparator_1_eq));  // open: gt, lt
  not not_2 (not_2_out, comparator_1_eq);
  Hex_Digit_Display hex_digit_display_2 (.value(LedData[23:20]));  // open: dp
  Hex_Digit_Display hex_digit_display_3 (.value(LedData[27:24]));  // open: dp
  Counter #(.width(16), .max('hffff), .ongoal("wrap"), .trigger("rising"), .behavior("old")) counter_1 (
    .D({16{1'b0}}), .count(not_1_out), .Q(\总周期数 ), .clk(CLK));  // open: load, carry, clr, preset
  Register #(.width(32), .trigger("rising"), .Select("low")) u_PC (
    .D(multiplexer_2_out), .en(not_1_out), .Q(PC_q), .clk(CLK));  // open: clr
  and and_1 (\output , Syscall, comparator_1_eq);
  and and_2 (stop, not_2_out, Syscall);
  Hex_Digit_Display hex_digit_display_4 (.value(LedData[19:16]));  // open: dp
  Hex_Digit_Display hex_digit_display_5 (.value(LedData[15:12]));  // open: dp
  Adder #(.width(32)) adder_1 (.a(PC_q), .b(32'h4), .out(PC), .cin(1'b0));  // open: cout
  Hex_Digit_Display hex_digit_display_6 (.value(LedData[7:4]));  // open: dp
  Hex_Digit_Display hex_digit_display_7 (.value(LedData[11:8]));  // open: dp
  // Probe on \总周期数 
  assign controlled_buffer_1_out = \output  ? a0 : 32'bz;  // Controlled_Buffer controlled_buffer_1
  Hex_Digit_Display hex_digit_display_8 (.value(LedData[3:0]));  // open: dp
  \流水接口2  \u_流水接口2_1  (
    .IR(IR), .PC(PC), .CLK(CLK), .IR_2({\流水接口2_1_ir_2 , imm16_t}), .PC_2(\流水接口2_1_pc_2 ),
    .\同步清零_高电平有效 (or_1_out), .\使能端_低电平有效 (stop));  // open: J, JR, JAL, BEQ, BNE, regdst, regwrite, memchoose, memwrite, aluop, alusrcb, A, B, IMM, IMM2, J_2, JR_2, JAL_2, BEQ_2, BNE_2, regdst_2, regwrite_2, memchoose_2, memwrite_2, aluop_2, alusrcb_2, A_2, B_2, IMM_2, IMM2_2, A_prime, A_prime_2, B_prime, B_prime_2, writereg, writereg_2, shamt, shamt_2, cR1, cR1_2, cR2, cR2_2, BLEZ_2, BLEZ, LB_2, LB
  ROM #(.addrWidth(10), .dataWidth(32), .Select("high")) rom_1 (.addr(PC_q[11:2]), .data(IR));
  or or_1 (or_1_out, JMP, EXBranch);
  Register #(.width(32), .trigger("rising"), .Select("low")) PC_2 (
    .D(controlled_buffer_1_out), .Q(LedData), .clk(CLK));  // open: en, clr
  \单周期硬布线控制器  \u_单周期硬布线控制器_1  (
    .Func(imm16_t[5:0]), .OP(\流水接口2_1_ir_2 [31:26]), .ALU_OP(\单周期硬布线控制器_1_alu_op ),
    .MemToReg(\单周期硬布线控制器_1_memtoreg ), .MemWrite(\单周期硬布线控制器_1_memwrite ), .ALU_SRC(\单周期硬布线控制器_1_alu_src ),
    .RegWrite(\单周期硬布线控制器_1_regwrite ), .SysCALL(\单周期硬布线控制器_1_syscall ), .SignedExt(SignedExt),
    .RegDst(\单周期硬布线控制器_1_regdst ), .JR(\单周期硬布线控制器_1_jr ), .JMP(\单周期硬布线控制器_1_jmp ), .Beq(\单周期硬布线控制器_1_beq ),
    .JAL(\单周期硬布线控制器_1_jal ), .Bne(\单周期硬布线控制器_1_bne ));  // open: BLEZ, LB
  Multiplexer #(.select(1), .width(5), .disabled("Z"), .enable("false")) multiplexer_3 (
    .in0(\流水接口2_1_ir_2 [25:21]), .in1(5'b00010), .out(multiplexer_3_out), .sel(\单周期硬布线控制器_1_syscall ));
  Multiplexer #(.select(1), .width(5), .disabled("Z"), .enable("false")) multiplexer_4 (
    .in0(\流水接口2_1_ir_2 [20:16]), .in1(5'b00100), .out(multiplexer_4_out), .sel(\单周期硬布线控制器_1_syscall ));
  Multiplexer #(.select(1), .width(5), .disabled("Z"), .enable("false")) multiplexer_5 (
    .in0(\流水接口2_4_ir_2 [20:16]), .in1(\流水接口2_4_ir_2 [15:11]), .out(multiplexer_5_out),
    .sel(\流水接口2_4_regdst_2 ));
  Multiplexer #(.select(1), .width(5), .disabled("Z"), .enable("false")) multiplexer_6 (
    .in0(multiplexer_5_out), .in1({5{1'b1}}), .out(multiplexer_6_out), .sel(\流水接口2_4_jal_2 ));
  assign bit_extender_1_out = {{6{\流水接口2_1_ir_2 [25]}}, {\流水接口2_1_ir_2 [25:16], imm16_t}};  // Bit_Extender bit_extender_1
  assign bit_extender_2_out = {{16{1'b0}}, imm16_t};  // Bit_Extender bit_extender_2
  Multiplexer #(.select(1), .width(32), .disabled("Z"), .enable("false")) multiplexer_7 (
    .in0(bit_extender_2_out), .in1(bit_extender_3_out), .out(IMM16), .sel(SignedExt));
  assign bit_extender_3_out = {{16{imm16_t[15]}}, imm16_t};  // Bit_Extender bit_extender_3
  MIPS_Regifile mips_regifile_1 (
    .Din(RDin), .Clk(CLK), .R1(mips_regifile_1_r1), .R2(mips_regifile_1_r2), .WE(RegWrite),
    .W_num(multiplexer_6_out), .R1_num(multiplexer_3_out), .R2_num(multiplexer_4_out));
  \流水接口2  \u_流水接口2_2  (
    .J(\单周期硬布线控制器_1_jmp ), .JR(\单周期硬布线控制器_1_jr ), .JAL(\单周期硬布线控制器_1_jal ), .BEQ(\单周期硬布线控制器_1_beq ),
    .BNE(\单周期硬布线控制器_1_bne ), .regdst(\单周期硬布线控制器_1_regdst ), .regwrite(\单周期硬布线控制器_1_regwrite ),
    .memchoose(\单周期硬布线控制器_1_memtoreg ), .memwrite(\单周期硬布线控制器_1_memwrite ), .aluop(\单周期硬布线控制器_1_alu_op ),
    .alusrcb(\单周期硬布线控制器_1_alu_src ), .A(mips_regifile_1_r1), .B(mips_regifile_1_r2),
    .IR({\流水接口2_1_ir_2 , imm16_t}), .IMM(IMM16), .IMM2(bit_extender_1_out), .PC(\流水接口2_1_pc_2 ), .CLK(CLK),
    .J_2(JMP), .JR_2(JR), .JAL_2(\流水接口2_2_jal_2 ), .BEQ_2(\流水接口2_2_beq_2 ), .BNE_2(\流水接口2_2_bne_2 ),
    .regdst_2(\流水接口2_2_regdst_2 ), .regwrite_2(\流水接口2_2_regwrite_2 ), .memchoose_2(\流水接口2_2_memchoose_2 ),
    .memwrite_2(\流水接口2_2_memwrite_2 ), .aluop_2(\流水接口2_2_aluop_2 ), .alusrcb_2(\流水接口2_2_alusrcb_2 ),
    .A_2(\流水接口2_2_a_2 ), .B_2(\流水接口2_2_b_2 ), .IR_2(\流水接口2_2_ir_2 ), .IMM_2(\流水接口2_2_imm_2 ),
    .IMM2_2(\流水接口2_2_imm2_2 ), .PC_2({JMP_PC[31:28], \流水接口2_2_pc_2 }), .\同步清零_高电平有效 (or_1_out),
    .\使能端_低电平有效 (stop), .A_prime(mips_regifile_1_r1), .A_prime_2(JR_PC), .B_prime(mips_regifile_1_r2),
    .B_prime_2(\流水接口2_2_b_prime_2 ));  // open: writereg, writereg_2, shamt, shamt_2, cR1, cR1_2, cR2, cR2_2, BLEZ_2, BLEZ, LB_2, LB
  or or_2 (EXBranch, and_3_out, and_4_out);
  and and_3 (and_3_out, \流水接口2_2_bne_2 , not_3_out);
  not not_3 (not_3_out, mips_alu_1_equal);
  Multiplexer #(.select(1), .width(32), .disabled("Z"), .enable("false")) multiplexer_8 (
    .in0(\流水接口2_2_b_2 ), .in1(\流水接口2_2_imm_2 ), .out(multiplexer_8_out), .sel(\流水接口2_2_alusrcb_2 ));
  Shifter #(.width(32), .shift("ll")) shifter_1 (
    .in(\流水接口2_2_imm2_2 ), .\dist (5'b00010), .out({shifter_1_out, JMP_PC[27:0]}));
  and and_4 (and_4_out, \流水接口2_2_beq_2 , mips_alu_1_equal);
  MIPS_ALU mips_alu_1 (
    .X(\流水接口2_2_a_2 ), .Y(multiplexer_8_out), .AluOP(\流水接口2_2_aluop_2 ), .Equal(mips_alu_1_equal),
    .Result(mips_alu_1_result), .shamt({5{1'b0}}));  // open: Result_2, BLEZ
  Shifter #(.width(32), .shift("ll")) shifter_2 (.in(\流水接口2_2_imm_2 ), .\dist (5'b00010), .out(shifter_2_out));
  \流水接口2  \u_流水接口2_3  (
    .JAL(\流水接口2_2_jal_2 ), .regdst(\流水接口2_2_regdst_2 ), .regwrite(\流水接口2_2_regwrite_2 ),
    .memchoose(\流水接口2_2_memchoose_2 ), .memwrite(\流水接口2_2_memwrite_2 ), .A(mips_alu_1_result),
    .B(\流水接口2_2_b_2 ), .IR(\流水接口2_2_ir_2 ), .PC({JMP_PC[31:28], \流水接口2_2_pc_2 }), .CLK(CLK),
    .JAL_2(\流水接口2_3_jal_2 ), .regdst_2(\流水接口2_3_regdst_2 ), .regwrite_2(\流水接口2_3_regwrite_2 ),
    .memchoose_2(\流水接口2_3_memchoose_2 ), .memwrite_2(MemWrite), .A_2(\流水接口2_3_a_2 ), .B_2(MDin),
    .IR_2(\流水接口2_3_ir_2 ), .PC_2(\流水接口2_3_pc_2 ), .\使能端_低电平有效 (stop), .A_prime(JR_PC),
    .A_prime_2(\流水接口2_3_a_prime_2 ), .B_prime(\流水接口2_2_b_prime_2 ), .B_prime_2(\流水接口2_3_b_prime_2 ));  // open: J, JR, BEQ, BNE, aluop, alusrcb, IMM, IMM2, J_2, JR_2, BEQ_2, BNE_2, aluop_2, alusrcb_2, IMM_2, IMM2_2, 同步清零_高电平有效, writereg, writereg_2, shamt, shamt_2, cR1, cR1_2, cR2, cR2_2, BLEZ_2, BLEZ, LB_2, LB
  Adder #(.width(32)) adder_2 (
    .a({JMP_PC[31:28], \流水接口2_2_pc_2 }), .b(shifter_2_out), .out(adder_2_out));  // open: cin, cout
  \流水接口2  \u_流水接口2_4  (
    .JAL(\流水接口2_3_jal_2 ), .regdst(\流水接口2_3_regdst_2 ), .regwrite(\流水接口2_3_regwrite_2 ),
    .memchoose(\流水接口2_3_memchoose_2 ), .A(\流水接口2_3_a_2 ), .B(ram_1_data), .IR(\流水接口2_3_ir_2 ),
    .PC(\流水接口2_3_pc_2 ), .CLK(CLK), .JAL_2(\流水接口2_4_jal_2 ), .regdst_2(\流水接口2_4_regdst_2 ),
    .regwrite_2(RegWrite), .memchoose_2(\流水接口2_4_memchoose_2 ), .A_2(\流水接口2_4_a_2 ), .B_2(\流水接口2_4_b_2 ),
    .IR_2(\流水接口2_4_ir_2 ), .PC_2(\流水接口2_4_pc_2 ), .\使能端_低电平有效 (stop), .A_prime(\流水接口2_3_a_prime_2 ),
    .A_prime_2(v0), .B_prime(\流水接口2_3_b_prime_2 ), .B_prime_2(a0));  // open: J, JR, BEQ, BNE, memwrite, aluop, alusrcb, IMM, IMM2, J_2, JR_2, BEQ_2, BNE_2, memwrite_2, aluop_2, alusrcb_2, IMM_2, IMM2_2, 同步清零_高电平有效, writereg, writereg_2, shamt, shamt_2, cR1, cR1_2, cR2, cR2_2, BLEZ_2, BLEZ, LB_2, LB
  RAM #(.addrWidth(10), .dataWidth(32), .bus("separate"), .Select("high")) ram_1 (
    .addr(\流水接口2_3_a_2 [11:2]), .din(MDin), .data(ram_1_data), .str(MemWrite), .sel(1'b1), .clk(CLK));  // open: ld, clr
  Multiplexer #(.select(1), .width(32), .disabled("Z"), .enable("false")) multiplexer_9 (
    .in0(\流水接口2_4_a_2 ), .in1(\流水接口2_4_b_2 ), .out(multiplexer_9_out), .sel(\流水接口2_4_memchoose_2 ));
  Multiplexer #(.select(1), .width(32), .disabled("Z"), .enable("false")) multiplexer_10 (
    .in0(multiplexer_9_out), .in1(\流水接口2_4_pc_2 ), .out(RDin), .sel(\流水接口2_4_jal_2 ));
  Comparator #(.width(32), .mode("twosComplement")) comparator_2 (
    .a(\流水接口2_4_ir_2 ), .b(32'hc), .eq(Syscall));  // open: gt, lt

  // Notes on the sheet:
  //   中断源
  //   中断等待指示
  //   总复位信号应将除ROM以外所有存储组件全部清零
  //   数码管输出
  //   数码管输出应该用寄存器锁存，否则显示数据只能一闪而过
  //   指令存储器
  //   contents of rom_1 (hex, n*v repeats v):
  //   20110020 20020022 8000006 20110004 20120005 20130006 10000003 20110007 20120008 20130009 14110003
  //   2011000a 2012000b 2013000c c000014 2002000a 0 0 0 c 2231ffff 0 0 0 112020 0 0 0 c 1620fff6 3e00008
  //   rs
  //   rt
  //   rt
  //   rd
  //   JMP
  //   JR
  //   OP
  //   Func
  //   Beq
  //   Bne
  //   MemToReg
  //   MemWrite
  //   AluOP
  //   AluSrcB
  //   RegWrite
  //   JAL
  //   RegDst
  //   为方便自动评测，需要输出PC，IR，寄存器文件写入端口RDin，内存写入端口MDin等信号
endmodule

module \流水接口2  (
  input  J,
  input  JR,
  input  JAL,
  input  BEQ,
  input  BNE,
  input  regdst,
  input  regwrite,
  input  memchoose,
  input  memwrite,
  input  BLEZ,
  input  LB,
  input  [3:0] aluop,
  input  alusrcb,
  input  [31:0] A,
  input  [31:0] B,
  input  [31:0] A_prime,
  input  [31:0] B_prime,
  input  [31:0] IR,
  input  [31:0] IMM,
  input  [4:0] writereg,
  input  [4:0] shamt,
  input  [31:0] IMM2,
  input  [31:0] PC,
  input  [1:0] cR1,
  input  [1:0] cR2,
  input  CLK,
  input  \同步清零_高电平有效 ,
  input  \使能端_低电平有效 ,
  output J_2,
  output JR_2,
  output JAL_2,
  output BEQ_2,
  output BNE_2,
  output regdst_2,
  output regwrite_2,
  output memchoose_2,
  output memwrite_2,
  output BLEZ_2,
  output LB_2,
  output [3:0] aluop_2,
  output alusrcb_2,
  output [31:0] A_2,
  output [31:0] B_2,
  output [31:0] A_prime_2,
  output [31:0] B_prime_2,
  output [31:0] IR_2,
  output [31:0] IMM_2,
  output [4:0] writereg_2,
  output [4:0] shamt_2,
  output [31:0] IMM2_2,
  output [31:0] PC_2,
  output [1:0] cR1_2,
  output [1:0] cR2_2
);

  wire multiplexer_1_out, multiplexer_2_out, multiplexer_3_out, multiplexer_4_out, multiplexer_5_out,
       multiplexer_6_out, multiplexer_7_out, multiplexer_8_out, multiplexer_9_out, multiplexer_10_out,
       multiplexer_11_out, multiplexer_13_out, pull_resistor_2_node;
  wire [1:0] multiplexer_24_out, multiplexer_25_out;
  wire [3:0] multiplexer_12_out;
  wire [4:0] multiplexer_20_out, multiplexer_21_out;
  wire [31:0] multiplexer_14_out, multiplexer_15_out, multiplexer_16_out, multiplexer_17_out,
       multiplexer_18_out, multiplexer_19_out, multiplexer_22_out, multiplexer_23_out;

  Multiplexer #(.select(1), .width(1), .disabled("Z"), .enable("false")) multiplexer_1 (
    .in0(J), .in1(1'b0), .out(multiplexer_1_out), .sel(\同步清零_高电平有效 ));
  Multiplexer #(.select(1), .width(1), .disabled("Z"), .enable("false")) multiplexer_2 (
    .in0(JR), .in1(1'b0), .out(multiplexer_2_out), .sel(\同步清零_高电平有效 ));
  Multiplexer #(.select(1), .width(1), .disabled("Z"), .enable("false")) multiplexer_3 (
    .in0(JAL), .in1(1'b0), .out(multiplexer_3_out), .sel(\同步清零_高电平有效 ));
  Multiplexer #(.select(1), .width(1), .disabled("Z"), .enable("false")) multiplexer_4 (
    .in0(BEQ), .in1(1'b0), .out(multiplexer_4_out), .sel(\同步清零_高电平有效 ));
  Multiplexer #(.select(1), .width(1), .disabled("Z"), .enable("false")) multiplexer_5 (
    .in0(BNE), .in1(1'b0), .out(multiplexer_5_out), .sel(\同步清零_高电平有效 ));
  Multiplexer #(.select(1), .width(1), .disabled("Z"), .enable("false")) multiplexer_6 (
    .in0(regdst), .in1(1'b0), .out(multiplexer_6_out), .sel(\同步清零_高电平有效 ));
  Multiplexer #(.select(1), .width(1), .disabled("Z"), .enable("false")) multiplexer_7 (
    .in0(regwrite), .in1(1'b0), .out(multiplexer_7_out), .sel(\同步清零_高电平有效 ));
  Multiplexer #(.select(1), .width(1), .disabled("Z"), .enable("false")) multiplexer_8 (
    .in0(memchoose), .in1(1'b0), .out(multiplexer_8_out), .sel(\同步清零_高电平有效 ));
  Multiplexer #(.select(1), .width(1), .disabled("Z"), .enable("false")) multiplexer_9 (
    .in0(memwrite), .in1(1'b0), .out(multiplexer_9_out), .sel(\同步清零_高电平有效 ));
  Multiplexer #(.select(1), .width(1), .disabled("Z"), .enable("false")) multiplexer_10 (
    .in0(BLEZ), .in1(1'b0), .out(multiplexer_10_out), .sel(\同步清零_高电平有效 ));
  Multiplexer #(.select(1), .width(1), .disabled("Z"), .enable("false")) multiplexer_11 (
    .in0(LB), .in1(1'b0), .out(multiplexer_11_out), .sel(\同步清零_高电平有效 ));
  Multiplexer #(.select(1), .width(4), .disabled("Z"), .enable("false")) multiplexer_12 (
    .in0(aluop), .in1(4'b0000), .out(multiplexer_12_out), .sel(\同步清零_高电平有效 ));
  Multiplexer #(.select(1), .width(1), .disabled("Z"), .enable("false")) multiplexer_13 (
    .in0(alusrcb), .in1(1'b0), .out(multiplexer_13_out), .sel(\同步清零_高电平有效 ));
  Multiplexer #(.select(1), .width(32), .disabled("Z"), .enable("false")) multiplexer_14 (
    .in0(A), .in1({32{1'b0}}), .out(multiplexer_14_out), .sel(\同步清零_高电平有效 ));
  Multiplexer #(.select(1), .width(32), .disabled("Z"), .enable("false")) multiplexer_15 (
    .in0(B), .in1({32{1'b0}}), .out(multiplexer_15_out), .sel(\同步清零_高电平有效 ));
  Multiplexer #(.select(1), .width(32), .disabled("Z"), .enable("false")) multiplexer_16 (
    .in0(A_prime), .in1({32{1'b0}}), .out(multiplexer_16_out), .sel(\同步清零_高电平有效 ));
  Multiplexer #(.select(1), .width(32), .disabled("Z"), .enable("false")) multiplexer_17 (
    .in0(B_prime), .in1({32{1'b0}}), .out(multiplexer_17_out), .sel(\同步清零_高电平有效 ));
  Multiplexer #(.select(1), .width(32), .disabled("Z"), .enable("false")) multiplexer_18 (
    .in0(IR), .in1({32{1'b0}}), .out(multiplexer_18_out), .sel(\同步清零_高电平有效 ));
  Multiplexer #(.select(1), .width(32), .disabled("Z"), .enable("false")) multiplexer_19 (
    .in0(IMM), .in1({32{1'b0}}), .out(multiplexer_19_out), .sel(\同步清零_高电平有效 ));
  Multiplexer #(.select(1), .width(5), .disabled("Z"), .enable("false")) multiplexer_20 (
    .in0(writereg), .in1({5{1'b0}}), .out(multiplexer_20_out), .sel(\同步清零_高电平有效 ));
  Multiplexer #(.select(1), .width(5), .disabled("Z"), .enable("false")) multiplexer_21 (
    .in0(shamt), .in1({5{1'b0}}), .out(multiplexer_21_out), .sel(\同步清零_高电平有效 ));
  Multiplexer #(.select(1), .width(32), .disabled("Z"), .enable("false")) multiplexer_22 (
    .in0(IMM2), .in1({32{1'b0}}), .out(multiplexer_22_out), .sel(\同步清零_高电平有效 ));
  Multiplexer #(.select(1), .width(32), .disabled("Z"), .enable("false")) multiplexer_23 (
    .in0(PC), .in1({32{1'b0}}), .out(multiplexer_23_out), .sel(\同步清零_高电平有效 ));
  Multiplexer #(.select(1), .width(2), .disabled("Z"), .enable("false")) multiplexer_24 (
    .in0(cR1), .in1(2'b00), .out(multiplexer_24_out), .sel(\同步清零_高电平有效 ));
  Multiplexer #(.select(1), .width(2), .disabled("Z"), .enable("false")) multiplexer_25 (
    .in0(cR2), .in1(2'b00), .out(multiplexer_25_out), .sel(\同步清零_高电平有效 ));
  Pull_Resistor #(.pull(0)) pull_resistor_1 (.node(\同步清零_高电平有效 ));
  Register #(.width(1), .trigger("rising"), .Select("low")) register_1 (
    .D(multiplexer_1_out), .en(pull_resistor_2_node), .Q(J_2), .clk(CLK));  // open: clr
  Register #(.width(1), .trigger("rising"), .Select("low")) register_2 (
    .D(multiplexer_2_out), .en(pull_resistor_2_node), .Q(JR_2), .clk(CLK));  // open: clr
  Register #(.width(1), .trigger("rising"), .Select("low")) register_3 (
    .D(multiplexer_3_out), .en(pull_resistor_2_node), .Q(JAL_2), .clk(CLK));  // open: clr
  Register #(.width(1), .trigger("rising"), .Select("low")) register_4 (
    .D(multiplexer_4_out), .en(pull_resistor_2_node), .Q(BEQ_2), .clk(CLK));  // open: clr
  Register #(.width(1), .trigger("rising"), .Select("low")) register_5 (
    .D(multiplexer_5_out), .en(pull_resistor_2_node), .Q(BNE_2), .clk(CLK));  // open: clr
  Register #(.width(1), .trigger("rising"), .Select("low")) register_6 (
    .D(multiplexer_6_out), .en(pull_resistor_2_node), .Q(regdst_2), .clk(CLK));  // open: clr
  Register #(.width(1), .trigger("rising"), .Select("low")) register_7 (
    .D(multiplexer_7_out), .en(pull_resistor_2_node), .Q(regwrite_2), .clk(CLK));  // open: clr
  Register #(.width(1), .trigger("rising"), .Select("low")) register_8 (
    .D(multiplexer_8_out), .en(pull_resistor_2_node), .Q(memchoose_2), .clk(CLK));  // open: clr
  Register #(.width(1), .trigger("rising"), .Select("low")) register_9 (
    .D(multiplexer_9_out), .en(pull_resistor_2_node), .Q(memwrite_2), .clk(CLK));  // open: clr
  Register #(.width(1), .trigger("rising"), .Select("low")) register_10 (
    .D(multiplexer_10_out), .en(pull_resistor_2_node), .Q(BLEZ_2), .clk(CLK));  // open: clr
  Register #(.width(1), .trigger("rising"), .Select("low")) register_11 (
    .D(multiplexer_11_out), .en(pull_resistor_2_node), .Q(LB_2), .clk(CLK));  // open: clr
  Register #(.width(4), .trigger("rising"), .Select("low")) register_12 (
    .D(multiplexer_12_out), .en(pull_resistor_2_node), .Q(aluop_2), .clk(CLK));  // open: clr
  Register #(.width(1), .trigger("rising"), .Select("low")) register_13 (
    .D(multiplexer_13_out), .en(pull_resistor_2_node), .Q(alusrcb_2), .clk(CLK));  // open: clr
  Register #(.width(32), .trigger("rising"), .Select("low")) register_14 (
    .D(multiplexer_14_out), .en(pull_resistor_2_node), .Q(A_2), .clk(CLK));  // open: clr
  Register #(.width(32), .trigger("rising"), .Select("low")) register_15 (
    .D(multiplexer_15_out), .en(pull_resistor_2_node), .Q(B_2), .clk(CLK));  // open: clr
  Register #(.width(32), .trigger("rising"), .Select("low")) register_16 (
    .D(multiplexer_16_out), .en(pull_resistor_2_node), .Q(A_prime_2), .clk(CLK));  // open: clr
  Register #(.width(32), .trigger("rising"), .Select("low")) register_17 (
    .D(multiplexer_17_out), .en(pull_resistor_2_node), .Q(B_prime_2), .clk(CLK));  // open: clr
  Register #(.width(32), .trigger("rising"), .Select("low")) register_18 (
    .D(multiplexer_18_out), .en(pull_resistor_2_node), .Q(IR_2), .clk(CLK));  // open: clr
  Register #(.width(32), .trigger("rising"), .Select("low")) register_19 (
    .D(multiplexer_19_out), .en(pull_resistor_2_node), .Q(IMM_2), .clk(CLK));  // open: clr
  Register #(.width(5), .trigger("rising"), .Select("low")) register_20 (
    .D(multiplexer_20_out), .en(pull_resistor_2_node), .Q(writereg_2), .clk(CLK));  // open: clr
  Register #(.width(5), .trigger("rising"), .Select("low")) register_21 (
    .D(multiplexer_21_out), .en(pull_resistor_2_node), .Q(shamt_2), .clk(CLK));  // open: clr
  Register #(.width(32), .trigger("rising"), .Select("low")) register_22 (
    .D(multiplexer_22_out), .en(pull_resistor_2_node), .Q(IMM2_2), .clk(CLK));  // open: clr
  Register #(.width(32), .trigger("rising"), .Select("low")) register_23 (
    .D(multiplexer_23_out), .en(pull_resistor_2_node), .Q(PC_2), .clk(CLK));  // open: clr
  Register #(.width(2), .trigger("rising"), .Select("low")) register_24 (
    .D(multiplexer_24_out), .en(pull_resistor_2_node), .Q(cR1_2), .clk(CLK));  // open: clr
  Register #(.width(2), .trigger("rising"), .Select("low")) register_25 (
    .D(multiplexer_25_out), .en(pull_resistor_2_node), .Q(cR2_2), .clk(CLK));  // open: clr
  Pull_Resistor #(.pull(0)) pull_resistor_2 (.node(pull_resistor_2_node));
  not not_1 (pull_resistor_2_node, \使能端_低电平有效 );

  // Notes on the sheet:
  //   使能端_低电平有效: pull=down
  //   同步清零_高电平有效: pull=down
  //   下拉电阻使得引脚可以悬空
endmodule

module \源寄存器使用情况  (
  input  OP0,
  input  OP1,
  input  OP2,
  input  OP3,
  input  OP4,
  input  OP5,
  input  F0,
  input  F1,
  input  F2,
  input  F3,
  input  F4,
  input  F5,
  output R1used,
  output R2used
);

  wire and_1_out, and_2_out, and_3_out, and_4_out, and_5_out, and_6_out, and_7_out, and_8_out, and_9_out,
       and_10_out, and_11_out, and_12_out, and_13_out, and_14_out, and_15_out, and_16_out, and_17_out,
       and_18_out, and_19_out, and_20_out, and_21_out, and_22_out, and_23_out, and_24_out, and_25_out,
       and_26_out, and_27_out, and_28_out, and_29_out, and_30_out, and_31_out, and_32_out, and_33_out,
       and_34_out, and_35_out, and_36_out, and_37_out, and_38_out, and_39_out, and_40_out, and_41_out,
       and_42_out, and_43_out, not_1_out, not_2_out, not_3_out, not_4_out, not_5_out, not_6_out, not_7_out,
       not_8_out, not_9_out, not_10_out, not_11_out, not_12_out, not_13_out, not_14_out, not_15_out,
       not_16_out, not_17_out, not_18_out, not_19_out, not_20_out, not_21_out, not_22_out, not_23_out,
       not_24_out, not_25_out, not_26_out, not_27_out, not_28_out, not_29_out, not_30_out, not_31_out,
       not_32_out, not_33_out, not_34_out, not_35_out, not_36_out, not_37_out, not_38_out, not_39_out,
       not_40_out, not_41_out, not_42_out, not_43_out, not_44_out, not_45_out, not_46_out, not_47_out,
       not_48_out, not_49_out, not_50_out, not_51_out, not_52_out, not_53_out, not_54_out, not_55_out,
       not_56_out, not_57_out, not_58_out, not_59_out, not_60_out, not_61_out, not_62_out, not_63_out,
       not_64_out, not_65_out, not_66_out, not_67_out, not_68_out, not_69_out, not_70_out, not_71_out,
       not_72_out, not_73_out, not_74_out, not_75_out, not_76_out, not_77_out, not_78_out, not_79_out,
       not_80_out, not_81_out, not_82_out, not_83_out, not_84_out, not_85_out, not_86_out, not_87_out,
       not_88_out, not_89_out, not_90_out, not_91_out, not_92_out, not_93_out, not_94_out, not_95_out,
       not_96_out, not_97_out, not_98_out, not_99_out, not_100_out, not_101_out, not_102_out, not_103_out,
       not_104_out, not_105_out, not_106_out, not_107_out, not_108_out, not_109_out, not_110_out,
       not_111_out, not_112_out, not_113_out, not_114_out, not_115_out, not_116_out, not_117_out,
       not_118_out, not_119_out, not_120_out, not_121_out, not_122_out, not_123_out, not_124_out,
       not_125_out, not_126_out, not_127_out, not_128_out, not_129_out, not_130_out, not_131_out,
       not_132_out, not_133_out, not_134_out, not_135_out, not_136_out, not_137_out, not_138_out,
       not_139_out, not_140_out, not_141_out, not_142_out, not_143_out, not_144_out, not_145_out,
       not_146_out, not_147_out, not_148_out, not_149_out, not_150_out, not_151_out, not_152_out,
       not_153_out, not_154_out, not_155_out, not_156_out, not_157_out, not_158_out, not_159_out,
       not_160_out, not_161_out, not_162_out, not_163_out, not_164_out, not_165_out, not_166_out,
       not_167_out, not_168_out, not_169_out, not_170_out, not_171_out, not_172_out, not_173_out,
       not_174_out, not_175_out, not_176_out, not_177_out, not_178_out, not_179_out, not_180_out,
       not_181_out, not_182_out, not_183_out, not_184_out, not_185_out, not_186_out, not_187_out,
       not_188_out, not_189_out, not_190_out, not_191_out, not_192_out, not_193_out, not_194_out,
       not_195_out, not_196_out, not_197_out, not_198_out, not_199_out, not_200_out, not_201_out,
       not_202_out, not_203_out, not_204_out, not_205_out, not_206_out, not_207_out, not_208_out,
       not_209_out, not_210_out, not_211_out, not_212_out, not_213_out, not_214_out, not_215_out,
       not_216_out, not_217_out, not_218_out, not_219_out, not_220_out, not_221_out, not_222_out,
       not_223_out, not_224_out, not_225_out, not_226_out, not_227_out, not_228_out, not_229_out,
       not_230_out, not_231_out, not_232_out, not_233_out, not_234_out, not_235_out, not_236_out,
       not_237_out, not_238_out, not_239_out, not_240_out, not_241_out, not_242_out, not_243_out,
       not_244_out, not_245_out, not_246_out, not_247_out, not_248_out, not_249_out, not_250_out,
       not_251_out, not_252_out, not_253_out, not_254_out, not_255_out, not_256_out, not_257_out,
       not_258_out, not_259_out, not_260_out, not_261_out, not_262_out, not_263_out, not_264_out,
       not_265_out, not_266_out, not_267_out, not_268_out, not_269_out, not_270_out, not_271_out,
       not_272_out, not_273_out, not_274_out, not_275_out, not_276_out, not_277_out, not_278_out,
       not_279_out, not_280_out, not_281_out, not_282_out, not_283_out, not_284_out, not_285_out,
       not_286_out, not_287_out, not_288_out, not_289_out, not_290_out, not_291_out, not_292_out,
       not_293_out, not_294_out, not_295_out, not_296_out, not_297_out, not_298_out, not_299_out,
       not_300_out, not_301_out, not_302_out, not_303_out, not_304_out, not_305_out, not_306_out,
       not_307_out, not_308_out, not_309_out, not_310_out, not_311_out, not_312_out, not_313_out,
       not_314_out, not_315_out, not_316_out, not_317_out, not_318_out, not_319_out, not_320_out,
       not_321_out, not_322_out, not_323_out, not_324_out, not_325_out, not_326_out, not_327_out,
       not_328_out, not_329_out, not_330_out, not_331_out, not_332_out, not_333_out, not_334_out,
       not_335_out, not_336_out, not_337_out;

  not not_1 (not_1_out, OP5);
  not not_2 (not_2_out, OP4);
  not not_3 (not_3_out, OP3);
  not not_4 (not_4_out, OP2);
  not not_5 (not_5_out, OP1);
  not not_6 (not_6_out, OP0);
  not not_7 (not_7_out, F5);
  not not_8 (not_8_out, F4);
  not not_9 (not_9_out, F3);
  not not_10 (not_10_out, F2);
  not not_11 (not_11_out, F1);
  not not_12 (not_12_out, F0);
  not not_13 (not_13_out, OP5);
  not not_14 (not_14_out, OP4);
  not not_15 (not_15_out, OP3);
  not not_16 (not_16_out, OP2);
  not not_17 (not_17_out, OP1);
  not not_18 (not_18_out, OP0);
  not not_19 (not_19_out, F5);
  not not_20 (not_20_out, F4);
  not not_21 (not_21_out, F3);
  not not_22 (not_22_out, F2);
  not not_23 (not_23_out, OP5);
  not not_24 (not_24_out, OP4);
  not not_25 (not_25_out, OP3);
  not not_26 (not_26_out, OP2);
  not not_27 (not_27_out, OP1);
  not not_28 (not_28_out, OP0);
  not not_29 (not_29_out, F5);
  not not_30 (not_30_out, F4);
  not not_31 (not_31_out, F3);
  not not_32 (not_32_out, F2);
  not not_33 (not_33_out, F0);
  not not_34 (not_34_out, OP5);
  not not_35 (not_35_out, OP4);
  not not_36 (not_36_out, OP3);
  not not_37 (not_37_out, OP2);
  not not_38 (not_38_out, OP1);
  not not_39 (not_39_out, OP0);
  not not_40 (not_40_out, F4);
  not not_41 (not_41_out, F3);
  not not_42 (not_42_out, F2);
  not not_43 (not_43_out, F1);
  not not_44 (not_44_out, F0);
  not not_45 (not_45_out, OP5);
  not not_46 (not_46_out, OP4);
  not not_47 (not_47_out, OP3);
  not not_48 (not_48_out, OP2);
  not not_49 (not_49_out, OP1);
  not not_50 (not_50_out, OP0);
  not not_51 (not_51_out, F4);
  not not_52 (not_52_out, F3);
  not not_53 (not_53_out, F2);
  not not_54 (not_54_out, F1);
  not not_55 (not_55_out, OP5);
  not not_56 (not_56_out, OP4);
  not not_57 (not_57_out, OP3);
  not not_58 (not_58_out, OP2);
  not not_59 (not_59_out, OP1);
  not not_60 (not_60_out, OP0);
  not not_61 (not_61_out, F4);
  not not_62 (not_62_out, F3);
  not not_63 (not_63_out, F2);
  not not_64 (not_64_out, F0);
  not not_65 (not_65_out, OP5);
  not not_66 (not_66_out, OP4);
  not not_67 (not_67_out, OP3);
  not not_68 (not_68_out, OP2);
  not not_69 (not_69_out, OP1);
  not not_70 (not_70_out, OP0);
  not not_71 (not_71_out, F4);
  not not_72 (not_72_out, F3);
  not not_73 (not_73_out, F1);
  not not_74 (not_74_out, F0);
  not not_75 (not_75_out, OP5);
  not not_76 (not_76_out, OP4);
  not not_77 (not_77_out, OP3);
  not not_78 (not_78_out, OP2);
  not not_79 (not_79_out, OP1);
  not not_80 (not_80_out, OP0);
  not not_81 (not_81_out, F4);
  not not_82 (not_82_out, F3);
  not not_83 (not_83_out, F1);
  not not_84 (not_84_out, OP5);
  not not_85 (not_85_out, OP4);
  not not_86 (not_86_out, OP3);
  not not_87 (not_87_out, OP2);
  not not_88 (not_88_out, OP1);
  not not_89 (not_89_out, OP0);
  not not_90 (not_90_out, F4);
  not not_91 (not_91_out, F3);
  not not_92 (not_92_out, OP5);
  not not_93 (not_93_out, OP4);
  not not_94 (not_94_out, OP3);
  not not_95 (not_95_out, OP2);
  not not_96 (not_96_out, OP1);
  not not_97 (not_97_out, OP0);
  not not_98 (not_98_out, F4);
  not not_99 (not_99_out, F2);
  not not_100 (not_100_out, F0);
  not not_101 (not_101_out, OP5);
  not not_102 (not_102_out, OP4);
  not not_103 (not_103_out, OP3);
  not not_104 (not_104_out, OP2);
  not not_105 (not_105_out, OP1);
  not not_106 (not_106_out, OP0);
  not not_107 (not_107_out, F4);
  not not_108 (not_108_out, F2);
  not not_109 (not_109_out, OP5);
  not not_110 (not_110_out, OP4);
  not not_111 (not_111_out, OP3);
  not not_112 (not_112_out, OP2);
  not not_113 (not_113_out, OP1);
  not not_114 (not_114_out, OP0);
  not not_115 (not_115_out, F5);
  not not_116 (not_116_out, F4);
  not not_117 (not_117_out, F2);
  not not_118 (not_118_out, F1);
  not not_119 (not_119_out, F0);
  not not_120 (not_120_out, OP5);
  not not_121 (not_121_out, OP4);
  not not_122 (not_122_out, OP3);
  not not_123 (not_123_out, OP2);
  not not_124 (not_124_out, OP1);
  not not_125 (not_125_out, OP0);
  not not_126 (not_126_out, F5);
  not not_127 (not_127_out, F4);
  not not_128 (not_128_out, F1);
  not not_129 (not_129_out, F0);
  not not_130 (not_130_out, OP5);
  not not_131 (not_131_out, OP4);
  not not_132 (not_132_out, OP3);
  not not_133 (not_133_out, OP1);
  not not_134 (not_134_out, OP0);
  not not_135 (not_135_out, OP5);
  not not_136 (not_136_out, OP4);
  not not_137 (not_137_out, OP3);
  not not_138 (not_138_out, OP1);
  not not_139 (not_139_out, OP5);
  not not_140 (not_140_out, OP4);
  not not_141 (not_141_out, OP2);
  not not_142 (not_142_out, OP1);
  not not_143 (not_143_out, OP0);
  not not_144 (not_144_out, OP5);
  not not_145 (not_145_out, OP4);
  not not_146 (not_146_out, OP1);
  not not_147 (not_147_out, OP0);
  not not_148 (not_148_out, OP5);
  not not_149 (not_149_out, OP4);
  not not_150 (not_150_out, OP2);
  not not_151 (not_151_out, OP1);
  not not_152 (not_152_out, OP5);
  not not_153 (not_153_out, OP4);
  not not_154 (not_154_out, OP2);
  not not_155 (not_155_out, OP0);
  not not_156 (not_156_out, OP5);
  not not_157 (not_157_out, OP4);
  not not_158 (not_158_out, OP1);
  not not_159 (not_159_out, OP4);
  not not_160 (not_160_out, OP3);
  not not_161 (not_161_out, OP2);
  not not_162 (not_162_out, OP4);
  not not_163 (not_163_out, OP2);
  not not_164 (not_164_out, OP5);
  not not_165 (not_165_out, OP4);
  not not_166 (not_166_out, OP3);
  not not_167 (not_167_out, OP2);
  not not_168 (not_168_out, OP1);
  not not_169 (not_169_out, OP0);
  not not_170 (not_170_out, F4);
  not not_171 (not_171_out, F3);
  not not_172 (not_172_out, F0);
  not not_173 (not_173_out, OP5);
  not not_174 (not_174_out, OP4);
  not not_175 (not_175_out, OP3);
  not not_176 (not_176_out, OP2);
  not not_177 (not_177_out, OP1);
  not not_178 (not_178_out, OP0);
  not not_179 (not_179_out, F4);
  not not_180 (not_180_out, F3);
  not not_181 (not_181_out, F2);
  not not_182 (not_182_out, OP4);
  not not_183 (not_183_out, OP3);
  not not_184 (not_184_out, OP2);
  not not_185 (not_185_out, OP1);
  not not_186 (not_186_out, OP0);
  not not_187 (not_187_out, OP5);
  not not_188 (not_188_out, OP4);
  not not_189 (not_189_out, OP3);
  not not_190 (not_190_out, OP0);
  not not_191 (not_191_out, OP5);
  not not_192 (not_192_out, OP4);
  not not_193 (not_193_out, OP3);
  not not_194 (not_194_out, OP2);
  not not_195 (not_195_out, OP1);
  not not_196 (not_196_out, OP0);
  not not_197 (not_197_out, F5);
  not not_198 (not_198_out, F4);
  not not_199 (not_199_out, F3);
  not not_200 (not_200_out, F2);
  not not_201 (not_201_out, F1);
  not not_202 (not_202_out, F0);
  not not_203 (not_203_out, OP5);
  not not_204 (not_204_out, OP4);
  not not_205 (not_205_out, OP3);
  not not_206 (not_206_out, OP2);
  not not_207 (not_207_out, OP1);
  not not_208 (not_208_out, OP0);
  not not_209 (not_209_out, F5);
  not not_210 (not_210_out, F4);
  not not_211 (not_211_out, F3);
  not not_212 (not_212_out, F2);
  not not_213 (not_213_out, OP5);
  not not_214 (not_214_out, OP4);
  not not_215 (not_215_out, OP3);
  not not_216 (not_216_out, OP2);
  not not_217 (not_217_out, OP1);
  not not_218 (not_218_out, OP0);
  not not_219 (not_219_out, F5);
  not not_220 (not_220_out, F4);
  not not_221 (not_221_out, F3);
  not not_222 (not_222_out, F2);
  not not_223 (not_223_out, F0);
  not not_224 (not_224_out, OP5);
  not not_225 (not_225_out, OP4);
  not not_226 (not_226_out, OP3);
  not not_227 (not_227_out, OP2);
  not not_228 (not_228_out, OP1);
  not not_229 (not_229_out, OP0);
  not not_230 (not_230_out, F4);
  not not_231 (not_231_out, F3);
  not not_232 (not_232_out, F2);
  not not_233 (not_233_out, F1);
  not not_234 (not_234_out, F0);
  not not_235 (not_235_out, OP5);
  not not_236 (not_236_out, OP4);
  not not_237 (not_237_out, OP3);
  not not_238 (not_238_out, OP2);
  not not_239 (not_239_out, OP1);
  not not_240 (not_240_out, OP0);
  not not_241 (not_241_out, F4);
  not not_242 (not_242_out, F3);
  not not_243 (not_243_out, F2);
  not not_244 (not_244_out, F1);
  not not_245 (not_245_out, OP5);
  not not_246 (not_246_out, OP4);
  not not_247 (not_247_out, OP3);
  not not_248 (not_248_out, OP2);
  not not_249 (not_249_out, OP1);
  not not_250 (not_250_out, OP0);
  not not_251 (not_251_out, F4);
  not not_252 (not_252_out, F3);
  not not_253 (not_253_out, F2);
  not not_254 (not_254_out, F0);
  not not_255 (not_255_out, OP5);
  not not_256 (not_256_out, OP4);
  not not_257 (not_257_out, OP3);
  not not_258 (not_258_out, OP2);
  not not_259 (not_259_out, OP1);
  not not_260 (not_260_out, OP0);
  not not_261 (not_261_out, F4);
  not not_262 (not_262_out, F3);
  not not_263 (not_263_out, F1);
  not not_264 (not_264_out, F0);
  not not_265 (not_265_out, OP5);
  not not_266 (not_266_out, OP4);
  not not_267 (not_267_out, OP3);
  not not_268 (not_268_out, OP2);
  not not_269 (not_269_out, OP1);
  not not_270 (not_270_out, OP0);
  not not_271 (not_271_out, F4);
  not not_272 (not_272_out, F3);
  not not_273 (not_273_out, F1);
  not not_274 (not_274_out, OP5);
  not not_275 (not_275_out, OP4);
  not not_276 (not_276_out, OP3);
  not not_277 (not_277_out, OP2);
  not not_278 (not_278_out, OP1);
  not not_279 (not_279_out, OP0);
  not not_280 (not_280_out, F4);
  not not_281 (not_281_out, F3);
  not not_282 (not_282_out, OP5);
  not not_283 (not_283_out, OP4);
  not not_284 (not_284_out, OP3);
  not not_285 (not_285_out, OP2);
  not not_286 (not_286_out, OP1);
  not not_287 (not_287_out, OP0);
  not not_288 (not_288_out, F4);
  not not_289 (not_289_out, F2);
  not not_290 (not_290_out, F0);
  not not_291 (not_291_out, OP5);
  not not_292 (not_292_out, OP4);
  not not_293 (not_293_out, OP3);
  not not_294 (not_294_out, OP2);
  not not_295 (not_295_out, OP1);
  not not_296 (not_296_out, OP0);
  not not_297 (not_297_out, F4);
  not not_298 (not_298_out, F2);
  not not_299 (not_299_out, OP5);
  not not_300 (not_300_out, OP4);
  not not_301 (not_301_out, OP3);
  not not_302 (not_302_out, OP2);
  not not_303 (not_303_out, OP1);
  not not_304 (not_304_out, OP0);
  not not_305 (not_305_out, F5);
  not not_306 (not_306_out, F4);
  not not_307 (not_307_out, F1);
  not not_308 (not_308_out, F0);
  not not_309 (not_309_out, OP5);
  not not_310 (not_310_out, OP4);
  not not_311 (not_311_out, OP3);
  not not_312 (not_312_out, OP1);
  not not_313 (not_313_out, OP0);
  not not_314 (not_314_out, OP5);
  not not_315 (not_315_out, OP4);
  not not_316 (not_316_out, OP3);
  not not_317 (not_317_out, OP1);
  not not_318 (not_318_out, OP4);
  not not_319 (not_319_out, OP2);
  not not_320 (not_320_out, OP5);
  not not_321 (not_321_out, OP4);
  not not_322 (not_322_out, OP3);
  not not_323 (not_323_out, OP2);
  not not_324 (not_324_out, OP1);
  not not_325 (not_325_out, OP0);
  not not_326 (not_326_out, F4);
  not not_327 (not_327_out, F3);
  not not_328 (not_328_out, F0);
  not not_329 (not_329_out, OP5);
  not not_330 (not_330_out, OP4);
  not not_331 (not_331_out, OP3);
  not not_332 (not_332_out, OP2);
  not not_333 (not_333_out, OP1);
  not not_334 (not_334_out, OP0);
  not not_335 (not_335_out, F4);
  not not_336 (not_336_out, F3);
  not not_337 (not_337_out, F2);
  and and_1 (and_1_out, not_1_out, not_2_out, not_3_out, not_4_out, not_5_out, not_6_out, not_7_out, not_8_out, not_9_out, not_10_out, not_11_out, not_12_out);
  and and_2 (and_2_out, not_13_out, not_14_out, not_15_out, not_16_out, not_17_out, not_18_out, not_19_out, not_20_out, not_21_out, not_22_out, F1, F0);
  and and_3 (and_3_out, not_23_out, not_24_out, not_25_out, not_26_out, not_27_out, not_28_out, not_29_out, not_30_out, not_31_out, not_32_out, F1, not_33_out);
  and and_4 (and_4_out, not_34_out, not_35_out, not_36_out, not_37_out, not_38_out, not_39_out, F5, not_40_out, not_41_out, not_42_out, not_43_out, not_44_out);
  and and_5 (and_5_out, not_45_out, not_46_out, not_47_out, not_48_out, not_49_out, not_50_out, F5, not_51_out, not_52_out, not_53_out, not_54_out, F0);
  and and_6 (and_6_out, not_55_out, not_56_out, not_57_out, not_58_out, not_59_out, not_60_out, F5, not_61_out, not_62_out, not_63_out, F1, not_64_out);
  and and_7 (and_7_out, not_65_out, not_66_out, not_67_out, not_68_out, not_69_out, not_70_out, F5, not_71_out, not_72_out, F2, not_73_out, not_74_out);
  and and_8 (and_8_out, not_75_out, not_76_out, not_77_out, not_78_out, not_79_out, not_80_out, F5, not_81_out, not_82_out, F2, not_83_out, F0);
  and and_9 (and_9_out, not_84_out, not_85_out, not_86_out, not_87_out, not_88_out, not_89_out, F5, not_90_out, not_91_out, F2, F1, F0);
  and and_10 (and_10_out, not_92_out, not_93_out, not_94_out, not_95_out, not_96_out, not_97_out, F5, not_98_out, F3, not_99_out, F1, not_100_out);
  and and_11 (and_11_out, not_101_out, not_102_out, not_103_out, not_104_out, not_105_out, not_106_out, F5, not_107_out, F3, not_108_out, F1, F0);
  and and_12 (and_12_out, not_109_out, not_110_out, not_111_out, not_112_out, not_113_out, not_114_out, not_115_out, not_116_out, F3, not_117_out, not_118_out, not_119_out);
  and and_13 (and_13_out, not_120_out, not_121_out, not_122_out, not_123_out, not_124_out, not_125_out, not_126_out, not_127_out, F3, F2, not_128_out, not_129_out);
  and and_14 (and_14_out, not_130_out, not_131_out, not_132_out, OP2, not_133_out, not_134_out);
  and and_15 (and_15_out, not_135_out, not_136_out, not_137_out, OP2, not_138_out, OP0);
  and and_16 (and_16_out, not_139_out, not_140_out, OP3, not_141_out, not_142_out, not_143_out);
  and and_17 (and_17_out, not_144_out, not_145_out, OP3, OP2, not_146_out, not_147_out);
  and and_18 (and_18_out, not_148_out, not_149_out, OP3, not_150_out, not_151_out, OP0);
  and and_19 (and_19_out, not_152_out, not_153_out, OP3, not_154_out, OP1, not_155_out);
  and and_20 (and_20_out, not_156_out, not_157_out, OP3, OP2, not_158_out, OP0);
  and and_21 (and_21_out, OP5, not_159_out, not_160_out, not_161_out, OP1, OP0);
  and and_22 (and_22_out, OP5, not_162_out, OP3, not_163_out, OP1, OP0);
  and and_23 (and_23_out, not_164_out, not_165_out, not_166_out, not_167_out, not_168_out, not_169_out, F5, not_170_out, not_171_out, F2, F1, not_172_out);
  and and_24 (and_24_out, not_173_out, not_174_out, not_175_out, not_176_out, not_177_out, not_178_out, F5, not_179_out, not_180_out, not_181_out, F1, F0);
  and and_25 (and_25_out, OP5, not_182_out, not_183_out, not_184_out, not_185_out, not_186_out);
  and and_26 (and_26_out, not_187_out, not_188_out, not_189_out, OP2, OP1, not_190_out);
  and and_27 (and_27_out, not_191_out, not_192_out, not_193_out, not_194_out, not_195_out, not_196_out, not_197_out, not_198_out, not_199_out, not_200_out, not_201_out, not_202_out);
  and and_28 (and_28_out, not_203_out, not_204_out, not_205_out, not_206_out, not_207_out, not_208_out, not_209_out, not_210_out, not_211_out, not_212_out, F1, F0);
  and and_29 (and_29_out, not_213_out, not_214_out, not_215_out, not_216_out, not_217_out, not_218_out, not_219_out, not_220_out, not_221_out, not_222_out, F1, not_223_out);
  and and_30 (and_30_out, not_224_out, not_225_out, not_226_out, not_227_out, not_228_out, not_229_out, F5, not_230_out, not_231_out, not_232_out, not_233_out, not_234_out);
  and and_31 (and_31_out, not_235_out, not_236_out, not_237_out, not_238_out, not_239_out, not_240_out, F5, not_241_out, not_242_out, not_243_out, not_244_out, F0);
  and and_32 (and_32_out, not_245_out, not_246_out, not_247_out, not_248_out, not_249_out, not_250_out, F5, not_251_out, not_252_out, not_253_out, F1, not_254_out);
  and and_33 (and_33_out, not_255_out, not_256_out, not_257_out, not_258_out, not_259_out, not_260_out, F5, not_261_out, not_262_out, F2, not_263_out, not_264_out);
  and and_34 (and_34_out, not_265_out, not_266_out, not_267_out, not_268_out, not_269_out, not_270_out, F5, not_271_out, not_272_out, F2, not_273_out, F0);
  and and_35 (and_35_out, not_274_out, not_275_out, not_276_out, not_277_out, not_278_out, not_279_out, F5, not_280_out, not_281_out, F2, F1, F0);
  and and_36 (and_36_out, not_282_out, not_283_out, not_284_out, not_285_out, not_286_out, not_287_out, F5, not_288_out, F3, not_289_out, F1, not_290_out);
  and and_37 (and_37_out, not_291_out, not_292_out, not_293_out, not_294_out, not_295_out, not_296_out, F5, not_297_out, F3, not_298_out, F1, F0);
  and and_38 (and_38_out, not_299_out, not_300_out, not_301_out, not_302_out, not_303_out, not_304_out, not_305_out, not_306_out, F3, F2, not_307_out, not_308_out);
  and and_39 (and_39_out, not_309_out, not_310_out, not_311_out, OP2, not_312_out, not_313_out);
  and and_40 (and_40_out, not_314_out, not_315_out, not_316_out, OP2, not_317_out, OP0);
  and and_41 (and_41_out, OP5, not_318_out, OP3, not_319_out, OP1, OP0);
  and and_42 (and_42_out, not_320_out, not_321_out, not_322_out, not_323_out, not_324_out, not_325_out, F5, not_326_out, not_327_out, F2, F1, not_328_out);
  and and_43 (and_43_out, not_329_out, not_330_out, not_331_out, not_332_out, not_333_out, not_334_out, F5, not_335_out, not_336_out, not_337_out, F1, F0);
  or or_1 (R1used, and_1_out, and_2_out, and_3_out, and_4_out, and_5_out, and_6_out, and_7_out, and_8_out, and_9_out, and_10_out, and_11_out, and_12_out, and_13_out, and_14_out, and_15_out, and_16_out, and_17_out, and_18_out, and_19_out, and_20_out, and_21_out, and_22_out, and_23_out, and_24_out, and_25_out, and_26_out);
  or or_2 (R2used, and_27_out, and_28_out, and_29_out, and_30_out, and_31_out, and_32_out, and_33_out, and_34_out, and_35_out, and_36_out, and_37_out, and_38_out, and_39_out, and_40_out, and_41_out, and_42_out, and_43_out);
endmodule

module \数据相关检测逻辑  (
  input  R1used,
  input  EX_RegWrite,
  input  [4:0] R1_num,
  input  [4:0] R2_num,
  input  [4:0] EX_WriteReg_num,
  input  [4:0] MEM_WriteReg_num,
  input  R2used,
  input  MEM_RegWrite,
  output relative
);

  wire and_1_out, and_2_out, and_3_out, and_4_out, comparator_1_eq, comparator_2_eq, comparator_3_eq,
       comparator_4_eq, comparator_5_eq, comparator_6_eq, not_1_out, not_2_out;

  Comparator #(.width(5), .mode("twosComplement")) comparator_1 (
    .a({5{1'b0}}), .b(R1_num), .eq(comparator_1_eq));  // open: gt, lt
  Comparator #(.width(5), .mode("twosComplement")) comparator_2 (
    .a(R1_num), .b(EX_WriteReg_num), .eq(comparator_2_eq));  // open: gt, lt
  Comparator #(.width(5), .mode("twosComplement")) comparator_3 (
    .a(R1_num), .b(MEM_WriteReg_num), .eq(comparator_3_eq));  // open: gt, lt
  Comparator #(.width(5), .mode("twosComplement")) comparator_4 (
    .a(R2_num), .b(EX_WriteReg_num), .eq(comparator_4_eq));  // open: gt, lt
  Comparator #(.width(5), .mode("twosComplement")) comparator_5 (
    .a(R2_num), .b(MEM_WriteReg_num), .eq(comparator_5_eq));  // open: gt, lt
  Comparator #(.width(5), .mode("twosComplement")) comparator_6 (
    .a(R2_num), .b({5{1'b0}}), .eq(comparator_6_eq));  // open: gt, lt
  not not_1 (not_1_out, comparator_1_eq);
  not not_2 (not_2_out, comparator_6_eq);
  and and_1 (and_1_out, EX_RegWrite, R1used, not_1_out, comparator_2_eq);
  and and_2 (and_2_out, not_1_out, R1used, comparator_3_eq, MEM_RegWrite);
  and and_3 (and_3_out, EX_RegWrite, comparator_4_eq, not_2_out, R2used);
  and and_4 (and_4_out, comparator_5_eq, not_2_out, R2used, MEM_RegWrite);
  or or_1 (relative, and_1_out, and_2_out, and_3_out, and_4_out);
endmodule

module \LOAD_USE检测  (
  input  R1used,
  input  EX_RegWrite,
  input  [4:0] R1_num,
  input  [4:0] EX_WriteReg_num,
  input  [4:0] R2_num,
  input  R2used,
  input  [5:0] OP,
  output relative
);

  wire and_1_out, and_2_out, comparator_1_eq, comparator_2_eq, comparator_3_eq, comparator_4_eq,
       comparator_5_eq, comparator_6_eq, not_1_out, not_2_out, or_1_out;

  Comparator #(.width(5), .mode("twosComplement")) comparator_1 (
    .a({5{1'b0}}), .b(R1_num), .eq(comparator_1_eq));  // open: gt, lt
  Comparator #(.width(5), .mode("twosComplement")) comparator_2 (
    .a(R1_num), .b(EX_WriteReg_num), .eq(comparator_2_eq));  // open: gt, lt
  Comparator #(.width(5), .mode("twosComplement")) comparator_3 (
    .a(EX_WriteReg_num), .b(R2_num), .eq(comparator_3_eq));  // open: gt, lt
  Comparator #(.width(5), .mode("twosComplement")) comparator_4 (
    .a(R2_num), .b({5{1'b0}}), .eq(comparator_4_eq));  // open: gt, lt
  Comparator #(.width(6), .mode("twosComplement")) comparator_5 (
    .a(OP), .b(6'b100011), .eq(comparator_5_eq));  // open: gt, lt
  Comparator #(.width(6), .mode("twosComplement")) comparator_6 (
    .a(OP), .b(6'b100000), .eq(comparator_6_eq));  // open: gt, lt
  not not_1 (not_1_out, comparator_1_eq);
  not not_2 (not_2_out, comparator_4_eq);
  or or_1 (or_1_out, comparator_5_eq, comparator_6_eq);
  and and_1 (and_1_out, R1used, EX_RegWrite, or_1_out, not_1_out, comparator_2_eq);
  and and_2 (and_2_out, EX_RegWrite, comparator_3_eq, or_1_out, not_2_out, R2used);
  or or_2 (relative, and_1_out, and_2_out);
endmodule

module \重定向逻辑信号  (
  input  R1used,
  input  EX_RegWrite,
  input  [4:0] R1_num,
  input  [4:0] R2_num,
  input  [4:0] EX_WriteReg_num,
  input  [4:0] MEM_WriteReg_num,
  input  R2used,
  input  MEM_RegWrite,
  input  [5:0] OP,
  output [1:0] ChooseR1,
  output [1:0] ChooseR2
);

  wire and_3_out, and_4_out, comparator_1_eq, comparator_2_eq, comparator_3_eq, comparator_4_eq,
       comparator_5_eq, comparator_6_eq, comparator_7_eq, comparator_8_eq, EX_R1, EX_R2, MEM_ALU_R1,
       MEM_ALU_R2, MEM_WB_R1, MEM_WB_R2, not_1_out, not_2_out, not_3_out, not_4_out, not_5_out, or_1_out;

  not not_1 (not_1_out, comparator_1_eq);
  Comparator #(.width(5), .mode("twosComplement")) comparator_1 (
    .a({5{1'b0}}), .b(R1_num), .eq(comparator_1_eq));  // open: gt, lt
  Comparator #(.width(5), .mode("twosComplement")) comparator_2 (
    .a(R1_num), .b(EX_WriteReg_num), .eq(comparator_2_eq));  // open: gt, lt
  not not_2 (not_2_out, comparator_2_eq);
  Comparator #(.width(5), .mode("twosComplement")) comparator_3 (
    .a(R1_num), .b(MEM_WriteReg_num), .eq(comparator_3_eq));  // open: gt, lt
  Comparator #(.width(5), .mode("twosComplement")) comparator_4 (
    .a(R2_num), .b(EX_WriteReg_num), .eq(comparator_4_eq));  // open: gt, lt
  not not_3 (not_3_out, comparator_4_eq);
  Comparator #(.width(5), .mode("twosComplement")) comparator_5 (
    .a(R2_num), .b(MEM_WriteReg_num), .eq(comparator_5_eq));  // open: gt, lt
  not not_4 (not_4_out, comparator_6_eq);
  Comparator #(.width(5), .mode("twosComplement")) comparator_6 (
    .a(R2_num), .b({5{1'b0}}), .eq(comparator_6_eq));  // open: gt, lt
  Comparator #(.width(6), .mode("twosComplement")) comparator_7 (
    .a(OP), .b(6'b100011), .eq(comparator_7_eq));  // open: gt, lt
  Comparator #(.width(6), .mode("twosComplement")) comparator_8 (
    .a(OP), .b(6'b100000), .eq(comparator_8_eq));  // open: gt, lt
  Multiplexer #(.select(3), .width(2), .disabled("Z"), .enable("false")) multiplexer_1 (
    .in0(2'b00), .in1(2'b01), .in2(2'b10), .in4(2'b11), .out(ChooseR1), .sel({MEM_WB_R1, MEM_ALU_R1, EX_R1}));  // open: in3, in5, in6, in7
  and and_1 (EX_R1, R1used, EX_RegWrite, not_1_out, comparator_2_eq);
  and and_2 (EX_R2, EX_RegWrite, not_4_out, R2used, comparator_4_eq);
  and and_3 (and_3_out, R1used, not_1_out, not_2_out, comparator_3_eq, MEM_RegWrite);
  and and_4 (and_4_out, not_3_out, comparator_5_eq, R2used, not_4_out, MEM_RegWrite);
  or or_1 (or_1_out, comparator_7_eq, comparator_8_eq);
  and and_5 (MEM_WB_R1, and_3_out, or_1_out);
  and and_6 (MEM_ALU_R1, and_3_out, not_5_out);
  not not_5 (not_5_out, or_1_out);
  and and_7 (MEM_ALU_R2, not_5_out, and_4_out);
  and and_8 (MEM_WB_R2, or_1_out, and_4_out);
  Multiplexer #(.select(3), .width(2), .disabled("Z"), .enable("false")) multiplexer_2 (
    .in0(2'b00), .in1(2'b01), .in2(2'b10), .in4(2'b11), .out(ChooseR2), .sel({MEM_WB_R2, MEM_ALU_R2, EX_R2}));  // open: in3, in5, in6, in7
endmodule

module \中断按键参考电路  (
  input  IR1,
  input  IR2,
  input  IR3,
  output RegWrite,
  output MemWrite,
  output [31:0] PC,
  output [31:0] IR,
  output [31:0] RDin,
  output [31:0] MDin,
  output [31:0] LedData
);

  wire and_1_out, and_2_out, and_3_out, and_4_out, and_5_out, and_6_out, and_7_out, and_8_out, and_9_out,
       and_10_out, and_11_out, and_12_out, and_13_out, and_14_out, and_15_out, and_16_out, and_17_out,
       and_18_out, and_24_out, and_25_out, BLEZ, branch, CLK, comparator_1_eq, comparator_2_eq,
       comparator_3_eq, comparator_4_eq, comparator_5_eq, comparator_6_eq, \CPU中断请求 , d_ff_1_q, d_ff_2_q,
       d_ff_3_q, d_ff_4_q, d_ff_5_q, d_ff_6_q, decoder_1_out1, decoder_1_out2, decoder_1_out3,
       decoder_2_out0, decoder_2_out1, decoder_2_out2, demultiplexer_1_out1, demultiplexer_1_out2,
       demultiplexer_1_out3, ERET, Go, IE_q, IR1_2_q, IR1_q, IR1_t, IR2_2_q, IR2_q, IR2_t, IR3_2_q, IR3_q,
       IR3_t, IRA, IRB, IRC, JAL, JMP, JR, LB, MFC0, mips_alu_1_equal, MTC0, not_1_out, not_2_out, not_3_out,
       not_4_out, or_4_out, or_5_out, or_6_out, or_7_out, or_8_out, or_9_out, or_13_out, or_14_out, \output ,
       register_1_q, SignedExt, stop, Syscall, W1, W2, W3, \单周期硬布线控制器_1_alu_src , \单周期硬布线控制器_1_beq ,
       \单周期硬布线控制器_1_bne , \单周期硬布线控制器_1_memtoreg , \单周期硬布线控制器_1_regdst , \有中断吗 ;
  wire [1:0] count, IM_q, priority_encoder_1_out, priority_encoder_2_out;
  wire [3:0] \单周期硬布线控制器_1_alu_op ;
  wire [4:0] multiplexer_9_out, multiplexer_10_out, multiplexer_11_out, multiplexer_12_out;
  wire [7:0] undriven;
  wire [15:0] \总周期数 , \无条件跳转数 , \有条件跳转数 ;
  wire [27:0] PC_4;
  wire [31:0] adder_2_out, bit_extender_1_out, bit_extender_2_out, bit_extender_3_out, bit_extender_4_out,
       controlled_buffer_1_out, EPC, EPC_2_q, EPC_3_q, EPC_q, JMP_PC, JR_PC, mips_alu_1_result,
       multiplexer_1_out, multiplexer_3_out, multiplexer_6_out, multiplexer_7_out, multiplexer_8_out,
       multiplexer_13_out, multiplexer_14_out, multiplexer_16_out, \PC存储点 , ram_1_data, shifter_2_out,
       \中断入口地址 ;
  wire [31:28] shifter_1_out;

  Clock #(.highDuration(1), .lowDuration(1)) clock_1 (.out(CLK));
  Button _1 (.out(IRA));
  Button _2 (.out(IRB));
  Button _3 (.out(IRC));
  Button \u_继续运行  (.out(Go));
  LED #(.active("true")) led_1 (.in(W1));
  LED #(.active("true")) led_2 (.in(W2));
  LED #(.active("true")) led_3 (.in(W3));
  or or_1 (W1, IR1_2_q, d_ff_1_q);
  or or_2 (W2, IR2_2_q, d_ff_2_q);
  or or_3 (W3, IR3_2_q, d_ff_3_q);
  Decoder #(.select(2), .tristate("false"), .disabled("Z"), .enable("false")) decoder_1 (
    .out1(decoder_1_out1), .out2(decoder_1_out2), .out3(decoder_1_out3), .sel(priority_encoder_1_out));  // open: out0
  Hex_Digit_Display hex_digit_display_1 (.value(LedData[31:28]));  // open: dp
  D_Flip_Flop #(.trigger("rising"), .Pre_Clr_Positions("LEGACY"), .NegatePresetClear("false"), .enable("true"), .NewFFLayout("false")) d_ff_1 (
    .clk(IR1_t), .D(1'b1), .Q(d_ff_1_q), .reset(IR1_2_q));  // open: Qn, preset, en
  D_Flip_Flop #(.trigger("rising"), .Pre_Clr_Positions("LEGACY"), .NegatePresetClear("false"), .enable("true"), .NewFFLayout("false")) d_ff_2 (
    .clk(IR2_t), .D(1'b1), .Q(d_ff_2_q), .reset(IR2_2_q));  // open: Qn, preset, en
  D_Flip_Flop #(.trigger("rising"), .Pre_Clr_Positions("LEGACY"), .NegatePresetClear("false"), .enable("true"), .NewFFLayout("false")) d_ff_3 (
    .clk(IR3_t), .D(1'b1), .Q(d_ff_3_q), .reset(IR3_2_q));  // open: Qn, preset, en
  and and_1 (and_1_out, IR1_2_q, decoder_1_out1);
  and and_2 (and_2_out, IR2_2_q, decoder_1_out2);
  and and_3 (and_3_out, IR3_2_q, decoder_1_out3);
  Hex_Digit_Display hex_digit_display_2 (.value(LedData[23:20]));  // open: dp
  Hex_Digit_Display hex_digit_display_3 (.value(LedData[27:24]));  // open: dp
  or or_4 (or_4_out, d_ff_1_q, IR1_2_q);
  or or_5 (or_5_out, d_ff_2_q, IR2_2_q);
  or or_6 (or_6_out, d_ff_3_q, IR3_2_q);
  D_Flip_Flop #(.trigger("rising"), .Pre_Clr_Positions("LEGACY"), .NegatePresetClear("false"), .enable("true"), .NewFFLayout("false")) d_ff_4 (
    .clk(and_1_out), .D(1'b1), .Q(d_ff_4_q), .reset(IR1_q));  // open: Qn, preset, en
  or or_7 (or_7_out, d_ff_4_q, IR1_q);
  D_Flip_Flop #(.trigger("rising"), .Pre_Clr_Positions("LEGACY"), .NegatePresetClear("false"), .enable("true"), .NewFFLayout("false")) d_ff_5 (
    .clk(and_2_out), .D(1'b1), .Q(d_ff_5_q), .reset(IR2_q));  // open: Qn, preset, en
  or or_8 (or_8_out, d_ff_5_q, IR2_q);
  D_Flip_Flop #(.trigger("rising"), .Pre_Clr_Positions("LEGACY"), .NegatePresetClear("false"), .enable("true"), .NewFFLayout("false")) d_ff_6 (
    .clk(and_3_out), .D(1'b1), .Q(d_ff_6_q), .reset(IR3_q));  // open: Qn, preset, en
  or or_9 (or_9_out, d_ff_6_q, IR3_q);
  Hex_Digit_Display hex_digit_display_4 (.value(LedData[15:12]));  // open: dp
  Hex_Digit_Display hex_digit_display_5 (.value(LedData[19:16]));  // open: dp
  and and_4 (and_4_out, ~W3, W1);  // AND_Gate
  or or_10 (\有中断吗 , and_4_out, and_5_out);
  and and_5 (and_5_out, W1, ~W2);  // AND_Gate
  Hex_Digit_Display hex_digit_display_6 (.value(LedData[7:4]));  // open: dp
  Hex_Digit_Display hex_digit_display_7 (.value(LedData[11:8]));  // open: dp
  // Probe on \总周期数 
  and and_6 (and_6_out, or_4_out, ~demultiplexer_1_out1);  // AND_Gate
  and and_7 (and_7_out, or_5_out, ~demultiplexer_1_out2);  // AND_Gate
  and and_8 (and_8_out, or_6_out, ~demultiplexer_1_out3);  // AND_Gate
  D_Flip_Flop #(.trigger("rising"), .Pre_Clr_Positions("LEGACY"), .NegatePresetClear("false"), .enable("true"), .NewFFLayout("false")) u_IR1 (
    .clk(CLK), .D(and_9_out), .Q(IR1_q));  // open: Qn, preset, en, reset
  and and_9 (and_9_out, or_7_out, ~demultiplexer_1_out1);  // AND_Gate
  D_Flip_Flop #(.trigger("rising"), .Pre_Clr_Positions("LEGACY"), .NegatePresetClear("false"), .enable("true"), .NewFFLayout("false")) u_IR2 (
    .clk(CLK), .D(and_10_out), .Q(IR2_q));  // open: Qn, preset, en, reset
  and and_10 (and_10_out, or_8_out, ~demultiplexer_1_out2);  // AND_Gate
  D_Flip_Flop #(.trigger("rising"), .Pre_Clr_Positions("LEGACY"), .NegatePresetClear("false"), .enable("true"), .NewFFLayout("false")) u_IR3 (
    .clk(CLK), .D(and_11_out), .Q(IR3_q));  // open: Qn, preset, en, reset
  and and_11 (and_11_out, or_9_out, ~demultiplexer_1_out3);  // AND_Gate
  Hex_Digit_Display hex_digit_display_8 (.value(LedData[3:0]));  // open: dp
  // Probe on \无条件跳转数 
  // Probe on \有条件跳转数 
  D_Flip_Flop #(.trigger("rising"), .Pre_Clr_Positions("LEGACY"), .NegatePresetClear("false"), .enable("true"), .NewFFLayout("false")) IR1_2 (
    .clk(CLK), .D(and_6_out), .Q(IR1_2_q));  // open: Qn, preset, en, reset
  D_Flip_Flop #(.trigger("rising"), .Pre_Clr_Positions("LEGACY"), .NegatePresetClear("false"), .enable("true"), .NewFFLayout("false")) IR2_2 (
    .clk(CLK), .D(and_7_out), .Q(IR2_2_q));  // open: Qn, preset, en, reset
  D_Flip_Flop #(.trigger("rising"), .Pre_Clr_Positions("LEGACY"), .NegatePresetClear("false"), .enable("true"), .NewFFLayout("false")) IR3_2 (
    .clk(CLK), .D(and_8_out), .Q(IR3_2_q));  // open: Qn, preset, en, reset
  Register #(.width(1), .trigger("rising"), .Select("low")) register_1 (
    .D(IR3_q), .Q(register_1_q), .clk(CLK));  // open: en, clr
  // Probe on PC
  // Probe on IR
  // Probe on RDin
  Priority_Encoder #(.select(2), .disabled("Z")) priority_encoder_1 (
    .in0(1'b1), .in1(IR1_2_q), .in2(IR2_2_q), .in3(IR3_2_q), .out(priority_encoder_1_out));  // open: gs, en_out, en_in
  and and_12 (and_12_out, IR1_2_q, ~IR1_q, ~IR2_q, ~register_1_q);  // AND_Gate
  and and_13 (and_13_out, IR2_2_q, ~IR2_q, ~register_1_q);  // AND_Gate
  and and_14 (and_14_out, IR3_2_q, ~register_1_q);  // AND_Gate
  or or_11 (IR1_t, IR1, IRA);
  Demultiplexer #(.select(2), .width(1), .tristate("false"), .disabled(0), .enable("false")) demultiplexer_1 (
    .out1(demultiplexer_1_out1), .out2(demultiplexer_1_out2), .out3(demultiplexer_1_out3), .in(ERET),
    .sel(priority_encoder_1_out));  // open: out0
  or or_12 (IR2_t, IR2, IRB);
  Multiplexer #(.select(1), .width(32), .disabled("Z"), .enable("false")) multiplexer_1 (
    .in0({JMP_PC[31:28], PC_4}), .in1(\PC存储点 ), .out(multiplexer_1_out), .sel(branch));
  Multiplexer #(.select(2), .width(32), .disabled("Z"), .enable("false")) multiplexer_2 (
    .in0(EPC), .in1(32'h30ac), .in2(32'h3158), .in3(32'h3204), .out(\中断入口地址 ), .sel(priority_encoder_2_out));
  Priority_Encoder #(.select(2), .disabled("Z")) priority_encoder_2 (
    .in0(1'b1), .in1(and_12_out), .in2(and_13_out), .in3(and_14_out), .out(priority_encoder_2_out));  // open: gs, en_out, en_in
  or or_13 (or_13_out, ERET, \CPU中断请求 );
  Counter #(.width(2), .max('h3), .ongoal("stay"), .trigger("rising"), .behavior("new")) counter_1 (
    .D(2'b00), .count(or_13_out), .Q(count), .clk(CLK), .down(ERET));  // open: load, carry, clr, preset
  Register #(.width(2), .trigger("rising"), .Select("low")) IM (
    .D(priority_encoder_2_out), .Q(IM_q), .clk(CLK), .clr(not_1_out));  // open: en
  not not_1 (not_1_out, or_14_out);
  or or_14 (or_14_out, W1, W2, W3);
  or or_15 (IR3_t, IR3, IRC);
  Decoder #(.select(2), .tristate("false"), .disabled("Z"), .enable("false")) decoder_2 (
    .out0(decoder_2_out0), .out1(decoder_2_out1), .out2(decoder_2_out2), .sel(count));  // open: out3
  Multiplexer #(.select(2), .width(32), .disabled("Z"), .enable("false")) multiplexer_3 (
    .in0(multiplexer_1_out), .in1(JMP_PC), .in2(JR_PC), .in3(JR_PC), .out(multiplexer_3_out), .sel({JR, JMP}));
  Comparator #(.width(2), .mode("unsigned")) comparator_1 (
    .a(priority_encoder_2_out), .b(IM_q), .eq(comparator_1_eq));  // open: gt, lt
  Register #(.width(1), .trigger("rising"), .Select("low")) IE (
    .D(and_15_out), .Q(IE_q), .clk(CLK), .preset(MTC0));  // open: en, clr, cs
  nor nor_1 (\CPU中断请求 , comparator_1_eq, IE_q);
  and and_15 (and_15_out, \CPU中断请求 , ~MFC0, ~ERET);  // AND_Gate
  Register #(.width(32), .trigger("rising"), .Select("low")) u_EPC (
    .D(multiplexer_3_out), .en(and_16_out), .Q(EPC_q), .clk(CLK));  // open: clr
  and and_16 (and_16_out, decoder_2_out0, \CPU中断请求 );
  Register #(.width(32), .trigger("rising"), .Select("low")) EPC_2 (
    .D(multiplexer_3_out), .en(and_17_out), .Q(EPC_2_q), .clk(CLK));  // open: clr
  and and_17 (and_17_out, decoder_2_out1, \CPU中断请求 );
  Register #(.width(32), .trigger("rising"), .Select("low")) EPC_3 (
    .D(multiplexer_3_out), .en(and_18_out), .Q(EPC_3_q), .clk(CLK));  // open: clr
  and and_18 (and_18_out, decoder_2_out2, \CPU中断请求 );
  Multiplexer #(.select(2), .width(32), .disabled("Z"), .enable("false")) multiplexer_4 (
    .in1(EPC_q), .in2(EPC_2_q), .in3(EPC_3_q), .out(EPC), .sel(count));  // open: in0
  Comparator #(.width(6), .mode("twosComplement")) comparator_2 (
    .a(IR[31:26]), .b(6'b010000), .eq(comparator_2_eq));  // open: gt, lt
  Comparator #(.width(6), .mode("twosComplement")) comparator_3 (
    .a(IR[5:0]), .b(6'b011000), .eq(comparator_3_eq));  // open: gt, lt
  Comparator #(.width(5), .mode("twosComplement")) comparator_4 (
    .a(IR[25:21]), .b({5{1'b0}}), .eq(comparator_4_eq));  // open: gt, lt
  Comparator #(.width(5), .mode("twosComplement")) comparator_5 (
    .a(IR[25:21]), .b(5'b00100), .eq(comparator_5_eq));  // open: gt, lt
  and and_19 (ERET, comparator_2_eq, comparator_3_eq);
  and and_20 (MFC0, comparator_2_eq, comparator_4_eq);
  and and_21 (MTC0, comparator_2_eq, comparator_5_eq);
  Multiplexer #(.select(1), .width(32), .disabled("Z"), .enable("false")) multiplexer_5 (
    .in0({JMP_PC[31:28], PC_4}), .in1(adder_2_out), .out(\PC存储点 ), .sel(branch));
  Multiplexer #(.select(1), .width(32), .disabled("Z"), .enable("false")) multiplexer_6 (
    .in0(\PC存储点 ), .in1(EPC), .out(multiplexer_6_out), .sel(ERET));
  Multiplexer #(.select(1), .width(32), .disabled("Z"), .enable("false")) multiplexer_7 (
    .in0(multiplexer_6_out), .in1(\中断入口地址 ), .out(multiplexer_7_out), .sel(\CPU中断请求 ));
  Comparator #(.width(32), .mode("twosComplement")) comparator_6 (
    .a(JR_PC), .b(32'h22), .eq(comparator_6_eq));  // open: gt, lt
  Multiplexer #(.select(2), .width(32), .disabled("Z"), .enable("false")) multiplexer_8 (
    .in0(multiplexer_7_out), .in1(JMP_PC), .in2(JR_PC), .in3(JR_PC), .out(multiplexer_8_out), .sel({JR, JMP}));
  not not_2 (not_2_out, stop);
  not not_3 (not_3_out, comparator_6_eq);
  Register #(.width(32), .trigger("rising"), .Select("low")) u_PC (
    .D(multiplexer_8_out), .en(not_2_out), .Q(PC), .clk(CLK), .clr(1'b0));
  Counter #(.width(16), .max('hffff), .ongoal("wrap"), .trigger("rising"), .behavior("old")) counter_2 (
    .D({16{1'b0}}), .count(not_2_out), .Q(\总周期数 ), .clk(CLK), .clr(1'b0));  // open: load, carry, preset
  and and_22 (\output , Syscall, comparator_6_eq);
  and and_23 (stop, not_3_out, Syscall);
  assign controlled_buffer_1_out = \output  ? MDin : 32'bz;  // Controlled_Buffer controlled_buffer_1
  Adder #(.width(32)) adder_1 (.a(PC), .b(32'h4), .out({JMP_PC[31:28], PC_4}), .cin(1'b0));  // open: cout
  Register #(.width(32), .trigger("rising"), .Select("low")) PC_2 (
    .D(controlled_buffer_1_out), .Q(LedData), .clk(CLK));  // open: en, clr
  ROM #(.addrWidth(10), .dataWidth(32), .Select("high")) rom_1 ();  // open: addr, data
  ROM #(.addrWidth(10), .dataWidth(32), .Select("high")) rom_2 (.addr(PC[11:2]), .data(IR));
  Multiplexer #(.select(1), .width(5), .disabled("Z"), .enable("false")) multiplexer_9 (
    .in0(IR[20:16]), .in1(IR[15:11]), .out(multiplexer_9_out), .sel(\单周期硬布线控制器_1_regdst ));
  \单周期硬布线控制器  \u_单周期硬布线控制器_1  (
    .Func(IR[5:0]), .OP(IR[31:26]), .ALU_OP(\单周期硬布线控制器_1_alu_op ), .MemToReg(\单周期硬布线控制器_1_memtoreg ),
    .MemWrite(MemWrite), .ALU_SRC(\单周期硬布线控制器_1_alu_src ), .RegWrite(RegWrite), .SysCALL(Syscall),
    .SignedExt(SignedExt), .RegDst(\单周期硬布线控制器_1_regdst ), .JR(JR), .JMP(JMP), .Beq(\单周期硬布线控制器_1_beq ),
    .JAL(JAL), .Bne(\单周期硬布线控制器_1_bne ), .BLEZ(BLEZ), .LB(LB));
  Multiplexer #(.select(1), .width(5), .disabled("Z"), .enable("false")) multiplexer_10 (
    .in0(IR[25:21]), .in1(5'b00010), .out(multiplexer_10_out), .sel(Syscall));
  Multiplexer #(.select(1), .width(5), .disabled("Z"), .enable("false")) multiplexer_11 (
    .in0(IR[20:16]), .in1(5'b00100), .out(multiplexer_11_out), .sel(Syscall));
  Multiplexer #(.select(1), .width(5), .disabled("Z"), .enable("false")) multiplexer_12 (
    .in0(multiplexer_9_out), .in1({5{1'b1}}), .out(multiplexer_12_out), .sel(JAL));
  assign bit_extender_1_out = {{6{1'b0}}, IR[25:0]};  // Bit_Extender bit_extender_1
  assign bit_extender_2_out = {{16{1'b0}}, IR[15:0]};  // Bit_Extender bit_extender_2
  assign bit_extender_3_out = {{16{IR[15]}}, IR[15:0]};  // Bit_Extender bit_extender_3
  Counter #(.width(16), .max('hffff), .ongoal("wrap"), .trigger("rising"), .behavior("old")) counter_3 (
    .D({16{1'b0}}), .count(JMP), .Q(\无条件跳转数 ), .clk(CLK));  // open: load, carry, clr, preset
  Shifter #(.width(32), .shift("ll")) shifter_1 (
    .in(bit_extender_1_out), .\dist (5'b00010), .out({shifter_1_out, JMP_PC[27:0]}));
  Multiplexer #(.select(1), .width(32), .disabled("Z"), .enable("false")) multiplexer_13 (
    .in0(bit_extender_2_out), .in1(bit_extender_3_out), .out(multiplexer_13_out), .sel(SignedExt));
  Shifter #(.width(32), .shift("ll")) shifter_2 (.in(bit_extender_3_out), .\dist (5'b00010), .out(shifter_2_out));
  and and_24 (and_24_out, \单周期硬布线控制器_1_beq , mips_alu_1_equal);
  MIPS_Regifile mips_regifile_1 (
    .Din(RDin), .Clk(CLK), .R1(JR_PC), .R2(MDin), .WE(RegWrite), .W_num(multiplexer_12_out),
    .R1_num(multiplexer_10_out), .R2_num(multiplexer_11_out));
  Multiplexer #(.select(1), .width(32), .disabled("Z"), .enable("false")) multiplexer_14 (
    .in0(MDin), .in1(multiplexer_13_out), .out(multiplexer_14_out), .sel(\单周期硬布线控制器_1_alu_src ));
  Adder #(.width(32)) adder_2 (
    .a(shifter_2_out), .b({JMP_PC[31:28], PC_4}), .out(adder_2_out), .cin(1'b0));  // open: cout
  or or_16 (branch, and_24_out, and_25_out);
  and and_25 (and_25_out, \单周期硬布线控制器_1_bne , not_4_out);
  not not_4 (not_4_out, mips_alu_1_equal);
  MIPS_ALU mips_alu_1 (
    .X(JR_PC), .Y(multiplexer_14_out), .AluOP(\单周期硬布线控制器_1_alu_op ), .Equal(mips_alu_1_equal),
    .Result(mips_alu_1_result), .shamt(IR[10:6]));  // open: Result_2, BLEZ
  Counter #(.width(16), .max('hffff), .ongoal("wrap"), .trigger("rising"), .behavior("old")) counter_4 (
    .D({16{1'b0}}), .count(branch), .Q(\有条件跳转数 ), .clk(CLK));  // open: load, carry, clr, preset
  Multiplexer #(.select(1), .width(32), .disabled("Z"), .enable("false")) multiplexer_15 (
    .in0(multiplexer_16_out), .in1({JMP_PC[31:28], PC_4}), .out(RDin), .sel(JAL));
  RAM #(.addrWidth(10), .dataWidth(32), .bus("separate"), .Select("high")) ram_1 (
    .addr(mips_alu_1_result[11:2]), .din(MDin), .data(ram_1_data), .str(MemWrite), .sel(1'b1), .clk(CLK),
    .clr(1'b0));  // open: ld
  assign bit_extender_4_out = {{24{undriven[7]}}, undriven};  // Bit_Extender bit_extender_4
  Multiplexer #(.select(1), .width(32), .disabled("Z"), .enable("false")) multiplexer_16 (
    .in0(mips_alu_1_result), .in1(ram_1_data), .out(multiplexer_16_out), .sel(\单周期硬布线控制器_1_memtoreg ));

  // Other names for the same wires on the sheet: a0[31:0] = MDin; FUNC[5:0] = IR[5:0]; MF[4:0] = IR[25:21];
  //   OP[5:0] = IR[31:26]; PC_4[31:28] = JMP_PC[31:28]; v0[31:0] = JR_PC

  // Notes on the sheet:
  //   中断等待指示
  //   数码管输出
  //   Reset 
  //   Reset 
  //   Reset 
  //   Reset 
  //   Reset 
  //   Reset 
  //   中断信号采样参考电路
  //   为方便自动评测，需要输出PC，IR，寄存器堆写如数据RDin
  //   RAM写使能MemWrite、RAM写入数据MDin等信号
  //   总复位信号应将除ROM以外所有存储组件全部清零
  //   数码管输出应该用寄存器锁存，否则显示数据只能一闪而过
  //   指令存储器
  //   contents of rom_1 (hex, n*v repeats v):
  //   20110001 8000c05 20110001 20120002 20130003 8000c09 20110001 20120002 20130003 8000c0d 20110001
  //   20120002 20130003 8000c11 20110001 20120002 20130003 c000cb8 20100001 20110001 118fc0 112020
  //   20020022 c 118882 12200001 8000c15 112020 20020022 c 20110001 118880 112020 20020022 c 12200001
  //   8000c1f 20110001 118fc0 112020 20020022 c 1188c3 112020 20020022 c 118903 112020 20020022 c 118903
  //   112020 20020022 c 118903 112020 20020022 c 118903 112020 20020022 c 118903 112020 20020022 c 118903
  //   112020 20020022 c 118903 112020 20020022 c 20100001 109fc0 139fc3 8021 2012000c 24160003 26100001
  //   3210000f 20080008 20090001 139900 2709825 132020 20020022 c 1094022 1500fff9 22100001 2018000f
  //   2188024 108700 20080008 20090001 139902 2709825 132021 20020022 c 1094022 1500fff9 108702 2c9b022
  //   12c00001 8000c50 4020 1084027 84400 3508ffff 82021 20020022 c 2010ffff 20110000 ae300000 22100001
  //   22310004 ae300000 22100001 22310004 ae300000 22100001 22310004 ae300000 22100001 22310004 ae300000
  //   22100001 22310004 ae300000 22100001 22310004 ae300000 22100001 22310004 ae300000 22100001 22310004
  //   ae300000 22100001 22310004 ae300000 22100001 22310004 ae300000 22100001 22310004 ae300000 22100001
  //   22310004 ae300000 22100001 22310004 ae300000 22100001 22310004 ae300000 22100001 22310004 ae300000
  //   22100001 22310004 22100001 8020 2011003c 8e130000 8e340000 274402a 11000002 ae330000 ae140000
  //   2231fffc 1611fff8 102020 20020022 c 22100004 2011003c 1611fff2 2002000a c 20100000 22100001 102020
  //   20020022 c 22100002 102020 20020022 c 22100003 102020 20020022 c 22100004 102020 20020022 c 22100005
  //   102020 20020022 c 22100006 102020 20020022 c 22100007 102020 20020022 c 22100008 102020 20020022
  //   20020022 c 3e00008
  //   contents of rom_2 (hex, n*v repeats v):
  //   201d07d0 20100001 109fc0 139fc3 8021 2012000c 24160008 26100001 3210000f 20080008 20090001 139900
  //   2709825 132020 20020022 c 1094022 1500fff9 22100001 2018000f 2188024 108700 20080008 20090001 139902
  //   2709825 132021 20020022 c 1094022 1500fff9 108702 2c9b022 12c00001 8000c07 4020 1084027 84400
  //   3508ffff 82021 20020022 c 8000c01 afa20000 23bd0004 afa40000 23bd0004 afb00000 23bd0004 afb30000
  //   23bd0004 afb40000 23bd0004 afb50000 23bd0004 afb60000 23bd0004 40000000 20160001 20140003 20150001
  //   168020 108100 2149825 132020 20020022 c 1600fffa 295a022 1680fff7 40800000 23bdfffc 8fb60000
  //   23bdfffc 8fb50000 23bdfffc 8fb40000 23bdfffc 8fb30000 23bdfffc 8fb00000 23bdfffc 8fa40000 23bdfffc
  //   8fa20000 42000018 afa20000 23bd0004 afa40000 23bd0004 afb00000 23bd0004 afb30000 23bd0004 afb40000
  //   23bd0004 afb50000 23bd0004 afb60000 23bd0004 40000000 20160002 20140003 20150001 168020 108100
  //   2149825 132020 20020022 c 1600fffa 295a022 1680fff7 40800000 23bdfffc 8fb60000 23bdfffc 8fb50000
  //   23bdfffc 8fb40000 23bdfffc 8fb30000 23bdfffc 8fb00000 23bdfffc 8fa40000 23bdfffc 8fa20000 42000018
  //   afa20000 23bd0004 afa40000 23bd0004 afb00000 23bd0004 afb30000 23bd0004 afb40000 23bd0004 afb50000
  //   23bd0004 afb60000 23bd0004 40000000 20160003 20140003 20150001 168020 108100 2149825 132020 20020022
  //   c 1600fffa 295a022 1680fff7 40800000 23bdfffc 8fb60000 23bdfffc 8fb50000 23bdfffc 8fb40000 23bdfffc
  //   8fb30000 23bdfffc 8fb00000 23bdfffc 8fa40000 23bdfffc 8fa20000 42000018
  //   JMP
  //   JR
  //   OP
  //   Func
  //   rs
  //   rt
  //   rd
  //   shamt
  //   Beq
  //   Bne
  //   MemToReg
  //   MemWrite
  //   AluOP
  //   AluSrcB
  //   RegWrite
  //   JAL
  //   RegDst
endmodule

module \单周期MIPS_单级中断  (
  input  IR1,
  input  IR2,
  input  IR3,
  output RegWrite,
  output MemWrite,
  output [31:0] PC,
  output [31:0] IR,
  output [31:0] RDin,
  output [31:0] MDin,
  output [31:0] LedData
);

  wire and_1_out, and_2_out, and_3_out, and_5_out, and_6_out, and_10_out, and_11_out, branch, CLK,
       comparator_1_eq, comparator_2_eq, comparator_3_eq, \CPU中断请求 , d_ff_1_q, d_ff_2_q, d_ff_3_q,
       demultiplexer_1_out1, demultiplexer_1_out2, demultiplexer_1_out3, ERET, Go, IE_q, IR1_q, IR1_t, IR2_q,
       IR2_t, IR3_q, IR3_t, IRA, IRB, IRC, JAL, JMP, JR, mips_alu_1_equal, not_1_out, not_2_out, not_3_out,
       not_4_out, or_4_out, or_5_out, or_6_out, \output , priority_encoder_1_gs, SignedExt, stop, Syscall,
       W1, W2, W3, \单周期硬布线控制器_1_alu_src , \单周期硬布线控制器_1_beq , \单周期硬布线控制器_1_bne , \单周期硬布线控制器_1_memtoreg ,
       \单周期硬布线控制器_1_regdst ;
  wire [1:0] priority_encoder_1_out, register_1_q;
  wire [3:0] \单周期硬布线控制器_1_alu_op ;
  wire [4:0] multiplexer_8_out, multiplexer_9_out, multiplexer_10_out, multiplexer_11_out;
  wire [15:0] \总周期数 , \无条件跳转数 , \有条件跳转数 ;
  wire [27:0] PC_4;
  wire [31:0] adder_2_out, bit_extender_1_out, bit_extender_2_out, bit_extender_3_out,
       controlled_buffer_1_out, EPC, JMP_PC, JR_PC, mips_alu_1_result, multiplexer_1_out, multiplexer_3_out,
       multiplexer_5_out, multiplexer_6_out, multiplexer_7_out, multiplexer_12_out, multiplexer_13_out,
       multiplexer_15_out, \PC存储点 , ram_1_data, shifter_2_out, \中断入口地址 ;
  wire [31:28] shifter_1_out;

  Clock #(.highDuration(1), .lowDuration(1)) clock_1 (.out(CLK));
  Button _1 (.out(IRA));
  Button _2 (.out(IRB));
  Button _3 (.out(IRC));
  Button \u_继续运行  (.out(Go));
  LED #(.active("true")) led_1 (.in(W1));
  LED #(.active("true")) led_2 (.in(W2));
  LED #(.active("true")) led_3 (.in(W3));
  or or_1 (W1, IR1_q, d_ff_1_q);
  or or_2 (W2, IR2_q, d_ff_2_q);
  or or_3 (W3, IR3_q, d_ff_3_q);
  Hex_Digit_Display hex_digit_display_1 (.value(LedData[31:28]));  // open: dp
  D_Flip_Flop #(.trigger("rising"), .Pre_Clr_Positions("LEGACY"), .NegatePresetClear("false"), .enable("true"), .NewFFLayout("false")) d_ff_1 (
    .clk(IR1_t), .D(1'b1), .Q(d_ff_1_q), .reset(IR1_q));  // open: Qn, preset, en
  D_Flip_Flop #(.trigger("rising"), .Pre_Clr_Positions("LEGACY"), .NegatePresetClear("false"), .enable("true"), .NewFFLayout("false")) d_ff_2 (
    .clk(IR2_t), .D(1'b1), .Q(d_ff_2_q), .reset(IR2_q));  // open: Qn, preset, en
  D_Flip_Flop #(.trigger("rising"), .Pre_Clr_Positions("LEGACY"), .NegatePresetClear("false"), .enable("true"), .NewFFLayout("false")) d_ff_3 (
    .clk(IR3_t), .D(1'b1), .Q(d_ff_3_q), .reset(IR3_q));  // open: Qn, preset, en
  Hex_Digit_Display hex_digit_display_2 (.value(LedData[27:24]));  // open: dp
  Hex_Digit_Display hex_digit_display_3 (.value(LedData[23:20]));  // open: dp
  or or_4 (or_4_out, d_ff_1_q, IR1_q);
  or or_5 (or_5_out, d_ff_2_q, IR2_q);
  or or_6 (or_6_out, d_ff_3_q, IR3_q);
  Hex_Digit_Display hex_digit_display_4 (.value(LedData[19:16]));  // open: dp
  Hex_Digit_Display hex_digit_display_5 (.value(LedData[15:12]));  // open: dp
  and and_1 (and_1_out, or_4_out, ~demultiplexer_1_out1);  // AND_Gate
  and and_2 (and_2_out, or_5_out, ~demultiplexer_1_out2);  // AND_Gate
  and and_3 (and_3_out, or_6_out, ~demultiplexer_1_out3);  // AND_Gate
  Hex_Digit_Display hex_digit_display_6 (.value(LedData[11:8]));  // open: dp
  Hex_Digit_Display hex_digit_display_7 (.value(LedData[7:4]));  // open: dp
  // Probe on \总周期数 
  D_Flip_Flop #(.trigger("rising"), .Pre_Clr_Positions("LEGACY"), .NegatePresetClear("false"), .enable("true"), .NewFFLayout("false")) u_IR1 (
    .clk(CLK), .D(and_1_out), .Q(IR1_q));  // open: Qn, preset, en, reset
  D_Flip_Flop #(.trigger("rising"), .Pre_Clr_Positions("LEGACY"), .NegatePresetClear("false"), .enable("true"), .NewFFLayout("false")) u_IR2 (
    .clk(CLK), .D(and_2_out), .Q(IR2_q));  // open: Qn, preset, en, reset
  D_Flip_Flop #(.trigger("rising"), .Pre_Clr_Positions("LEGACY"), .NegatePresetClear("false"), .enable("true"), .NewFFLayout("false")) u_IR3 (
    .clk(CLK), .D(and_3_out), .Q(IR3_q));  // open: Qn, preset, en, reset
  not not_1 (not_1_out, IE_q);
  Hex_Digit_Display hex_digit_display_8 (.value(LedData[3:0]));  // open: dp
  // Probe on \无条件跳转数 
  // Probe on \有条件跳转数 
  Register #(.width(1), .trigger("rising"), .Select("low")) IE (
    .D(\CPU中断请求 ), .en(not_1_out), .Q(IE_q), .clk(CLK), .clr(ERET));
  Multiplexer #(.select(1), .width(32), .disabled("Z"), .enable("false")) multiplexer_1 (
    .in0({JMP_PC[31:28], PC_4}), .in1(\PC存储点 ), .out(multiplexer_1_out), .sel(branch));
  // Probe on PC
  // Probe on IR
  // Probe on RDin
  Demultiplexer #(.select(2), .width(1), .tristate("false"), .disabled("Z"), .enable("false")) demultiplexer_1 (
    .out1(demultiplexer_1_out1), .out2(demultiplexer_1_out2), .out3(demultiplexer_1_out3), .in(ERET),
    .sel(register_1_q));  // open: out0
  Priority_Encoder #(.select(2), .disabled("Z")) priority_encoder_1 (
    .in0(1'b0), .in1(IR1_q), .in2(IR2_q), .in3(IR3_q), .out(priority_encoder_1_out),
    .gs(priority_encoder_1_gs));  // open: en_out, en_in
  and and_4 (\CPU中断请求 , priority_encoder_1_gs, ~IE_q);  // AND_Gate
  or or_7 (IR1_t, IR1, IRA);
  Multiplexer #(.select(2), .width(32), .disabled("Z"), .enable("false")) multiplexer_2 (
    .in1(32'h30ac), .in2(32'h3150), .in3(32'h31f4), .out(\中断入口地址 ), .sel(priority_encoder_1_out));  // open: in0
  and and_5 (and_5_out, \CPU中断请求 , ~ERET);  // AND_Gate
  Multiplexer #(.select(2), .width(32), .disabled("Z"), .enable("false")) multiplexer_3 (
    .in0(multiplexer_1_out), .in1(JMP_PC), .in2(JR_PC), .in3(JR_PC), .out(multiplexer_3_out), .sel({JR, JMP}));
  or or_8 (IR2_t, IR2, IRB);
  Register #(.width(2), .trigger("rising"), .Select("low")) register_1 (
    .D(priority_encoder_1_out), .Q(register_1_q), .clk(and_6_out));  // open: en, clr
  and and_6 (and_6_out, \CPU中断请求 , ~ERET);  // AND_Gate
  Register #(.width(32), .trigger("rising"), .Select("low")) u_EPC (
    .D(multiplexer_3_out), .en(and_5_out), .Q(EPC), .clk(CLK));  // open: clr
  or or_9 (IR3_t, IR3, IRC);
  Comparator #(.width(6), .mode("twosComplement")) comparator_1 (
    .a(IR[31:26]), .b(6'b010000), .eq(comparator_1_eq));  // open: gt, lt
  Comparator #(.width(6), .mode("twosComplement")) comparator_2 (
    .a(IR[5:0]), .b(6'b011000), .eq(comparator_2_eq));  // open: gt, lt
  and and_7 (ERET, comparator_1_eq, comparator_2_eq);
  Multiplexer #(.select(1), .width(32), .disabled("Z"), .enable("false")) multiplexer_4 (
    .in0({JMP_PC[31:28], PC_4}), .in1(adder_2_out), .out(\PC存储点 ), .sel(branch));
  Multiplexer #(.select(1), .width(32), .disabled("Z"), .enable("false")) multiplexer_5 (
    .in0(\PC存储点 ), .in1(\中断入口地址 ), .out(multiplexer_5_out), .sel(\CPU中断请求 ));
  Multiplexer #(.select(1), .width(32), .disabled("Z"), .enable("false")) multiplexer_6 (
    .in0(multiplexer_5_out), .in1(EPC), .out(multiplexer_6_out), .sel(ERET));
  Comparator #(.width(32), .mode("twosComplement")) comparator_3 (
    .a(JR_PC), .b(32'h22), .eq(comparator_3_eq));  // open: gt, lt
  Multiplexer #(.select(2), .width(32), .disabled("Z"), .enable("false")) multiplexer_7 (
    .in0(multiplexer_6_out), .in1(JMP_PC), .in2(JR_PC), .in3(JR_PC), .out(multiplexer_7_out), .sel({JR, JMP}));
  not not_2 (not_2_out, stop);
  not not_3 (not_3_out, comparator_3_eq);
  Register #(.width(32), .trigger("rising"), .Select("low")) u_PC (
    .D(multiplexer_7_out), .en(not_2_out), .Q(PC), .clk(CLK), .clr(1'b0));
  Counter #(.width(16), .max('hffff), .ongoal("wrap"), .trigger("rising"), .behavior("old")) counter_1 (
    .D({16{1'b0}}), .count(not_2_out), .Q(\总周期数 ), .clk(CLK), .clr(1'b0));  // open: load, carry, preset
  and and_8 (\output , Syscall, comparator_3_eq);
  and and_9 (stop, not_3_out, Syscall);
  Adder #(.width(32)) adder_1 (.a(PC), .b(32'h4), .out({JMP_PC[31:28], PC_4}), .cin(1'b0));  // open: cout
  assign controlled_buffer_1_out = \output  ? MDin : 32'bz;  // Controlled_Buffer controlled_buffer_1
  Register #(.width(32), .trigger("rising"), .Select("low")) PC_2 (
    .D(controlled_buffer_1_out), .Q(LedData), .clk(CLK));  // open: en, clr
  ROM #(.addrWidth(10), .dataWidth(32), .Select("high")) rom_1 (.addr(PC[11:2]), .data(IR));
  \单周期硬布线控制器  \u_单周期硬布线控制器_1  (
    .Func(IR[5:0]), .OP(IR[31:26]), .ALU_OP(\单周期硬布线控制器_1_alu_op ), .MemToReg(\单周期硬布线控制器_1_memtoreg ),
    .MemWrite(MemWrite), .ALU_SRC(\单周期硬布线控制器_1_alu_src ), .RegWrite(RegWrite), .SysCALL(Syscall),
    .SignedExt(SignedExt), .RegDst(\单周期硬布线控制器_1_regdst ), .JR(JR), .JMP(JMP), .Beq(\单周期硬布线控制器_1_beq ),
    .JAL(JAL), .Bne(\单周期硬布线控制器_1_bne ));  // open: BLEZ, LB
  Multiplexer #(.select(1), .width(5), .disabled("Z"), .enable("false")) multiplexer_8 (
    .in0(IR[20:16]), .in1(IR[15:11]), .out(multiplexer_8_out), .sel(\单周期硬布线控制器_1_regdst ));
  Multiplexer #(.select(1), .width(5), .disabled("Z"), .enable("false")) multiplexer_9 (
    .in0(IR[25:21]), .in1(5'b00010), .out(multiplexer_9_out), .sel(Syscall));
  Multiplexer #(.select(1), .width(5), .disabled("Z"), .enable("false")) multiplexer_10 (
    .in0(IR[20:16]), .in1(5'b00100), .out(multiplexer_10_out), .sel(Syscall));
  Multiplexer #(.select(1), .width(5), .disabled("Z"), .enable("false")) multiplexer_11 (
    .in0(multiplexer_8_out), .in1({5{1'b1}}), .out(multiplexer_11_out), .sel(JAL));
  assign bit_extender_1_out = {{6{1'b0}}, IR[25:0]};  // Bit_Extender bit_extender_1
  assign bit_extender_2_out = {{16{1'b0}}, IR[15:0]};  // Bit_Extender bit_extender_2
  assign bit_extender_3_out = {{16{IR[15]}}, IR[15:0]};  // Bit_Extender bit_extender_3
  Counter #(.width(16), .max('hffff), .ongoal("wrap"), .trigger("rising"), .behavior("old")) counter_2 (
    .D({16{1'b0}}), .count(JMP), .Q(\无条件跳转数 ), .clk(CLK));  // open: load, carry, clr, preset
  MIPS_Regifile mips_regifile_1 (
    .Din(RDin), .Clk(CLK), .R1(JR_PC), .R2(MDin), .WE(RegWrite), .W_num(multiplexer_11_out),
    .R1_num(multiplexer_9_out), .R2_num(multiplexer_10_out));
  Shifter #(.width(32), .shift("ll")) shifter_1 (
    .in(bit_extender_1_out), .\dist (5'b00010), .out({shifter_1_out, JMP_PC[27:0]}));
  Multiplexer #(.select(1), .width(32), .disabled("Z"), .enable("false")) multiplexer_12 (
    .in0(bit_extender_2_out), .in1(bit_extender_3_out), .out(multiplexer_12_out), .sel(SignedExt));
  Shifter #(.width(32), .shift("ll")) shifter_2 (.in(bit_extender_3_out), .\dist (5'b00010), .out(shifter_2_out));
  and and_10 (and_10_out, \单周期硬布线控制器_1_beq , mips_alu_1_equal);
  Multiplexer #(.select(1), .width(32), .disabled("Z"), .enable("false")) multiplexer_13 (
    .in0(MDin), .in1(multiplexer_12_out), .out(multiplexer_13_out), .sel(\单周期硬布线控制器_1_alu_src ));
  Adder #(.width(32)) adder_2 (
    .a(shifter_2_out), .b({JMP_PC[31:28], PC_4}), .out(adder_2_out), .cin(1'b0));  // open: cout
  or or_10 (branch, and_10_out, and_11_out);
  and and_11 (and_11_out, \单周期硬布线控制器_1_bne , not_4_out);
  not not_4 (not_4_out, mips_alu_1_equal);
  MIPS_ALU mips_alu_1 (
    .X(JR_PC), .Y(multiplexer_13_out), .AluOP(\单周期硬布线控制器_1_alu_op ), .Equal(mips_alu_1_equal),
    .Result(mips_alu_1_result), .shamt(IR[10:6]));  // open: Result_2, BLEZ
  Counter #(.width(16), .max('hffff), .ongoal("wrap"), .trigger("rising"), .behavior("old")) counter_3 (
    .D({16{1'b0}}), .count(branch), .Q(\有条件跳转数 ), .clk(CLK));  // open: load, carry, clr, preset
  Multiplexer #(.select(1), .width(32), .disabled("Z"), .enable("false")) multiplexer_14 (
    .in0(multiplexer_15_out), .in1({JMP_PC[31:28], PC_4}), .out(RDin), .sel(JAL));
  RAM #(.addrWidth(10), .dataWidth(32), .bus("separate"), .Select("high")) ram_1 (
    .addr(mips_alu_1_result[11:2]), .din(MDin), .data(ram_1_data), .str(MemWrite), .sel(1'b1), .clk(CLK),
    .clr(1'b0));  // open: ld
  Multiplexer #(.select(1), .width(32), .disabled("Z"), .enable("false")) multiplexer_15 (
    .in0(mips_alu_1_result), .in1(ram_1_data), .out(multiplexer_15_out), .sel(\单周期硬布线控制器_1_memtoreg ));

  // Other names for the same wires on the sheet: a0[31:0] = MDin; FUNC[5:0] = IR[5:0]; MF[4:0] = IR[25:21];
  //   OP[5:0] = IR[31:26]; PC_4[31:28] = JMP_PC[31:28]; v0[31:0] = JR_PC

  // Notes on the sheet:
  //   中断等待指示
  //   数码管输出
  //   Reset 
  //   Reset 
  //   Reset 
  //   总复位信号应将除ROM以外所有存储组件全部清零
  //   数码管输出应该用寄存器锁存，否则显示数据只能一闪而过
  //   中断信号采样参考电路
  //   为方便自动评测，需要输出PC，IR，寄存器堆写如数据RDin
  //   RAM写使能MemWrite、RAM写入数据MDin等信号
  //   指令存储器
  //   contents of rom_1 (hex, n*v repeats v):
  //   201d07d0 20100001 109fc0 139fc3 8021 2012000c 24160008 26100001 3210000f 20080008 20090001 139900
  //   2709825 132020 20020022 c 1094022 1500fff9 22100001 2018000f 2188024 108700 20080008 20090001 139902
  //   2709825 132021 20020022 c 1094022 1500fff9 108702 2c9b022 12c00001 8000c07 4020 1084027 84400
  //   3508ffff 82021 20020022 c 8000c01 afa20000 23bd0004 afa40000 23bd0004 afb00000 23bd0004 afb30000
  //   23bd0004 afb40000 23bd0004 afb50000 23bd0004 afb60000 23bd0004 20160001 20140003 20150001 168020
  //   108100 2149825 132020 20020022 c 1600fffa 295a022 1680fff7 23bdfffc 8fb60000 23bdfffc 8fb50000
  //   23bdfffc 8fb40000 23bdfffc 8fb30000 23bdfffc 8fb00000 23bdfffc 8fa40000 23bdfffc 8fa20000 42000018
  //   afa20000 23bd0004 afa40000 23bd0004 afb00000 23bd0004 afb30000 23bd0004 afb40000 23bd0004 afb50000
  //   23bd0004 afb60000 23bd0004 20160002 20140003 20150001 168020 108100 2149825 132020 20020022 c
  //   1600fffa 295a022 1680fff7 23bdfffc 8fb60000 23bdfffc 8fb50000 23bdfffc 8fb40000 23bdfffc 8fb30000
  //   23bdfffc 8fb00000 23bdfffc 8fa40000 23bdfffc 8fa20000 42000018 afa20000 23bd0004 afa40000 23bd0004
  //   afb00000 23bd0004 afb30000 23bd0004 afb40000 23bd0004 afb50000 23bd0004 afb60000 23bd0004 20160003
  //   20140003 20150001 168020 108100 2149825 132020 20020022 c 1600fffa 295a022 1680fff7 23bdfffc
  //   8fb60000 23bdfffc 8fb50000 23bdfffc 8fb40000 23bdfffc 8fb30000 23bdfffc 8fb00000 23bdfffc 8fa40000
  //   23bdfffc 8fa20000 42000018
  //   JMP
  //   JR
  //   OP
  //   Func
  //   rs
  //   rt
  //   rd
  //   shamt
  //   Beq
  //   Bne
  //   MemToReg
  //   MemWrite
  //   AluOP
  //   AluSrcB
  //   RegWrite
  //   JAL
  //   RegDst
endmodule
module \单周期MIPS_多级中断  (
  input  IR1,
  input  IR2,
  input  IR3,
  output RegWrite,
  output MemWrite,
  output [31:0] PC,
  output [31:0] IR,
  output [31:0] RDin,
  output [31:0] MDin,
  output [31:0] LedData
);

  wire and_1_out, and_2_out, and_3_out, and_4_out, and_5_out, and_6_out, and_7_out, and_8_out, and_9_out,
       and_10_out, and_11_out, and_12_out, and_13_out, and_14_out, and_15_out, and_16_out, and_22_out,
       and_23_out, BLEZ, branch, CLK, comparator_1_eq, comparator_2_eq, comparator_3_eq, comparator_4_eq,
       comparator_5_eq, comparator_6_eq, \CPU中断请求 , d_ff_1_q, d_ff_2_q, d_ff_3_q, d_ff_4_q, d_ff_5_q,
       d_ff_6_q, decoder_1_out1, decoder_1_out2, decoder_1_out3, decoder_2_out0, decoder_2_out1,
       decoder_2_out2, demultiplexer_1_out1, demultiplexer_1_out2, demultiplexer_1_out3, ERET, Go, IE,
       IR1_2_q, IR1_q, IR1_t, IR2_2_q, IR2_q, IR2_t, IR3_2_q, IR3_q, IR3_t, IRA, IRB, IRC, JAL, JMP, JR, LB,
       MFC0, mips_alu_1_equal, MTC0, not_1_out, not_2_out, not_3_out, not_4_out, or_4_out, or_5_out,
       or_6_out, or_7_out, or_8_out, or_9_out, or_12_out, or_14_out, \output , SignedExt, stop, Syscall, W1,
       W2, W3, \单周期硬布线控制器_1_alu_src , \单周期硬布线控制器_1_beq , \单周期硬布线控制器_1_bne , \单周期硬布线控制器_1_memtoreg ,
       \单周期硬布线控制器_1_regdst ;
  wire [1:0] counter_1_q, IM_q, priority_encoder_1_out, priority_encoder_2_out;
  wire [3:0] \单周期硬布线控制器_1_alu_op ;
  wire [4:0] multiplexer_9_out, multiplexer_10_out, multiplexer_11_out, multiplexer_12_out;
  wire [7:0] undriven;
  wire [15:0] \总周期数 , \无条件跳转数 , \有条件跳转数 ;
  wire [27:0] PC_4;
  wire [31:0] adder_2_out, bit_extender_1_out, bit_extender_2_out, bit_extender_3_out, bit_extender_4_out,
       controlled_buffer_1_out, EPC, EPC_2_q, EPC_3_q, EPC_q, JMP_PC, JR_PC, mips_alu_1_result,
       multiplexer_2_out, multiplexer_3_out, multiplexer_6_out, multiplexer_7_out, multiplexer_8_out,
       multiplexer_13_out, multiplexer_14_out, multiplexer_16_out, \PC存储点 , ram_1_data, shifter_2_out,
       \中断入口地址 ;
  wire [31:28] shifter_1_out;

  Clock #(.highDuration(1), .lowDuration(1)) clock_1 (.out(CLK));
  Button _1 (.out(IRA));
  Button _2 (.out(IRB));
  Button _3 (.out(IRC));
  Button \u_继续运行  (.out(Go));
  LED #(.active("true")) led_1 (.in(W1));
  LED #(.active("true")) led_2 (.in(W2));
  LED #(.active("true")) led_3 (.in(W3));
  or or_1 (W1, IR1_2_q, d_ff_1_q);
  or or_2 (W2, IR2_2_q, d_ff_2_q);
  or or_3 (W3, IR3_2_q, d_ff_3_q);
  Decoder #(.select(2), .tristate("false"), .disabled("Z"), .enable("false")) decoder_1 (
    .out1(decoder_1_out1), .out2(decoder_1_out2), .out3(decoder_1_out3), .sel(IM_q));  // open: out0
  Hex_Digit_Display hex_digit_display_1 (.value(LedData[31:28]));  // open: dp
  D_Flip_Flop #(.trigger("rising"), .Pre_Clr_Positions("LEGACY"), .NegatePresetClear("false"), .enable("true"), .NewFFLayout("false")) d_ff_1 (
    .clk(IR1_t), .D(1'b1), .Q(d_ff_1_q), .reset(IR1_2_q));  // open: Qn, preset, en
  D_Flip_Flop #(.trigger("rising"), .Pre_Clr_Positions("LEGACY"), .NegatePresetClear("false"), .enable("true"), .NewFFLayout("false")) d_ff_2 (
    .clk(IR2_t), .D(1'b1), .Q(d_ff_2_q), .reset(IR2_2_q));  // open: Qn, preset, en
  D_Flip_Flop #(.trigger("rising"), .Pre_Clr_Positions("LEGACY"), .NegatePresetClear("false"), .enable("true"), .NewFFLayout("false")) d_ff_3 (
    .clk(IR3_t), .D(1'b1), .Q(d_ff_3_q), .reset(IR3_2_q));  // open: Qn, preset, en
  and and_1 (and_1_out, IR1_2_q, decoder_1_out1);
  and and_2 (and_2_out, IR2_2_q, decoder_1_out2);
  and and_3 (and_3_out, IR3_2_q, decoder_1_out3);
  Hex_Digit_Display hex_digit_display_2 (.value(LedData[27:24]));  // open: dp
  Hex_Digit_Display hex_digit_display_3 (.value(LedData[23:20]));  // open: dp
  or or_4 (or_4_out, d_ff_1_q, IR1_2_q);
  or or_5 (or_5_out, d_ff_2_q, IR2_2_q);
  or or_6 (or_6_out, d_ff_3_q, IR3_2_q);
  D_Flip_Flop #(.trigger("rising"), .Pre_Clr_Positions("LEGACY"), .NegatePresetClear("false"), .enable("true"), .NewFFLayout("false")) d_ff_4 (
    .clk(and_1_out), .D(1'b1), .Q(d_ff_4_q), .reset(IR1_q));  // open: Qn, preset, en
  or or_7 (or_7_out, d_ff_4_q, IR1_q);
  D_Flip_Flop #(.trigger("rising"), .Pre_Clr_Positions("LEGACY"), .NegatePresetClear("false"), .enable("true"), .NewFFLayout("false")) d_ff_5 (
    .clk(and_2_out), .D(1'b1), .Q(d_ff_5_q), .reset(IR2_q));  // open: Qn, preset, en
  or or_8 (or_8_out, d_ff_5_q, IR2_q);
  D_Flip_Flop #(.trigger("rising"), .Pre_Clr_Positions("LEGACY"), .NegatePresetClear("false"), .enable("true"), .NewFFLayout("false")) d_ff_6 (
    .clk(and_3_out), .D(1'b1), .Q(d_ff_6_q), .reset(IR3_q));  // open: Qn, preset, en
  or or_9 (or_9_out, d_ff_6_q, IR3_q);
  Hex_Digit_Display hex_digit_display_4 (.value(LedData[19:16]));  // open: dp
  Hex_Digit_Display hex_digit_display_5 (.value(LedData[15:12]));  // open: dp
  Hex_Digit_Display hex_digit_display_6 (.value(LedData[11:8]));  // open: dp
  Hex_Digit_Display hex_digit_display_7 (.value(LedData[7:4]));  // open: dp
  // Probe on \总周期数 
  and and_4 (and_4_out, or_4_out, ~demultiplexer_1_out1);  // AND_Gate
  and and_5 (and_5_out, or_5_out, ~demultiplexer_1_out2);  // AND_Gate
  and and_6 (and_6_out, or_6_out, ~demultiplexer_1_out3);  // AND_Gate
  D_Flip_Flop #(.trigger("rising"), .Pre_Clr_Positions("LEGACY"), .NegatePresetClear("false"), .enable("true"), .NewFFLayout("false")) u_IR1 (
    .clk(CLK), .D(and_7_out), .Q(IR1_q));  // open: Qn, preset, en, reset
  and and_7 (and_7_out, or_7_out, ~demultiplexer_1_out1);  // AND_Gate
  D_Flip_Flop #(.trigger("rising"), .Pre_Clr_Positions("LEGACY"), .NegatePresetClear("false"), .enable("true"), .NewFFLayout("false")) u_IR2 (
    .clk(CLK), .D(and_8_out), .Q(IR2_q));  // open: Qn, preset, en, reset
  and and_8 (and_8_out, or_8_out, ~demultiplexer_1_out2);  // AND_Gate
  D_Flip_Flop #(.trigger("rising"), .Pre_Clr_Positions("LEGACY"), .NegatePresetClear("false"), .enable("true"), .NewFFLayout("false")) u_IR3 (
    .clk(CLK), .D(and_9_out), .Q(IR3_q));  // open: Qn, preset, en, reset
  and and_9 (and_9_out, or_9_out, ~demultiplexer_1_out3);  // AND_Gate
  Hex_Digit_Display hex_digit_display_8 (.value(LedData[3:0]));  // open: dp
  // Probe on \无条件跳转数 
  // Probe on \有条件跳转数 
  D_Flip_Flop #(.trigger("rising"), .Pre_Clr_Positions("LEGACY"), .NegatePresetClear("false"), .enable("true"), .NewFFLayout("false")) IR1_2 (
    .clk(CLK), .D(and_4_out), .Q(IR1_2_q));  // open: Qn, preset, en, reset
  D_Flip_Flop #(.trigger("rising"), .Pre_Clr_Positions("LEGACY"), .NegatePresetClear("false"), .enable("true"), .NewFFLayout("false")) IR2_2 (
    .clk(CLK), .D(and_5_out), .Q(IR2_2_q));  // open: Qn, preset, en, reset
  D_Flip_Flop #(.trigger("rising"), .Pre_Clr_Positions("LEGACY"), .NegatePresetClear("false"), .enable("true"), .NewFFLayout("false")) IR3_2 (
    .clk(CLK), .D(and_6_out), .Q(IR3_2_q));  // open: Qn, preset, en, reset
  // Probe on PC
  // Probe on IR
  // Probe on RDin
  Priority_Encoder #(.select(2), .disabled("Z")) priority_encoder_1 (
    .in0(1'b1), .in1(IR1_2_q), .in2(IR2_2_q), .in3(IR3_2_q), .out(priority_encoder_1_out));  // open: gs, en_out, en_in
  not not_1 (not_1_out, IE);
  or or_10 (IR1_t, IR1, IRA);
  Demultiplexer #(.select(2), .width(1), .tristate("false"), .disabled(0), .enable("false")) demultiplexer_1 (
    .out1(demultiplexer_1_out1), .out2(demultiplexer_1_out2), .out3(demultiplexer_1_out3), .in(ERET),
    .sel(IM_q));  // open: out0
  Register #(.width(2), .trigger("rising"), .Select("low")) IM (
    .D(priority_encoder_1_out), .en(not_1_out), .Q(IM_q), .clk(CLK));  // open: clr
  and and_10 (and_10_out, IR1_2_q, ~IR1_q, ~IR2_q, ~IR3_q);  // AND_Gate
  and and_11 (and_11_out, IR2_2_q, ~IR2_q, ~IR3_q);  // AND_Gate
  and and_12 (and_12_out, IR3_2_q, ~IR3_q);  // AND_Gate
  or or_11 (IR2_t, IR2, IRB);
  Multiplexer #(.select(2), .width(32), .disabled("Z"), .enable("false")) multiplexer_1 (
    .in0(EPC), .in1(32'h30ac), .in2(32'h3158), .in3(32'h3204), .out(\中断入口地址 ), .sel(priority_encoder_2_out));
  Priority_Encoder #(.select(2), .disabled(0)) priority_encoder_2 (
    .in0(1'b1), .in1(and_10_out), .in2(and_11_out), .in3(and_12_out), .out(priority_encoder_2_out));  // open: gs, en_out, en_in
  or or_12 (or_12_out, ERET, \CPU中断请求 );
  Counter #(.width(2), .max('h3), .ongoal("wrap"), .trigger("rising"), .behavior("new")) counter_1 (
    .D(2'b00), .count(or_12_out), .Q(counter_1_q), .clk(CLK), .down(ERET));  // open: load, carry, clr, preset
  Multiplexer #(.select(1), .width(32), .disabled("Z"), .enable("false")) multiplexer_2 (
    .in0({JMP_PC[31:28], PC_4}), .in1(\PC存储点 ), .out(multiplexer_2_out), .sel(branch));
  or or_13 (IR3_t, IR3, IRC);
  Decoder #(.select(2), .tristate("false"), .disabled("Z"), .enable("false")) decoder_2 (
    .out0(decoder_2_out0), .out1(decoder_2_out1), .out2(decoder_2_out2), .sel(counter_1_q));  // open: out3
  Comparator #(.width(2), .mode("unsigned")) comparator_1 (
    .a(2'b00), .b(priority_encoder_2_out), .eq(comparator_1_eq));  // open: gt, lt
  Register #(.width(1), .trigger("rising"), .Select("low")) u_IE (
    .D(and_13_out), .en(or_14_out), .Q(IE), .clk(CLK), .preset(MTC0));  // open: clr, cs
  Multiplexer #(.select(2), .width(32), .disabled("Z"), .enable("false")) multiplexer_3 (
    .in0(multiplexer_2_out), .in1(JMP_PC), .in2(JR_PC), .in3(JR_PC), .out(multiplexer_3_out), .sel({JR, JMP}));
  nor nor_1 (\CPU中断请求 , comparator_1_eq, IE);
  and and_13 (and_13_out, \CPU中断请求 , ~MFC0, ~ERET);  // AND_Gate
  or or_14 (or_14_out, ~IE, MFC0, ERET, MTC0);  // OR_Gate
  Register #(.width(32), .trigger("rising"), .Select("low")) u_EPC (
    .D(multiplexer_3_out), .en(and_14_out), .Q(EPC_q), .clk(CLK));  // open: clr
  and and_14 (and_14_out, decoder_2_out0, \CPU中断请求 );
  Register #(.width(32), .trigger("rising"), .Select("low")) EPC_2 (
    .D(multiplexer_3_out), .en(and_15_out), .Q(EPC_2_q), .clk(CLK));  // open: clr
  and and_15 (and_15_out, decoder_2_out1, \CPU中断请求 );
  Register #(.width(32), .trigger("rising"), .Select("low")) EPC_3 (
    .D(multiplexer_3_out), .en(and_16_out), .Q(EPC_3_q), .clk(CLK));  // open: clr
  and and_16 (and_16_out, decoder_2_out2, \CPU中断请求 );
  Multiplexer #(.select(2), .width(32), .disabled("Z"), .enable("false")) multiplexer_4 (
    .in1(EPC_q), .in2(EPC_2_q), .in3(EPC_3_q), .out(EPC), .sel(counter_1_q));  // open: in0
  Comparator #(.width(6), .mode("twosComplement")) comparator_2 (
    .a(IR[31:26]), .b(6'b010000), .eq(comparator_2_eq));  // open: gt, lt
  Comparator #(.width(6), .mode("twosComplement")) comparator_3 (
    .a(IR[5:0]), .b(6'b011000), .eq(comparator_3_eq));  // open: gt, lt
  Comparator #(.width(5), .mode("twosComplement")) comparator_4 (
    .a(IR[25:21]), .b({5{1'b0}}), .eq(comparator_4_eq));  // open: gt, lt
  Comparator #(.width(5), .mode("twosComplement")) comparator_5 (
    .a(IR[25:21]), .b(5'b00100), .eq(comparator_5_eq));  // open: gt, lt
  and and_17 (ERET, comparator_2_eq, comparator_3_eq);
  and and_18 (MFC0, comparator_2_eq, comparator_4_eq);
  and and_19 (MTC0, comparator_2_eq, comparator_5_eq);
  Multiplexer #(.select(1), .width(32), .disabled("Z"), .enable("false")) multiplexer_5 (
    .in0({JMP_PC[31:28], PC_4}), .in1(adder_2_out), .out(\PC存储点 ), .sel(branch));
  Multiplexer #(.select(1), .width(32), .disabled("Z"), .enable("false")) multiplexer_6 (
    .in0(\PC存储点 ), .in1(EPC), .out(multiplexer_6_out), .sel(ERET));
  Multiplexer #(.select(1), .width(32), .disabled("Z"), .enable("false")) multiplexer_7 (
    .in0(multiplexer_6_out), .in1(\中断入口地址 ), .out(multiplexer_7_out), .sel(\CPU中断请求 ));
  Comparator #(.width(32), .mode("twosComplement")) comparator_6 (
    .a(JR_PC), .b(32'h22), .eq(comparator_6_eq));  // open: gt, lt
  Multiplexer #(.select(2), .width(32), .disabled("Z"), .enable("false")) multiplexer_8 (
    .in0(multiplexer_7_out), .in1(JMP_PC), .in2(JR_PC), .in3(JR_PC), .out(multiplexer_8_out), .sel({JR, JMP}));
  not not_2 (not_2_out, stop);
  not not_3 (not_3_out, comparator_6_eq);
  Register #(.width(32), .trigger("rising"), .Select("low")) u_PC (
    .D(multiplexer_8_out), .en(not_2_out), .Q(PC), .clk(CLK), .clr(1'b0));
  Counter #(.width(16), .max('hffff), .ongoal("wrap"), .trigger("rising"), .behavior("old")) counter_2 (
    .D({16{1'b0}}), .count(not_2_out), .Q(\总周期数 ), .clk(CLK), .clr(1'b0));  // open: load, carry, preset
  and and_20 (\output , Syscall, comparator_6_eq);
  and and_21 (stop, not_3_out, Syscall);
  assign controlled_buffer_1_out = \output  ? MDin : 32'bz;  // Controlled_Buffer controlled_buffer_1
  Adder #(.width(32)) adder_1 (.a(PC), .b(32'h4), .out({JMP_PC[31:28], PC_4}), .cin(1'b0));  // open: cout
  Register #(.width(32), .trigger("rising"), .Select("low")) PC_2 (
    .D(controlled_buffer_1_out), .Q(LedData), .clk(CLK));  // open: en, clr
  ROM #(.addrWidth(10), .dataWidth(32), .Select("high")) rom_1 ();  // open: addr, data
  ROM #(.addrWidth(10), .dataWidth(32), .Select("high")) rom_2 (.addr(PC[11:2]), .data(IR));
  Multiplexer #(.select(1), .width(5), .disabled("Z"), .enable("false")) multiplexer_9 (
    .in0(IR[20:16]), .in1(IR[15:11]), .out(multiplexer_9_out), .sel(\单周期硬布线控制器_1_regdst ));
  \单周期硬布线控制器  \u_单周期硬布线控制器_1  (
    .Func(IR[5:0]), .OP(IR[31:26]), .ALU_OP(\单周期硬布线控制器_1_alu_op ), .MemToReg(\单周期硬布线控制器_1_memtoreg ),
    .MemWrite(MemWrite), .ALU_SRC(\单周期硬布线控制器_1_alu_src ), .RegWrite(RegWrite), .SysCALL(Syscall),
    .SignedExt(SignedExt), .RegDst(\单周期硬布线控制器_1_regdst ), .JR(JR), .JMP(JMP), .Beq(\单周期硬布线控制器_1_beq ),
    .JAL(JAL), .Bne(\单周期硬布线控制器_1_bne ), .BLEZ(BLEZ), .LB(LB));
  Multiplexer #(.select(1), .width(5), .disabled("Z"), .enable("false")) multiplexer_10 (
    .in0(IR[25:21]), .in1(5'b00010), .out(multiplexer_10_out), .sel(Syscall));
  Multiplexer #(.select(1), .width(5), .disabled("Z"), .enable("false")) multiplexer_11 (
    .in0(IR[20:16]), .in1(5'b00100), .out(multiplexer_11_out), .sel(Syscall));
  Multiplexer #(.select(1), .width(5), .disabled("Z"), .enable("false")) multiplexer_12 (
    .in0(multiplexer_9_out), .in1({5{1'b1}}), .out(multiplexer_12_out), .sel(JAL));
  assign bit_extender_1_out = {{6{1'b0}}, IR[25:0]};  // Bit_Extender bit_extender_1
  assign bit_extender_2_out = {{16{1'b0}}, IR[15:0]};  // Bit_Extender bit_extender_2
  assign bit_extender_3_out = {{16{IR[15]}}, IR[15:0]};  // Bit_Extender bit_extender_3
  Counter #(.width(16), .max('hffff), .ongoal("wrap"), .trigger("rising"), .behavior("old")) counter_3 (
    .D({16{1'b0}}), .count(JMP), .Q(\无条件跳转数 ), .clk(CLK));  // open: load, carry, clr, preset
  Shifter #(.width(32), .shift("ll")) shifter_1 (
    .in(bit_extender_1_out), .\dist (5'b00010), .out({shifter_1_out, JMP_PC[27:0]}));
  Multiplexer #(.select(1), .width(32), .disabled("Z"), .enable("false")) multiplexer_13 (
    .in0(bit_extender_2_out), .in1(bit_extender_3_out), .out(multiplexer_13_out), .sel(SignedExt));
  Shifter #(.width(32), .shift("ll")) shifter_2 (.in(bit_extender_3_out), .\dist (5'b00010), .out(shifter_2_out));
  and and_22 (and_22_out, \单周期硬布线控制器_1_beq , mips_alu_1_equal);
  MIPS_Regifile mips_regifile_1 (
    .Din(RDin), .Clk(CLK), .R1(JR_PC), .R2(MDin), .WE(RegWrite), .W_num(multiplexer_12_out),
    .R1_num(multiplexer_10_out), .R2_num(multiplexer_11_out));
  Multiplexer #(.select(1), .width(32), .disabled("Z"), .enable("false")) multiplexer_14 (
    .in0(MDin), .in1(multiplexer_13_out), .out(multiplexer_14_out), .sel(\单周期硬布线控制器_1_alu_src ));
  Adder #(.width(32)) adder_2 (
    .a(shifter_2_out), .b({JMP_PC[31:28], PC_4}), .out(adder_2_out), .cin(1'b0));  // open: cout
  or or_15 (branch, and_22_out, and_23_out);
  and and_23 (and_23_out, \单周期硬布线控制器_1_bne , not_4_out);
  not not_4 (not_4_out, mips_alu_1_equal);
  MIPS_ALU mips_alu_1 (
    .X(JR_PC), .Y(multiplexer_14_out), .AluOP(\单周期硬布线控制器_1_alu_op ), .Equal(mips_alu_1_equal),
    .Result(mips_alu_1_result), .shamt(IR[10:6]));  // open: Result_2, BLEZ
  Counter #(.width(16), .max('hffff), .ongoal("wrap"), .trigger("rising"), .behavior("old")) counter_4 (
    .D({16{1'b0}}), .count(branch), .Q(\有条件跳转数 ), .clk(CLK));  // open: load, carry, clr, preset
  Multiplexer #(.select(1), .width(32), .disabled("Z"), .enable("false")) multiplexer_15 (
    .in0(multiplexer_16_out), .in1({JMP_PC[31:28], PC_4}), .out(RDin), .sel(JAL));
  RAM #(.addrWidth(10), .dataWidth(32), .bus("separate"), .Select("high")) ram_1 (
    .addr(mips_alu_1_result[11:2]), .din(MDin), .data(ram_1_data), .str(MemWrite), .sel(1'b1), .clk(CLK),
    .clr(1'b0));  // open: ld
  assign bit_extender_4_out = {{24{undriven[7]}}, undriven};  // Bit_Extender bit_extender_4
  Multiplexer #(.select(1), .width(32), .disabled("Z"), .enable("false")) multiplexer_16 (
    .in0(mips_alu_1_result), .in1(ram_1_data), .out(multiplexer_16_out), .sel(\单周期硬布线控制器_1_memtoreg ));

  // Other names for the same wires on the sheet: a0[31:0] = MDin; FUNC[5:0] = IR[5:0]; MF[4:0] = IR[25:21];
  //   OP[5:0] = IR[31:26]; PC_4[31:28] = JMP_PC[31:28]; v0[31:0] = JR_PC

  // Notes on the sheet:
  //   中断等待指示
  //   数码管输出
  //   Reset 
  //   Reset 
  //   Reset 
  //   Reset 
  //   Reset 
  //   Reset 
  //   中断信号采样参考电路
  //   为方便自动评测，需要输出PC，IR，寄存器堆写如数据RDin
  //   RAM写使能MemWrite、RAM写入数据MDin等信号
  //   总复位信号应将除ROM以外所有存储组件全部清零
  //   数码管输出应该用寄存器锁存，否则显示数据只能一闪而过
  //   指令存储器
  //   contents of rom_1 (hex, n*v repeats v):
  //   20110001 8000c05 20110001 20120002 20130003 8000c09 20110001 20120002 20130003 8000c0d 20110001
  //   20120002 20130003 8000c11 20110001 20120002 20130003 c000cb8 20100001 20110001 118fc0 112020
  //   20020022 c 118882 12200001 8000c15 112020 20020022 c 20110001 118880 112020 20020022 c 12200001
  //   8000c1f 20110001 118fc0 112020 20020022 c 1188c3 112020 20020022 c 118903 112020 20020022 c 118903
  //   112020 20020022 c 118903 112020 20020022 c 118903 112020 20020022 c 118903 112020 20020022 c 118903
  //   112020 20020022 c 118903 112020 20020022 c 20100001 109fc0 139fc3 8021 2012000c 24160003 26100001
  //   3210000f 20080008 20090001 139900 2709825 132020 20020022 c 1094022 1500fff9 22100001 2018000f
  //   2188024 108700 20080008 20090001 139902 2709825 132021 20020022 c 1094022 1500fff9 108702 2c9b022
  //   12c00001 8000c50 4020 1084027 84400 3508ffff 82021 20020022 c 2010ffff 20110000 ae300000 22100001
  //   22310004 ae300000 22100001 22310004 ae300000 22100001 22310004 ae300000 22100001 22310004 ae300000
  //   22100001 22310004 ae300000 22100001 22310004 ae300000 22100001 22310004 ae300000 22100001 22310004
  //   ae300000 22100001 22310004 ae300000 22100001 22310004 ae300000 22100001 22310004 ae300000 22100001
  //   22310004 ae300000 22100001 22310004 ae300000 22100001 22310004 ae300000 22100001 22310004 ae300000
  //   22100001 22310004 22100001 8020 2011003c 8e130000 8e340000 274402a 11000002 ae330000 ae140000
  //   2231fffc 1611fff8 102020 20020022 c 22100004 2011003c 1611fff2 2002000a c 20100000 22100001 102020
  //   20020022 c 22100002 102020 20020022 c 22100003 102020 20020022 c 22100004 102020 20020022 c 22100005
  //   102020 20020022 c 22100006 102020 20020022 c 22100007 102020 20020022 c 22100008 102020 20020022
  //   20020022 c 3e00008
  //   contents of rom_2 (hex, n*v repeats v):
  //   201d07d0 20100001 109fc0 139fc3 8021 2012000c 24160008 26100001 3210000f 20080008 20090001 139900
  //   2709825 132020 20020022 c 1094022 1500fff9 22100001 2018000f 2188024 108700 20080008 20090001 139902
  //   2709825 132021 20020022 c 1094022 1500fff9 108702 2c9b022 12c00001 8000c07 4020 1084027 84400
  //   3508ffff 82021 20020022 c 8000c01 afa20000 23bd0004 afa40000 23bd0004 afb00000 23bd0004 afb30000
  //   23bd0004 afb40000 23bd0004 afb50000 23bd0004 afb60000 23bd0004 40000000 20160001 20140003 20150001
  //   168020 108100 2149825 132020 20020022 c 1600fffa 295a022 1680fff7 40800000 23bdfffc 8fb60000
  //   23bdfffc 8fb50000 23bdfffc 8fb40000 23bdfffc 8fb30000 23bdfffc 8fb00000 23bdfffc 8fa40000 23bdfffc
  //   8fa20000 42000018 afa20000 23bd0004 afa40000 23bd0004 afb00000 23bd0004 afb30000 23bd0004 afb40000
  //   23bd0004 afb50000 23bd0004 afb60000 23bd0004 40000000 20160002 20140003 20150001 168020 108100
  //   2149825 132020 20020022 c 1600fffa 295a022 1680fff7 40800000 23bdfffc 8fb60000 23bdfffc 8fb50000
  //   23bdfffc 8fb40000 23bdfffc 8fb30000 23bdfffc 8fb00000 23bdfffc 8fa40000 2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
  //   JMP
  //   JR
  //   OP
  //   Func
  //   rs
  //   rt
  //   rd
  //   shamt
  //   Beq
  //   Bne
  //   MemToReg
  //   MemWrite
  //   AluOP
  //   AluSrcB
  //   RegWrite
  //   JAL
  //   RegDst
endmodule
