// Logisim project 团队任务.circ as structural Verilog: 11 circuits, main circuit ◇单周期MIPS
module \单周期MIPS  (
  input  [9:0] in_1,
  input  in_2,
  input  in_3,
  output RegWrite,
  output MemWrite,
  output [31:0] PC,
  output [31:0] IR,
  output [31:0] RDin,
  output [31:0] MDin,
  output [31:0] LedData,
  output [31:0] R1,
  output [31:0] R2
);

  wire and_2_out, and_3_out, and_4_out, and_5_out, and_7_out, and_8_out, beq, BGEZ, bne, CLK, clock_2_out,
       clock_3_out, comparator_1_eq, comparator_2_eq, comparator_3_eq, ctrl_disp, demultiplexer_1_out1,
       demultiplexer_1_out2, demultiplexer_1_out3, ERET, Go, IR1, IR2, IR3, JAL, JR, jump, keyboard_1_avail,
       LBU, nor_1_out, not_1_out, not_2_out, not_3_out, not_4_out, not_5_out, not_6_out, not_7_out,
       not_8_out, not_9_out, not_10_out, or_1_out, or_2_out, or_3_out, or_5_out, pcnext,
       priority_encoder_1_gs, RegDst, RST, signalequal, SignedExt, sys_stop, syscall, W1, W2, W3, \中断使能_q ,
       \中断信号 , \中断信号产生_1__2号 , \中断信号产生_1__3号 , \中断信号产生_1_与中断屏蔽位与 , \单周期硬布线控制器_1_alu_src ,
       \单周期硬布线控制器_1_memtoreg ;
  wire [1:0] priority_encoder_1_out, register_1_q;
  wire [3:0] \单周期硬布线控制器_1_alu_op ;
  wire [4:0] multiplexer_8_out, R1_t, R2_t, W_num;
  wire [6:0] keyboard_1_data;
  wire [7:0] multiplexer_16_out, multiplexer_16_out_2, multiplexer_16_out_3, multiplexer_16_out_4,
       multiplexer_17_out;
  wire [15:0] counter_2_q, counter_3_q, \总周期数 ;
  wire [27:0] pc_4;
  wire [31:0] a0, adder_2_out, bit_extender_1_out, bit_extender_2_out, bit_extender_3_out, EPC, IRS_PC,
       mips_alu_1_result, multiplexer_1_out, multiplexer_2_out, multiplexer_3_out, multiplexer_4_out,
       multiplexer_5_out, multiplexer_10_out, multiplexer_11_out, multiplexer_12_out, multiplexer_15_out,
       multiplexer_18_out, ram_2_data, shifter_1_out;
  wire [31:28] J_PC;

  Button \u_总复位  (.out(RST));
  Button _1 (.out(IR1));
  Button _2 (.out(IR2));
  Button _3 (.out(IR3));
  Button \u_继续运行  (.out(Go));
  LED #(.active("true")) led_1 (.in(W1));
  LED #(.active("true")) led_2 (.in(W2));
  LED #(.active("true")) led_3 (.in(W3));
  Multiplexer #(.select(1), .width(32), .disabled("Z"), .enable("false")) multiplexer_1 (
    .in0({J_PC, pc_4}), .in1(adder_2_out), .out(multiplexer_1_out), .sel(pcnext));
  Multiplexer #(.select(1), .width(32), .disabled("Z"), .enable("false")) multiplexer_2 (
    .in0(multiplexer_1_out), .in1({J_PC, IR[25:0], 2'b00}), .out(multiplexer_2_out), .sel(jump));
  Hex_Digit_Display hex_digit_display_1 (.value(LedData[31:28]));  // open: dp
  Multiplexer #(.select(1), .width(32), .disabled("Z"), .enable("false")) multiplexer_3 (
    .in0(multiplexer_2_out), .in1(a0), .out(multiplexer_3_out), .sel(JR));
  Clock #(.highDuration(1), .lowDuration(1)) clock_1 (.out(CLK));
  Keyboard #(.Char_bit_width(7), .buflen(32), .trigger("rising")) keyboard_1 (
    .clk(clock_2_out), .re(in_2), .clr(in_3), .avail(keyboard_1_avail), .data(keyboard_1_data));
  Clock #(.highDuration(1), .lowDuration(1)) clock_2 (.out(clock_2_out));
  Hex_Digit_Display hex_digit_display_2 (.value(LedData[27:24]));  // open: dp
  Hex_Digit_Display hex_digit_display_3 (.value(LedData[23:20]));  // open: dp
  Multiplexer #(.select(1), .width(32), .disabled("Z"), .enable("false")) multiplexer_4 (
    .in0(multiplexer_3_out), .in1(IRS_PC), .out(multiplexer_4_out), .sel(\中断信号 ));
  Multiplexer #(.select(1), .width(32), .disabled("Z"), .enable("false")) multiplexer_5 (
    .in0(multiplexer_4_out), .in1(EPC), .out(multiplexer_5_out), .sel(ERET));
  Hex_Digit_Display hex_digit_display_4 (.value(LedData[15:12]));  // open: dp
  Hex_Digit_Display hex_digit_display_5 (.value(LedData[19:16]));  // open: dp
  not not_1 (not_1_out, sys_stop);
  or or_1 (or_1_out, Go, not_1_out);
  Register #(.width(32), .trigger("rising"), .Select("low")) u_PC (
    .D(multiplexer_5_out), .en(or_1_out), .Q(PC), .clk(CLK), .clr(RST));
  Hex_Digit_Display hex_digit_display_6 (.value(LedData[7:4]));  // open: dp
  Hex_Digit_Display hex_digit_display_7 (.value(LedData[11:8]));  // open: dp
  // Probe on \总周期数 
  Hex_Digit_Display hex_digit_display_8 (.value(LedData[3:0]));  // open: dp
  Adder #(.width(32)) adder_1 (.a(PC), .b(32'h4), .out({J_PC, pc_4}));  // open: cin, cout
  // LCD_Video lcd_video_1: pin names not known
  ROM #(.addrWidth(10), .dataWidth(32), .Select("high")) rom_1 (.addr(PC[11:2]), .data(IR));
  RAM #(.addrWidth(10), .dataWidth(7), .bus("separate"), .Select("low")) ram_1 (
    .addr(in_1), .din(keyboard_1_data), .str(keyboard_1_avail), .clk(clock_2_out));  // open: data, sel, ld, clr
  Multiplexer #(.select(1), .width(5), .disabled("Z"), .enable("false")) multiplexer_6 (
    .in0(IR[25:21]), .in1(5'b00100), .out(R1_t), .sel(syscall));
  Multiplexer #(.select(1), .width(5), .disabled("Z"), .enable("false")) multiplexer_7 (
    .in0(IR[20:16]), .in1(5'b00010), .out(R2_t), .sel(syscall));
  Multiplexer #(.select(1), .width(5), .disabled("Z"), .enable("false")) multiplexer_8 (
    .in0(IR[20:16]), .in1(IR[15:11]), .out(multiplexer_8_out), .sel(RegDst));
  \单周期硬布线控制器  \u_单周期硬布线控制器_1  (
    .Func(IR[5:0]), .OP(IR[31:26]), .ALU_OP(\单周期硬布线控制器_1_alu_op ), .MemToReg(\单周期硬布线控制器_1_memtoreg ),
    .MemWrite(MemWrite), .ALU_SRC(\单周期硬布线控制器_1_alu_src ), .RegWrite(RegWrite), .SysCALL(syscall),
    .SignedExt(SignedExt), .RegDst(RegDst), .JR(JR), .JMP(jump), .Beq(beq), .JAL(JAL), .Bne(bne),
    .BGEZ(BGEZ), .LBU(LBU));  // open: XORI, SLTIU
  Multiplexer #(.select(1), .width(5), .disabled("Z"), .enable("false")) multiplexer_9 (
    .in0(multiplexer_8_out), .in1({5{1'b1}}), .out(W_num), .sel(JAL));
  Clock #(.highDuration(1), .lowDuration(1)) clock_3 (.out(clock_3_out));
  \中断信号产生  \u_中断信号产生_1  (
    .\_1号中断 (IR1), .\_1号中断等待指示灯 (W1), .\_2号中断 (IR2), .\_2号中断等待指示灯 (W2), .\_3号中断 (IR3), .\_3号中断等待指示灯 (W3),
    .\与中断屏蔽位与 (\中断信号产生_1_与中断屏蔽位与 ), .\_2号 (\中断信号产生_1__2号 ), .\_3号 (\中断信号产生_1__3号 ),
    .\_1号清零 (demultiplexer_1_out1), .\_2号清零信号 (demultiplexer_1_out2), .\_3号清零信号 (demultiplexer_1_out3),
    .clk(clock_3_out));
  or or_2 (or_2_out, \中断信号产生_1_与中断屏蔽位与 , \中断信号产生_1__2号 , \中断信号产生_1__3号 );
  Comparator #(.width(6), .mode("twosComplement")) comparator_1 (
    .a(IR[31:26]), .b(6'b010000), .eq(comparator_1_eq));  // open: gt, lt
  Comparator #(.width(6), .mode("twosComplement")) comparator_2 (
    .a(IR[5:0]), .b(6'b011000), .eq(comparator_2_eq));  // open: gt, lt
  MIPS_Regifile mips_regifile_1 (
    .Din(RDin), .Clk(CLK), .R1(a0), .R2(MDin), .WE(RegWrite), .W_num(W_num), .R1_num(R1_t), .R2_num(R2_t));
  assign bit_extender_1_out = {{16{IR[15]}}, IR[15:0]};  // Bit_Extender bit_extender_1
  assign bit_extender_2_out = {{16{1'b0}}, IR[15:0]};  // Bit_Extender bit_extender_2
  not not_2 (not_2_out, or_2_out);
  not not_3 (not_3_out, signalequal);
  not not_4 (not_4_out, mips_alu_1_result[0]);
  Multiplexer #(.select(1), .width(32), .disabled("Z"), .enable("false")) multiplexer_10 (
    .in0(MDin), .in1(multiplexer_11_out), .out(multiplexer_10_out), .sel(\单周期硬布线控制器_1_alu_src ));
  Multiplexer #(.select(1), .width(32), .disabled("Z"), .enable("false")) multiplexer_11 (
    .in0(bit_extender_2_out), .in1(bit_extender_1_out), .out(multiplexer_11_out), .sel(SignedExt));
  Shifter #(.width(32), .shift("ll")) shifter_1 (.in(bit_extender_1_out), .\dist (5'b00010), .out(shifter_1_out));
  Priority_Encoder #(.select(2), .disabled("Z")) priority_encoder_1 (
    .in0(1'b0), .in1(\中断信号产生_1_与中断屏蔽位与 ), .in2(\中断信号产生_1__2号 ), .in3(\中断信号产生_1__3号 ),
    .out(priority_encoder_1_out), .gs(priority_encoder_1_gs), .en_in(1'b1));  // open: en_out
  Demultiplexer #(.select(2), .width(1), .tristate("false"), .disabled(0), .enable("true")) demultiplexer_1 (
    .out1(demultiplexer_1_out1), .out2(demultiplexer_1_out2), .out3(demultiplexer_1_out3), .in(ERET),
    .sel(register_1_q), .en(priority_encoder_1_gs));  // open: out0
  and and_1 (ERET, comparator_1_eq, comparator_2_eq);
  and and_2 (and_2_out, not_4_out, BGEZ);
  and and_3 (and_3_out, signalequal, beq);
  and and_4 (and_4_out, not_3_out, bne);
  Multiplexer #(.select(1), .width(32), .disabled("Z"), .enable("false")) multiplexer_12 (
    .in0(multiplexer_10_out), .in1({32{1'b0}}), .out(multiplexer_12_out), .sel(BGEZ));
  Adder #(.width(32)) adder_2 (.a(shifter_1_out), .b({J_PC, pc_4}), .out(adder_2_out));  // open: cin, cout
  Multiplexer #(.select(2), .width(32), .disabled("Z"), .enable("false")) multiplexer_13 (
    .in1(32'h4), .in2(32'h8), .in3(32'hc), .out(IRS_PC), .sel(register_1_q));  // open: in0
  Register #(.width(2), .trigger("low"), .Select("low")) register_1 (
    .D(priority_encoder_1_out), .en(or_3_out), .Q(register_1_q), .clk(clock_3_out), .clr(not_2_out));
  nor nor_1 (nor_1_out, register_1_q[0], register_1_q[1]);
  or or_3 (or_3_out, nor_1_out, ERET);
  or or_4 (pcnext, and_2_out, and_3_out, and_4_out);
  MIPS_ALU mips_alu_1 (
    .X(a0), .Y(multiplexer_12_out), .AluOP(\单周期硬布线控制器_1_alu_op ), .Equal(signalequal),
    .Result(mips_alu_1_result), .shamt(IR[10:6]));  // open: Result_2
  not not_5 (not_5_out, \中断使能_q );
  Register #(.width(1), .trigger("rising"), .Select("low")) \u_中断使能  (
    .D(priority_encoder_1_gs), .en(not_5_out), .Q(\中断使能_q ), .clk(CLK), .clr(ERET));
  // Probe on PC
  and and_5 (and_5_out, \中断信号 , not_6_out);
  not not_6 (not_6_out, ERET);
  not not_7 (not_7_out, \中断使能_q );
  Register #(.width(32), .trigger("rising"), .Select("low")) u_EPC (
    .D(PC), .en(and_5_out), .Q(EPC), .clk(CLK));  // open: clr
  RAM #(.addrWidth(10), .dataWidth(32), .bus("separate"), .Select("high")) ram_2 (
    .addr(mips_alu_1_result[11:2]), .din(MDin), .data(ram_2_data), .str(MemWrite), .sel(1'b1), .clk(CLK),
    .clr(RST));  // open: ld
  Multiplexer #(.select(1), .width(32), .disabled("Z"), .enable("false")) multiplexer_14 (
    .in0(multiplexer_15_out), .in1({J_PC, pc_4}), .out(RDin), .sel(JAL));
  and and_6 (\中断信号 , priority_encoder_1_gs, not_7_out);
  // Probe on EPC
  Multiplexer #(.select(1), .width(32), .disabled("Z"), .enable("false")) multiplexer_15 (
    .in0({multiplexer_16_out_4, multiplexer_16_out_3, multiplexer_16_out_2, multiplexer_16_out}),
    .in1(bit_extender_3_out), .out(multiplexer_15_out), .sel(LBU));
  Multiplexer #(.select(1), .width(32), .disabled("Z"), .enable("false")) multiplexer_16 (
    .in0(mips_alu_1_result), .in1(ram_2_data),
    .out({multiplexer_16_out_4, multiplexer_16_out_3, multiplexer_16_out_2, multiplexer_16_out}),
    .sel(\单周期硬布线控制器_1_memtoreg ));
  Multiplexer #(.select(2), .width(8), .disabled("Z"), .enable("false")) multiplexer_17 (
    .in0(multiplexer_16_out), .in1(multiplexer_16_out_2), .in2(multiplexer_16_out_3),
    .in3(multiplexer_16_out_4), .out(multiplexer_17_out), .sel(mips_alu_1_result[1:0]));
  assign bit_extender_3_out = {{24{1'b0}}, multiplexer_17_out};  // Bit_Extender bit_extender_3
  not not_8 (not_8_out, sys_stop);
  not not_9 (not_9_out, signalequal);
  Multiplexer #(.select(1), .width(32), .disabled("Z"), .enable("false")) multiplexer_18 (
    .in1(a0), .out(multiplexer_18_out), .sel(ctrl_disp));  // open: in0
  // Probe on RDin
  Counter #(.width(16), .max('hffff), .ongoal("wrap"), .trigger("rising"), .behavior("old")) counter_1 (
    .D({16{1'b0}}), .count(not_8_out), .Q(\总周期数 ), .clk(CLK), .clr(RST));  // open: load, carry, preset
  or or_5 (or_5_out, and_8_out, and_7_out);
  and and_7 (and_7_out, signalequal, beq);
  and and_8 (and_8_out, not_9_out, bne);
  Register #(.width(32), .trigger("rising"), .Select("low")) register_2 (
    .D(multiplexer_18_out), .Q(LedData), .clk(CLK), .clr(RST));  // open: en
  // Probe on \总周期数 
  // Probe on counter_2_q
  Counter #(.width(16), .max('hffff), .ongoal("wrap"), .trigger("rising"), .behavior("old")) counter_2 (
    .D({16{1'b0}}), .count(or_5_out), .Q(counter_2_q), .clk(CLK), .clr(RST));  // open: load, carry, preset
  Comparator #(.width(32), .mode("twosComplement")) comparator_3 (
    .a(MDin), .b(32'h22), .eq(comparator_3_eq));  // open: gt, lt
  not not_10 (not_10_out, comparator_3_eq);
  // RegisterFile registerfile_1: pin names not known; wires that end beside it: RDin, CLK, RegWrite, W_num, R1_t, R2_t, R1, R2
  and and_9 (ctrl_disp, syscall, comparator_3_eq);
  and and_10 (sys_stop, syscall, not_10_out);
  // Probe on counter_3_q
  Counter #(.width(16), .max('hffff), .ongoal("wrap"), .trigger("rising"), .behavior("old")) counter_3 (
    .D({16{1'b0}}), .count(jump), .Q(counter_3_q), .clk(CLK), .clr(RST));  // open: load, carry, preset

  // Other names for the same wires on the sheet: J_PC[27:2] = IR[25:0]; pc_4[31:28] = J_PC; JR_PC[31:0] = a0;
  //   v0[31:0] = MDin

  // Notes on the sheet:
  //   in_3: pull=down
  //   in_2: pull=down
  //   in_1: pull=down
  //   中断源
  //   中断等待指示
  //   总复位信号应将除ROM以外所有存储组件全部清零
  //   数码管输出
  //   数码管输出应该用寄存器锁存，否则显示数据只能一闪而过
  //   指令存储器
  //   OP
  //   rs
  //   指令字
  //   contents of rom_1 (hex, n*v repeats v):
  //   20110001 8000c05 20110001 20120002 20130003 8000c09 20110001 20120002 20130003 8000c0d 20110001
  //   20120002 20130003 8000c11 20110001 20120002 20130003 c000cb8 20100001 20110001 118fc0 112020
  //   20020022 c 118882 12200001 8000c15 112020 20020022 c 20110001 118880 112020 20020022 c 12200001
  //   8000c1f 20110001 118fc0 112020 20020022 c 1188c3 112020 20020022 c 118903 112020 20020022 c 118903
  //   112020 20020022 c 118903 112020 20020022 c 118903 112020 20020022 c 118903 112020 20020022 c 118903
  //   112020 20020022 c 118903 112020 20020022 c 20100001 109fc0 139fc3 8021 2012000c 24160003 26100001
  //   3210000f 20080008 20090001 139900 2709825 132020 20020022 c 1094022 1500fff9 22100001 2018000f
  //   2188024 108700 20080008 20090001 139902 2709825 132021 20020022 c 1094022 1500fff9 108702 2c9b022
  //   12c00001 8000c50 4020 1084027 84400 3508ffff 82021 20020022 c 2010ffff 20110000 ae300000 22100001
  //   22310004 ae300000 22100001 22310004 ae300000 22100001 22310004 ae300000 22100001 22310004 ae300000
  //   22100001 22310004 ae300000 22100001 22310004 ae300000 22100001 22310004 ae300000 22100001 22310004
  //   ae300000 22100001 22310004 ae300000 22100001 22310004 ae300000 22100001 22310004 ae300000 22100001
  //   22310004 ae300000 22100001 22310004 ae300000 22100001 22310004 ae300000 22100001 22310004 ae300000
  //   22100001 22310004 22100001 8020 2011003c 8e130000 8e340000 274402a 11000002 ae330000 ae140000
  //   2231fffc 1611fff8 102020 20020022 c 22100004 2011003c 1611fff2 20020032 c 20100000 22100001 102020
  //   20020022 c 22100002 102020 20020022 c 22100003 102020 20020022 c 22100004 102020 20020022 c 22100005
  //   102020 20020022 c 22100006 102020 20020022 c 22100007 102020 20020022 c 22100008 102020 20020022
  //   20020022 c 3e00008
  //   rt
  //   rd
  //   JMP
  //   JR
  //   OP
  //   Func
  //   Func
  //   返回判断
  //   Beq
  //   Bne
  //   AluOP
  //   AluSrcB
  //   RegWrite
  //   JAL
  //   RegDst
  //   Syscall
  //   单级中断，修改上下跳沿奇怪版
  //   为方便自动评测，需要输出PC，IR，寄存器文件写入端口RDin，内存写入端口MDin等信号
  //   MemToReg
  //   MemWrite
  //   EPC寄存
  //   寄存器组内容显示
  //   周期数计算
  //   条件分支数
  //   syscall 调用判断
  //   无条件分支数
endmodule

// 单周期硬布线控制器
module \单周期硬布线控制器  (
  input  [5:0] OP,
  input  [5:0] Func,
  output [3:0] ALU_OP,
  output MemToReg,
  output MemWrite,
  output ALU_SRC,
  output RegWrite,
  output SysCALL,
  output SignedExt,
  output RegDst,
  output Beq,
  output Bne,
  output JR,
  output JMP,
  output JAL,
  output BGEZ,
  output XORI,
  output SLTIU,
  output LBU
);

  \运算控制器自动生成  \u_运算控制器自动生成_1  (
    .OP0(OP[0]), .OP1(OP[1]), .OP2(OP[2]), .OP3(OP[3]), .OP4(OP[4]), .OP5(OP[5]), .F0(Func[0]), .F1(Func[1]),
    .F2(Func[2]), .F3(Func[3]), .F4(Func[4]), .F5(Func[5]), .S0(ALU_OP[0]), .S1(ALU_OP[1]), .S2(ALU_OP[2]),
    .S3(ALU_OP[3]));
  \控制信号自动生成  \u_控制信号自动生成_1  (
    .OP0(OP[0]), .OP1(OP[1]), .OP2(OP[2]), .OP3(OP[3]), .OP4(OP[4]), .OP5(OP[5]), .F0(Func[0]), .F1(Func[1]),
    .F2(Func[2]), .F3(Func[3]), .F4(Func[4]), .F5(Func[5]), .MemToReg(MemToReg), .MemWrite(MemWrite),
    .ALU_SRC(ALU_SRC), .RegWrite(RegWrite), .SysCALL(SysCALL), .SignedExt(SignedExt), .RegDst(RegDst),
    .BEQ(Beq), .BNE(Bne), .JR(JR), .JUMP(JMP), .JAL(JAL), .BGEZ(BGEZ), .XORI(XORI), .SLTIU(SLTIU), .LBU(LBU));

  // Other names for the same wires on the sheet: OP_CODE[5:0] = OP

  // Notes on the sheet:
  //   运算器控制器，根据指令生成运算器功能选择信号
  //   控制信号生成，产生数据通路需要的其他控制信号
endmodule

// 运算器控制器
module \运算控制器自动生成  (
  input  OP0,
  input  OP1,
  input  OP2,
  input  OP3,
  input  OP4,
  input  OP5,
  input  F0,
  input  F1,
  input  F2,
  input  F3,
  input  F4,
  input  F5,
  output S0,
  output S1,
  output S2,
  output S3
);

  wire and_1_out, and_2_out, and_3_out, and_4_out, and_5_out, and_6_out, and_7_out, and_8_out, and_9_out,
       and_10_out, and_11_out, and_12_out, and_13_out, and_14_out, and_15_out, and_16_out, and_17_out,
       and_18_out, and_19_out, and_20_out, and_21_out, and_22_out, and_23_out, and_24_out, and_25_out,
       and_26_out, and_27_out, and_28_out, and_29_out, and_30_out, and_31_out, and_32_out, and_33_out,
       and_34_out, and_35_out, and_36_out, and_37_out, and_38_out, and_39_out, and_40_out, and_41_out,
       and_42_out, and_43_out, not_1_out, not_2_out, not_3_out, not_4_out, not_5_out, not_6_out, not_7_out,
       not_8_out, not_9_out, not_10_out, not_11_out, not_12_out, not_13_out, not_14_out, not_15_out,
       not_16_out, not_17_out, not_18_out, not_19_out, not_20_out, not_21_out, not_22_out, not_23_out,
       not_24_out, not_25_out, not_26_out, not_27_out, not_28_out, not_29_out, not_30_out, not_31_out,
       not_32_out, not_33_out, not_34_out, not_35_out, not_36_out, not_37_out, not_38_out, not_39_out,
       not_40_out, not_41_out, not_42_out, not_43_out, not_44_out, not_45_out, not_46_out, not_47_out,
       not_48_out, not_49_out, not_50_out, not_51_out, not_52_out, not_53_out, not_54_out, not_55_out,
       not_56_out, not_57_out, not_58_out, not_59_out, not_60_out, not_61_out, not_62_out, not_63_out,
       not_64_out, not_65_out, not_66_out, not_67_out, not_68_out, not_69_out, not_70_out, not_71_out,
       not_72_out, not_73_out, not_74_out, not_75_out, not_76_out, not_77_out, not_78_out, not_79_out,
       not_80_out, not_81_out, not_82_out, not_83_out, not_84_out, not_85_out, not_86_out, not_87_out,
       not_88_out, not_89_out, not_90_out, not_91_out, not_92_out, not_93_out, not_94_out, not_95_out,
       not_96_out, not_97_out, not_98_out, not_99_out, not_100_out, not_101_out, not_102_out, not_103_out,
       not_104_out, not_105_out, not_106_out, not_107_out, not_108_out, not_109_out, not_110_out,
       not_111_out, not_112_out, not_113_out, not_114_out, not_115_out, not_116_out, not_117_out,
       not_118_out, not_119_out, not_120_out, not_121_out, not_122_out, not_123_out, not_124_out,
       not_125_out, not_126_out, not_127_out, not_128_out, not_129_out, not_130_out, not_131_out,
       not_132_out, not_133_out, not_134_out, not_135_out, not_136_out, not_137_out, not_138_out,
       not_139_out, not_140_out, not_141_out, not_142_out, not_143_out, not_144_out, not_145_out,
       not_146_out, not_147_out, not_148_out, not_149_out, not_150_out, not_151_out, not_152_out,
       not_153_out, not_154_out, not_155_out, not_156_out, not_157_out, not_158_out, not_159_out,
       not_160_out, not_161_out, not_162_out, not_163_out, not_164_out, not_165_out, not_166_out,
       not_167_out, not_168_out, not_169_out, not_170_out, not_171_out, not_172_out, not_173_out,
       not_174_out, not_175_out, not_176_out, not_177_out, not_178_out, not_179_out, not_180_out,
       not_181_out, not_182_out, not_183_out, not_184_out, not_185_out, not_186_out, not_187_out,
       not_188_out, not_189_out, not_190_out, not_191_out, not_192_out, not_193_out, not_194_out,
       not_195_out, not_196_out, not_197_out, not_198_out, not_199_out, not_200_out, not_201_out,
       not_202_out, not_203_out, not_204_out, not_205_out, not_206_out, not_207_out, not_208_out,
       not_209_out, not_210_out, not_211_out, not_212_out, not_213_out, not_214_out, not_215_out,
       not_216_out, not_217_out, not_218_out, not_219_out, not_220_out, not_221_out, not_222_out,
       not_223_out, not_224_out, not_225_out, not_226_out, not_227_out, not_228_out, not_229_out,
       not_230_out, not_231_out, not_232_out, not_233_out, not_234_out, not_235_out, not_236_out,
       not_237_out, not_238_out, not_239_out, not_240_out, not_241_out, not_242_out, not_243_out,
       not_244_out, not_245_out, not_246_out, not_247_out, not_248_out, not_249_out, not_250_out,
       not_251_out, not_252_out, not_253_out, not_254_out, not_255_out, not_256_out, not_257_out,
       not_258_out, not_259_out, not_260_out, not_261_out, not_262_out, not_263_out, not_264_out,
       not_265_out, not_266_out, not_267_out, not_268_out, not_269_out, not_270_out, not_271_out;

  not not_1 (not_1_out, OP5);
  not not_2 (not_2_out, OP4);
  not not_3 (not_3_out, OP3);
  not not_4 (not_4_out, OP2);
  not not_5 (not_5_out, OP1);
  not not_6 (not_6_out, OP0);
  not not_7 (not_7_out, F5);
  not not_8 (not_8_out, F4);
  not not_9 (not_9_out, F3);
  not not_10 (not_10_out, F2);
  not not_11 (not_11_out, OP5);
  not not_12 (not_12_out, OP4);
  not not_13 (not_13_out, OP3);
  not not_14 (not_14_out, OP2);
  not not_15 (not_15_out, OP1);
  not not_16 (not_16_out, OP0);
  not not_17 (not_17_out, F4);
  not not_18 (not_18_out, F3);
  not not_19 (not_19_out, F2);
  not not_20 (not_20_out, F1);
  not not_21 (not_21_out, F0);
  not not_22 (not_22_out, OP5);
  not not_23 (not_23_out, OP4);
  not not_24 (not_24_out, OP3);
  not not_25 (not_25_out, OP2);
  not not_26 (not_26_out, OP1);
  not not_27 (not_27_out, OP0);
  not not_28 (not_28_out, F4);
  not not_29 (not_29_out, F3);
  not not_30 (not_30_out, F2);
  not not_31 (not_31_out, F1);
  not not_32 (not_32_out, OP5);
  not not_33 (not_33_out, OP4);
  not not_34 (not_34_out, OP3);
  not not_35 (not_35_out, OP2);
  not not_36 (not_36_out, OP1);
  not not_37 (not_37_out, OP0);
  not not_38 (not_38_out, F4);
  not not_39 (not_39_out, F3);
  not not_40 (not_40_out, F1);
  not not_41 (not_41_out, F0);
  not not_42 (not_42_out, OP5);
  not not_43 (not_43_out, OP4);
  not not_44 (not_44_out, OP3);
  not not_45 (not_45_out, OP2);
  not not_46 (not_46_out, OP1);
  not not_47 (not_47_out, OP0);
  not not_48 (not_48_out, F4);
  not not_49 (not_49_out, F2);
  not not_50 (not_50_out, F0);
  not not_51 (not_51_out, OP5);
  not not_52 (not_52_out, OP4);
  not not_53 (not_53_out, OP2);
  not not_54 (not_54_out, OP1);
  not not_55 (not_55_out, OP0);
  not not_56 (not_56_out, OP5);
  not not_57 (not_57_out, OP4);
  not not_58 (not_58_out, OP1);
  not not_59 (not_59_out, OP0);
  not not_60 (not_60_out, OP5);
  not not_61 (not_61_out, OP4);
  not not_62 (not_62_out, OP2);
  not not_63 (not_63_out, OP1);
  not not_64 (not_64_out, OP5);
  not not_65 (not_65_out, OP4);
  not not_66 (not_66_out, OP2);
  not not_67 (not_67_out, OP0);
  not not_68 (not_68_out, OP4);
  not not_69 (not_69_out, OP3);
  not not_70 (not_70_out, OP2);
  not not_71 (not_71_out, OP4);
  not not_72 (not_72_out, OP2);
  not not_73 (not_73_out, OP5);
  not not_74 (not_74_out, OP4);
  not not_75 (not_75_out, OP0);
  not not_76 (not_76_out, OP4);
  not not_77 (not_77_out, OP3);
  not not_78 (not_78_out, OP1);
  not not_79 (not_79_out, OP0);
  not not_80 (not_80_out, OP5);
  not not_81 (not_81_out, OP4);
  not not_82 (not_82_out, OP3);
  not not_83 (not_83_out, OP2);
  not not_84 (not_84_out, OP1);
  not not_85 (not_85_out, OP5);
  not not_86 (not_86_out, OP4);
  not not_87 (not_87_out, OP3);
  not not_88 (not_88_out, OP2);
  not not_89 (not_89_out, OP1);
  not not_90 (not_90_out, OP0);
  not not_91 (not_91_out, F5);
  not not_92 (not_92_out, F4);
  not not_93 (not_93_out, F3);
  not not_94 (not_94_out, F2);
  not not_95 (not_95_out, F0);
  not not_96 (not_96_out, OP5);
  not not_97 (not_97_out, OP4);
  not not_98 (not_98_out, OP3);
  not not_99 (not_99_out, OP2);
  not not_100 (not_100_out, OP1);
  not not_101 (not_101_out, OP0);
  not not_102 (not_102_out, F4);
  not not_103 (not_103_out, F3);
  not not_104 (not_104_out, F2);
  not not_105 (not_105_out, F0);
  not not_106 (not_106_out, OP5);
  not not_107 (not_107_out, OP4);
  not not_108 (not_108_out, OP3);
  not not_109 (not_109_out, OP2);
  not not_110 (not_110_out, OP1);
  not not_111 (not_111_out, OP0);
  not not_112 (not_112_out, F4);
  not not_113 (not_113_out, F3);
  not not_114 (not_114_out, F1);
  not not_115 (not_115_out, F0);
  not not_116 (not_116_out, OP5);
  not not_117 (not_117_out, OP4);
  not not_118 (not_118_out, OP3);
  not not_119 (not_119_out, OP2);
  not not_120 (not_120_out, OP1);
  not not_121 (not_121_out, OP0);
  not not_122 (not_122_out, F4);
  not not_123 (not_123_out, F3);
  not not_124 (not_124_out, OP5);
  not not_125 (not_125_out, OP4);
  not not_126 (not_126_out, OP3);
  not not_127 (not_127_out, OP2);
  not not_128 (not_128_out, OP1);
  not not_129 (not_129_out, OP0);
  not not_130 (not_130_out, F4);
  not not_131 (not_131_out, F2);
  not not_132 (not_132_out, F0);
  not not_133 (not_133_out, OP5);
  not not_134 (not_134_out, OP4);
  not not_135 (not_135_out, OP1);
  not not_136 (not_136_out, OP0);
  not not_137 (not_137_out, OP5);
  not not_138 (not_138_out, OP4);
  not not_139 (not_139_out, OP2);
  not not_140 (not_140_out, OP0);
  not not_141 (not_141_out, OP5);
  not not_142 (not_142_out, OP4);
  not not_143 (not_143_out, OP3);
  not not_144 (not_144_out, OP2);
  not not_145 (not_145_out, OP1);
  not not_146 (not_146_out, OP5);
  not not_147 (not_147_out, OP4);
  not not_148 (not_148_out, OP3);
  not not_149 (not_149_out, OP2);
  not not_150 (not_150_out, OP1);
  not not_151 (not_151_out, OP0);
  not not_152 (not_152_out, F4);
  not not_153 (not_153_out, F3);
  not not_154 (not_154_out, F2);
  not not_155 (not_155_out, F1);
  not not_156 (not_156_out, F0);
  not not_157 (not_157_out, OP5);
  not not_158 (not_158_out, OP4);
  not not_159 (not_159_out, OP3);
  not not_160 (not_160_out, OP2);
  not not_161 (not_161_out, OP1);
  not not_162 (not_162_out, OP0);
  not not_163 (not_163_out, F4);
  not not_164 (not_164_out, F3);
  not not_165 (not_165_out, F2);
  not not_166 (not_166_out, F1);
  not not_167 (not_167_out, OP5);
  not not_168 (not_168_out, OP4);
  not not_169 (not_169_out, OP3);
  not not_170 (not_170_out, OP2);
  not not_171 (not_171_out, OP1);
  not not_172 (not_172_out, OP0);
  not not_173 (not_173_out, F4);
  not not_174 (not_174_out, F3);
  not not_175 (not_175_out, F2);
  not not_176 (not_176_out, F0);
  not not_177 (not_177_out, OP5);
  not not_178 (not_178_out, OP4);
  not not_179 (not_179_out, OP3);
  not not_180 (not_180_out, OP2);
  not not_181 (not_181_out, OP1);
  not not_182 (not_182_out, OP0);
  not not_183 (not_183_out, F4);
  not not_184 (not_184_out, F3);
  not not_185 (not_185_out, F1);
  not not_186 (not_186_out, F0);
  not not_187 (not_187_out, OP5);
  not not_188 (not_188_out, OP4);
  not not_189 (not_189_out, OP3);
  not not_190 (not_190_out, OP2);
  not not_191 (not_191_out, OP1);
  not not_192 (not_192_out, OP0);
  not not_193 (not_193_out, F4);
  not not_194 (not_194_out, F2);
  not not_195 (not_195_out, OP5);
  not not_196 (not_196_out, OP4);
  not not_197 (not_197_out, OP2);
  not not_198 (not_198_out, OP1);
  not not_199 (not_199_out, OP0);
  not not_200 (not_200_out, OP5);
  not not_201 (not_201_out, OP4);
  not not_202 (not_202_out, OP1);
  not not_203 (not_203_out, OP0);
  not not_204 (not_204_out, OP5);
  not not_205 (not_205_out, OP4);
  not not_206 (not_206_out, OP2);
  not not_207 (not_207_out, OP1);
  not not_208 (not_208_out, OP4);
  not not_209 (not_209_out, OP3);
  not not_210 (not_210_out, OP2);
  not not_211 (not_211_out, OP4);
  not not_212 (not_212_out, OP2);
  not not_213 (not_213_out, OP5);
  not not_214 (not_214_out, OP4);
  not not_215 (not_215_out, OP2);
  not not_216 (not_216_out, OP4);
  not not_217 (not_217_out, OP3);
  not not_218 (not_218_out, OP1);
  not not_219 (not_219_out, OP0);
  not not_220 (not_220_out, OP5);
  not not_221 (not_221_out, OP4);
  not not_222 (not_222_out, OP3);
  not not_223 (not_223_out, OP2);
  not not_224 (not_224_out, OP1);
  not not_225 (not_225_out, OP0);
  not not_226 (not_226_out, F4);
  not not_227 (not_227_out, F3);
  not not_228 (not_228_out, F1);
  not not_229 (not_229_out, OP5);
  not not_230 (not_230_out, OP4);
  not not_231 (not_231_out, OP3);
  not not_232 (not_232_out, OP2);
  not not_233 (not_233_out, OP1);
  not not_234 (not_234_out, OP0);
  not not_235 (not_235_out, F4);
  not not_236 (not_236_out, F3);
  not not_237 (not_237_out, OP5);
  not not_238 (not_238_out, OP4);
  not not_239 (not_239_out, OP3);
  not not_240 (not_240_out, OP2);
  not not_241 (not_241_out, OP1);
  not not_242 (not_242_out, OP0);
  not not_243 (not_243_out, F4);
  not not_244 (not_244_out, F2);
  not not_245 (not_245_out, F0);
  not not_246 (not_246_out, OP5);
  not not_247 (not_247_out, OP4);
  not not_248 (not_248_out, OP3);
  not not_249 (not_249_out, OP2);
  not not_250 (not_250_out, OP1);
  not not_251 (not_251_out, OP0);
  not not_252 (not_252_out, F4);
  not not_253 (not_253_out, F2);
  not not_254 (not_254_out, OP5);
  not not_255 (not_255_out, OP4);
  not not_256 (not_256_out, OP2);
  not not_257 (not_257_out, OP0);
  not not_258 (not_258_out, OP5);
  not not_259 (not_259_out, OP4);
  not not_260 (not_260_out, OP1);
  not not_261 (not_261_out, OP5);
  not not_262 (not_262_out, OP4);
  not not_263 (not_263_out, OP0);
  not not_264 (not_264_out, OP5);
  not not_265 (not_265_out, OP4);
  not not_266 (not_266_out, OP2);
  not not_267 (not_267_out, OP5);
  not not_268 (not_268_out, OP4);
  not not_269 (not_269_out, OP3);
  not not_270 (not_270_out, OP2);
  not not_271 (not_271_out, OP1);
  and and_1 (and_1_out, not_1_out, not_2_out, not_3_out, not_4_out, not_5_out, not_6_out, not_7_out, not_8_out, not_9_out, not_10_out, F1, F0);
  and and_2 (and_2_out, not_11_out, not_12_out, not_13_out, not_14_out, not_15_out, not_16_out, F5, not_17_out, not_18_out, not_19_out, not_20_out, not_21_out);
  and and_3 (and_3_out, not_22_out, not_23_out, not_24_out, not_25_out, not_26_out, not_27_out, F5, not_28_out, not_29_out, not_30_out, not_31_out, F0);
  and and_4 (and_4_out, not_32_out, not_33_out, not_34_out, not_35_out, not_36_out, not_37_out, F5, not_38_out, not_39_out, F2, not_40_out, not_41_out);
  and and_5 (and_5_out, not_42_out, not_43_out, not_44_out, not_45_out, not_46_out, not_47_out, F5, not_48_out, F3, not_49_out, F1, not_50_out);
  and and_6 (and_6_out, not_51_out, not_52_out, OP3, not_53_out, not_54_out, not_55_out);
  and and_7 (and_7_out, not_56_out, not_57_out, OP3, OP2, not_58_out, not_59_out);
  and and_8 (and_8_out, not_60_out, not_61_out, OP3, not_62_out, not_63_out, OP0);
  and and_9 (and_9_out, not_64_out, not_65_out, OP3, not_66_out, OP1, not_67_out);
  and and_10 (and_10_out, OP5, not_68_out, not_69_out, not_70_out, OP1, OP0);
  and and_11 (and_11_out, OP5, not_71_out, OP3, not_72_out, OP1, OP0);
  and and_12 (and_12_out, not_73_out, not_74_out, OP3, OP2, OP1, not_75_out);
  and and_13 (and_13_out, OP5, not_76_out, not_77_out, OP2, not_78_out, not_79_out);
  and and_14 (and_14_out, not_80_out, not_81_out, not_82_out, not_83_out, not_84_out, OP0);
  and and_15 (and_15_out, not_85_out, not_86_out, not_87_out, not_88_out, not_89_out, not_90_out, not_91_out, not_92_out, not_93_out, not_94_out, F1, not_95_out);
  and and_16 (and_16_out, not_96_out, not_97_out, not_98_out, not_99_out, not_100_out, not_101_out, F5, not_102_out, not_103_out, not_104_out, F1, not_105_out);
  and and_17 (and_17_out, not_106_out, not_107_out, not_108_out, not_109_out, not_110_out, not_111_out, F5, not_112_out, not_113_out, F2, not_114_out, not_115_out);
  and and_18 (and_18_out, not_116_out, not_117_out, not_118_out, not_119_out, not_120_out, not_121_out, F5, not_122_out, not_123_out, F2, F1, F0);
  and and_19 (and_19_out, not_124_out, not_125_out, not_126_out, not_127_out, not_128_out, not_129_out, F5, not_130_out, F3, not_131_out, F1, not_132_out);
  and and_20 (and_20_out, not_133_out, not_134_out, OP3, OP2, not_135_out, not_136_out);
  and and_21 (and_21_out, not_137_out, not_138_out, OP3, not_139_out, OP1, not_140_out);
  and and_22 (and_22_out, not_141_out, not_142_out, not_143_out, not_144_out, not_145_out, OP0);
  and and_23 (and_23_out, not_146_out, not_147_out, not_148_out, not_149_out, not_150_out, not_151_out, F5, not_152_out, not_153_out, not_154_out, not_155_out, not_156_out);
  and and_24 (and_24_out, not_157_out, not_158_out, not_159_out, not_160_out, not_161_out, not_162_out, F5, not_163_out, not_164_out, not_165_out, not_166_out, F0);
  and and_25 (and_25_out, not_167_out, not_168_out, not_169_out, not_170_out, not_171_out, not_172_out, F5, not_173_out, not_174_out, not_175_out, F1, not_176_out);
  and and_26 (and_26_out, not_177_out, not_178_out, not_179_out, not_180_out, not_181_out, not_182_out, F5, not_183_out, not_184_out, F2, not_185_out, not_186_out);
  and and_27 (and_27_out, not_187_out, not_188_out, not_189_out, not_190_out, not_191_out, not_192_out, F5, not_193_out, F3, not_194_out, F1, F0);
  and and_28 (and_28_out, not_195_out, not_196_out, OP3, not_197_out, not_198_out, not_199_out);
  and and_29 (and_29_out, not_200_out, not_201_out, OP3, OP2, not_202_out, not_203_out);
  and and_30 (and_30_out, not_204_out, not_205_out, OP3, not_206_out, not_207_out, OP0);
  and and_31 (and_31_out, OP5, not_208_out, not_209_out, not_210_out, OP1, OP0);
  and and_32 (and_32_out, OP5, not_211_out, OP3, not_212_out, OP1, OP0);
  and and_33 (and_33_out, not_213_out, not_214_out, OP3, not_215_out, OP1, OP0);
  and and_34 (and_34_out, OP5, not_216_out, not_217_out, OP2, not_218_out, not_219_out);
  and and_35 (and_35_out, not_220_out, not_221_out, not_222_out, not_223_out, not_224_out, not_225_out, F5, not_226_out, not_227_out, F2, not_228_out, F0);
  and and_36 (and_36_out, not_229_out, not_230_out, not_231_out, not_232_out, not_233_out, not_234_out, F5, not_235_out, not_236_out, F2, F1, F0);
  and and_37 (and_37_out, not_237_out, not_238_out, not_239_out, not_240_out, not_241_out, not_242_out, F5, not_243_out, F3, not_244_out, F1, not_245_out);
  and and_38 (and_38_out, not_246_out, not_247_out, not_248_out, not_249_out, not_250_out, not_251_out, F5, not_252_out, F3, not_253_out, F1, F0);
  and and_39 (and_39_out, not_254_out, not_255_out, OP3, not_256_out, OP1, not_257_out);
  and and_40 (and_40_out, not_258_out, not_259_out, OP3, OP2, not_260_out, OP0);
  and and_41 (and_41_out, not_261_out, not_262_out, OP3, OP2, OP1, not_263_out);
  and and_42 (and_42_out, not_264_out, not_265_out, OP3, not_266_out, OP1, OP0);
  and and_43 (and_43_out, not_267_out, not_268_out, not_269_out, not_270_out, not_271_out, OP0);
  or or_1 (S1, and_15_out, and_16_out, and_17_out, and_18_out, and_19_out, and_20_out, and_21_out, and_22_out);
  or or_2 (S3, and_35_out, and_36_out, and_37_out, and_38_out, and_39_out, and_40_out, and_41_out, and_42_out, and_43_out);
  or or_3 (S0, and_1_out, and_2_out, and_3_out, and_4_out, and_5_out, and_6_out, and_7_out, and_8_out, and_9_out, and_10_out, and_11_out, and_12_out, and_13_out, and_14_out);
  or or_4 (S2, and_23_out, and_24_out, and_25_out, and_26_out, and_27_out, and_28_out, and_29_out, and_30_out, and_31_out, and_32_out, and_33_out, and_34_out);
endmodule

// 控制信号生成
module \控制信号自动生成  (
  input  OP0,
  input  OP1,
  input  OP2,
  input  OP3,
  input  OP4,
  input  OP5,
  input  F0,
  input  F1,
  input  F2,
  input  F3,
  input  F4,
  input  F5,
  output MemToReg,
  output MemWrite,
  output ALU_SRC,
  output RegWrite,
  output SysCALL,
  output SignedExt,
  output RegDst,
  output BEQ,
  output BNE,
  output JR,
  output JUMP,
  output JAL,
  output BGEZ,
  output XORI,
  output SLTIU,
  output LBU
);

  wire and_1_out, and_2_out, and_4_out, and_5_out, and_6_out, and_7_out, and_8_out, and_9_out, and_10_out,
       and_11_out, and_12_out, and_13_out, and_14_out, and_15_out, and_16_out, and_17_out, and_18_out,
       and_20_out, and_21_out, and_22_out, and_23_out, and_24_out, and_25_out, and_26_out, and_27_out,
       and_28_out, and_29_out, and_30_out, and_31_out, and_32_out, and_33_out, and_34_out, and_38_out,
       and_39_out, not_1_out, not_2_out, not_3_out, not_4_out, not_5_out, not_6_out, not_7_out, not_8_out,
       not_9_out, not_10_out, not_11_out, not_12_out, not_13_out, not_14_out, not_15_out, not_16_out,
       not_17_out, not_18_out, not_19_out, not_20_out, not_21_out, not_22_out, not_23_out, not_24_out,
       not_25_out, not_26_out, not_27_out, not_28_out, not_29_out, not_30_out, not_31_out, not_32_out,
       not_33_out, not_34_out, not_35_out, not_36_out, not_37_out, not_38_out, not_39_out, not_40_out,
       not_41_out, not_42_out, not_43_out, not_44_out, not_45_out, not_46_out, not_47_out, not_48_out,
       not_49_out, not_50_out, not_51_out, not_52_out, not_53_out, not_54_out, not_55_out, not_56_out,
       not_57_out, not_58_out, not_59_out, not_60_out, not_61_out, not_62_out, not_63_out, not_64_out,
       not_65_out, not_66_out, not_67_out, not_68_out, not_69_out, not_70_out, not_71_out, not_72_out,
       not_73_out, not_74_out, not_75_out, not_76_out, not_77_out, not_78_out, not_79_out, not_80_out,
       not_81_out, not_82_out, not_83_out, not_84_out, not_85_out, not_86_out, not_87_out, not_88_out,
       not_89_out, not_90_out, not_91_out, not_92_out, not_93_out, not_94_out, not_95_out, not_96_out,
       not_97_out, not_98_out, not_99_out, not_100_out, not_101_out, not_102_out, not_103_out, not_104_out,
       not_105_out, not_106_out, not_107_out, not_108_out, not_109_out, not_110_out, not_111_out,
       not_112_out, not_113_out, not_114_out, not_115_out, not_116_out, not_117_out, not_118_out,
       not_119_out, not_120_out, not_121_out, not_122_out, not_123_out, not_124_out, not_125_out,
       not_126_out, not_127_out, not_128_out, not_129_out, not_130_out, not_131_out, not_132_out,
       not_133_out, not_134_out, not_135_out, not_136_out, not_137_out, not_138_out, not_139_out,
       not_140_out, not_141_out, not_142_out, not_143_out, not_144_out, not_145_out, not_146_out,
       not_147_out, not_148_out, not_149_out, not_150_out, not_151_out, not_152_out, not_153_out,
       not_154_out, not_155_out, not_156_out, not_157_out, not_158_out, not_159_out, not_160_out,
       not_161_out, not_162_out, not_163_out, not_164_out, not_165_out, not_166_out, not_167_out,
       not_168_out, not_169_out, not_170_out, not_171_out, not_172_out, not_173_out, not_174_out,
       not_175_out, not_176_out, not_177_out, not_178_out, not_179_out, not_180_out, not_181_out,
       not_182_out, not_183_out, not_184_out, not_185_out, not_186_out, not_187_out, not_188_out,
       not_189_out, not_190_out, not_191_out, not_192_out, not_193_out, not_194_out, not_195_out,
       not_196_out, not_197_out, not_198_out, not_199_out, not_200_out, not_201_out, not_202_out,
       not_203_out, not_204_out, not_205_out, not_206_out, not_207_out, not_208_out, not_209_out,
       not_210_out, not_211_out, not_212_out, not_213_out, not_214_out, not_215_out, not_216_out,
       not_217_out, not_218_out, not_219_out, not_220_out, not_221_out, not_222_out, not_223_out,
       not_224_out, not_225_out, not_226_out, not_227_out, not_228_out, not_229_out, not_230_out,
       not_231_out, not_232_out, not_233_out;

  not not_1 (not_1_out, OP0);
  not not_2 (not_2_out, OP1);
  not not_3 (not_3_out, OP3);
  not not_4 (not_4_out, OP4);
  not not_5 (not_5_out, OP2);
  not not_6 (not_6_out, OP3);
  not not_7 (not_7_out, OP4);
  not not_8 (not_8_out, OP2);
  not not_9 (not_9_out, OP4);
  not not_10 (not_10_out, OP0);
  not not_11 (not_11_out, OP4);
  not not_12 (not_12_out, OP5);
  not not_13 (not_13_out, OP1);
  not not_14 (not_14_out, OP4);
  not not_15 (not_15_out, OP5);
  not not_16 (not_16_out, OP2);
  not not_17 (not_17_out, OP4);
  not not_18 (not_18_out, OP5);
  not not_19 (not_19_out, OP0);
  not not_20 (not_20_out, OP1);
  not not_21 (not_21_out, OP3);
  not not_22 (not_22_out, OP4);
  not not_23 (not_23_out, OP2);
  not not_24 (not_24_out, OP4);
  not not_25 (not_25_out, OP0);
  not not_26 (not_26_out, OP1);
  not not_27 (not_27_out, OP2);
  not not_28 (not_28_out, OP4);
  not not_29 (not_29_out, OP5);
  not not_30 (not_30_out, F0);
  not not_31 (not_31_out, F2);
  not not_32 (not_32_out, F3);
  not not_33 (not_33_out, F4);
  not not_34 (not_34_out, OP0);
  not not_35 (not_35_out, OP1);
  not not_36 (not_36_out, OP2);
  not not_37 (not_37_out, OP4);
  not not_38 (not_38_out, OP5);
  not not_39 (not_39_out, F1);
  not not_40 (not_40_out, F3);
  not not_41 (not_41_out, F4);
  not not_42 (not_42_out, OP0);
  not not_43 (not_43_out, OP1);
  not not_44 (not_44_out, OP2);
  not not_45 (not_45_out, OP4);
  not not_46 (not_46_out, OP5);
  not not_47 (not_47_out, F2);
  not not_48 (not_48_out, F3);
  not not_49 (not_49_out, F4);
  not not_50 (not_50_out, F5);
  not not_51 (not_51_out, OP0);
  not not_52 (not_52_out, OP1);
  not not_53 (not_53_out, OP2);
  not not_54 (not_54_out, OP4);
  not not_55 (not_55_out, OP5);
  not not_56 (not_56_out, F2);
  not not_57 (not_57_out, F4);
  not not_58 (not_58_out, OP0);
  not not_59 (not_59_out, OP1);
  not not_60 (not_60_out, OP2);
  not not_61 (not_61_out, OP4);
  not not_62 (not_62_out, OP5);
  not not_63 (not_63_out, F3);
  not not_64 (not_64_out, F4);
  not not_65 (not_65_out, OP0);
  not not_66 (not_66_out, OP4);
  not not_67 (not_67_out, OP5);
  not not_68 (not_68_out, OP1);
  not not_69 (not_69_out, OP4);
  not not_70 (not_70_out, OP5);
  not not_71 (not_71_out, OP2);
  not not_72 (not_72_out, OP4);
  not not_73 (not_73_out, OP5);
  not not_74 (not_74_out, OP0);
  not not_75 (not_75_out, OP1);
  not not_76 (not_76_out, OP3);
  not not_77 (not_77_out, OP4);
  not not_78 (not_78_out, OP2);
  not not_79 (not_79_out, OP3);
  not not_80 (not_80_out, OP4);
  not not_81 (not_81_out, OP0);
  not not_82 (not_82_out, OP1);
  not not_83 (not_83_out, OP2);
  not not_84 (not_84_out, OP3);
  not not_85 (not_85_out, OP4);
  not not_86 (not_86_out, OP5);
  not not_87 (not_87_out, F0);
  not not_88 (not_88_out, F1);
  not not_89 (not_89_out, F4);
  not not_90 (not_90_out, F5);
  not not_91 (not_91_out, OP5);
  not not_92 (not_92_out, OP4);
  not not_93 (not_93_out, OP3);
  not not_94 (not_94_out, OP1);
  not not_95 (not_95_out, OP0);
  not not_96 (not_96_out, OP5);
  not not_97 (not_97_out, OP4);
  not not_98 (not_98_out, OP3);
  not not_99 (not_99_out, OP1);
  not not_100 (not_100_out, OP5);
  not not_101 (not_101_out, OP4);
  not not_102 (not_102_out, OP2);
  not not_103 (not_103_out, OP1);
  not not_104 (not_104_out, OP0);
  not not_105 (not_105_out, OP5);
  not not_106 (not_106_out, OP4);
  not not_107 (not_107_out, OP2);
  not not_108 (not_108_out, OP1);
  not not_109 (not_109_out, OP5);
  not not_110 (not_110_out, OP4);
  not not_111 (not_111_out, OP2);
  not not_112 (not_112_out, OP0);
  not not_113 (not_113_out, OP4);
  not not_114 (not_114_out, OP3);
  not not_115 (not_115_out, OP2);
  not not_116 (not_116_out, OP4);
  not not_117 (not_117_out, OP2);
  not not_118 (not_118_out, OP5);
  not not_119 (not_119_out, OP4);
  not not_120 (not_120_out, OP2);
  not not_121 (not_121_out, OP4);
  not not_122 (not_122_out, OP3);
  not not_123 (not_123_out, OP1);
  not not_124 (not_124_out, OP0);
  not not_125 (not_125_out, OP0);
  not not_126 (not_126_out, OP1);
  not not_127 (not_127_out, OP2);
  not not_128 (not_128_out, OP3);
  not not_129 (not_129_out, OP4);
  not not_130 (not_130_out, OP5);
  not not_131 (not_131_out, F0);
  not not_132 (not_132_out, F1);
  not not_133 (not_133_out, F2);
  not not_134 (not_134_out, F4);
  not not_135 (not_135_out, F5);
  not not_136 (not_136_out, OP0);
  not not_137 (not_137_out, OP1);
  not not_138 (not_138_out, OP2);
  not not_139 (not_139_out, OP3);
  not not_140 (not_140_out, OP4);
  not not_141 (not_141_out, OP5);
  not not_142 (not_142_out, F0);
  not not_143 (not_143_out, F2);
  not not_144 (not_144_out, F3);
  not not_145 (not_145_out, F4);
  not not_146 (not_146_out, OP0);
  not not_147 (not_147_out, OP1);
  not not_148 (not_148_out, OP2);
  not not_149 (not_149_out, OP3);
  not not_150 (not_150_out, OP4);
  not not_151 (not_151_out, OP5);
  not not_152 (not_152_out, F1);
  not not_153 (not_153_out, F3);
  not not_154 (not_154_out, F4);
  not not_155 (not_155_out, OP0);
  not not_156 (not_156_out, OP1);
  not not_157 (not_157_out, OP2);
  not not_158 (not_158_out, OP3);
  not not_159 (not_159_out, OP4);
  not not_160 (not_160_out, OP5);
  not not_161 (not_161_out, F2);
  not not_162 (not_162_out, F3);
  not not_163 (not_163_out, F4);
  not not_164 (not_164_out, F5);
  not not_165 (not_165_out, OP0);
  not not_166 (not_166_out, OP1);
  not not_167 (not_167_out, OP2);
  not not_168 (not_168_out, OP3);
  not not_169 (not_169_out, OP4);
  not not_170 (not_170_out, OP5);
  not not_171 (not_171_out, F2);
  not not_172 (not_172_out, F4);
  not not_173 (not_173_out, OP0);
  not not_174 (not_174_out, OP1);
  not not_175 (not_175_out, OP2);
  not not_176 (not_176_out, OP3);
  not not_177 (not_177_out, OP4);
  not not_178 (not_178_out, OP5);
  not not_179 (not_179_out, F3);
  not not_180 (not_180_out, F4);
  not not_181 (not_181_out, OP0);
  not not_182 (not_182_out, OP1);
  not not_183 (not_183_out, OP3);
  not not_184 (not_184_out, OP4);
  not not_185 (not_185_out, OP5);
  not not_186 (not_186_out, OP1);
  not not_187 (not_187_out, OP3);
  not not_188 (not_188_out, OP4);
  not not_189 (not_189_out, OP5);
  not not_190 (not_190_out, OP0);
  not not_191 (not_191_out, OP1);
  not not_192 (not_192_out, OP2);
  not not_193 (not_193_out, OP3);
  not not_194 (not_194_out, OP4);
  not not_195 (not_195_out, OP5);
  not not_196 (not_196_out, F0);
  not not_197 (not_197_out, F1);
  not not_198 (not_198_out, F2);
  not not_199 (not_199_out, F4);
  not not_200 (not_200_out, F5);
  not not_201 (not_201_out, OP0);
  not not_202 (not_202_out, OP2);
  not not_203 (not_203_out, OP3);
  not not_204 (not_204_out, OP4);
  not not_205 (not_205_out, OP5);
  not not_206 (not_206_out, F0);
  not not_207 (not_207_out, F1);
  not not_208 (not_208_out, F2);
  not not_209 (not_209_out, F4);
  not not_210 (not_210_out, F5);
  not not_211 (not_211_out, OP2);
  not not_212 (not_212_out, OP3);
  not not_213 (not_213_out, OP4);
  not not_214 (not_214_out, OP5);
  not not_215 (not_215_out, OP2);
  not not_216 (not_216_out, OP3);
  not not_217 (not_217_out, OP4);
  not not_218 (not_218_out, OP5);
  not not_219 (not_219_out, OP1);
  not not_220 (not_220_out, OP2);
  not not_221 (not_221_out, OP3);
  not not_222 (not_222_out, OP4);
  not not_223 (not_223_out, OP5);
  not not_224 (not_224_out, OP0);
  not not_225 (not_225_out, OP4);
  not not_226 (not_226_out, OP5);
  not not_227 (not_227_out, OP2);
  not not_228 (not_228_out, OP4);
  not not_229 (not_229_out, OP5);
  not not_230 (not_230_out, OP0);
  not not_231 (not_231_out, OP1);
  not not_232 (not_232_out, OP3);
  not not_233 (not_233_out, OP4);
  and and_1 (and_1_out, not_1_out, not_2_out, OP2, not_3_out, not_4_out, OP5);
  and and_2 (and_2_out, OP0, OP1, not_5_out, not_6_out, not_7_out, OP5);
  and and_3 (MemWrite, OP0, OP1, not_8_out, OP3, not_9_out, OP5);
  and and_4 (and_4_out, not_10_out, OP3, not_11_out, not_12_out);
  and and_5 (and_5_out, not_13_out, OP3, not_14_out, not_15_out);
  and and_6 (and_6_out, not_16_out, OP3, not_17_out, not_18_out);
  and and_7 (and_7_out, not_19_out, not_20_out, OP2, not_21_out, not_22_out, OP5);
  and and_8 (and_8_out, OP0, OP1, not_23_out, not_24_out, OP5);
  and and_9 (and_9_out, not_25_out, not_26_out, not_27_out, not_28_out, not_29_out, not_30_out, not_31_out, not_32_out, not_33_out);
  and and_10 (and_10_out, not_34_out, not_35_out, not_36_out, not_37_out, not_38_out, not_39_out, not_40_out, not_41_out, F5);
  and and_11 (and_11_out, not_42_out, not_43_out, not_44_out, not_45_out, not_46_out, F1, not_47_out, not_48_out, not_49_out, not_50_out);
  and and_12 (and_12_out, not_51_out, not_52_out, not_53_out, not_54_out, not_55_out, F1, not_56_out, F3, not_57_out, F5);
  and and_13 (and_13_out, not_58_out, not_59_out, not_60_out, not_61_out, not_62_out, F0, F2, not_63_out, not_64_out, F5);
  and and_14 (and_14_out, not_65_out, OP3, not_66_out, not_67_out);
  and and_15 (and_15_out, not_68_out, OP3, not_69_out, not_70_out);
  and and_16 (and_16_out, not_71_out, OP3, not_72_out, not_73_out);
  and and_17 (and_17_out, not_74_out, not_75_out, OP2, not_76_out, not_77_out, OP5);
  and and_18 (and_18_out, OP0, OP1, not_78_out, not_79_out, not_80_out);
  and and_19 (SysCALL, not_81_out, not_82_out, not_83_out, not_84_out, not_85_out, not_86_out, not_87_out, not_88_out, F2, F3, not_89_out, not_90_out);
  and and_20 (and_20_out, not_91_out, not_92_out, not_93_out, OP2, not_94_out, not_95_out);
  and and_21 (and_21_out, not_96_out, not_97_out, not_98_out, OP2, not_99_out, OP0);
  and and_22 (and_22_out, not_100_out, not_101_out, OP3, not_102_out, not_103_out, not_104_out);
  and and_23 (and_23_out, not_105_out, not_106_out, OP3, not_107_out, not_108_out, OP0);
  and and_24 (and_24_out, not_109_out, not_110_out, OP3, not_111_out, OP1, not_112_out);
  and and_25 (and_25_out, OP5, not_113_out, not_114_out, not_115_out, OP1, OP0);
  and and_26 (and_26_out, OP5, not_116_out, OP3, not_117_out, OP1, OP0);
  and and_27 (and_27_out, not_118_out, not_119_out, OP3, not_120_out, OP1, OP0);
  and and_28 (and_28_out, OP5, not_121_out, not_122_out, OP2, not_123_out, not_124_out);
  and and_29 (and_29_out, not_125_out, not_126_out, not_127_out, not_128_out, not_129_out, not_130_out, not_131_out, not_132_out, not_133_out, not_134_out, not_135_out);
  and and_30 (and_30_out, not_136_out, not_137_out, not_138_out, not_139_out, not_140_out, not_141_out, not_142_out, not_143_out, not_144_out, not_145_out);
  and and_31 (and_31_out, not_146_out, not_147_out, not_148_out, not_149_out, not_150_out, not_151_out, not_152_out, not_153_out, not_154_out, F5);
  and and_32 (and_32_out, not_155_out, not_156_out, not_157_out, not_158_out, not_159_out, not_160_out, F1, not_161_out, not_162_out, not_163_out, not_164_out);
  and and_33 (and_33_out, not_165_out, not_166_out, not_167_out, not_168_out, not_169_out, not_170_out, F1, not_171_out, F3, not_172_out, F5);
  and and_34 (and_34_out, not_173_out, not_174_out, not_175_out, not_176_out, not_177_out, not_178_out, F0, F2, not_179_out, not_180_out, F5);
  and and_35 (BEQ, not_181_out, not_182_out, OP2, not_183_out, not_184_out, not_185_out);
  and and_36 (BNE, OP0, not_186_out, OP2, not_187_out, not_188_out, not_189_out);
  and and_37 (JR, not_190_out, not_191_out, not_192_out, not_193_out, not_194_out, not_195_out, not_196_out, not_197_out, not_198_out, F3, not_199_out, not_200_out);
  and and_38 (and_38_out, not_201_out, not_202_out, not_203_out, not_204_out, not_205_out, not_206_out, not_207_out, not_208_out, F3, not_209_out, not_210_out);
  and and_39 (and_39_out, OP1, not_211_out, not_212_out, not_213_out, not_214_out);
  and and_40 (JAL, OP0, OP1, not_215_out, not_216_out, not_217_out, not_218_out);
  and and_41 (BGEZ, OP0, not_219_out, not_220_out, not_221_out, not_222_out, not_223_out);
  and and_42 (XORI, not_224_out, OP1, OP2, OP3, not_225_out, not_226_out);
  and and_43 (SLTIU, OP0, OP1, not_227_out, OP3, not_228_out, not_229_out);
  and and_44 (LBU, not_230_out, not_231_out, OP2, not_232_out, not_233_out, OP5);
  or or_1 (MemToReg, and_1_out, and_2_out);
  or or_2 (ALU_SRC, and_4_out, and_5_out, and_6_out, and_7_out, and_8_out);
  or or_3 (RegWrite, and_9_out, and_10_out, and_11_out, and_12_out, and_13_out, and_14_out, and_15_out, and_16_out, and_17_out, and_18_out);
  or or_4 (SignedExt, and_20_out, and_21_out, and_22_out, and_23_out, and_24_out, and_25_out, and_26_out, and_27_out, and_28_out);
  or or_5 (RegDst, and_29_out, and_30_out, and_31_out, and_32_out, and_33_out, and_34_out);
  or or_6 (JUMP, and_38_out, and_39_out);
endmodule

// ALU
module MIPS_ALU (
  input  [4:0] shamt,
  input  [31:0] X,
  input  [31:0] Y,
  input  [3:0] AluOP,
  output Equal,
  output [31:0] Result,
  output [31:0] Result_2
);

  wire [0:0] comparator_1_lt, comparator_2_lt;
  wire [31:0] adder_1_out, AND_out, divider_1_out, divider_1_rem, multiplier_1_cout, multiplier_1_out,
       NOR_out, OR_out, shifter_1_out, shifter_2_out, shifter_3_out, subtractor_1_out, XOR_out;

  assign AND_out = X & Y;  // AND_Gate AND, 32 bits wide
  assign OR_out = X | Y;  // OR_Gate OR, 32 bits wide
  Shifter #(.width(32), .shift("ll")) shifter_1 (.in(Y), .\dist (shamt), .out(shifter_1_out));
  Shifter #(.width(32), .shift("ar")) shifter_2 (.in(Y), .\dist (shamt), .out(shifter_2_out));
  Shifter #(.width(32), .shift("lr")) shifter_3 (.in(Y), .\dist (shamt), .out(shifter_3_out));
  Multiplier #(.width(32)) multiplier_1 (.a(X), .b(Y), .out(multiplier_1_out), .cout(multiplier_1_cout));  // open: cin
  Divider #(.width(32)) divider_1 (.a(X), .b(Y), .out(divider_1_out), .rem(divider_1_rem));  // open: upper
  Adder #(.width(32)) adder_1 (.a(X), .b(Y), .out(adder_1_out));  // open: cin, cout
  Subtractor #(.width(32)) subtractor_1 (.a(X), .b(Y), .out(subtractor_1_out));  // open: bin, bout
  assign XOR_out = X ^ Y;  // XOR_Gate XOR, 32 bits wide
  assign NOR_out = ~(X | Y);  // NOR_Gate NOR, 32 bits wide
  Comparator #(.width(32), .mode("twosComplement")) comparator_1 (
    .a(X), .b(Y), .eq(Equal), .lt(comparator_1_lt[0]));  // open: gt
  Comparator #(.width(32), .mode("unsigned")) comparator_2 (.a(X), .b(Y), .lt(comparator_2_lt[0]));  // open: gt, eq
  Multiplexer #(.select(4), .width(32), .disabled("Z"), .enable("false")) multiplexer_1 (
    .in0(shifter_1_out), .in1(shifter_2_out), .in2(shifter_3_out), .in3(multiplier_1_out),
    .in4(divider_1_out), .in5(adder_1_out), .in6(subtractor_1_out), .in7(AND_out), .in8(OR_out),
    .in9(XOR_out), .in10(NOR_out), .in11({{31{1'b0}}, comparator_1_lt[0]}),
    .in12({{31{1'b0}}, comparator_2_lt[0]}), .in13({32{1'b0}}), .in14({32{1'b0}}), .in15({32{1'b0}}),
    .out(Result), .sel(AluOP));
  Multiplexer #(.select(4), .width(32), .disabled("Z"), .enable("false")) multiplexer_2 (
    .in0({32{1'b0}}), .in1({32{1'b0}}), .in2({32{1'b0}}), .in3(multiplier_1_cout), .in4(divider_1_rem),
    .in5({32{1'b0}}), .in6({32{1'b0}}), .in7({32{1'b0}}), .in8({32{1'b0}}), .in9({32{1'b0}}),
    .in10({32{1'b0}}), .in11({32{1'b0}}), .in12({32{1'b0}}), .in13({32{1'b0}}), .in14({32{1'b0}}),
    .in15({32{1'b0}}), .out(Result_2), .sel(AluOP));

  // Other names for the same wires on the sheet: Result2[31:0] = Result_2; S[3:0] = AluOP

  // Notes on the sheet:
  //   不要改变此引脚区域内容，也不要改变ALU封装形式
  //   输入引脚
  //   输出引脚
endmodule

module MIPS_Regifile (
  input  [31:0] Din,
  input  Clk,
  input  WE,
  input  [4:0] R1_num,
  input  [4:0] W_num,
  input  [4:0] R2_num,
  output [31:0] R1,
  output [31:0] R2
);

  // RegisterFile registerfile_1: pin names not known; wires that end beside it: Din, Clk, WE, W_num, R1_num, R2_num, R1, R2
endmodule

module \中断按键参考电路  (
  input  \同步清零信号 ,
  output \与中断屏蔽位与 
);

  wire \_1号中断_out , and_1_out, clock_1_out, d_ff_1_q, or_1_out, or_2_out;

  Clock #(.highDuration(1), .lowDuration(1)) clock_1 (.out(clock_1_out));
  Button \_1号中断  (.out(\_1号中断_out ));
  or or_1 (or_1_out, \与中断屏蔽位与 , d_ff_1_q);
  LED #(.active("true")) \_1号中断等待指示灯  (.in(or_1_out));
  D_Flip_Flop #(.trigger("rising"), .Pre_Clr_Positions("LEGACY"), .NegatePresetClear("false"), .enable("true"), .NewFFLayout("false")) d_ff_1 (
    .clk(\_1号中断_out ), .D(1'b1), .Q(d_ff_1_q), .reset(\与中断屏蔽位与 ));  // open: Qn, preset, en
  or or_2 (or_2_out, d_ff_1_q, \与中断屏蔽位与 );
  and and_1 (and_1_out, or_2_out, ~\同步清零信号 );  // AND_Gate
  D_Flip_Flop #(.trigger("rising"), .Pre_Clr_Positions("LEGACY"), .NegatePresetClear("false"), .enable("true"), .NewFFLayout("false")) IR1 (
    .clk(clock_1_out), .D(and_1_out), .Q(\与中断屏蔽位与 ));  // open: Qn, preset, en, reset

  // Notes on the sheet:
  //   中断信号采样参考电路
  //   Reset 
endmodule

module \中断信号产生  (
  input  clk,
  input  \_1号中断 ,
  input  \_1号清零 ,
  input  \_2号中断 ,
  input  \_2号清零信号 ,
  input  \_3号中断 ,
  input  \_3号清零信号 ,
  output \与中断屏蔽位与 ,
  output \_1号中断等待指示灯 ,
  output \_2号 ,
  output \_2号中断等待指示灯 ,
  output \_3号 ,
  output \_3号中断等待指示灯 
);

  wire and_1_out, and_2_out, and_3_out, d_ff_1_q, d_ff_2_q, d_ff_3_q, or_4_out, or_5_out, or_6_out;

  or or_1 (\_1号中断等待指示灯 , \与中断屏蔽位与 , d_ff_1_q);
  or or_2 (\_2号中断等待指示灯 , \_2号 , d_ff_2_q);
  or or_3 (\_3号中断等待指示灯 , \_3号 , d_ff_3_q);
  D_Flip_Flop #(.trigger("rising"), .Pre_Clr_Positions("LEGACY"), .NegatePresetClear("false"), .enable("true"), .NewFFLayout("false")) d_ff_1 (
    .clk(\_1号中断 ), .D(1'b1), .Q(d_ff_1_q), .reset(\与中断屏蔽位与 ));  // open: Qn, preset, en
  D_Flip_Flop #(.trigger("rising"), .Pre_Clr_Positions("LEGACY"), .NegatePresetClear("false"), .enable("true"), .NewFFLayout("false")) d_ff_2 (
    .clk(\_2号中断 ), .D(1'b1), .Q(d_ff_2_q), .reset(\_2号 ));  // open: Qn, preset, en
  D_Flip_Flop #(.trigger("rising"), .Pre_Clr_Positions("LEGACY"), .NegatePresetClear("false"), .enable("true"), .NewFFLayout("false")) d_ff_3 (
    .clk(\_3号中断 ), .D(1'b1), .Q(d_ff_3_q), .reset(\_3号 ));  // open: Qn, preset, en
  or or_4 (or_4_out, d_ff_1_q, \与中断屏蔽位与 );
  or or_5 (or_5_out, d_ff_2_q, \_2号 );
  or or_6 (or_6_out, d_ff_3_q, \_3号 );
  and and_1 (and_1_out, or_4_out, ~\_1号清零 );  // AND_Gate
  and and_2 (and_2_out, or_5_out, ~\_2号清零信号 );  // AND_Gate
  and and_3 (and_3_out, or_6_out, ~\_3号清零信号 );  // AND_Gate
  D_Flip_Flop #(.trigger("falling"), .Pre_Clr_Positions("LEGACY"), .NegatePresetClear("false"), .enable("true"), .NewFFLayout("false")) IR1 (
    .clk(clk), .D(and_1_out), .Q(\与中断屏蔽位与 ));  // open: Qn, preset, en, reset
  D_Flip_Flop #(.trigger("falling"), .Pre_Clr_Positions("LEGACY"), .NegatePresetClear("false"), .enable("true"), .NewFFLayout("false")) IR2 (
    .clk(clk), .D(and_2_out), .Q(\_2号 ));  // open: Qn, preset, en, reset
  D_Flip_Flop #(.trigger("falling"), .Pre_Clr_Positions("LEGACY"), .NegatePresetClear("false"), .enable("true"), .NewFFLayout("false")) IR3 (
    .clk(clk), .D(and_3_out), .Q(\_3号 ));  // open: Qn, preset, en, reset

  // Notes on the sheet:
  //   Reset 
  //   Reset 
  //   Reset 
endmodule

module \中断信号产生_上跳沿  (
  input  clk,
  input  \_1号中断 ,
  input  \_1号清零 ,
  input  \_2号中断 ,
  input  \_2号清零信号 ,
  input  \_3号中断 ,
  input  \_3号清零信号 ,
  output \与中断屏蔽位与 ,
  output \_1号中断等待指示灯 ,
  output \_2号 ,
  output \_2号中断等待指示灯 ,
  output \_3号 ,
  output \_3号中断等待指示灯 
);

  wire and_1_out, and_2_out, and_3_out, d_ff_1_q, d_ff_2_q, d_ff_3_q, or_4_out, or_5_out, or_6_out;

  or or_1 (\_1号中断等待指示灯 , \与中断屏蔽位与 , d_ff_1_q);
  or or_2 (\_2号中断等待指示灯 , \_2号 , d_ff_2_q);
  or or_3 (\_3号中断等待指示灯 , \_3号 , d_ff_3_q);
  D_Flip_Flop #(.trigger("rising"), .Pre_Clr_Positions("LEGACY"), .NegatePresetClear("false"), .enable("true"), .NewFFLayout("false")) d_ff_1 (
    .clk(\_1号中断 ), .D(1'b1), .Q(d_ff_1_q), .reset(\与中断屏蔽位与 ));  // open: Qn, preset, en
  D_Flip_Flop #(.trigger("rising"), .Pre_Clr_Positions("LEGACY"), .NegatePresetClear("false"), .enable("true"), .NewFFLayout("false")) d_ff_2 (
    .clk(\_2号中断 ), .D(1'b1), .Q(d_ff_2_q), .reset(\_2号 ));  // open: Qn, preset, en
  D_Flip_Flop #(.trigger("rising"), .Pre_Clr_Positions("LEGACY"), .NegatePresetClear("false"), .enable("true"), .NewFFLayout("false")) d_ff_3 (
    .clk(\_3号中断 ), .D(1'b1), .Q(d_ff_3_q), .reset(\_3号 ));  // open: Qn, preset, en
  or or_4 (or_4_out, d_ff_1_q, \与中断屏蔽位与 );
  or or_5 (or_5_out, d_ff_2_q, \_2号 );
  or or_6 (or_6_out, d_ff_3_q, \_3号 );
  and and_1 (and_1_out, or_4_out, ~\_1号清零 );  // AND_Gate
  and and_2 (and_2_out, or_5_out, ~\_2号清零信号 );  // AND_Gate
  and and_3 (and_3_out, or_6_out, ~\_3号清零信号 );  // AND_Gate
  D_Flip_Flop #(.trigger("rising"), .Pre_Clr_Positions("LEGACY"), .NegatePresetClear("false"), .enable("true"), .NewFFLayout("false")) IR1 (
    .clk(clk), .D(and_1_out), .Q(\与中断屏蔽位与 ));  // open: Qn, preset, en, reset
  D_Flip_Flop #(.trigger("rising"), .Pre_Clr_Positions("LEGACY"), .NegatePresetClear("false"), .enable("true"), .NewFFLayout("false")) IR2 (
    .clk(clk), .D(and_2_out), .Q(\_2号 ));  // open: Qn, preset, en, reset
  D_Flip_Flop #(.trigger("rising"), .Pre_Clr_Positions("LEGACY"), .NegatePresetClear("false"), .enable("true"), .NewFFLayout("false")) IR3 (
    .clk(clk), .D(and_3_out), .Q(\_3号 ));  // open: Qn, preset, en, reset

  // Notes on the sheet:
  //   Reset 
  //   Reset 
  //   Reset 
endmodule

module \井字棋  (
  output RegWrite,
  output MemWrite,
  output [31:0] PC,
  output [31:0] IR,
  output [31:0] RDin,
  output [31:0] MDin,
  output [31:0] R1,
  output [31:0] R2
);

  wire and_1_out, and_2_out, and_3_out, and_4_out, and_5_out, and_7_out, and_8_out, and_9_out, and_10_out,
       and_13_out, beq, BGEZ, bne, clear, CLK, comparator_1_eq, comparator_2_eq, comparator_3_eq,
       comparator_4_eq, comparator_5_eq, comparator_6_eq, comparator_7_eq, comparator_8_eq, comparator_9_eq,
       ctrl_disp, demultiplexer_1_out1, demultiplexer_1_out2, demultiplexer_1_out3, demultiplexer_1_out4,
       demultiplexer_1_out5, demultiplexer_1_out6, demultiplexer_1_out7, demultiplexer_1_out8,
       demultiplexer_1_out9, ERET, Go, IR1, IR2, IR3, IR4, IR5, IR6, IR7, IR8, IR9, JAL, JR, jump, LBU,
       not_1_out, not_2_out, not_3_out, not_4_out, not_5_out, not_6_out, not_7_out, not_8_out, not_9_out,
       not_10_out, not_11_out, or_1_out, or_2_out, or_4_out, pcnext, priority_encoder_1_gs, RegDst, RST,
       show1, show2, signalequal, SignedExt, sys_stop, syscall, W1, W2, W3, W4, W5, W6, W7, W8, W9, \中断使能_q ,
       \中断信号 , \井字棋中断信号产生_1__2号 , \井字棋中断信号产生_1__3号 , \井字棋中断信号产生_1__4号 , \井字棋中断信号产生_1__5号 , \井字棋中断信号产生_1__6号 ,
       \井字棋中断信号产生_1__7号 , \井字棋中断信号产生_1__8号 , \井字棋中断信号产生_1__9号 , \井字棋中断信号产生_1_与中断屏蔽位与 , \单周期硬布线控制器_1_alu_src ,
       \单周期硬布线控制器_1_memtoreg ;
  wire [3:0] priority_encoder_1_out, register_6_q, \单周期硬布线控制器_1_alu_op ;
  wire [4:0] multiplexer_12_out, R1_t, R2_t, W_num;
  wire [6:0] keyboard_1_data, multiplexer_6_out, multiplexer_7_out, multiplexer_8_out, multiplexer_9_out,
       multiplexer_13_out, register_1_q, register_2_q, register_3_q, register_4_q, register_5_q;
  wire [7:0] multiplexer_22_out;
  wire [15:0] counter_2_q, counter_3_q, \总周期数 ;
  wire [27:0] pc_4;
  wire [31:0] a0, adder_2_out, bit_extender_1_out, bit_extender_2_out, bit_extender_3_out,
       bit_extender_4_out, EPC, IRS_PC, LedData, mips_alu_1_result, multiplexer_1_out, multiplexer_2_out,
       multiplexer_3_out, multiplexer_4_out, multiplexer_5_out, multiplexer_15_out, multiplexer_16_out,
       multiplexer_17_out, multiplexer_18_out, multiplexer_20_out, multiplexer_21_out, ram_1_data,
       ram_2_data, shifter_1_out;
  wire [31:28] J_PC;

  Button \u_总复位  (.out(RST));
  Button \u_继续运行  (.out(Go));
  Multiplexer #(.select(1), .width(32), .disabled("Z"), .enable("false")) multiplexer_1 (
    .in0({J_PC, pc_4}), .in1(adder_2_out), .out(multiplexer_1_out), .sel(pcnext));
  Multiplexer #(.select(1), .width(32), .disabled("Z"), .enable("false")) multiplexer_2 (
    .in0(multiplexer_1_out), .in1({J_PC, IR[25:0], 2'b00}), .out(multiplexer_2_out), .sel(jump));
  Hex_Digit_Display hex_digit_display_1 (.value(LedData[31:28]));  // open: dp
  Multiplexer #(.select(1), .width(32), .disabled("Z"), .enable("false")) multiplexer_3 (
    .in0(multiplexer_2_out), .in1(a0), .out(multiplexer_3_out), .sel(JR));
  Clock #(.highDuration(1), .lowDuration(1)) clock_1 (.out(CLK));
  Hex_Digit_Display hex_digit_display_2 (.value(LedData[23:20]));  // open: dp
  Hex_Digit_Display hex_digit_display_3 (.value(LedData[27:24]));  // open: dp
  Multiplexer #(.select(1), .width(32), .disabled("Z"), .enable("false")) multiplexer_4 (
    .in0(multiplexer_3_out), .in1(IRS_PC), .out(multiplexer_4_out), .sel(\中断信号 ));
  Multiplexer #(.select(1), .width(32), .disabled("Z"), .enable("false")) multiplexer_5 (
    .in0(multiplexer_4_out), .in1(EPC), .out(multiplexer_5_out), .sel(ERET));
  or or_1 (or_1_out, show1, show2);
  Hex_Digit_Display hex_digit_display_4 (.value(LedData[19:16]));  // open: dp
  Hex_Digit_Display hex_digit_display_5 (.value(LedData[15:12]));  // open: dp
  not not_1 (not_1_out, sys_stop);
  or or_2 (or_2_out, Go, not_1_out);
  Register #(.width(32), .trigger("rising"), .Select("low")) u_PC (
    .D(multiplexer_5_out), .en(or_2_out), .Q(PC), .clk(CLK), .clr(RST));
  Multiplexer #(.select(1), .width(7), .disabled("Z"), .enable("false")) multiplexer_6 (
    .in0({7{1'b0}}), .in1({7{1'b0}}), .out(multiplexer_6_out), .sel(show2));
  Hex_Digit_Display hex_digit_display_6 (.value(LedData[7:4]));  // open: dp
  Hex_Digit_Display hex_digit_display_7 (.value(LedData[11:8]));  // open: dp
  // Probe on \总周期数 
  Register #(.width(7), .trigger("rising"), .Select("low")) register_1 (
    .D(multiplexer_6_out), .en(or_1_out), .Q(register_1_q), .clk(CLK));  // open: clr
  Multiplexer #(.select(1), .width(7), .disabled("Z"), .enable("false")) multiplexer_7 (
    .in0({7{1'b0}}), .in1(7'b0101110), .out(multiplexer_7_out), .sel(show2));
  Hex_Digit_Display hex_digit_display_8 (.value(LedData[3:0]));  // open: dp
  Adder #(.width(32)) adder_1 (.a(PC), .b(32'h4), .out({J_PC, pc_4}));  // open: cin, cout
  Register #(.width(7), .trigger("rising"), .Select("low")) register_2 (
    .D(multiplexer_7_out), .en(or_1_out), .Q(register_2_q), .clk(CLK));  // open: clr
  Multiplexer #(.select(1), .width(7), .disabled("Z"), .enable("false")) multiplexer_8 (
    .in0(7'b0111110), .in1(7'b0101010), .out(multiplexer_8_out), .sel(show2));
  // Mips_Probe mips_probe_1: pin names not known; wires that end beside it: IR
  ROM #(.addrWidth(11), .dataWidth(32), .Select("high")) rom_1 (.addr(PC[12:2]), .data(IR));
  Register #(.width(7), .trigger("rising"), .Select("low")) register_3 (
    .D(multiplexer_8_out), .en(or_1_out), .Q(register_3_q), .clk(CLK));  // open: clr
  Multiplexer #(.select(1), .width(7), .disabled("Z"), .enable("false")) multiplexer_9 (
    .in0({7{1'b0}}), .in1(7'b0111010), .out(multiplexer_9_out), .sel(show2));
  Multiplexer #(.select(1), .width(5), .disabled("Z"), .enable("false")) multiplexer_10 (
    .in0(IR[25:21]), .in1(5'b00100), .out(R1_t), .sel(syscall));
  Multiplexer #(.select(1), .width(5), .disabled("Z"), .enable("false")) multiplexer_11 (
    .in0(IR[20:16]), .in1(5'b00010), .out(R2_t), .sel(syscall));
  Multiplexer #(.select(1), .width(5), .disabled("Z"), .enable("false")) multiplexer_12 (
    .in0(IR[20:16]), .in1(IR[15:11]), .out(multiplexer_12_out), .sel(RegDst));
  Register #(.width(7), .trigger("rising"), .Select("low")) register_4 (
    .D(multiplexer_9_out), .en(or_1_out), .Q(register_4_q), .clk(CLK));  // open: clr
  Multiplexer #(.select(1), .width(7), .disabled("Z"), .enable("false")) multiplexer_13 (
    .in0({7{1'b0}}), .in1({7{1'b0}}), .out(multiplexer_13_out), .sel(show2));
  \单周期硬布线控制器  \u_单周期硬布线控制器_1  (
    .Func(IR[5:0]), .OP(IR[31:26]), .ALU_OP(\单周期硬布线控制器_1_alu_op ), .MemToReg(\单周期硬布线控制器_1_memtoreg ),
    .MemWrite(MemWrite), .ALU_SRC(\单周期硬布线控制器_1_alu_src ), .RegWrite(RegWrite), .SysCALL(syscall),
    .SignedExt(SignedExt), .RegDst(RegDst), .JR(JR), .JMP(jump), .Beq(beq), .JAL(JAL), .Bne(bne),
    .BGEZ(BGEZ), .LBU(LBU));  // open: XORI, SLTIU
  Multiplexer #(.select(1), .width(5), .disabled("Z"), .enable("false")) multiplexer_14 (
    .in0(multiplexer_12_out), .in1({5{1'b1}}), .out(W_num), .sel(JAL));
  Register #(.width(7), .trigger("rising"), .Select("low")) register_5 (
    .D(multiplexer_13_out), .en(or_1_out), .Q(register_5_q), .clk(CLK));  // open: clr
  MIPS_Regifile mips_regifile_1 (
    .Din(RDin), .Clk(CLK), .R1(a0), .R2(MDin), .WE(RegWrite), .W_num(W_num), .R1_num(R1_t), .R2_num(R2_t));
  assign bit_extender_1_out = {{16{IR[15]}}, IR[15:0]};  // Bit_Extender bit_extender_1
  assign bit_extender_2_out = {{16{1'b0}}, IR[15:0]};  // Bit_Extender bit_extender_2
  not not_2 (not_2_out, signalequal);
  not not_3 (not_3_out, mips_alu_1_result[0]);
  Multiplexer #(.select(1), .width(32), .disabled("Z"), .enable("false")) multiplexer_15 (
    .in0(MDin), .in1(multiplexer_16_out), .out(multiplexer_15_out), .sel(\单周期硬布线控制器_1_alu_src ));
  Multiplexer #(.select(1), .width(32), .disabled("Z"), .enable("false")) multiplexer_16 (
    .in0(bit_extender_2_out), .in1(bit_extender_1_out), .out(multiplexer_16_out), .sel(SignedExt));
  Shifter #(.width(32), .shift("ll")) shifter_1 (.in(bit_extender_1_out), .\dist (5'b00010), .out(shifter_1_out));
  and and_1 (and_1_out, not_3_out, BGEZ);
  and and_2 (and_2_out, signalequal, beq);
  and and_3 (and_3_out, not_2_out, bne);
  Multiplexer #(.select(1), .width(32), .disabled("Z"), .enable("false")) multiplexer_17 (
    .in0(multiplexer_15_out), .in1({32{1'b0}}), .out(multiplexer_17_out), .sel(BGEZ));
  Adder #(.width(32)) adder_2 (.a(shifter_1_out), .b({J_PC, pc_4}), .out(adder_2_out));  // open: cin, cout
  Keyboard #(.Char_bit_width(7), .buflen(32), .trigger("rising")) keyboard_1 (
    .clk(CLK), .re(1'b1), .data(keyboard_1_data));  // open: clr, avail
  Button _1 (.out(IR1));
  Button _4 (.out(IR4));
  Button _7 (.out(IR7));
  or or_3 (pcnext, and_1_out, and_2_out, and_3_out);
  MIPS_ALU mips_alu_1 (
    .X(a0), .Y(multiplexer_17_out), .AluOP(\单周期硬布线控制器_1_alu_op ), .Equal(signalequal),
    .Result(mips_alu_1_result), .shamt(IR[10:6]));  // open: Result_2
  assign bit_extender_3_out = {{25{1'b0}}, keyboard_1_data};  // Bit_Extender bit_extender_3
  DotMatrix #(.inputtype("column"), .matrixcols(5), .matrixrows(7), .persist(0), .dotshape("square")) dotmatrix_1 (
    .col0(register_1_q), .col1(register_2_q), .col2(register_3_q), .col3(register_4_q), .col4(register_5_q));
  Button _2 (.out(IR2));
  Button _5 (.out(IR5));
  Button _8 (.out(IR8));
  Button _3 (.out(IR3));
  Button _6 (.out(IR6));
  Button _9 (.out(IR9));
  // LCD_Video lcd_video_1: pin names not known; wires that end beside it: clear, CLK, ctrl_disp, a0[22:16], a0[6:0], {16{1'b1}}
  RAM #(.addrWidth(10), .dataWidth(32), .bus("separate"), .Select("high")) ram_1 (
    .addr(mips_alu_1_result[11:2]), .din(MDin), .data(ram_1_data), .str(MemWrite), .sel(1'b1), .clk(CLK),
    .clr(RST));  // open: ld
  RAM #(.addrWidth(10), .dataWidth(32), .bus("separate"), .Select("high")) ram_2 (
    .addr(mips_alu_1_result[11:2]), .din(bit_extender_3_out), .data(ram_2_data), .str(MemWrite), .sel(1'b1),
    .clk(CLK));  // open: ld, clr
  LED #(.active("true")) led_1 (.in(W1));
  LED #(.active("true")) led_2 (.in(W4));
  LED #(.active("true")) led_3 (.in(W7));
  Multiplexer #(.select(1), .width(32), .disabled("Z"), .enable("false")) multiplexer_18 (
    .in0(ram_1_data), .in1(ram_2_data), .out(multiplexer_18_out), .sel(mips_alu_1_result[12]));
  Multiplexer #(.select(1), .width(32), .disabled("Z"), .enable("false")) multiplexer_19 (
    .in0(multiplexer_21_out), .in1({J_PC, pc_4}), .out(RDin), .sel(JAL));
  LED #(.active("true")) led_4 (.in(W2));
  LED #(.active("true")) led_5 (.in(W5));
  LED #(.active("true")) led_6 (.in(W8));
  Multiplexer #(.select(1), .width(32), .disabled("Z"), .enable("false")) multiplexer_20 (
    .in0(mips_alu_1_result), .in1(multiplexer_18_out), .out(multiplexer_20_out), .sel(\单周期硬布线控制器_1_memtoreg ));
  Multiplexer #(.select(1), .width(32), .disabled("Z"), .enable("false")) multiplexer_21 (
    .in0(multiplexer_20_out), .in1(bit_extender_4_out), .out(multiplexer_21_out), .sel(LBU));
  LED #(.active("true")) led_7 (.in(W3));
  LED #(.active("true")) led_8 (.in(W6));
  LED #(.active("true")) led_9 (.in(W9));
  Multiplexer #(.select(2), .width(8), .disabled("Z"), .enable("false")) multiplexer_22 (
    .in0(multiplexer_20_out[7:0]), .in1(multiplexer_20_out[15:8]), .in2(multiplexer_20_out[23:16]),
    .in3(multiplexer_20_out[31:24]), .out(multiplexer_22_out), .sel(mips_alu_1_result[1:0]));
  assign bit_extender_4_out = {{24{1'b0}}, multiplexer_22_out};  // Bit_Extender bit_extender_4
  not not_4 (not_4_out, sys_stop);
  not not_5 (not_5_out, signalequal);
  // Probe on RDin
  Counter #(.width(16), .max('hffff), .ongoal("wrap"), .trigger("rising"), .behavior("old")) counter_1 (
    .D({16{1'b0}}), .count(not_4_out), .Q(\总周期数 ), .clk(CLK), .clr(RST));  // open: load, carry, preset
  or or_4 (or_4_out, and_5_out, and_4_out);
  and and_4 (and_4_out, signalequal, beq);
  and and_5 (and_5_out, not_5_out, bne);
  // Probe on \总周期数 
  Counter #(.width(16), .max('hffff), .ongoal("wrap"), .trigger("rising"), .behavior("old")) counter_2 (
    .D({16{1'b0}}), .count(or_4_out), .Q(counter_2_q), .clk(CLK), .clr(RST));  // open: load, carry, preset
  // Probe on counter_2_q
  Comparator #(.width(32), .mode("twosComplement")) comparator_1 (
    .a(MDin), .b(32'h22), .eq(comparator_1_eq));  // open: gt, lt
  Comparator #(.width(32), .mode("twosComplement")) comparator_2 (
    .a(MDin), .b(32'h1), .eq(comparator_2_eq));  // open: gt, lt
  not not_6 (not_6_out, comparator_1_eq);
  not not_7 (not_7_out, comparator_2_eq);
  Comparator #(.width(32), .mode("twosComplement")) comparator_3 (
    .a(MDin), .b(32'h2), .eq(comparator_3_eq));  // open: gt, lt
  not not_8 (not_8_out, comparator_3_eq);
  Comparator #(.width(32), .mode("twosComplement")) comparator_4 (
    .a(MDin), .b(32'h4d), .eq(comparator_4_eq));  // open: gt, lt
  not not_9 (not_9_out, comparator_4_eq);
  \井字棋中断信号产生  \u_井字棋中断信号产生_1  (
    .clk(CLK), .\_1号中断 (IR1), .\_1号中断等待指示灯 (W1), .\_2号中断 (IR2), .\_2号中断等待指示灯 (W2), .\_3号中断 (IR3),
    .\_3号中断等待指示灯 (W3), .\_4号中断 (IR4), .\_4号中断等待指示灯 (W4), .\_5号中断 (IR5), .\_5号中断等待指示灯 (W5), .\_6号中断 (IR6),
    .\_6号中断等待指示灯 (W6), .\_7号中断 (IR7), .\_7号中断等待指示灯 (W7), .\_8号中断 (IR8), .\_8号中断等待指示灯 (W8), .\_9号中断 (IR9),
    .\_9号中断等待指示灯 (W9), .\与中断屏蔽位与 (\井字棋中断信号产生_1_与中断屏蔽位与 ), .\_2号 (\井字棋中断信号产生_1__2号 ),
    .\_3号 (\井字棋中断信号产生_1__3号 ), .\_4号 (\井字棋中断信号产生_1__4号 ), .\_5号 (\井字棋中断信号产生_1__5号 ),
    .\_6号 (\井字棋中断信号产生_1__6号 ), .\_7号 (\井字棋中断信号产生_1__7号 ), .\_8号 (\井字棋中断信号产生_1__8号 ),
    .\_9号 (\井字棋中断信号产生_1__9号 ), .\_7号清零 (demultiplexer_1_out7), .\_8号清零信号 (demultiplexer_1_out8),
    .\_9号清零信号 (demultiplexer_1_out9), .\_1号清零 (demultiplexer_1_out1), .\_2号清零信号 (demultiplexer_1_out2),
    .\_3号清零信号 (demultiplexer_1_out3), .\_4号清零 (demultiplexer_1_out4), .\_5号清零信号 (demultiplexer_1_out5),
    .\_6号清零信号 (demultiplexer_1_out6));
  // RegisterFile registerfile_1: pin names not known; wires that end beside it: RDin, CLK, RegWrite, W_num, R1_t, R2_t, R1, R2
  and and_6 (ctrl_disp, syscall, comparator_1_eq);
  and and_7 (and_7_out, syscall, not_6_out);
  and and_8 (and_8_out, syscall, not_7_out);
  and and_9 (and_9_out, syscall, not_8_out);
  and and_10 (and_10_out, syscall, not_9_out);
  Comparator #(.width(6), .mode("twosComplement")) comparator_5 (
    .a(IR[31:26]), .b(6'b010000), .eq(comparator_5_eq));  // open: gt, lt
  Comparator #(.width(6), .mode("twosComplement")) comparator_6 (
    .a(IR[5:0]), .b(6'b011000), .eq(comparator_6_eq));  // open: gt, lt
  // Probe on counter_3_q
  Counter #(.width(16), .max('hffff), .ongoal("wrap"), .trigger("rising"), .behavior("old")) counter_3 (
    .D({16{1'b0}}), .count(jump), .Q(counter_3_q), .clk(CLK), .clr(RST));  // open: load, carry, preset
  and and_11 (sys_stop, and_7_out, and_8_out, and_9_out, and_10_out);
  Demultiplexer #(.select(4), .width(1), .tristate("false"), .disabled(0), .enable("true")) demultiplexer_1 (
    .out1(demultiplexer_1_out1), .out2(demultiplexer_1_out2), .out3(demultiplexer_1_out3),
    .out4(demultiplexer_1_out4), .out5(demultiplexer_1_out5), .out6(demultiplexer_1_out6),
    .out7(demultiplexer_1_out7), .out8(demultiplexer_1_out8), .out9(demultiplexer_1_out9), .in(ERET),
    .sel(register_6_q), .en(priority_encoder_1_gs));  // open: out0, out10, out11, out12, out13, out14, out15
  and and_12 (ERET, comparator_5_eq, comparator_6_eq);
  Priority_Encoder #(.select(4), .disabled("Z")) priority_encoder_1 (
    .in1(\井字棋中断信号产生_1_与中断屏蔽位与 ), .in2(\井字棋中断信号产生_1__2号 ), .in3(\井字棋中断信号产生_1__3号 ), .in4(\井字棋中断信号产生_1__4号 ),
    .in5(\井字棋中断信号产生_1__5号 ), .in6(\井字棋中断信号产生_1__6号 ), .in7(\井字棋中断信号产生_1__7号 ), .in8(\井字棋中断信号产生_1__8号 ),
    .in9(\井字棋中断信号产生_1__9号 ), .out(priority_encoder_1_out), .gs(priority_encoder_1_gs));  // open: in0, in10, in11, in12, in13, in14, in15, en_out, en_in
  Multiplexer #(.select(4), .width(32), .disabled("Z"), .enable("false")) multiplexer_23 (
    .in1(32'h4), .in2(32'h8), .in3(32'hc), .in4(32'h10), .in5(32'h14), .in6(32'h18), .in7(32'h1c),
    .in8(32'h20), .in9(32'h24), .out(IRS_PC), .sel(priority_encoder_1_out));  // open: in0, in10, in11, in12, in13, in14, in15
  Comparator #(.width(32), .mode("twosComplement")) comparator_7 (
    .a(MDin), .b(32'h1), .eq(comparator_7_eq));  // open: gt, lt
  Comparator #(.width(32), .mode("twosComplement")) comparator_8 (
    .a(MDin), .b(32'h2), .eq(comparator_8_eq));  // open: gt, lt
  Comparator #(.width(32), .mode("twosComplement")) comparator_9 (
    .a(MDin), .b(32'h4d), .eq(comparator_9_eq));  // open: gt, lt
  Register #(.width(4), .trigger("rising"), .Select("low")) register_6 (
    .D(priority_encoder_1_out), .en(\中断信号 ), .Q(register_6_q), .clk(CLK));  // open: clr
  Register #(.width(1), .trigger("rising"), .Select("low")) \u_中断使能  (
    .D(priority_encoder_1_gs), .Q(\中断使能_q ), .clk(CLK), .clr(ERET));  // open: en
  not not_10 (not_10_out, ERET);
  not not_11 (not_11_out, \中断使能_q );
  // Probe on PC
  and and_13 (and_13_out, \中断信号 , not_10_out);
  and and_14 (show1, syscall, comparator_7_eq);
  and and_15 (show2, syscall, comparator_8_eq);
  and and_16 (clear, syscall, comparator_9_eq);
  and and_17 (\中断信号 , priority_encoder_1_gs, not_11_out);
  // Probe on EPC
  Register #(.width(32), .trigger("rising"), .Select("low")) u_EPC (
    .D(PC), .en(and_13_out), .Q(EPC), .clk(CLK));  // open: clr

  // Other names for the same wires on the sheet: J_PC[27:2] = IR[25:0]; pc_4[31:28] = J_PC; JR_PC[31:0] = a0;
  //   v0[31:0] = MDin

  // Notes on the sheet:
  //   总复位信号应将除ROM以外所有存储组件全部清零
  //   数码管输出
  //   数码管输出应该用寄存器锁存，否则显示数据只能一闪而过
  //   指令存储器
  //   OP
  //   rs
  //   指令字
  //   contents of rom_1 (hex, n*v repeats v):
  //   810000a 81000d6 8100130 810018a 81001e4 810023e 8100298 81002f2 810034c 81003a6 20090010 200a0010
  //   200b0070 21240000 42400 8a2020 20020022 c 20020020 114b0002 214a0001 810000d 20090010 200a0010
  //   200b0070 21240000 42400 8a2020 20020022 c 20020020 112b0002 21290001 8100019 20090070 200a0010
  //   200b0070 21240000 42400 8a2020 20020022 c 20020020 114b0002 214a0001 8100025 20090010 200a0070
  //   200b0070 21240000 42400 8a2020 20020022 c 20020020 112b0002 21290001 8100031 20090030 200a0010
  //   200b0070 21240000 42400 8a2020 20020022 c 20020020 114b0002 214a0001 810003d 20090050 200a0010
  //   200b0070 21240000 42400 8a2020 20020022 c 20020020 114b0002 214a0001 8100049 20090010 200a0030
  //   200b0070 21240000 42400 8a2020 20020022 c 20020020 112b0002 21290001 8100055 20090010 200a0050
  //   200b0070 21240000 42400 8a2020 20020022 c 20020020 112b0002 21290001 8100061 20080000 20110000
  //   20090000 200a0000 200b0000 200c0000 200d0000 200e0000 200f0000 20180000 20190000 20010009 10280001
  //   8100075 2002004d c 20020000 20090010 200a0010 200b0070 21240000 42400 8a2020 20020022 c 20020020
  //   114b0002 214a0001 810007e 20090010 200a0010 200b0070 21240000 42400 8a2020 20020022 c 20020020
  //   112b0002 21290001 810008a 20090070 200a0010 200b0070 21240000 42400 8a2020 20020022 c 20020020
  //   114b0002 214a0001 8100096 20090010 200a0070 200b0070 21240000 42400 8a2020 20020022 c 20020020
  //   112b0002 21290001 81000a2 20090030 200a0030 21240000 42400 8a2020 20020022 c 20020020 20090050
  //   200a0030 21240000 42400 8a2020 20020022 c 20020020 20090030 200a0050 200b0040 21240000 42400 8a2020
  //   20020022 c 20020020 112b0003 21290001 214a0001 81000be 20090040 200a0060 200b0050 21240000 42400
  //   8a2020 20020022 c 20020020 112b0003 21290001 214affff 81000cb c 15200057 16200020 20020001 c
  //   20020000 20110001 21080001 20090001 20120018 20130018 20140028 22440000 42400 932020 20020022 c
  //   20020020 12540003 22520001 22730001 81000e1 20120018 20130028 20140028 22440000 42400 932020
  //   20020022 c 20020020 12540039 22520001 2273ffff 81000ee 20020002 c 20020000 20110000 21080001
  //   20090002 20120018 20130018 20140028 22440000 42400 932020 20020022 c 20020020 12540002 22520001
  //   8100101 20120018 20130028 20140028 22440000 42400 932020 20020022 c 20020020 12540002 22520001
  //   810010d 20120028 20130018 20140028 22440000 42400 932020 20020022 c 20020020 12740002 22730001
  //   8100119 20120018 20130018 20140028 22440000 42400 932020 20020022 c 20020020 12740002 22730001
  //   8100125 c1003fa 42000018 15400057 16200020 20020001 c 20020000 20110001 21080001 200a0001 20120038
  //   20130018 20140048 22440000 42400 932020 20020022 c 20020020 12540003 22520001 22730001 810013b
  //   20120038 20130028 20140048 22440000 42400 932020 20020022 c 20020020 12540039 22520001 2273ffff
  //   8100148 20020002 c 20020000 20110000 21080001 200a0002 20120038 20130018 20140048 22440000 42400
  //   932020 20020022 c 20020020 12540002 22520001 810015b 20120038 20130028 20140048 22440000 42400
  //   932020 20020022 c 20020020 12540002 22520001 8100167 20120038 20130018 20140028 22440000 42400
  //   932020 20020022 c 20020020 12740002 22730001 8100173 20120048 20130018 20140028 22440000 42400
  //   932020 20020022 c 20020020 12740002 22730001 810017f c1003fa 42000018 15600057 16200020 20020001 c
  //   20020000 20110001 21080001 200b0001 20120058 20130018 20140068 22440000 42400 932020 20020022 c
  //   20020020 12540003 22520001 22730001 8100195 20120058 20130028 20140068 22440000 42400 932020
  //   20020022 c 20020020 12540039 22520001 2273ffff 81001a2 20020002 c 20020000 20110000 21080001
  //   200b0002 20120058 20130018 20140068 22440000 42400 932020 20020022 c 20020020 12540002 22520001
  //   81001b5 20120058 20130028 20140068 22440000 42400 932020 20020022 c 20020020 12540002 22520001
  //   81001c1 20120058 20130018 20140028 22440000 42400 932020 20020022 c 20020020 12740002 22730001
  //   81001cd 20120068 20130018 20140028 22440000 42400 932020 20020022 c 20020020 12740002 22730001
  //   81001d9 c1003fa 42000018 15800057 16200020 20020001 c 20020000 20110001 21080001 200c0001 20120018
  //   20130038 20140028 22440000 42400 932020 20020022 c 20020020 12540003 22520001 22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
  //   rt
  //   rd
  //   JMP
  //   JR
  //   OP
  //   Func
  //   Func
  //   Beq
  //   Bne
  //   AluOP
  //   AluSrcB
  //   RegWrite
  //   JAL
  //   RegDst
  //   Syscall
  //   为方便自动评测，需要输出PC，IR，寄存器文件写入端口RDin，内存写入端口MDin等信号
  //   MemToReg
  //   MemWrite
  //   syscall 调用判断
  //   寄存器组内容显示
  //   周期数计算
  //   条件分支数
  //   中断返回判断
  //   无条件分支数
  //   中断的PC保存
endmodule

module \井字棋中断信号产生  (
  input  clk,
  input  \_1号中断 ,
  input  \_1号清零 ,
  input  \_2号中断 ,
  input  \_2号清零信号 ,
  input  \_3号中断 ,
  input  \_3号清零信号 ,
  input  \_4号中断 ,
  input  \_4号清零 ,
  input  \_5号中断 ,
  input  \_5号清零信号 ,
  input  \_6号中断 ,
  input  \_6号清零信号 ,
  input  \_7号中断 ,
  input  \_7号清零 ,
  input  \_8号中断 ,
  input  \_8号清零信号 ,
  input  \_9号中断 ,
  input  \_9号清零信号 ,
  output \与中断屏蔽位与 ,
  output \_1号中断等待指示灯 ,
  output \_2号 ,
  output \_2号中断等待指示灯 ,
  output \_3号 ,
  output \_3号中断等待指示灯 ,
  output \_4号 ,
  output \_4号中断等待指示灯 ,
  output \_5号 ,
  output \_5号中断等待指示灯 ,
  output \_6号 ,
  output \_6号中断等待指示灯 ,
  output \_7号 ,
  output \_7号中断等待指示灯 ,
  output \_8号 ,
  output \_8号中断等待指示灯 ,
  output \_9号 ,
  output \_9号中断等待指示灯 
);

  wire and_1_out, and_2_out, and_3_out, and_4_out, and_5_out, and_6_out, and_7_out, and_8_out, and_9_out,
       d_ff_1_q, d_ff_2_q, d_ff_3_q, d_ff_4_q, d_ff_5_q, d_ff_6_q, d_ff_7_q, d_ff_8_q, d_ff_9_q, or_10_out,
       or_11_out, or_12_out, or_13_out, or_14_out, or_15_out, or_16_out, or_17_out, or_18_out;

  or or_1 (\_1号中断等待指示灯 , \与中断屏蔽位与 , d_ff_1_q);
  or or_2 (\_2号中断等待指示灯 , \_2号 , d_ff_2_q);
  or or_3 (\_3号中断等待指示灯 , \_3号 , d_ff_3_q);
  or or_4 (\_4号中断等待指示灯 , \_4号 , d_ff_4_q);
  or or_5 (\_5号中断等待指示灯 , \_5号 , d_ff_5_q);
  or or_6 (\_6号中断等待指示灯 , \_6号 , d_ff_6_q);
  or or_7 (\_7号中断等待指示灯 , \_7号 , d_ff_7_q);
  or or_8 (\_8号中断等待指示灯 , \_8号 , d_ff_8_q);
  or or_9 (\_9号中断等待指示灯 , \_9号 , d_ff_9_q);
  D_Flip_Flop #(.trigger("rising"), .Pre_Clr_Positions("LEGACY"), .NegatePresetClear("false"), .enable("true"), .NewFFLayout("false")) d_ff_1 (
    .clk(\_1号中断 ), .D(1'b1), .Q(d_ff_1_q), .reset(\与中断屏蔽位与 ));  // open: Qn, preset, en
  D_Flip_Flop #(.trigger("rising"), .Pre_Clr_Positions("LEGACY"), .NegatePresetClear("false"), .enable("true"), .NewFFLayout("false")) d_ff_2 (
    .clk(\_2号中断 ), .D(1'b1), .Q(d_ff_2_q), .reset(\_2号 ));  // open: Qn, preset, en
  D_Flip_Flop #(.trigger("rising"), .Pre_Clr_Positions("LEGACY"), .NegatePresetClear("false"), .enable("true"), .NewFFLayout("false")) d_ff_3 (
    .clk(\_3号中断 ), .D(1'b1), .Q(d_ff_3_q), .reset(\_3号 ));  // open: Qn, preset, en
  D_Flip_Flop #(.trigger("rising"), .Pre_Clr_Positions("LEGACY"), .NegatePresetClear("false"), .enable("true"), .NewFFLayout("false")) d_ff_4 (
    .clk(\_4号中断 ), .D(1'b1), .Q(d_ff_4_q), .reset(\_4号 ));  // open: Qn, preset, en
  D_Flip_Flop #(.trigger("rising"), .Pre_Clr_Positions("LEGACY"), .NegatePresetClear("false"), .enable("true"), .NewFFLayout("false")) d_ff_5 (
    .clk(\_5号中断 ), .D(1'b1), .Q(d_ff_5_q), .reset(\_5号 ));  // open: Qn, preset, en
  D_Flip_Flop #(.trigger("rising"), .Pre_Clr_Positions("LEGACY"), .NegatePresetClear("false"), .enable("true"), .NewFFLayout("false")) d_ff_6 (
    .clk(\_6号中断 ), .D(1'b1), .Q(d_ff_6_q), .reset(\_6号 ));  // open: Qn, preset, en
  D_Flip_Flop #(.trigger("rising"), .Pre_Clr_Positions("LEGACY"), .NegatePresetClear("false"), .enable("true"), .NewFFLayout("false")) d_ff_7 (
    .clk(\_7号中断 ), .D(1'b1), .Q(d_ff_7_q), .reset(\_7号 ));  // open: Qn, preset, en
  D_Flip_Flop #(.trigger("rising"), .Pre_Clr_Positions("LEGACY"), .NegatePresetClear("false"), .enable("true"), .NewFFLayout("false")) d_ff_8 (
    .clk(\_8号中断 ), .D(1'b1), .Q(d_ff_8_q), .reset(\_8号 ));  // open: Qn, preset, en
  D_Flip_Flop #(.trigger("rising"), .Pre_Clr_Positions("LEGACY"), .NegatePresetClear("false"), .enable("true"), .NewFFLayout("false")) d_ff_9 (
    .clk(\_9号中断 ), .D(1'b1), .Q(d_ff_9_q), .reset(\_9号 ));  // open: Qn, preset, en
  or or_10 (or_10_out, d_ff_1_q, \与中断屏蔽位与 );
  or or_11 (or_11_out, d_ff_2_q, \_2号 );
  or or_12 (or_12_out, d_ff_3_q, \_3号 );
  or or_13 (or_13_out, d_ff_4_q, \_4号 );
  or or_14 (or_14_out, d_ff_5_q, \_5号 );
  or or_15 (or_15_out, d_ff_6_q, \_6号 );
  or or_16 (or_16_out, d_ff_7_q, \_7号 );
  or or_17 (or_17_out, d_ff_8_q, \_8号 );
  or or_18 (or_18_out, d_ff_9_q, \_9号 );
  and and_1 (and_1_out, or_10_out, ~\_1号清零 );  // AND_Gate
  and and_2 (and_2_out, or_11_out, ~\_2号清零信号 );  // AND_Gate
  and and_3 (and_3_out, or_12_out, ~\_3号清零信号 );  // AND_Gate
  and and_4 (and_4_out, or_13_out, ~\_4号清零 );  // AND_Gate
  and and_5 (and_5_out, or_14_out, ~\_5号清零信号 );  // AND_Gate
  and and_6 (and_6_out, or_15_out, ~\_6号清零信号 );  // AND_Gate
  and and_7 (and_7_out, or_16_out, ~\_7号清零 );  // AND_Gate
  and and_8 (and_8_out, or_17_out, ~\_8号清零信号 );  // AND_Gate
  and and_9 (and_9_out, or_18_out, ~\_9号清零信号 );  // AND_Gate
  D_Flip_Flop #(.trigger("rising"), .Pre_Clr_Positions("LEGACY"), .NegatePresetClear("false"), .enable("true"), .NewFFLayout("false")) IR1 (
    .clk(clk), .D(and_1_out), .Q(\与中断屏蔽位与 ));  // open: Qn, preset, en, reset
  D_Flip_Flop #(.trigger("rising"), .Pre_Clr_Positions("LEGACY"), .NegatePresetClear("false"), .enable("true"), .NewFFLayout("false")) IR2 (
    .clk(clk), .D(and_2_out), .Q(\_2号 ));  // open: Qn, preset, en, reset
  D_Flip_Flop #(.trigger("rising"), .Pre_Clr_Positions("LEGACY"), .NegatePresetClear("false"), .enable("true"), .NewFFLayout("false")) IR3 (
    .clk(clk), .D(and_3_out), .Q(\_3号 ));  // open: Qn, preset, en, reset
  D_Flip_Flop #(.trigger("rising"), .Pre_Clr_Positions("LEGACY"), .NegatePresetClear("false"), .enable("true"), .NewFFLayout("false")) IR4 (
    .clk(clk), .D(and_4_out), .Q(\_4号 ));  // open: Qn, preset, en, reset
  D_Flip_Flop #(.trigger("rising"), .Pre_Clr_Positions("LEGACY"), .NegatePresetClear("false"), .enable("true"), .NewFFLayout("false")) IR5 (
    .clk(clk), .D(and_5_out), .Q(\_5号 ));  // open: Qn, preset, en, reset
  D_Flip_Flop #(.trigger("rising"), .Pre_Clr_Positions("LEGACY"), .NegatePresetClear("false"), .enable("true"), .NewFFLayout("false")) IR6 (
    .clk(clk), .D(and_6_out), .Q(\_6号 ));  // open: Qn, preset, en, reset
  D_Flip_Flop #(.trigger("rising"), .Pre_Clr_Positions("LEGACY"), .NegatePresetClear("false"), .enable("true"), .NewFFLayout("false")) IR7 (
    .clk(clk), .D(and_7_out), .Q(\_7号 ));  // open: Qn, preset, en, reset
  D_Flip_Flop #(.trigger("rising"), .Pre_Clr_Positions("LEGACY"), .NegatePresetClear("false"), .enable("true"), .NewFFLayout("false")) IR8 (
    .clk(clk), .D(and_8_out), .Q(\_8号 ));  // open: Qn, preset, en, reset
  D_Flip_Flop #(.trigger("rising"), .Pre_Clr_Positions("LEGACY"), .NegatePresetClear("false"), .enable("true"), .NewFFLayout("false")) IR9 (
    .clk(clk), .D(and_9_out), .Q(\_9号 ));  // open: Qn, preset, en, reset

  // Notes on the sheet:
  //   Reset 
  //   Reset 
  //   Reset 
  //   Reset 
  //   Reset 
  //   Reset 
  //   Reset 
  //   Reset 
  //   Reset 
endmodule
